// Logisim project cpu21-riscv -ccab - branchprediction.circ as structural Verilog: 25 circuits, main circuit ◇单周期RISC-V
module \单周期RISC_V  (
  input  IR1,
  input  IR2,
  input  IR3,
  output RegWrite,
  output MemWrite,
  output [31:0] PC,
  output [31:0] IR,
  output [31:0] RDin,
  output [31:0] MDin,
  output [31:0] LedData
);

  wire alu_1_equal, alu_1_out_4, AluSrc, and_4_out, and_5_out, and_6_out, AUIPC, Branch, CLK, clock_1_out,
       comparator_1_eq, comparator_2_eq, comparator_2_lt, d_ff_1_q, ecall, ecallEq, Go, halt, IR1_t, IR2_t,
       IR3_t, IRA, IRB, IRC, Jal, Jalr, LBU, Mem2Reg, nand_1_out, not_1_out, not_2_out, not_3_out, or_1_out,
       or_6_out, RST, S_type, URET, W1, W2, W3, \单周期硬布线控制器_1_beq , \单周期硬布线控制器_1_bge , \单周期硬布线控制器_1_bne ;
  wire [3:0] \单周期硬布线控制器_1_alu_op ;
  wire [4:0] multiplexer_5_out, multiplexer_6_out, multiplexer_8_out, multiplexer_10_out;
  wire [11:0] multiplexer_4_out;
  wire [12:0] CNT_num;
  wire [15:0] \总周期数 ;
  wire [31:0] a7, ALUresult, bit_extender_1_out, bit_extender_2_out, bit_extender_3_out, bit_extender_4_out,
       BranchPC, jalPC, JalrPC, LBUReasult, multiplexer_1_out, multiplexer_2_out, multiplexer_3_out,
       multiplexer_7_out, multiplexer_9_out, multiplexer_11_out, PC_4, ram_1_data, shifter_1_out,
       shifter_2_out, shifter_3_out, shifter_4_out, shifter_5_out, \U型pc , Write2Reg;

  Button \u_继续运行  (.out(Go));
  Button _1 (.out(IRA));
  Button _2 (.out(IRB));
  Button _3 (.out(IRC));
  Button button_1 (.out(RST));
  LED #(.active("true")) led_1 (.in(W1));
  LED #(.active("true")) led_2 (.in(W2));
  LED #(.active("true")) led_3 (.in(W3));
  Multiplexer #(.select(1), .width(32), .disabled("Z"), .enable("false")) multiplexer_1 (
    .in0(PC_4), .in1(BranchPC), .out(multiplexer_1_out), .sel(Branch));
  Multiplexer #(.select(1), .width(32), .disabled("Z"), .enable("false")) multiplexer_2 (
    .in0(multiplexer_1_out), .in1(jalPC), .out(multiplexer_2_out), .sel(Jal));
  Hex_Digit_Display hex_digit_display_1 (.value(LedData[31:28]));  // open: dp
  or or_1 (or_1_out, not_1_out, Go);
  Multiplexer #(.select(1), .width(32), .disabled("Z"), .enable("false")) multiplexer_3 (
    .in0(multiplexer_2_out), .in1(JalrPC), .out(multiplexer_3_out), .sel(Jalr));
  not not_1 (not_1_out, halt);
  Hex_Digit_Display hex_digit_display_2 (.value(LedData[23:20]));  // open: dp
  Hex_Digit_Display hex_digit_display_3 (.value(LedData[27:24]));  // open: dp
  Register #(.width(32), .trigger("rising"), .Select("low")) u_PC (
    .D(multiplexer_3_out), .en(or_1_out), .Q(PC), .clk(CLK), .clr(RST));
  Adder #(.width(32)) adder_1 (.a(PC), .b(32'h4), .out(PC_4));  // open: cin, cout
  Register #(.width(32), .trigger("rising"), .Select("low")) register_1 (
    .D(MDin), .en(ecallEq), .Q(LedData), .clk(CLK), .clr(RST));
  Hex_Digit_Display hex_digit_display_4 (.value(LedData[15:12]));  // open: dp
  Hex_Digit_Display hex_digit_display_5 (.value(LedData[19:16]));  // open: dp
  // RiscV_Probe riscv_probe_1: pin names not known; wires that end beside it: PC, IR
  Comparator #(.width(32), .mode("twosComplement")) comparator_1 (
    .a(a7), .b(32'h22), .eq(comparator_1_eq));  // open: gt, lt
  Hex_Digit_Display hex_digit_display_6 (.value(LedData[11:8]));  // open: dp
  Hex_Digit_Display hex_digit_display_7 (.value(LedData[7:4]));  // open: dp
  // Probe on \总周期数 
  ROM #(.addrWidth(10), .dataWidth(32), .Select("high")) rom_1 (.addr(PC[11:2]), .data(IR));
  and and_1 (ecallEq, ecall, comparator_1_eq);
  and and_2 (halt, ecall, ~comparator_1_eq);  // AND_Gate
  Hex_Digit_Display hex_digit_display_8 (.value(LedData[3:0]));  // open: dp
  not not_2 (not_2_out, halt);
  Counter #(.width(16), .max('hffff), .ongoal("wrap"), .trigger("rising"), .behavior("new")) counter_1 (
    .count(not_2_out), .Q(\总周期数 ), .clk(CLK), .clr(RST));  // open: load, D, carry, preset, down
  \单周期硬布线控制器  \u_单周期硬布线控制器_1  (
    .Funct({IR[30], IR[25], IR[14:12]}), .OP(IR[6:2]), .ALU_OP(\单周期硬布线控制器_1_alu_op ), .MemToReg(Mem2Reg),
    .MemWrite(MemWrite), .ALU_SRC(AluSrc), .RegWrite(RegWrite), .ecall(ecall), .S_type(S_type), .Jalr(Jalr),
    .Beq(\单周期硬布线控制器_1_beq ), .JAL(Jal), .Bne(\单周期硬布线控制器_1_bne ), .in_3(IR[21]), .uret(URET),
    .BGE(\单周期硬布线控制器_1_bge ), .LBU(LBU), .AUIPC(AUIPC));
  Multiplexer #(.select(1), .width(12), .disabled("Z"), .enable("false")) multiplexer_4 (
    .in0(IR[31:20]), .in1({IR[31:25], IR[11:7]}), .out(multiplexer_4_out), .sel(S_type));
  assign bit_extender_1_out = {{12{IR[31]}}, IR[31:12]};  // Bit_Extender bit_extender_1
  or or_2 (IR1_t, IR1, IRA);
  Multiplexer #(.select(1), .width(5), .disabled("Z"), .enable("false")) multiplexer_5 (
    .in0(IR[19:15]), .in1(5'b10001), .out(multiplexer_5_out), .sel(ecall));
  Multiplexer #(.select(1), .width(5), .disabled("Z"), .enable("false")) multiplexer_6 (
    .in0(IR[24:20]), .in1(5'b01010), .out(multiplexer_6_out), .sel(ecall));
  assign bit_extender_2_out = {{20{IR[31]}}, {IR[31], IR[7], IR[30:25], IR[11:8]}};  // Bit_Extender bit_extender_2
  assign bit_extender_3_out = {{12{IR[31]}}, {IR[31], IR[19:12], IR[20], IR[30:21]}};  // Bit_Extender bit_extender_3
  or or_3 (IR2_t, IR2, IRB);
  Regifile regifile_1 (
    .Din(RDin), .Clk(CLK), .R1(a7), .R2(MDin), .WE(RegWrite), .W_num(IR[11:7]), .R1_num(multiplexer_5_out),
    .R2_num(multiplexer_6_out));
  assign bit_extender_4_out = {{20{multiplexer_4_out[11]}}, multiplexer_4_out};  // Bit_Extender bit_extender_4
  Shifter #(.width(32), .shift("ll")) shifter_1 (.in(bit_extender_2_out), .\dist (5'b00001), .out(shifter_1_out));
  Multiplexer #(.select(1), .width(32), .disabled("Z"), .enable("false")) multiplexer_7 (
    .in0(MDin), .in1(bit_extender_4_out), .out(multiplexer_7_out), .sel(AluSrc));
  Adder #(.width(32)) adder_2 (.a(shifter_1_out), .b(PC), .out(BranchPC));  // open: cin, cout
  or or_4 (IR3_t, IR3, IRC);
  Shifter #(.width(32), .shift("ll")) shifter_2 (.in(bit_extender_3_out), .\dist (5'b00001), .out(shifter_2_out));
  assign JalrPC = ALUresult & 32'hfffffffe;  // AND_Gate and_3, 32 bits wide
  and and_4 (and_4_out, \单周期硬布线控制器_1_beq , alu_1_equal);
  not not_3 (not_3_out, alu_1_equal);
  and and_5 (and_5_out, not_3_out, \单周期硬布线控制器_1_bne );
  ALU alu_1 (
    .X(a7), .Y(multiplexer_7_out), .AluOP(\单周期硬布线控制器_1_alu_op ), .Equal(alu_1_equal), .Result(ALUresult),
    .out_4(alu_1_out_4));  // open: Result_2, out_6
  Adder #(.width(32)) adder_3 (.a(shifter_2_out), .b(PC), .out(jalPC));  // open: cin, cout
  Shifter #(.width(32), .shift("ll")) shifter_3 (.in(bit_extender_1_out), .\dist (5'b01100), .out(shifter_3_out));
  and and_6 (and_6_out, alu_1_out_4, \单周期硬布线控制器_1_bge );
  Adder #(.width(32)) adder_4 (.a(shifter_3_out), .b(PC), .out(\U型pc ));  // open: cin, cout
  or or_5 (Branch, and_4_out, and_6_out, and_5_out);
  Multiplexer #(.select(1), .width(5), .disabled("Z"), .enable("false")) multiplexer_8 (
    .in0(5'b10000), .in1({5{1'b0}}), .out(multiplexer_8_out), .sel(ALUresult[1]));
  Multiplexer #(.select(1), .width(32), .disabled("Z"), .enable("false")) multiplexer_9 (
    .in0(ALUresult), .in1(ram_1_data), .out(multiplexer_9_out), .sel(Mem2Reg));
  RAM #(.addrWidth(10), .dataWidth(32), .bus("separate"), .Select("high")) ram_1 (
    .addr(ALUresult[11:2]), .din(MDin), .data(ram_1_data), .str(MemWrite), .clk(CLK), .clr(RST));  // open: sel, ld
  Shifter #(.width(32), .shift("ll")) shifter_4 (.in(Write2Reg), .\dist (multiplexer_8_out), .out(shifter_4_out));
  or or_6 (or_6_out, Jal, Jalr);
  Shifter #(.width(32), .shift("ll")) shifter_5 (.in(shifter_4_out), .\dist (multiplexer_10_out), .out(shifter_5_out));
  Multiplexer #(.select(1), .width(5), .disabled("Z"), .enable("false")) multiplexer_10 (
    .in0(5'b01000), .in1({5{1'b0}}), .out(multiplexer_10_out), .sel(ALUresult[0]));
  Multiplexer #(.select(1), .width(32), .disabled("Z"), .enable("false")) multiplexer_11 (
    .in0(multiplexer_9_out), .in1(PC_4), .out(multiplexer_11_out), .sel(or_6_out));
  Multiplexer #(.select(1), .width(32), .disabled("Z"), .enable("false")) multiplexer_12 (
    .in0(Write2Reg), .in1(LBUReasult), .out(RDin), .sel(LBU));
  Shifter #(.width(32), .shift("lr")) shifter_6 (.in(shifter_5_out), .\dist (5'b11000), .out(LBUReasult));
  D_Flip_Flop #(.trigger("high"), .Pre_Clr_Positions("LEGACY"), .NegatePresetClear("false"), .enable("true"), .NewFFLayout("false")) d_ff_1 (.Q(d_ff_1_q));  // open: clk, D, Qn, preset, en, reset
  // Probe on 13'h292
  Multiplexer #(.select(1), .width(32), .disabled("Z"), .enable("false")) multiplexer_13 (
    .in0(multiplexer_11_out), .in1(\U型pc ), .out(Write2Reg), .sel(AUIPC));
  Comparator #(.width(13), .mode("twosComplement")) comparator_2 (
    .a(CNT_num), .b(13'h292), .eq(comparator_2_eq), .lt(comparator_2_lt));  // open: gt
  Clock #(.highDuration(1), .lowDuration(1)) clock_1 (.out(clock_1_out));
  Counter #(.width(13), .max('h1fff), .ongoal("stay"), .trigger("rising"), .behavior("old")) counter_2 (
    .count(comparator_2_lt), .Q(CNT_num), .clk(clock_1_out));  // open: load, D, carry, clr, preset
  nand nand_1 (nand_1_out, d_ff_1_q, comparator_2_eq);
  assign CLK = nand_1_out ? clock_1_out : 1'bz;  // Controlled_Buffer controlled_buffer_1
  Pull_Resistor #(.pull(1)) pull_resistor_1 (.node(CLK));

  // Other names for the same wires on the sheet: LBU0 = ALUresult[0]; LBU1 = ALUresult[1]

  // Notes on the sheet:
  //   中断源
  //   中断等待指示
  //   数码管输出应该用寄存器锁存，否则显示数据只能一闪而过
  //   ecall判断相等以及停机
  //   led显示a0
  //   数码管输出
  //   指令探针
  //   指令存储器
  //   指令字
  //   contents of rom_1 (hex, n*v repeats v):
  //   100493 100006f 100493 200913 300993 100006f 100493 200913 300993 100006f 100493 200913 300993
  //   100006f 100493 200913 300993 414000ef 100413 100493 1f49493 900533 2200893 73 24d493 48463 fedff06f
  //   900533 2200893 73 100493 249493 900533 2200893 73 48463 fedff06f 100493 1f49493 900533 2200893 73
  //   4034d493 900533 2200893 73 4044d493 900533 2200893 73 4044d493 900533 2200893 73 4044d493 900533
  //   2200893 73 4044d493 900533 2200893 73 4044d493 900533 2200893 73 4044d493 900533 2200893 73 4044d493
  //   900533 2200893 73 100413 1f41993 41f9d993 433 c00913 300b13 140413 f47413 800293 100313 499993
  //   89e9b3 1300533 2200893 73 406282b3 fe0294e3 140413 f00f93 1f47433 1c41413 800293 100313 49d993
  //   89e9b3 1300533 2200893 73 406282b3 fe0294e3 1c45413 406b0b33 b0463 f95ff06f 2b3 fff2c293 829293
  //   ff2e293 500533 2200893 73 fff00413 493 84a023 140413 448493 84a023 140413 448493 84a023 140413
  //   448493 84a023 140413 448493 84a023 140413 448493 84a023 140413 448493 84a023 140413 448493 84a023
  //   140413 448493 84a023 140413 448493 84a023 140413 448493 84a023 140413 448493 84a023 140413 448493
  //   84a023 140413 448493 84a023 140413 448493 84a023 140413 448493 84a023 140413 448493 140413 433
  //   3c00493 42983 4aa03 149a2b3 28663 134a023 1442023 ffc48493 fe9412e3 800533 2200893 73 440413 3c00493
  //   fc9416e3 a00893 73 100293 300313 800493 849493 7648493 1449493 900533 2200893 73 800e13 54d4b3
  //   64d4b3 900533 2200893 73 fffe0e13 fe0e14e3 a00893 73 13 430497 900533 2200893 73 430497 900533
  //   2200893 73 430497 900533 2200893 73 430497 900533 2200893 73 430497 900533 2200893 73 430497 900533
  //   2200893 73 430497 900533 2200893 73 430497 900533 2200893 73 a00893 73 313 1000e13 8400493 849493
  //   8348493 400913 891913 490913 849493 8248493 849493 8148493 891913 490913 891913 490913 932023
  //   12484b3 430313 fffe0e13 fe0e18e3 2000e13 313 34483 900533 2200893 73 130313 fffe0e13 fe0e14e3 a00893
  //   73 f00493 900533 2200893 73 fff48493 fe04d8e3 a00893 73 413 140413 800533 2200893 73 240413 800533
  //   2200893 73 340413 800533 2200893 73 440413 800533 2200893 73 540413 800533 2200893 73 640413 800533
  //   2200893 73 740413 800533 2200893 73 840413 800533 2200893 2200893 73 8067
  //   ecall暂停，统计周期
  //   JAL
  //   JALR
  //   URET
  //   I型imm
  //   U型imm
  //   Beq
  //   Bge
  //   Bne
  //   MemToReg
  //   MemWrite
  //   AluOP
  //   AluSrcB
  //   RegWrite
  //   S型imm
  //   B型imm
  //   J型imm
  //   ecall等待go按键
  //   jalr最低位置0
  //   lbu取字节
  //   为方便自动评测，需要输出PC，IR，寄存器堆写如数据RDin
  //   数据存储器
  //   RAM写使能MemWrite、RAM写入数据MDin等信号
  //   控制位
  //   暂停节拍，不能为0
  //   戳工具置1进入计数暂停模式，ctrl+k时钟自动运行到对应节拍暂停
  //   ctrl+k关闭时钟连续运行，将控制位置零，进入单步调试模式调试
  //   用这个时钟源需要去掉电路中的其他时钟源
  //   可计数暂停的时钟源
endmodule

// 单周期硬布线控制器
module \单周期硬布线控制器  (
  input  [4:0] OP,
  input  [4:0] Funct,
  input  in_3,
  output [3:0] ALU_OP,
  output uret,
  output MemToReg,
  output ecall,
  output MemWrite,
  output ALU_SRC,
  output RegWrite,
  output S_type,
  output Beq,
  output Bne,
  output Jalr,
  output JAL,
  output BGE,
  output LBU,
  output AUIPC
);

  wire \控制信号自动生成_1_ecall ;

  \运算控制器自动生成  \u_运算控制器自动生成_1  (
    .OP2(OP[0]), .OP3(OP[1]), .OP4(OP[2]), .OP5(OP[3]), .OP6(OP[4]), .F12(Funct[0]), .F13(Funct[1]),
    .F14(Funct[2]), .F25(Funct[3]), .F30(Funct[4]), .S0(ALU_OP[0]), .S1(ALU_OP[1]), .S2(ALU_OP[2]),
    .S3(ALU_OP[3]));
  \控制信号自动生成  \u_控制信号自动生成_1  (
    .OP2(OP[0]), .OP3(OP[1]), .OP4(OP[2]), .OP5(OP[3]), .MemToReg(MemToReg), .OP6(OP[4]), .F12(Funct[0]),
    .F13(Funct[1]), .F14(Funct[2]), .F25(Funct[3]), .F30(Funct[4]), .MemWrite(MemWrite), .ALU_SRC(ALU_SRC),
    .RegWrite(RegWrite), .ecall(\控制信号自动生成_1_ecall ), .S_Type(S_type), .BEQ(Beq), .BNE(Bne), .JALR(Jalr),
    .JAL(JAL), .BGE(BGE), .LBU(LBU), .AUIPC(AUIPC));
  and and_1 (uret, in_3, \控制信号自动生成_1_ecall );
  and and_2 (ecall, ~in_3, \控制信号自动生成_1_ecall );  // AND_Gate

  // Other names for the same wires on the sheet: IR21 = in_3; OP_CODE[4:0] = OP

  // Notes on the sheet:
  //   运算器控制器，根据指令生成运算器功能选择信号
  //   控制信号生成，产生数据通路需要的其他控制信号
endmodule

// 运算器控制器
module \运算控制器自动生成  (
  input  OP2,
  input  OP3,
  input  OP4,
  input  OP5,
  input  OP6,
  input  F12,
  input  F13,
  input  F14,
  input  F25,
  input  F30,
  output S0,
  output S1,
  output S2,
  output S3
);

  wire and_1_out, and_2_out, and_3_out, and_4_out, and_5_out, and_6_out, and_7_out, and_8_out, and_9_out,
       and_10_out, and_11_out, and_12_out, and_13_out, and_14_out, and_15_out, and_16_out, and_17_out,
       and_18_out, and_19_out, and_20_out, and_21_out, and_22_out, and_23_out, and_24_out, and_25_out,
       and_26_out, and_27_out, and_28_out, and_29_out, and_30_out, and_31_out, and_32_out, and_33_out,
       and_34_out, and_35_out, and_36_out, not_1_out, not_2_out, not_3_out, not_4_out, not_5_out, not_6_out,
       not_7_out, not_8_out, not_9_out, not_10_out, not_11_out, not_12_out, not_13_out, not_14_out,
       not_15_out, not_16_out, not_17_out, not_18_out, not_19_out, not_20_out, not_21_out, not_22_out,
       not_23_out, not_24_out, not_25_out, not_26_out, not_27_out, not_28_out, not_29_out, not_30_out,
       not_31_out, not_32_out, not_33_out, not_34_out, not_35_out, not_36_out, not_37_out, not_38_out,
       not_39_out, not_40_out, not_41_out, not_42_out, not_43_out, not_44_out, not_45_out, not_46_out,
       not_47_out, not_48_out, not_49_out, not_50_out, not_51_out, not_52_out, not_53_out, not_54_out,
       not_55_out, not_56_out, not_57_out, not_58_out, not_59_out, not_60_out, not_61_out, not_62_out,
       not_63_out, not_64_out, not_65_out, not_66_out, not_67_out, not_68_out, not_69_out, not_70_out,
       not_71_out, not_72_out, not_73_out, not_74_out, not_75_out, not_76_out, not_77_out, not_78_out,
       not_79_out, not_80_out, not_81_out, not_82_out, not_83_out, not_84_out, not_85_out, not_86_out,
       not_87_out, not_88_out, not_89_out, not_90_out, not_91_out, not_92_out, not_93_out, not_94_out,
       not_95_out, not_96_out, not_97_out, not_98_out, not_99_out, not_100_out, not_101_out, not_102_out,
       not_103_out, not_104_out, not_105_out, not_106_out, not_107_out, not_108_out, not_109_out,
       not_110_out, not_111_out, not_112_out, not_113_out, not_114_out, not_115_out, not_116_out,
       not_117_out, not_118_out, not_119_out, not_120_out, not_121_out, not_122_out, not_123_out,
       not_124_out, not_125_out, not_126_out, not_127_out, not_128_out, not_129_out, not_130_out,
       not_131_out, not_132_out, not_133_out, not_134_out, not_135_out, not_136_out, not_137_out,
       not_138_out, not_139_out, not_140_out, not_141_out, not_142_out, not_143_out, not_144_out,
       not_145_out, not_146_out, not_147_out, not_148_out, not_149_out, not_150_out, not_151_out,
       not_152_out, not_153_out, not_154_out, not_155_out, not_156_out, not_157_out, not_158_out,
       not_159_out, not_160_out, not_161_out, not_162_out, not_163_out, not_164_out, not_165_out,
       not_166_out, not_167_out, not_168_out, not_169_out, not_170_out, not_171_out, not_172_out,
       not_173_out, not_174_out, not_175_out, not_176_out, not_177_out, not_178_out, not_179_out,
       not_180_out, not_181_out, not_182_out, not_183_out, not_184_out, not_185_out, not_186_out,
       not_187_out, not_188_out, not_189_out, not_190_out, not_191_out, not_192_out, not_193_out,
       not_194_out, not_195_out, not_196_out, not_197_out, not_198_out, not_199_out, not_200_out,
       not_201_out, not_202_out, not_203_out, not_204_out, not_205_out, not_206_out, not_207_out,
       not_208_out, not_209_out;

  not not_1 (not_1_out, OP2);
  not not_2 (not_2_out, OP3);
  not not_3 (not_3_out, OP5);
  not not_4 (not_4_out, OP6);
  not not_5 (not_5_out, F12);
  not not_6 (not_6_out, F13);
  not not_7 (not_7_out, OP2);
  not not_8 (not_8_out, OP3);
  not not_9 (not_9_out, OP4);
  not not_10 (not_10_out, OP6);
  not not_11 (not_11_out, F12);
  not not_12 (not_12_out, F14);
  not not_13 (not_13_out, OP2);
  not not_14 (not_14_out, OP3);
  not not_15 (not_15_out, OP6);
  not not_16 (not_16_out, F12);
  not not_17 (not_17_out, F14);
  not not_18 (not_18_out, F25);
  not not_19 (not_19_out, F30);
  not not_20 (not_20_out, OP3);
  not not_21 (not_21_out, OP5);
  not not_22 (not_22_out, OP6);
  not not_23 (not_23_out, F12);
  not not_24 (not_24_out, F14);
  not not_25 (not_25_out, OP3);
  not not_26 (not_26_out, OP5);
  not not_27 (not_27_out, OP6);
  not not_28 (not_28_out, F13);
  not not_29 (not_29_out, F25);
  not not_30 (not_30_out, OP2);
  not not_31 (not_31_out, OP3);
  not not_32 (not_32_out, OP6);
  not not_33 (not_33_out, F25);
  not not_34 (not_34_out, F30);
  not not_35 (not_35_out, OP3);
  not not_36 (not_36_out, OP5);
  not not_37 (not_37_out, OP6);
  not not_38 (not_38_out, OP2);
  not not_39 (not_39_out, OP3);
  not not_40 (not_40_out, F12);
  not not_41 (not_41_out, F13);
  not not_42 (not_42_out, F14);
  not not_43 (not_43_out, F25);
  not not_44 (not_44_out, F30);
  not not_45 (not_45_out, OP3);
  not not_46 (not_46_out, OP4);
  not not_47 (not_47_out, F12);
  not not_48 (not_48_out, F13);
  not not_49 (not_49_out, F14);
  not not_50 (not_50_out, OP3);
  not not_51 (not_51_out, OP5);
  not not_52 (not_52_out, OP6);
  not not_53 (not_53_out, F25);
  not not_54 (not_54_out, F14);
  not not_55 (not_55_out, F13);
  not not_56 (not_56_out, F12);
  not not_57 (not_57_out, OP6);
  not not_58 (not_58_out, OP3);
  not not_59 (not_59_out, OP2);
  not not_60 (not_60_out, F30);
  not not_61 (not_61_out, F25);
  not not_62 (not_62_out, OP6);
  not not_63 (not_63_out, OP3);
  not not_64 (not_64_out, OP2);
  not not_65 (not_65_out, F30);
  not not_66 (not_66_out, F25);
  not not_67 (not_67_out, F14);
  not not_68 (not_68_out, F12);
  not not_69 (not_69_out, OP6);
  not not_70 (not_70_out, OP3);
  not not_71 (not_71_out, OP2);
  not not_72 (not_72_out, OP6);
  not not_73 (not_73_out, OP5);
  not not_74 (not_74_out, OP3);
  not not_75 (not_75_out, OP2);
  not not_76 (not_76_out, F14);
  not not_77 (not_77_out, F12);
  not not_78 (not_78_out, OP6);
  not not_79 (not_79_out, OP5);
  not not_80 (not_80_out, OP3);
  not not_81 (not_81_out, OP2);
  not not_82 (not_82_out, F30);
  not not_83 (not_83_out, F25);
  not not_84 (not_84_out, F13);
  not not_85 (not_85_out, OP6);
  not not_86 (not_86_out, OP5);
  not not_87 (not_87_out, OP3);
  not not_88 (not_88_out, OP2);
  not not_89 (not_89_out, F30);
  not not_90 (not_90_out, F25);
  not not_91 (not_91_out, F14);
  not not_92 (not_92_out, F13);
  not not_93 (not_93_out, F12);
  not not_94 (not_94_out, OP3);
  not not_95 (not_95_out, OP2);
  not not_96 (not_96_out, F30);
  not not_97 (not_97_out, F25);
  not not_98 (not_98_out, F13);
  not not_99 (not_99_out, OP6);
  not not_100 (not_100_out, OP3);
  not not_101 (not_101_out, OP2);
  not not_102 (not_102_out, F30);
  not not_103 (not_103_out, F25);
  not not_104 (not_104_out, F14);
  not not_105 (not_105_out, F13);
  not not_106 (not_106_out, F12);
  not not_107 (not_107_out, OP6);
  not not_108 (not_108_out, OP3);
  not not_109 (not_109_out, OP2);
  not not_110 (not_110_out, F25);
  not not_111 (not_111_out, F14);
  not not_112 (not_112_out, F13);
  not not_113 (not_113_out, F12);
  not not_114 (not_114_out, OP6);
  not not_115 (not_115_out, OP3);
  not not_116 (not_116_out, OP2);
  not not_117 (not_117_out, F30);
  not not_118 (not_118_out, F25);
  not not_119 (not_119_out, OP6);
  not not_120 (not_120_out, OP3);
  not not_121 (not_121_out, OP2);
  not not_122 (not_122_out, F30);
  not not_123 (not_123_out, F25);
  not not_124 (not_124_out, F14);
  not not_125 (not_125_out, OP6);
  not not_126 (not_126_out, OP3);
  not not_127 (not_127_out, OP2);
  not not_128 (not_128_out, F14);
  not not_129 (not_129_out, F13);
  not not_130 (not_130_out, F12);
  not not_131 (not_131_out, OP6);
  not not_132 (not_132_out, OP5);
  not not_133 (not_133_out, OP3);
  not not_134 (not_134_out, OP2);
  not not_135 (not_135_out, OP6);
  not not_136 (not_136_out, OP5);
  not not_137 (not_137_out, OP3);
  not not_138 (not_138_out, OP2);
  not not_139 (not_139_out, F14);
  not not_140 (not_140_out, F12);
  not not_141 (not_141_out, OP6);
  not not_142 (not_142_out, OP5);
  not not_143 (not_143_out, OP4);
  not not_144 (not_144_out, OP3);
  not not_145 (not_145_out, OP2);
  not not_146 (not_146_out, F14);
  not not_147 (not_147_out, F12);
  not not_148 (not_148_out, OP6);
  not not_149 (not_149_out, OP4);
  not not_150 (not_150_out, OP3);
  not not_151 (not_151_out, OP2);
  not not_152 (not_152_out, F14);
  not not_153 (not_153_out, F13);
  not not_154 (not_154_out, F12);
  not not_155 (not_155_out, OP4);
  not not_156 (not_156_out, OP3);
  not not_157 (not_157_out, OP6);
  not not_158 (not_158_out, OP5);
  not not_159 (not_159_out, OP3);
  not not_160 (not_160_out, F13);
  not not_161 (not_161_out, F12);
  not not_162 (not_162_out, OP6);
  not not_163 (not_163_out, OP5);
  not not_164 (not_164_out, OP4);
  not not_165 (not_165_out, OP3);
  not not_166 (not_166_out, OP2);
  not not_167 (not_167_out, F30);
  not not_168 (not_168_out, F25);
  not not_169 (not_169_out, F12);
  not not_170 (not_170_out, OP6);
  not not_171 (not_171_out, OP3);
  not not_172 (not_172_out, OP2);
  not not_173 (not_173_out, F30);
  not not_174 (not_174_out, F25);
  not not_175 (not_175_out, F14);
  not not_176 (not_176_out, F12);
  not not_177 (not_177_out, OP6);
  not not_178 (not_178_out, OP3);
  not not_179 (not_179_out, OP2);
  not not_180 (not_180_out, F30);
  not not_181 (not_181_out, F25);
  not not_182 (not_182_out, F14);
  not not_183 (not_183_out, OP6);
  not not_184 (not_184_out, OP3);
  not not_185 (not_185_out, OP2);
  not not_186 (not_186_out, F12);
  not not_187 (not_187_out, OP6);
  not not_188 (not_188_out, OP5);
  not not_189 (not_189_out, OP3);
  not not_190 (not_190_out, OP2);
  not not_191 (not_191_out, F13);
  not not_192 (not_192_out, F12);
  not not_193 (not_193_out, OP6);
  not not_194 (not_194_out, OP5);
  not not_195 (not_195_out, OP3);
  not not_196 (not_196_out, OP2);
  not not_197 (not_197_out, F14);
  not not_198 (not_198_out, F12);
  not not_199 (not_199_out, OP6);
  not not_200 (not_200_out, OP5);
  not not_201 (not_201_out, OP3);
  not not_202 (not_202_out, OP2);
  not not_203 (not_203_out, F30);
  not not_204 (not_204_out, F25);
  not not_205 (not_205_out, F14);
  not not_206 (not_206_out, F13);
  not not_207 (not_207_out, F12);
  not not_208 (not_208_out, OP3);
  not not_209 (not_209_out, OP2);
  and and_1 (and_1_out, not_1_out, not_2_out, not_3_out, not_4_out, not_5_out, not_6_out, F14);
  and and_2 (and_2_out, not_7_out, not_8_out, not_9_out, not_10_out, not_11_out, F13, not_12_out);
  and and_3 (and_3_out, not_13_out, not_14_out, OP4, not_15_out, not_16_out, not_17_out, not_18_out, not_19_out);
  and and_4 (and_4_out, not_20_out, OP4, not_21_out, not_22_out, not_23_out, not_24_out);
  and and_5 (and_5_out, not_25_out, OP4, not_26_out, not_27_out, not_28_out, F14, not_29_out, F30);
  and and_6 (and_6_out, not_30_out, not_31_out, OP4, not_32_out, F12, F13, F14, not_33_out, not_34_out);
  and and_7 (and_7_out, not_35_out, OP4, not_36_out, not_37_out, F12, F13, F14);
  and and_8 (and_8_out, not_38_out, not_39_out, OP4, OP5, not_40_out, not_41_out, not_42_out, not_43_out, not_44_out);
  and and_9 (and_9_out, OP2, not_45_out, not_46_out, OP5, OP6, not_47_out, not_48_out, not_49_out);
  and and_10 (and_10_out, OP2, not_50_out, OP4, not_51_out, not_52_out);
  and and_11 (and_11_out, F30, not_53_out, not_54_out, not_55_out, not_56_out, not_57_out, OP5, OP4, not_58_out, not_59_out);
  and and_12 (and_12_out, not_60_out, not_61_out, F14, F13, F12, not_62_out, OP5, OP4, not_63_out, not_64_out);
  and and_13 (and_13_out, not_65_out, not_66_out, not_67_out, F13, not_68_out, not_69_out, OP5, OP4, not_70_out, not_71_out);
  and and_14 (and_14_out, F14, F13, F12, not_72_out, not_73_out, OP4, not_74_out, not_75_out);
  and and_15 (and_15_out, not_76_out, F13, not_77_out, not_78_out, not_79_out, OP4, not_80_out, not_81_out);
  and and_16 (and_16_out, not_82_out, not_83_out, F14, not_84_out, F12, not_85_out, not_86_out, OP4, not_87_out, not_88_out);
  and and_17 (and_17_out, not_89_out, not_90_out, not_91_out, not_92_out, not_93_out, OP6, OP5, OP4, not_94_out, not_95_out);
  and and_18 (and_18_out, not_96_out, not_97_out, F14, not_98_out, F12, not_99_out, OP5, OP4, not_100_out, not_101_out);
  and and_19 (and_19_out, not_102_out, not_103_out, not_104_out, not_105_out, not_106_out, not_107_out, OP5, OP4, not_108_out, not_109_out);
  and and_20 (and_20_out, F30, not_110_out, not_111_out, not_112_out, not_113_out, not_114_out, OP5, OP4, not_115_out, not_116_out);
  and and_21 (and_21_out, not_117_out, not_118_out, F14, F13, F12, not_119_out, OP5, OP4, not_120_out, not_121_out);
  and and_22 (and_22_out, not_122_out, not_123_out, not_124_out, F13, F12, not_125_out, OP5, OP4, not_126_out, not_127_out);
  and and_23 (and_23_out, not_128_out, not_129_out, not_130_out, not_131_out, not_132_out, OP4, not_133_out, not_134_out);
  and and_24 (and_24_out, F14, F13, F12, not_135_out, not_136_out, OP4, not_137_out, not_138_out);
  and and_25 (and_25_out, not_139_out, F13, not_140_out, not_141_out, not_142_out, not_143_out, not_144_out, not_145_out);
  and and_26 (and_26_out, not_146_out, F13, not_147_out, not_148_out, OP5, not_149_out, not_150_out, not_151_out);
  and and_27 (and_27_out, not_152_out, not_153_out, not_154_out, OP6, OP5, not_155_out, not_156_out, OP2);
  and and_28 (and_28_out, not_157_out, not_158_out, OP4, not_159_out, OP2);
  and and_29 (and_29_out, F14, not_160_out, not_161_out, not_162_out, not_163_out, not_164_out, not_165_out, not_166_out);
  and and_30 (and_30_out, not_167_out, not_168_out, F14, F13, not_169_out, not_170_out, OP5, OP4, not_171_out, not_172_out);
  and and_31 (and_31_out, not_173_out, not_174_out, not_175_out, F13, not_176_out, not_177_out, OP5, OP4, not_178_out, not_179_out);
  and and_32 (and_32_out, not_180_out, not_181_out, not_182_out, F13, F12, not_183_out, OP5, OP4, not_184_out, not_185_out);
  and and_33 (and_33_out, F14, F13, not_186_out, not_187_out, not_188_out, OP4, not_189_out, not_190_out);
  and and_34 (and_34_out, F14, not_191_out, not_192_out, not_193_out, not_194_out, OP4, not_195_out, not_196_out);
  and and_35 (and_35_out, not_197_out, F13, not_198_out, not_199_out, not_200_out, OP4, not_201_out, not_202_out);
  and and_36 (and_36_out, not_203_out, not_204_out, not_205_out, not_206_out, not_207_out, OP6, OP5, OP4, not_208_out, not_209_out);
  or or_1 (S0, and_1_out, and_2_out, and_3_out, and_4_out, and_5_out, and_6_out, and_7_out, and_8_out, and_9_out, and_10_out);
  or or_2 (S1, and_11_out, and_12_out, and_13_out, and_14_out, and_15_out, and_16_out, and_17_out, and_18_out);
  or or_3 (S2, and_19_out, and_20_out, and_21_out, and_22_out, and_23_out, and_24_out, and_25_out, and_26_out, and_27_out, and_28_out, and_29_out);
  or or_4 (S3, and_30_out, and_31_out, and_32_out, and_33_out, and_34_out, and_35_out, and_36_out);
endmodule

// 控制信号生成
module \控制信号自动生成  (
  input  OP2,
  input  OP3,
  input  OP4,
  input  OP5,
  input  OP6,
  input  F12,
  input  F13,
  input  F14,
  input  F25,
  input  F30,
  output MemToReg,
  output MemWrite,
  output ALU_SRC,
  output RegWrite,
  output ecall,
  output S_Type,
  output BEQ,
  output BNE,
  output JALR,
  output JAL,
  output BGE,
  output LBU,
  output AUIPC
);

  wire and_1_out, and_2_out, and_4_out, and_5_out, and_6_out, and_7_out, and_8_out, and_9_out, and_10_out,
       and_11_out, and_12_out, and_13_out, and_14_out, and_15_out, and_16_out, and_17_out, and_18_out,
       and_19_out, and_20_out, and_21_out, and_22_out, and_23_out, and_24_out, and_25_out, and_26_out,
       and_27_out, and_28_out, and_29_out, and_30_out, and_31_out, and_32_out, and_33_out, and_34_out,
       and_35_out, not_1_out, not_2_out, not_3_out, not_4_out, not_5_out, not_6_out, not_7_out, not_8_out,
       not_9_out, not_10_out, not_11_out, not_12_out, not_13_out, not_14_out, not_15_out, not_16_out,
       not_17_out, not_18_out, not_19_out, not_20_out, not_21_out, not_22_out, not_23_out, not_24_out,
       not_25_out, not_26_out, not_27_out, not_28_out, not_29_out, not_30_out, not_31_out, not_32_out,
       not_33_out, not_34_out, not_35_out, not_36_out, not_37_out, not_38_out, not_39_out, not_40_out,
       not_41_out, not_42_out, not_43_out, not_44_out, not_45_out, not_46_out, not_47_out, not_48_out,
       not_49_out, not_50_out, not_51_out, not_52_out, not_53_out, not_54_out, not_55_out, not_56_out,
       not_57_out, not_58_out, not_59_out, not_60_out, not_61_out, not_62_out, not_63_out, not_64_out,
       not_65_out, not_66_out, not_67_out, not_68_out, not_69_out, not_70_out, not_71_out, not_72_out,
       not_73_out, not_74_out, not_75_out, not_76_out, not_77_out, not_78_out, not_79_out, not_80_out,
       not_81_out, not_82_out, not_83_out, not_84_out, not_85_out, not_86_out, not_87_out, not_88_out,
       not_89_out, not_90_out, not_91_out, not_92_out, not_93_out, not_94_out, not_95_out, not_96_out,
       not_97_out, not_98_out, not_99_out, not_100_out, not_101_out, not_102_out, not_103_out, not_104_out,
       not_105_out, not_106_out, not_107_out, not_108_out, not_109_out, not_110_out, not_111_out,
       not_112_out, not_113_out, not_114_out, not_115_out, not_116_out, not_117_out, not_118_out,
       not_119_out, not_120_out, not_121_out, not_122_out, not_123_out, not_124_out, not_125_out,
       not_126_out, not_127_out, not_128_out, not_129_out, not_130_out, not_131_out, not_132_out,
       not_133_out, not_134_out, not_135_out, not_136_out, not_137_out, not_138_out, not_139_out,
       not_140_out, not_141_out, not_142_out, not_143_out, not_144_out, not_145_out, not_146_out,
       not_147_out, not_148_out, not_149_out, not_150_out, not_151_out, not_152_out, not_153_out,
       not_154_out, not_155_out, not_156_out, not_157_out, not_158_out, not_159_out, not_160_out,
       not_161_out, not_162_out, not_163_out, not_164_out, not_165_out, not_166_out, not_167_out,
       not_168_out, not_169_out, not_170_out, not_171_out, not_172_out, not_173_out, not_174_out,
       not_175_out, not_176_out, not_177_out, not_178_out, not_179_out, not_180_out, not_181_out,
       not_182_out, not_183_out, not_184_out, not_185_out, not_186_out, not_187_out, not_188_out,
       not_189_out, not_190_out, not_191_out, not_192_out, not_193_out, not_194_out, not_195_out,
       not_196_out, not_197_out, not_198_out, not_199_out, not_200_out, not_201_out, not_202_out,
       not_203_out, not_204_out, not_205_out, not_206_out, not_207_out, not_208_out, not_209_out,
       not_210_out, not_211_out, not_212_out, not_213_out, not_214_out, not_215_out, not_216_out,
       not_217_out, not_218_out, not_219_out, not_220_out, not_221_out, not_222_out, not_223_out,
       not_224_out, not_225_out, not_226_out, not_227_out, not_228_out, not_229_out, not_230_out,
       not_231_out, not_232_out, not_233_out, not_234_out, not_235_out, not_236_out, not_237_out,
       not_238_out, not_239_out, not_240_out, not_241_out, not_242_out, not_243_out, not_244_out,
       not_245_out, not_246_out, not_247_out, not_248_out, not_249_out, not_250_out, not_251_out,
       not_252_out, not_253_out, not_254_out, not_255_out;

  not not_1 (not_1_out, F14);
  not not_2 (not_2_out, F12);
  not not_3 (not_3_out, OP6);
  not not_4 (not_4_out, OP5);
  not not_5 (not_5_out, OP4);
  not not_6 (not_6_out, OP3);
  not not_7 (not_7_out, OP2);
  not not_8 (not_8_out, F13);
  not not_9 (not_9_out, F12);
  not not_10 (not_10_out, OP6);
  not not_11 (not_11_out, OP5);
  not not_12 (not_12_out, OP4);
  not not_13 (not_13_out, OP3);
  not not_14 (not_14_out, OP2);
  not not_15 (not_15_out, F14);
  not not_16 (not_16_out, F12);
  not not_17 (not_17_out, OP6);
  not not_18 (not_18_out, OP4);
  not not_19 (not_19_out, OP3);
  not not_20 (not_20_out, OP2);
  not not_21 (not_21_out, F14);
  not not_22 (not_22_out, F13);
  not not_23 (not_23_out, F12);
  not not_24 (not_24_out, OP6);
  not not_25 (not_25_out, OP5);
  not not_26 (not_26_out, OP3);
  not not_27 (not_27_out, OP2);
  not not_28 (not_28_out, OP6);
  not not_29 (not_29_out, OP5);
  not not_30 (not_30_out, OP3);
  not not_31 (not_31_out, OP2);
  not not_32 (not_32_out, F12);
  not not_33 (not_33_out, OP6);
  not not_34 (not_34_out, OP5);
  not not_35 (not_35_out, OP3);
  not not_36 (not_36_out, OP2);
  not not_37 (not_37_out, F13);
  not not_38 (not_38_out, F12);
  not not_39 (not_39_out, OP6);
  not not_40 (not_40_out, OP5);
  not not_41 (not_41_out, OP3);
  not not_42 (not_42_out, OP2);
  not not_43 (not_43_out, F14);
  not not_44 (not_44_out, F12);
  not not_45 (not_45_out, OP6);
  not not_46 (not_46_out, OP5);
  not not_47 (not_47_out, OP3);
  not not_48 (not_48_out, OP2);
  not not_49 (not_49_out, F30);
  not not_50 (not_50_out, F25);
  not not_51 (not_51_out, F14);
  not not_52 (not_52_out, F13);
  not not_53 (not_53_out, OP6);
  not not_54 (not_54_out, OP5);
  not not_55 (not_55_out, OP3);
  not not_56 (not_56_out, OP2);
  not not_57 (not_57_out, F30);
  not not_58 (not_58_out, F25);
  not not_59 (not_59_out, F13);
  not not_60 (not_60_out, OP6);
  not not_61 (not_61_out, OP5);
  not not_62 (not_62_out, OP3);
  not not_63 (not_63_out, OP2);
  not not_64 (not_64_out, F25);
  not not_65 (not_65_out, F13);
  not not_66 (not_66_out, OP6);
  not not_67 (not_67_out, OP5);
  not not_68 (not_68_out, OP3);
  not not_69 (not_69_out, OP2);
  not not_70 (not_70_out, F14);
  not not_71 (not_71_out, F12);
  not not_72 (not_72_out, OP6);
  not not_73 (not_73_out, OP5);
  not not_74 (not_74_out, OP4);
  not not_75 (not_75_out, OP3);
  not not_76 (not_76_out, OP2);
  not not_77 (not_77_out, F14);
  not not_78 (not_78_out, F12);
  not not_79 (not_79_out, OP6);
  not not_80 (not_80_out, OP4);
  not not_81 (not_81_out, OP3);
  not not_82 (not_82_out, OP2);
  not not_83 (not_83_out, F14);
  not not_84 (not_84_out, F13);
  not not_85 (not_85_out, F12);
  not not_86 (not_86_out, OP4);
  not not_87 (not_87_out, OP3);
  not not_88 (not_88_out, F13);
  not not_89 (not_89_out, F12);
  not not_90 (not_90_out, OP6);
  not not_91 (not_91_out, OP5);
  not not_92 (not_92_out, OP4);
  not not_93 (not_93_out, OP3);
  not not_94 (not_94_out, OP2);
  not not_95 (not_95_out, F30);
  not not_96 (not_96_out, F25);
  not not_97 (not_97_out, F14);
  not not_98 (not_98_out, F13);
  not not_99 (not_99_out, F12);
  not not_100 (not_100_out, OP6);
  not not_101 (not_101_out, OP3);
  not not_102 (not_102_out, OP2);
  not not_103 (not_103_out, F25);
  not not_104 (not_104_out, F14);
  not not_105 (not_105_out, F13);
  not not_106 (not_106_out, F12);
  not not_107 (not_107_out, OP6);
  not not_108 (not_108_out, OP3);
  not not_109 (not_109_out, OP2);
  not not_110 (not_110_out, F30);
  not not_111 (not_111_out, F25);
  not not_112 (not_112_out, OP6);
  not not_113 (not_113_out, OP3);
  not not_114 (not_114_out, OP2);
  not not_115 (not_115_out, F30);
  not not_116 (not_116_out, F25);
  not not_117 (not_117_out, F12);
  not not_118 (not_118_out, OP6);
  not not_119 (not_119_out, OP3);
  not not_120 (not_120_out, OP2);
  not not_121 (not_121_out, F30);
  not not_122 (not_122_out, F25);
  not not_123 (not_123_out, F14);
  not not_124 (not_124_out, F12);
  not not_125 (not_125_out, OP6);
  not not_126 (not_126_out, OP3);
  not not_127 (not_127_out, OP2);
  not not_128 (not_128_out, F30);
  not not_129 (not_129_out, F25);
  not not_130 (not_130_out, F14);
  not not_131 (not_131_out, OP6);
  not not_132 (not_132_out, OP3);
  not not_133 (not_133_out, OP2);
  not not_134 (not_134_out, F14);
  not not_135 (not_135_out, F13);
  not not_136 (not_136_out, F12);
  not not_137 (not_137_out, OP6);
  not not_138 (not_138_out, OP5);
  not not_139 (not_139_out, OP3);
  not not_140 (not_140_out, OP2);
  not not_141 (not_141_out, OP6);
  not not_142 (not_142_out, OP5);
  not not_143 (not_143_out, OP3);
  not not_144 (not_144_out, OP2);
  not not_145 (not_145_out, F12);
  not not_146 (not_146_out, OP6);
  not not_147 (not_147_out, OP5);
  not not_148 (not_148_out, OP3);
  not not_149 (not_149_out, OP2);
  not not_150 (not_150_out, F13);
  not not_151 (not_151_out, F12);
  not not_152 (not_152_out, OP6);
  not not_153 (not_153_out, OP5);
  not not_154 (not_154_out, OP3);
  not not_155 (not_155_out, OP2);
  not not_156 (not_156_out, F14);
  not not_157 (not_157_out, F12);
  not not_158 (not_158_out, OP6);
  not not_159 (not_159_out, OP5);
  not not_160 (not_160_out, OP3);
  not not_161 (not_161_out, OP2);
  not not_162 (not_162_out, F30);
  not not_163 (not_163_out, F25);
  not not_164 (not_164_out, F14);
  not not_165 (not_165_out, F13);
  not not_166 (not_166_out, OP6);
  not not_167 (not_167_out, OP5);
  not not_168 (not_168_out, OP3);
  not not_169 (not_169_out, OP2);
  not not_170 (not_170_out, F30);
  not not_171 (not_171_out, F25);
  not not_172 (not_172_out, F13);
  not not_173 (not_173_out, OP6);
  not not_174 (not_174_out, OP5);
  not not_175 (not_175_out, OP3);
  not not_176 (not_176_out, OP2);
  not not_177 (not_177_out, F25);
  not not_178 (not_178_out, F13);
  not not_179 (not_179_out, OP6);
  not not_180 (not_180_out, OP5);
  not not_181 (not_181_out, OP3);
  not not_182 (not_182_out, OP2);
  not not_183 (not_183_out, F14);
  not not_184 (not_184_out, F12);
  not not_185 (not_185_out, OP6);
  not not_186 (not_186_out, OP5);
  not not_187 (not_187_out, OP4);
  not not_188 (not_188_out, OP3);
  not not_189 (not_189_out, OP2);
  not not_190 (not_190_out, OP4);
  not not_191 (not_191_out, F14);
  not not_192 (not_192_out, F13);
  not not_193 (not_193_out, F12);
  not not_194 (not_194_out, OP4);
  not not_195 (not_195_out, OP3);
  not not_196 (not_196_out, F30);
  not not_197 (not_197_out, F25);
  not not_198 (not_198_out, F13);
  not not_199 (not_199_out, OP6);
  not not_200 (not_200_out, OP3);
  not not_201 (not_201_out, OP2);
  not not_202 (not_202_out, OP6);
  not not_203 (not_203_out, OP5);
  not not_204 (not_204_out, OP3);
  not not_205 (not_205_out, F13);
  not not_206 (not_206_out, F12);
  not not_207 (not_207_out, OP6);
  not not_208 (not_208_out, OP5);
  not not_209 (not_209_out, OP4);
  not not_210 (not_210_out, OP3);
  not not_211 (not_211_out, OP2);
  not not_212 (not_212_out, F30);
  not not_213 (not_213_out, F25);
  not not_214 (not_214_out, F14);
  not not_215 (not_215_out, F13);
  not not_216 (not_216_out, F12);
  not not_217 (not_217_out, OP3);
  not not_218 (not_218_out, OP2);
  not not_219 (not_219_out, F14);
  not not_220 (not_220_out, F12);
  not not_221 (not_221_out, OP6);
  not not_222 (not_222_out, OP4);
  not not_223 (not_223_out, OP3);
  not not_224 (not_224_out, OP2);
  not not_225 (not_225_out, F14);
  not not_226 (not_226_out, F13);
  not not_227 (not_227_out, F12);
  not not_228 (not_228_out, OP4);
  not not_229 (not_229_out, OP3);
  not not_230 (not_230_out, OP2);
  not not_231 (not_231_out, F14);
  not not_232 (not_232_out, F13);
  not not_233 (not_233_out, OP4);
  not not_234 (not_234_out, OP3);
  not not_235 (not_235_out, OP2);
  not not_236 (not_236_out, F14);
  not not_237 (not_237_out, F13);
  not not_238 (not_238_out, F12);
  not not_239 (not_239_out, OP4);
  not not_240 (not_240_out, OP3);
  not not_241 (not_241_out, OP4);
  not not_242 (not_242_out, F13);
  not not_243 (not_243_out, OP4);
  not not_244 (not_244_out, OP3);
  not not_245 (not_245_out, OP2);
  not not_246 (not_246_out, F13);
  not not_247 (not_247_out, F12);
  not not_248 (not_248_out, OP6);
  not not_249 (not_249_out, OP5);
  not not_250 (not_250_out, OP4);
  not not_251 (not_251_out, OP3);
  not not_252 (not_252_out, OP2);
  not not_253 (not_253_out, OP6);
  not not_254 (not_254_out, OP5);
  not not_255 (not_255_out, OP3);
  and and_1 (and_1_out, not_1_out, F13, not_2_out, not_3_out, not_4_out, not_5_out, not_6_out, not_7_out);
  and and_2 (and_2_out, F14, not_8_out, not_9_out, not_10_out, not_11_out, not_12_out, not_13_out, not_14_out);
  and and_3 (MemWrite, not_15_out, F13, not_16_out, not_17_out, OP5, not_18_out, not_19_out, not_20_out);
  and and_4 (and_4_out, not_21_out, not_22_out, not_23_out, not_24_out, not_25_out, OP4, not_26_out, not_27_out);
  and and_5 (and_5_out, F14, F13, F12, not_28_out, not_29_out, OP4, not_30_out, not_31_out);
  and and_6 (and_6_out, F14, F13, not_32_out, not_33_out, not_34_out, OP4, not_35_out, not_36_out);
  and and_7 (and_7_out, F14, not_37_out, not_38_out, not_39_out, not_40_out, OP4, not_41_out, not_42_out);
  and and_8 (and_8_out, not_43_out, F13, not_44_out, not_45_out, not_46_out, OP4, not_47_out, not_48_out);
  and and_9 (and_9_out, not_49_out, not_50_out, not_51_out, not_52_out, F12, not_53_out, not_54_out, OP4, not_55_out, not_56_out);
  and and_10 (and_10_out, not_57_out, not_58_out, F14, not_59_out, F12, not_60_out, not_61_out, OP4, not_62_out, not_63_out);
  and and_11 (and_11_out, F30, not_64_out, F14, not_65_out, F12, not_66_out, not_67_out, OP4, not_68_out, not_69_out);
  and and_12 (and_12_out, not_70_out, F13, not_71_out, not_72_out, not_73_out, not_74_out, not_75_out, not_76_out);
  and and_13 (and_13_out, not_77_out, F13, not_78_out, not_79_out, OP5, not_80_out, not_81_out, not_82_out);
  and and_14 (and_14_out, not_83_out, not_84_out, not_85_out, OP6, OP5, not_86_out, not_87_out, OP2);
  and and_15 (and_15_out, F14, not_88_out, not_89_out, not_90_out, not_91_out, not_92_out, not_93_out, not_94_out);
  and and_16 (and_16_out, not_95_out, not_96_out, not_97_out, not_98_out, not_99_out, not_100_out, OP5, OP4, not_101_out, not_102_out);
  and and_17 (and_17_out, F30, not_103_out, not_104_out, not_105_out, not_106_out, not_107_out, OP5, OP4, not_108_out, not_109_out);
  and and_18 (and_18_out, not_110_out, not_111_out, F14, F13, F12, not_112_out, OP5, OP4, not_113_out, not_114_out);
  and and_19 (and_19_out, not_115_out, not_116_out, F14, F13, not_117_out, not_118_out, OP5, OP4, not_119_out, not_120_out);
  and and_20 (and_20_out, not_121_out, not_122_out, not_123_out, F13, not_124_out, not_125_out, OP5, OP4, not_126_out, not_127_out);
  and and_21 (and_21_out, not_128_out, not_129_out, not_130_out, F13, F12, not_131_out, OP5, OP4, not_132_out, not_133_out);
  and and_22 (and_22_out, not_134_out, not_135_out, not_136_out, not_137_out, not_138_out, OP4, not_139_out, not_140_out);
  and and_23 (and_23_out, F14, F13, F12, not_141_out, not_142_out, OP4, not_143_out, not_144_out);
  and and_24 (and_24_out, F14, F13, not_145_out, not_146_out, not_147_out, OP4, not_148_out, not_149_out);
  and and_25 (and_25_out, F14, not_150_out, not_151_out, not_152_out, not_153_out, OP4, not_154_out, not_155_out);
  and and_26 (and_26_out, not_156_out, F13, not_157_out, not_158_out, not_159_out, OP4, not_160_out, not_161_out);
  and and_27 (and_27_out, not_162_out, not_163_out, not_164_out, not_165_out, F12, not_166_out, not_167_out, OP4, not_168_out, not_169_out);
  and and_28 (and_28_out, not_170_out, not_171_out, F14, not_172_out, F12, not_173_out, not_174_out, OP4, not_175_out, not_176_out);
  and and_29 (and_29_out, F30, not_177_out, F14, not_178_out, F12, not_179_out, not_180_out, OP4, not_181_out, not_182_out);
  and and_30 (and_30_out, not_183_out, F13, not_184_out, not_185_out, not_186_out, not_187_out, not_188_out, not_189_out);
  and and_31 (and_31_out, OP6, OP5, not_190_out, OP3, OP2);
  and and_32 (and_32_out, not_191_out, not_192_out, not_193_out, OP6, OP5, not_194_out, not_195_out, OP2);
  and and_33 (and_33_out, not_196_out, not_197_out, F14, not_198_out, F12, not_199_out, OP5, OP4, not_200_out, not_201_out);
  and and_34 (and_34_out, not_202_out, not_203_out, OP4, not_204_out, OP2);
  and and_35 (and_35_out, F14, not_205_out, not_206_out, not_207_out, not_208_out, not_209_out, not_210_out, not_211_out);
  and and_36 (ecall, not_212_out, not_213_out, not_214_out, not_215_out, not_216_out, OP6, OP5, OP4, not_217_out, not_218_out);
  and and_37 (S_Type, not_219_out, F13, not_220_out, not_221_out, OP5, not_222_out, not_223_out, not_224_out);
  and and_38 (BEQ, not_225_out, not_226_out, not_227_out, OP6, OP5, not_228_out, not_229_out, not_230_out);
  and and_39 (BNE, not_231_out, not_232_out, F12, OP6, OP5, not_233_out, not_234_out, not_235_out);
  and and_40 (JALR, not_236_out, not_237_out, not_238_out, OP6, OP5, not_239_out, not_240_out, OP2);
  and and_41 (JAL, OP6, OP5, not_241_out, OP3, OP2);
  and and_42 (BGE, F14, not_242_out, F12, OP6, OP5, not_243_out, not_244_out, not_245_out);
  and and_43 (LBU, F14, not_246_out, not_247_out, not_248_out, not_249_out, not_250_out, not_251_out, not_252_out);
  and and_44 (AUIPC, not_253_out, not_254_out, OP4, not_255_out, OP2);
  or or_1 (MemToReg, and_1_out, and_2_out);
  or or_2 (ALU_SRC, and_4_out, and_5_out, and_6_out, and_7_out, and_8_out, and_9_out, and_10_out, and_11_out, and_12_out, and_13_out, and_14_out, and_15_out);
  or or_3 (RegWrite, and_16_out, and_17_out, and_18_out, and_19_out, and_20_out, and_21_out, and_22_out, and_23_out, and_24_out, and_25_out, and_26_out, and_27_out, and_28_out, and_29_out, and_30_out, and_31_out, and_32_out, and_33_out, and_34_out, and_35_out);
endmodule

// ALU
module ALU (
  input  [31:0] X,
  input  [31:0] Y,
  input  [3:0] AluOP,
  output out_4,
  output Equal,
  output out_6,
  output [31:0] Result,
  output [31:0] Result_2
);

  wire [0:0] comparator_1_lt, comparator_2_lt;
  wire [31:0] adder_1_out, AND_out, divider_1_out, divider_1_rem, multiplier_1_cout, multiplier_1_out,
       NOR_out, OR_out, shifter_1_out, shifter_2_out, shifter_3_out, subtractor_1_out, XOR_out;

  assign AND_out = X & Y;  // AND_Gate AND, 32 bits wide
  assign OR_out = X | Y;  // OR_Gate OR, 32 bits wide
  Shifter #(.width(32), .shift("ll")) shifter_1 (.in(X), .\dist (Y[4:0]), .out(shifter_1_out));
  Shifter #(.width(32), .shift("ar")) shifter_2 (.in(X), .\dist (Y[4:0]), .out(shifter_2_out));
  Shifter #(.width(32), .shift("lr")) shifter_3 (.in(X), .\dist (Y[4:0]), .out(shifter_3_out));
  Multiplier #(.width(32)) multiplier_1 (.a(X), .b(Y), .out(multiplier_1_out), .cout(multiplier_1_cout));  // open: cin
  Divider #(.width(32)) divider_1 (.a(X), .b(Y), .out(divider_1_out), .rem(divider_1_rem));  // open: upper
  Adder #(.width(32)) adder_1 (.a(X), .b(Y), .out(adder_1_out));  // open: cin, cout
  Subtractor #(.width(32)) subtractor_1 (.a(X), .b(Y), .out(subtractor_1_out));  // open: bin, bout
  assign XOR_out = X ^ Y;  // XOR_Gate XOR, 32 bits wide
  assign NOR_out = ~(X | Y);  // NOR_Gate NOR, 32 bits wide
  Comparator #(.width(32), .mode("twosComplement")) comparator_1 (
    .a(X), .b(Y), .eq(Equal), .lt(comparator_1_lt[0]));  // open: gt
  Comparator #(.width(32), .mode("unsigned")) comparator_2 (.a(X), .b(Y), .lt(comparator_2_lt[0]));  // open: gt, eq
  Multiplexer #(.select(4), .width(32), .disabled("Z"), .enable("false")) multiplexer_1 (
    .in0(shifter_1_out), .in1(shifter_2_out), .in2(shifter_3_out), .in3(multiplier_1_out),
    .in4(divider_1_out), .in5(adder_1_out), .in6(subtractor_1_out), .in7(AND_out), .in8(OR_out),
    .in9(XOR_out), .in10(NOR_out), .in11({{31{1'b0}}, comparator_1_lt[0]}),
    .in12({{31{1'b0}}, comparator_2_lt[0]}), .in13({32{1'b0}}), .in14({32{1'b0}}), .in15({32{1'b0}}),
    .out(Result), .sel(AluOP));
  Multiplexer #(.select(4), .width(32), .disabled("Z"), .enable("false")) multiplexer_2 (
    .in0({32{1'b0}}), .in1({32{1'b0}}), .in2({32{1'b0}}), .in3(multiplier_1_cout), .in4(divider_1_rem),
    .in5({32{1'b0}}), .in6({32{1'b0}}), .in7({32{1'b0}}), .in8({32{1'b0}}), .in9({32{1'b0}}),
    .in10({32{1'b0}}), .in11({32{1'b0}}), .in12({32{1'b0}}), .in13({32{1'b0}}), .in14({32{1'b0}}),
    .in15({32{1'b0}}), .out(Result_2), .sel(AluOP));
  Multiplexer #(.select(4), .width(1), .disabled("Z"), .enable("false")) multiplexer_3 (
    .in0(1'b0), .in1(1'b0), .in2(1'b0), .in3(1'b0), .in4(1'b0), .in5(1'b0), .in6(1'b0), .in7(1'b0),
    .in8(1'b0), .in9(1'b0), .in10(1'b0), .in11(comparator_1_lt[0]), .in12(comparator_2_lt[0]), .in13(1'b0),
    .in14(1'b0), .in15(1'b0), .out(out_6), .sel(AluOP));
  not not_1 (out_4, out_6);

  // Other names for the same wires on the sheet: Result2[31:0] = Result_2; S[3:0] = AluOP; tunnel = out_6;
  //   tunnel_t = out_4

  // Notes on the sheet:
  //   不要改变此引脚区域内容，也不要改变ALU封装形式
  //   输入引脚
  //   输出引脚
endmodule

module Regifile (
  input  [31:0] Din,
  input  Clk,
  input  WE,
  input  [4:0] R1_num,
  input  [4:0] W_num,
  input  [4:0] R2_num,
  output [31:0] R1,
  output [31:0] R2
);

  // RegisterFile registerfile_1: pin names not known; wires that end beside it: Din, Clk, WE, W_num, R1_num, R2_num, R1, R2
endmodule

module \理想流水线  (
  output RegWrite,
  output MemWrite,
  output [31:0] IF_PC,
  output [31:0] ID_PC,
  output [31:0] EX_PC,
  output [31:0] M_PC,
  output [31:0] WB_PC,
  output [31:0] RDin,
  output [31:0] MDin,
  output [31:0] LedData
);

  wire alu_1_equal, alu_1_out_4, and_3_out, and_6_out, and_7_out, and_8_out, \B型 , CLK, clock_1_out,
       comparator_1_eq, comparator_2_eq, comparator_2_lt, d_ff_1_q, ecall, ecallEq, ecallFB,
       ex_mem_1_auipc_2, ex_mem_1_ecall_2, ex_mem_1_jal_2, ex_mem_1_jalr_2, ex_mem_1_lbu_2,
       ex_mem_1_mem2reg_2, ex_mem_1_reg_write_2, Go, halt, id_ex_1_alu_src_2, id_ex_1_auipc_2, id_ex_1_beq_2,
       id_ex_1_bge_2, id_ex_1_bne_2, id_ex_1_ecall_2, id_ex_1_lbu_2, id_ex_1_mem2reg_2, id_ex_1_memwrite,
       id_ex_1_reg_write_2, IR1, IR2, IR3, Jal, Jalr, LBU0, LBU1, mem_wb_1_auipc_2, mem_wb_1_ecall_2,
       mem_wb_1_jal_2, mem_wb_1_jalr_2, mem_wb_1_lbu_2, mem_wb_1_mem2reg_2, nand_1_out, not_1_out, not_2_out,
       not_3_out, or_2_out, RST, URET, W1, W2, W3, WB_ecall, \单周期硬布线控制器_1_alu_src , \单周期硬布线控制器_1_auipc ,
       \单周期硬布线控制器_1_beq , \单周期硬布线控制器_1_bge , \单周期硬布线控制器_1_bne , \单周期硬布线控制器_1_ecall , \单周期硬布线控制器_1_jal ,
       \单周期硬布线控制器_1_jalr , \单周期硬布线控制器_1_lbu , \单周期硬布线控制器_1_memtoreg , \单周期硬布线控制器_1_memwrite ,
       \单周期硬布线控制器_1_regwrite , \单周期硬布线控制器_1_s_type , \单周期硬布线控制器_1_uret ;
  wire [3:0] id_ex_1_alu_op_2, \单周期硬布线控制器_1_alu_op ;
  wire [4:0] ex_mem_1_w_2, id_ex_1_w_2, multiplexer_4_out, multiplexer_5_out, multiplexer_7_out,
       multiplexer_9_out, WB_W;
  wire [11:0] multiplexer_6_out;
  wire [12:0] CNT_num;
  wire [15:0] \LoadUse次数 , \总周期数 , \插入气泡数 , \无条件分支数 , \条件分支成功数 ;
  wire [31:0] adder_4_out, ALUresult, bit_extender_1_out, bit_extender_2_out, bit_extender_3_out,
       bit_extender_4_out, BrachPC, BranchPC, EX_IR, ex_mem_1_r1_2, \ex_mem_1_u型_2 , EX_PC_4, EX_R1, EX_R2,
       id_ex_1_brachpc_2, id_ex_1_is_2, id_ex_1_jalpc_2, \id_ex_1_u型_2 , ID_IR, ID_PC_4, IF_IR, IF_PC_4,
       JalPC, JalrPC, LBUReasult, MEM_IR, MEM_PC_4, mem_wb_1_aluresult_2, mem_wb_1_memdata_2,
       mem_wb_1_pc_4_2, \mem_wb_1_u型_2 , multiplexer_1_out, multiplexer_2_out, multiplexer_3_out,
       multiplexer_8_out, multiplexer_10_out, multiplexer_11_out, ram_1_data, regifile_1_r1, regifile_1_r2,
       shifter_1_out, shifter_2_out, shifter_3_out, shifter_4_out, shifter_5_out, WB_IR, WB_R1, WB_R2,
       Write2Reg;
  wire [31:2] ex_mem_1_aluresult_2;

  Button \u_总复位  (.out(RST));
  Button _1 (.out(IR1));
  Button _2 (.out(IR2));
  Button _3 (.out(IR3));
  // Probe on \总周期数 
  // Probe on \总周期数 
  Button \u_继续运行  (.out(Go));
  LED #(.active("true")) led_1 (.in(W1));
  LED #(.active("true")) led_2 (.in(W2));
  LED #(.active("true")) led_3 (.in(W3));
  Hex_Digit_Display hex_digit_display_1 (.value(LedData[31:28]));  // open: dp
  // Probe on IF_PC[19:0]
  // RiscV_Probe riscv_probe_1: pin names not known; wires that end beside it: IF_IR
  Multiplexer #(.select(1), .width(32), .disabled("Z"), .enable("false")) multiplexer_1 (
    .in0(IF_PC_4), .in1(BranchPC), .out(multiplexer_1_out), .sel(\B型 ));
  Multiplexer #(.select(1), .width(32), .disabled("Z"), .enable("false")) multiplexer_2 (
    .in0(multiplexer_1_out), .in1(JalPC), .out(multiplexer_2_out), .sel(Jal));
  Comparator #(.width(32), .mode("twosComplement")) comparator_1 (
    .a(WB_R1), .b(32'h22), .eq(comparator_1_eq));  // open: gt, lt
  Register #(.width(32), .trigger("rising"), .Select("low")) register_1 (
    .D(WB_R2), .en(ecallEq), .Q(LedData), .clk(CLK), .clr(RST));
  Hex_Digit_Display hex_digit_display_2 (.value(LedData[27:24]));  // open: dp
  Hex_Digit_Display hex_digit_display_3 (.value(LedData[23:20]));  // open: dp
  // Probe on ID_PC[19:0]
  // RiscV_Probe riscv_probe_2: pin names not known; wires that end beside it: ID_IR
  not not_1 (not_1_out, halt);
  Multiplexer #(.select(1), .width(32), .disabled("Z"), .enable("false")) multiplexer_3 (
    .in0(multiplexer_2_out), .in1(JalrPC), .out(multiplexer_3_out), .sel(Jalr));
  Hex_Digit_Display hex_digit_display_4 (.value(LedData[19:16]));  // open: dp
  Hex_Digit_Display hex_digit_display_5 (.value(LedData[15:12]));  // open: dp
  Register #(.width(32), .trigger("rising"), .Select("low")) PC (
    .D(multiplexer_3_out), .en(not_1_out), .Q(IF_PC), .clk(CLK), .clr(RST));
  and and_1 (ecallEq, WB_ecall, comparator_1_eq);
  and and_2 (halt, WB_ecall, ~comparator_1_eq);  // AND_Gate
  not not_2 (not_2_out, halt);
  Counter #(.width(16), .max('hffff), .ongoal("wrap"), .trigger("rising"), .behavior("new")) counter_1 (
    .count(not_2_out), .Q(\总周期数 ), .clk(CLK), .clr(RST));  // open: load, D, carry, preset, down
  Hex_Digit_Display hex_digit_display_6 (.value(LedData[7:4]));  // open: dp
  Hex_Digit_Display hex_digit_display_7 (.value(LedData[11:8]));  // open: dp
  // Probe on EX_PC[19:0]
  // RiscV_Probe riscv_probe_3: pin names not known; wires that end beside it: EX_IR
  Adder #(.width(32)) adder_1 (.a(IF_PC), .b(32'h4), .out(IF_PC_4));  // open: cin, cout
  Hex_Digit_Display hex_digit_display_8 (.value(LedData[3:0]));  // open: dp
  ROM #(.addrWidth(10), .dataWidth(32), .Select("high")) rom_1 (.addr(IF_PC[11:2]), .data(IF_IR));
  // Probe on \总周期数 
  // Probe on M_PC[19:0]
  // RiscV_Probe riscv_probe_4: pin names not known; wires that end beside it: MEM_IR
  // RiscV_Probe riscv_probe_5: pin names not known; wires that end beside it: IF_IR, IF_PC_4
  // Probe on \总周期数 
  // Probe on \无条件分支数 
  // Probe on \条件分支成功数 
  // Probe on \插入气泡数 
  // Probe on \LoadUse次数 
  IF_ID if_id_1 (
    .IF_PC(IF_PC), .IF_IR(IF_IR), .IF_PC_4(IF_PC_4), .CLK(CLK), .RST(RST), .ID_PC(ID_PC), .ID_IR(ID_IR),
    .ID_PC_4(ID_PC_4));  // open: halt, PredictBranch, PredictBranch_2
  // Probe on IF_PC[11:0]
  // Probe on WB_PC[19:0]
  // RiscV_Probe riscv_probe_6: pin names not known; wires that end beside it: WB_IR
  and and_3 (and_3_out, Go, halt);
  // Probe on ID_PC[11:0]
  // Probe on EX_PC[11:0]
  Counter #(.width(1), .max('h1), .ongoal("stay"), .trigger("rising"), .behavior("new")) counter_2 (
    .D(and_3_out), .Q(ecallFB), .clk(and_3_out), .clr(RST));  // open: load, count, carry, preset, down
  assign JalrPC = ALUresult & 32'hfffffffe;  // AND_Gate and_4, 32 bits wide
  // Probe on M_PC[11:0]
  D_Flip_Flop #(.trigger("high"), .Pre_Clr_Positions("LEGACY"), .NegatePresetClear("false"), .enable("true"), .NewFFLayout("false")) d_ff_1 (.Q(d_ff_1_q));  // open: clk, D, Qn, preset, en, reset
  // Probe on 13'hc
  \单周期硬布线控制器  \u_单周期硬布线控制器_1  (
    .Funct({ID_IR[30], ID_IR[25], ID_IR[14:12]}), .OP(ID_IR[6:2]), .ALU_OP(\单周期硬布线控制器_1_alu_op ),
    .MemToReg(\单周期硬布线控制器_1_memtoreg ), .MemWrite(\单周期硬布线控制器_1_memwrite ), .ALU_SRC(\单周期硬布线控制器_1_alu_src ),
    .RegWrite(\单周期硬布线控制器_1_regwrite ), .ecall(\单周期硬布线控制器_1_ecall ), .S_type(\单周期硬布线控制器_1_s_type ),
    .Jalr(\单周期硬布线控制器_1_jalr ), .Beq(\单周期硬布线控制器_1_beq ), .JAL(\单周期硬布线控制器_1_jal ), .Bne(\单周期硬布线控制器_1_bne ),
    .in_3(ID_IR[21]), .uret(\单周期硬布线控制器_1_uret ), .BGE(\单周期硬布线控制器_1_bge ), .LBU(\单周期硬布线控制器_1_lbu ),
    .AUIPC(\单周期硬布线控制器_1_auipc ));
  and and_5 (ecall, ~ecallFB, \单周期硬布线控制器_1_ecall );  // AND_Gate
  assign bit_extender_1_out = {{12{ID_IR[31]}}, ID_IR[31:12]};  // Bit_Extender bit_extender_1
  // Probe on WB_PC[11:0]
  Comparator #(.width(13), .mode("twosComplement")) comparator_2 (
    .a(CNT_num), .b(13'hc), .eq(comparator_2_eq), .lt(comparator_2_lt));  // open: gt
  Clock #(.highDuration(1), .lowDuration(1)) clock_1 (.out(clock_1_out));
  Multiplexer #(.select(1), .width(5), .disabled("Z"), .enable("false")) multiplexer_4 (
    .in0(ID_IR[19:15]), .in1(5'b10001), .out(multiplexer_4_out), .sel(ecall));
  Multiplexer #(.select(1), .width(5), .disabled("Z"), .enable("false")) multiplexer_5 (
    .in0(ID_IR[24:20]), .in1(5'b01010), .out(multiplexer_5_out), .sel(ecall));
  Multiplexer #(.select(1), .width(12), .disabled("Z"), .enable("false")) multiplexer_6 (
    .in0(ID_IR[31:20]), .in1({ID_IR[31:25], ID_IR[11:7]}), .out(multiplexer_6_out), .sel(\单周期硬布线控制器_1_s_type ));
  assign bit_extender_2_out = {{20{ID_IR[31]}}, {ID_IR[31], ID_IR[7], ID_IR[30:25], ID_IR[11:8]}};  // Bit_Extender bit_extender_2
  assign bit_extender_3_out = {{12{ID_IR[31]}}, {ID_IR[31], ID_IR[19:12], ID_IR[20], ID_IR[30:21]}};  // Bit_Extender bit_extender_3
  nand nand_1 (nand_1_out, d_ff_1_q, comparator_2_eq);
  Counter #(.width(13), .max('h1fff), .ongoal("stay"), .trigger("rising"), .behavior("old")) counter_3 (
    .count(comparator_2_lt), .Q(CNT_num), .clk(clock_1_out));  // open: load, D, carry, clr, preset
  assign bit_extender_4_out = {{20{multiplexer_6_out[11]}}, multiplexer_6_out};  // Bit_Extender bit_extender_4
  assign CLK = nand_1_out ? clock_1_out : 1'bz;  // Controlled_Buffer controlled_buffer_1
  Regifile regifile_1 (
    .Din(RDin), .Clk(CLK), .R1(regifile_1_r1), .R2(regifile_1_r2), .WE(RegWrite), .W_num(WB_W),
    .R1_num(multiplexer_4_out), .R2_num(multiplexer_5_out));
  Pull_Resistor #(.pull(1)) pull_resistor_1 (.node(CLK));
  ID_EX id_ex_1 (
    .RST(RST), .CLK(CLK), .AUIPC(\单周期硬布线控制器_1_auipc ), .URET(\单周期硬布线控制器_1_uret ), .LBU(\单周期硬布线控制器_1_lbu ),
    .JALR(\单周期硬布线控制器_1_jalr ), .JAL(\单周期硬布线控制器_1_jal ), .Beq(\单周期硬布线控制器_1_beq ), .BGE(\单周期硬布线控制器_1_bge ),
    .BNE(\单周期硬布线控制器_1_bne ), .Mem2Reg(\单周期硬布线控制器_1_memtoreg ), .MenWrite(\单周期硬布线控制器_1_memwrite ),
    .ALU_OP(\单周期硬布线控制器_1_alu_op ), .ALU_SRC(\单周期硬布线控制器_1_alu_src ), .REG_WRITE(\单周期硬布线控制器_1_regwrite ),
    .ECALL(ecall), .PC(ID_PC), .R1(regifile_1_r1), .R2(regifile_1_r2), .IS(bit_extender_4_out), .IR(ID_IR),
    .JalPc(bit_extender_3_out), .BrachPc(bit_extender_2_out), .Pc_4(ID_PC_4), .W(ID_IR[11:7]),
    .\U型 (bit_extender_1_out), .AUIPC_2(id_ex_1_auipc_2), .URET_2(URET), .LBU_2(id_ex_1_lbu_2),
    .JALR_2(Jalr), .JAL_2(Jal), .BEQ_2(id_ex_1_beq_2), .BGE_2(id_ex_1_bge_2), .BNE_2(id_ex_1_bne_2),
    .MEM2REG_2(id_ex_1_mem2reg_2), .MEMWRITE(id_ex_1_memwrite), .ALU_OP_2(id_ex_1_alu_op_2),
    .ALU_SRC_2(id_ex_1_alu_src_2), .REG_WRITE_2(id_ex_1_reg_write_2), .ECALL_2(id_ex_1_ecall_2),
    .PC_2(EX_PC), .R1_2(EX_R1), .R2_2(EX_R2), .IS_2(id_ex_1_is_2), .IR_2(EX_IR), .JalPc_2(id_ex_1_jalpc_2),
    .BrachPc_2(id_ex_1_brachpc_2), .Pc_4_2(EX_PC_4), .W_2(id_ex_1_w_2), .\U型_2 (\id_ex_1_u型_2 ));  // open: halt, R1Fwd, R2Fwd, R1Fwd_2, R2Fwd_2, PredictBranch, PredictBranch_2
  Multiplexer #(.select(1), .width(5), .disabled("Z"), .enable("false")) multiplexer_7 (
    .in0(5'b10000), .in1({5{1'b0}}), .out(multiplexer_7_out), .sel(LBU1));
  Multiplexer #(.select(1), .width(32), .disabled("Z"), .enable("false")) multiplexer_8 (
    .in0(EX_R2), .in1(id_ex_1_is_2), .out(multiplexer_8_out), .sel(id_ex_1_alu_src_2));
  Shifter #(.width(32), .shift("ll")) shifter_1 (.in(Write2Reg), .\dist (multiplexer_7_out), .out(shifter_1_out));
  Shifter #(.width(32), .shift("ll")) shifter_2 (.in(id_ex_1_brachpc_2), .\dist (5'b00001), .out(shifter_2_out));
  Shifter #(.width(32), .shift("ll")) shifter_3 (.in(id_ex_1_jalpc_2), .\dist (5'b00001), .out(shifter_3_out));
  Shifter #(.width(32), .shift("ll")) shifter_4 (.in(shifter_1_out), .\dist (multiplexer_9_out), .out(shifter_4_out));
  Multiplexer #(.select(1), .width(5), .disabled("Z"), .enable("false")) multiplexer_9 (
    .in0(5'b01000), .in1({5{1'b0}}), .out(multiplexer_9_out), .sel(LBU0));
  ALU alu_1 (
    .X(EX_R1), .Y(multiplexer_8_out), .AluOP(id_ex_1_alu_op_2), .Equal(alu_1_equal), .Result(ALUresult),
    .out_4(alu_1_out_4));  // open: Result_2, out_6
  Adder #(.width(32)) adder_2 (.a(shifter_2_out), .b(EX_PC), .out(BrachPC));  // open: cin, cout
  Adder #(.width(32)) adder_3 (.a(shifter_3_out), .b(EX_PC), .out(JalPC));  // open: cin, cout
  Shifter #(.width(32), .shift("ll")) shifter_5 (.in(\id_ex_1_u型_2 ), .\dist (5'b01100), .out(shifter_5_out));
  Adder #(.width(32)) adder_4 (.a(shifter_5_out), .b(EX_PC), .out(adder_4_out));  // open: cin, cout
  Shifter #(.width(32), .shift("lr")) shifter_6 (.in(shifter_4_out), .\dist (5'b11000), .out(LBUReasult));
  and and_6 (and_6_out, id_ex_1_beq_2, alu_1_equal);
  not not_3 (not_3_out, alu_1_equal);
  and and_7 (and_7_out, not_3_out, id_ex_1_bne_2);
  or or_1 (\B型 , and_6_out, and_8_out, and_7_out);
  and and_8 (and_8_out, id_ex_1_bge_2, alu_1_out_4);
  EX_MEM ex_mem_1 (
    .RST(RST), .CLK(CLK), .AUIPC(id_ex_1_auipc_2), .AUIPC_2(ex_mem_1_auipc_2), .LBU(id_ex_1_lbu_2),
    .LBU_2(ex_mem_1_lbu_2), .JALR(Jalr), .JALR_2(ex_mem_1_jalr_2), .JAL(Jal), .JAL_2(ex_mem_1_jal_2),
    .Mem2Reg(id_ex_1_mem2reg_2), .MEM2REG_2(ex_mem_1_mem2reg_2), .MenWrite(id_ex_1_memwrite),
    .MEMWRITE(MemWrite), .REG_WRITE(id_ex_1_reg_write_2), .REG_WRITE_2(ex_mem_1_reg_write_2),
    .ECALL(id_ex_1_ecall_2), .ECALL_2(ex_mem_1_ecall_2), .PC(EX_PC), .PC_2(M_PC), .R1(EX_R1),
    .R1_2(ex_mem_1_r1_2), .R2(EX_R2), .R2_2(MDin), .IR(EX_IR), .IR_2(MEM_IR), .Pc_4(EX_PC_4),
    .Pc_4_2(MEM_PC_4), .W(id_ex_1_w_2), .W_2(ex_mem_1_w_2), .\U型 (adder_4_out), .\U型_2 (\ex_mem_1_u型_2 ),
    .ALUResult(ALUresult), .ALUResult_2({ex_mem_1_aluresult_2, LBU1, LBU0}));  // open: halt
  RAM #(.addrWidth(10), .dataWidth(32), .bus("separate"), .Select("high")) ram_1 (
    .addr(ex_mem_1_aluresult_2[11:2]), .din(MDin), .data(ram_1_data), .str(MemWrite), .clk(CLK), .clr(RST));  // open: sel, ld
  MEM_WB mem_wb_1 (
    .RST(RST), .CLK(CLK), .AUIPC(ex_mem_1_auipc_2), .LBU(ex_mem_1_lbu_2), .JALR(ex_mem_1_jalr_2),
    .JAL(ex_mem_1_jal_2), .Mem2Reg(ex_mem_1_mem2reg_2), .REG_WRITE(ex_mem_1_reg_write_2),
    .ECALL(ex_mem_1_ecall_2), .PC(M_PC), .R1(ex_mem_1_r1_2), .R2(MDin), .MemData(ram_1_data), .IR(MEM_IR),
    .ALUResult({ex_mem_1_aluresult_2, LBU1, LBU0}), .Pc_4(MEM_PC_4), .W(ex_mem_1_w_2),
    .\U型 (\ex_mem_1_u型_2 ), .AUIPC_2(mem_wb_1_auipc_2), .LBU_2(mem_wb_1_lbu_2), .JALR_2(mem_wb_1_jalr_2),
    .JAL_2(mem_wb_1_jal_2), .MEM2REG_2(mem_wb_1_mem2reg_2), .REG_WRITE_2(RegWrite),
    .ECALL_2(mem_wb_1_ecall_2), .PC_2(WB_PC), .R1_2(WB_R1), .R2_2(WB_R2), .MemData_2(mem_wb_1_memdata_2),
    .IR_2(WB_IR), .ALUResult_2(mem_wb_1_aluresult_2), .Pc_4_2(mem_wb_1_pc_4_2), .W_2(WB_W),
    .\U型_2 (\mem_wb_1_u型_2 ));  // open: halt, LBU0, LBU0_2, LBU1, LBU1_2
  Counter #(.width(1), .max('h1), .ongoal("stay"), .trigger("rising"), .behavior("new")) counter_4 (
    .D(mem_wb_1_ecall_2), .Q(WB_ecall), .clk(mem_wb_1_ecall_2), .clr(Go));  // open: load, count, carry, preset, down
  Multiplexer #(.select(1), .width(32), .disabled("Z"), .enable("false")) multiplexer_10 (
    .in0(mem_wb_1_aluresult_2), .in1(mem_wb_1_memdata_2), .out(multiplexer_10_out), .sel(mem_wb_1_mem2reg_2));
  or or_2 (or_2_out, mem_wb_1_jal_2, mem_wb_1_jalr_2);
  Multiplexer #(.select(1), .width(32), .disabled("Z"), .enable("false")) multiplexer_11 (
    .in0(multiplexer_10_out), .in1(mem_wb_1_pc_4_2), .out(multiplexer_11_out), .sel(or_2_out));
  Multiplexer #(.select(1), .width(32), .disabled("Z"), .enable("false")) multiplexer_12 (
    .in0(multiplexer_11_out), .in1(\mem_wb_1_u型_2 ), .out(Write2Reg), .sel(mem_wb_1_auipc_2));
  Multiplexer #(.select(1), .width(32), .disabled("Z"), .enable("false")) multiplexer_13 (
    .in0(Write2Reg), .in1(LBUReasult), .out(RDin), .sel(mem_wb_1_lbu_2));

  // Other names for the same wires on the sheet: W[4:0] = ID_IR[11:7]; MEM_PC[31:0] = M_PC

  // Notes on the sheet:
  //   中断源
  //   时空图监测，可删除
  //   led显示a0
  //   中断等待指示
  //   ecall判断相等以及停机
  //   数码管输出
  //   ecall暂停，统计周期
  //   指令存储器
  //   contents of rom_1 (hex, n*v repeats v):
  //   413 493 913 993 46413 14e493 296913 39e993 842023 942223 1242423 1342623 a00893 493 913 993 73
  //   指令探针
  //   指令字
  //   ecall等待go按键
  //   jalr最低位置0
  //   控制位
  //   a7
  //   a0
  //   U型imm
  //   流水调试日志用
  //   暂停节拍，不能为0
  //   I型imm
  //   S型imm
  //   B型imm
  //   J型imm
  //   戳工具置1进入计数暂停模式，ctrl+k时钟自动运行到对应节拍暂停
  //   ctrl+k关闭时钟连续运行，将控制位置零，进入单步调试模式调试
  //   用这个时钟源需要去掉电路中的其他时钟源
  //   可计数暂停的时钟源
  //   lbu取字节
  //   为方便自动评测，需要输出流水线各段保存的PC值，注意是PC不是PC+4，另外ID段寄存器写入信息，Mem段内存写入信息也要输出
  //   AUIPC
  //   LBU
  //   JALR
  //   JAL
  //   ALUResult
  //   MemData
endmodule

module \气泡流水线  (
  output RegWrite,
  output MemWrite,
  output [31:0] IF_PC,
  output [31:0] ID_PC,
  output [31:0] EX_PC,
  output [31:0] M_PC,
  output [31:0] WB_PC,
  output [31:0] RDin,
  output [31:0] MDin,
  output [31:0] LedData
);

  wire alu_1_equal, alu_1_out_4, and_1_out, and_4_out, and_7_out, and_8_out, and_9_out, Branch, \B型 , CLK,
       clock_1_out, comparator_1_eq, comparator_2_eq, comparator_3_eq, comparator_3_lt, d_ff_2_q,
       DataHazzard, ecall, ecallEq, ecallFB, ex_mem_1_auipc_2, ex_mem_1_ecall_2, ex_mem_1_jal_2,
       ex_mem_1_jalr_2, ex_mem_1_lbu_2, ex_mem_1_mem2reg_2, EX_RegWrite, Go, halt, id_ex_1_alu_src_2,
       id_ex_1_auipc_2, id_ex_1_beq_2, id_ex_1_bge_2, id_ex_1_bne_2, id_ex_1_ecall_2, id_ex_1_lbu_2,
       id_ex_1_mem2reg_2, id_ex_1_memwrite, IR1, IR2, IR3, Jal, Jalr, LBU0, LBU1, MEM_RegWrite,
       mem_wb_1_auipc_2, mem_wb_1_jal_2, mem_wb_1_jalr_2, mem_wb_1_lbu_2, mem_wb_1_mem2reg_2, nand_1_out,
       not_1_out, not_2_out, not_3_out, not_4_out, not_5_out, not_6_out, or_1_out, or_2_out, or_3_out,
       or_6_out, R1Used, R2Used, RST, Stop, URET, W1, W2, W3, WB_ecall, \单周期硬布线控制器_1_alu_src ,
       \单周期硬布线控制器_1_auipc , \单周期硬布线控制器_1_beq , \单周期硬布线控制器_1_bge , \单周期硬布线控制器_1_bne , \单周期硬布线控制器_1_ecall ,
       \单周期硬布线控制器_1_jal , \单周期硬布线控制器_1_jalr , \单周期硬布线控制器_1_lbu , \单周期硬布线控制器_1_memtoreg ,
       \单周期硬布线控制器_1_memwrite , \单周期硬布线控制器_1_regwrite , \单周期硬布线控制器_1_s_type , \单周期硬布线控制器_1_uret ;
  wire [3:0] id_ex_1_alu_op_2, \单周期硬布线控制器_1_alu_op ;
  wire [4:0] EX_W, Funct, MEM_W, multiplexer_7_out, multiplexer_9_out, R1_num, R2_num, WB_W;
  wire [11:0] multiplexer_6_out;
  wire [12:0] CNT_num;
  wire [15:0] \LoadUse次数 , \总周期数 , \插入气泡数 , \无条件分支数 , \条件分支成功数 ;
  wire [31:0] adder_4_out, ALUresult, bit_extender_1_out, bit_extender_2_out, bit_extender_3_out,
       bit_extender_4_out, BranchPC, EX_IR, ex_mem_1_r1_2, \ex_mem_1_u型_2 , EX_PC_4, EX_R1, EX_R2,
       id_ex_1_brachpc_2, id_ex_1_is_2, id_ex_1_jalpc_2, \id_ex_1_u型_2 , ID_IR, ID_PC_4, IF_IR, IF_PC_4,
       JalPC, JalrPC, LBUReasult, MEM_IR, MEM_PC_4, mem_wb_1_aluresult_2, mem_wb_1_memdata_2,
       mem_wb_1_pc_4_2, \mem_wb_1_u型_2 , multiplexer_1_out, multiplexer_2_out, multiplexer_3_out,
       multiplexer_8_out, multiplexer_10_out, multiplexer_11_out, ram_1_data, regifile_1_r1, regifile_1_r2,
       shifter_1_out, shifter_2_out, shifter_3_out, shifter_4_out, shifter_5_out, WB_IR, WB_R1, WB_R2,
       Write2Reg;
  wire [31:2] ex_mem_1_aluresult_2;

  Button \u_总复位  (.out(RST));
  Button _1 (.out(IR1));
  Button _2 (.out(IR2));
  Button _3 (.out(IR3));
  // Probe on \总周期数 
  // Probe on \总周期数 
  Button \u_继续运行  (.out(Go));
  LED #(.active("true")) led_1 (.in(W1));
  LED #(.active("true")) led_2 (.in(W2));
  LED #(.active("true")) led_3 (.in(W3));
  // Probe on ecallEq
  Hex_Digit_Display hex_digit_display_1 (.value(LedData[31:28]));  // open: dp
  // Probe on IF_PC[19:0]
  // RiscV_Probe riscv_probe_1: pin names not known; wires that end beside it: IF_IR
  Multiplexer #(.select(1), .width(32), .disabled("Z"), .enable("false")) multiplexer_1 (
    .in0(IF_PC_4), .in1(BranchPC), .out(multiplexer_1_out), .sel(\B型 ));
  Register #(.width(32), .trigger("rising"), .Select("low")) register_1 (
    .D(WB_R2), .en(ecallEq), .Q(LedData), .clk(CLK), .clr(RST));
  \R1R2Used检测  \r1r2used检测_1  (
    .OP2(ID_IR[2]), .OP3(ID_IR[3]), .OP4(ID_IR[4]), .OP5(ID_IR[5]), .OP6(ID_IR[6]), .F12(Funct[0]),
    .F13(Funct[1]), .F14(Funct[2]), .F25(Funct[3]), .F30(Funct[4]), .R1Used(R1Used), .R2Used(R2Used));
  Hex_Digit_Display hex_digit_display_2 (.value(LedData[23:20]));  // open: dp
  Hex_Digit_Display hex_digit_display_3 (.value(LedData[27:24]));  // open: dp
  // Probe on ID_PC[19:0]
  // RiscV_Probe riscv_probe_2: pin names not known; wires that end beside it: {ID_IR[31], Funct[4], ID_IR[29:26], Funct[3], ID_IR[24:15], Funct[2:0], ID_IR[11:0]}
  Multiplexer #(.select(1), .width(32), .disabled("Z"), .enable("false")) multiplexer_2 (
    .in0(multiplexer_1_out), .in1(JalPC), .out(multiplexer_2_out), .sel(Jal));
  Multiplexer #(.select(1), .width(32), .disabled("Z"), .enable("false")) multiplexer_3 (
    .in0(multiplexer_2_out), .in1(JalrPC), .out(multiplexer_3_out), .sel(Jalr));
  and and_1 (and_1_out, not_1_out, Stop);
  not not_1 (not_1_out, DataHazzard);
  Comparator #(.width(32), .mode("twosComplement")) comparator_1 (
    .a(WB_R1), .b(32'h22), .eq(comparator_1_eq));  // open: gt, lt
  Comparator #(.width(32), .mode("twosComplement")) comparator_2 (
    .a(WB_R1), .b(32'ha), .eq(comparator_2_eq));  // open: gt, lt
  Hex_Digit_Display hex_digit_display_4 (.value(LedData[15:12]));  // open: dp
  Hex_Digit_Display hex_digit_display_5 (.value(LedData[19:16]));  // open: dp
  Register #(.width(32), .trigger("rising"), .Select("low")) PC (
    .D(multiplexer_3_out), .en(and_1_out), .Q(IF_PC), .clk(CLK), .clr(RST));
  D_Flip_Flop #(.trigger("rising"), .Pre_Clr_Positions("LEGACY"), .NegatePresetClear("false"), .enable("true"), .NewFFLayout("false")) d_ff_1 (
    .Qn(Stop), .preset(halt), .reset(Go));  // open: clk, D, Q, en
  and and_2 (ecallEq, WB_ecall, comparator_1_eq);
  and and_3 (halt, WB_ecall, comparator_2_eq);
  Hex_Digit_Display hex_digit_display_6 (.value(LedData[11:8]));  // open: dp
  Hex_Digit_Display hex_digit_display_7 (.value(LedData[7:4]));  // open: dp
  // Probe on EX_PC[19:0]
  // RiscV_Probe riscv_probe_3: pin names not known; wires that end beside it: EX_IR
  Adder #(.width(32)) adder_1 (.a(IF_PC), .b(32'h4), .out(IF_PC_4));  // open: cin, cout
  Counter #(.width(16), .max('hffff), .ongoal("wrap"), .trigger("rising"), .behavior("new")) counter_1 (
    .count(Stop), .Q(\总周期数 ), .clk(CLK), .clr(RST));  // open: load, D, carry, preset, down
  Hex_Digit_Display hex_digit_display_8 (.value(LedData[3:0]));  // open: dp
  ROM #(.addrWidth(10), .dataWidth(32), .Select("high")) rom_1 (.addr(IF_PC[11:2]), .data(IF_IR));
  \数据相关检测  \u_数据相关检测_1  (
    .R1Used(R1Used), .R2Used(R2Used), .R1_num(R1_num), .R2_num(R2_num), .EX_W(EX_W),
    .EX_Regwrite(EX_RegWrite), .MEM_W(MEM_W), .MEM_Regwrite(MEM_RegWrite), .DataHazzard(DataHazzard));
  // Probe on \总周期数 
  // Probe on M_PC[19:0]
  // RiscV_Probe riscv_probe_4: pin names not known; wires that end beside it: MEM_IR
  // RiscV_Probe riscv_probe_5: pin names not known; wires that end beside it: IF_IR, IF_PC_4
  // Probe on \总周期数 
  // Probe on \无条件分支数 
  // Probe on \条件分支成功数 
  // Probe on \插入气泡数 
  // Probe on \LoadUse次数 
  or or_1 (or_1_out, RST, Branch);
  IF_ID if_id_1 (
    .IF_PC(IF_PC), .IF_IR(IF_IR), .IF_PC_4(IF_PC_4), .CLK(CLK), .RST(or_1_out), .ID_PC(ID_PC),
    .ID_IR({ID_IR[31], Funct[4], ID_IR[29:26], Funct[3], ID_IR[24:15], Funct[2:0], ID_IR[11:0]}),
    .ID_PC_4(ID_PC_4), .halt(or_2_out));  // open: PredictBranch, PredictBranch_2
  // Probe on IF_PC[11:0]
  // Probe on WB_PC[19:0]
  // RiscV_Probe riscv_probe_6: pin names not known; wires that end beside it: WB_IR
  not not_2 (not_2_out, Stop);
  or or_2 (or_2_out, not_2_out, DataHazzard);
  and and_4 (and_4_out, Go, halt);
  // Probe on ID_PC[11:0]
  // Probe on EX_PC[11:0]
  Counter #(.width(1), .max('h1), .ongoal("stay"), .trigger("rising"), .behavior("new")) counter_2 (
    .D(and_4_out), .Q(ecallFB), .clk(and_4_out), .clr(RST));  // open: load, count, carry, preset, down
  assign JalrPC = ALUresult & 32'hfffffffe;  // AND_Gate and_5, 32 bits wide
  // Probe on M_PC[11:0]
  D_Flip_Flop #(.trigger("high"), .Pre_Clr_Positions("LEGACY"), .NegatePresetClear("false"), .enable("true"), .NewFFLayout("false")) d_ff_2 (.Q(d_ff_2_q));  // open: clk, D, Qn, preset, en, reset
  // Probe on 13'h24e
  \单周期硬布线控制器  \u_单周期硬布线控制器_1  (
    .Funct(Funct), .OP(ID_IR[6:2]), .ALU_OP(\单周期硬布线控制器_1_alu_op ), .MemToReg(\单周期硬布线控制器_1_memtoreg ),
    .MemWrite(\单周期硬布线控制器_1_memwrite ), .ALU_SRC(\单周期硬布线控制器_1_alu_src ), .RegWrite(\单周期硬布线控制器_1_regwrite ),
    .ecall(\单周期硬布线控制器_1_ecall ), .S_type(\单周期硬布线控制器_1_s_type ), .Jalr(\单周期硬布线控制器_1_jalr ),
    .Beq(\单周期硬布线控制器_1_beq ), .JAL(\单周期硬布线控制器_1_jal ), .Bne(\单周期硬布线控制器_1_bne ), .in_3(ID_IR[21]),
    .uret(\单周期硬布线控制器_1_uret ), .BGE(\单周期硬布线控制器_1_bge ), .LBU(\单周期硬布线控制器_1_lbu ), .AUIPC(\单周期硬布线控制器_1_auipc ));
  and and_6 (ecall, ~ecallFB, \单周期硬布线控制器_1_ecall );  // AND_Gate
  assign bit_extender_1_out = {{12{ID_IR[31]}}, {ID_IR[31], Funct[4], ID_IR[29:26], Funct[3], ID_IR[24:15], Funct[2:0]}};  // Bit_Extender bit_extender_1
  // Probe on WB_PC[11:0]
  Comparator #(.width(13), .mode("twosComplement")) comparator_3 (
    .a(CNT_num), .b(13'h24e), .eq(comparator_3_eq), .lt(comparator_3_lt));  // open: gt
  Clock #(.highDuration(1), .lowDuration(1)) clock_1 (.out(clock_1_out));
  Multiplexer #(.select(1), .width(5), .disabled("Z"), .enable("false")) multiplexer_4 (
    .in0(ID_IR[19:15]), .in1(5'b10001), .out(R1_num), .sel(ecall));
  Multiplexer #(.select(1), .width(5), .disabled("Z"), .enable("false")) multiplexer_5 (
    .in0(ID_IR[24:20]), .in1(5'b01010), .out(R2_num), .sel(ecall));
  Multiplexer #(.select(1), .width(12), .disabled("Z"), .enable("false")) multiplexer_6 (
    .in0({ID_IR[31], Funct[4], ID_IR[29:26], Funct[3], ID_IR[24:20]}),
    .in1({ID_IR[31], Funct[4], ID_IR[29:26], Funct[3], ID_IR[11:7]}), .out(multiplexer_6_out),
    .sel(\单周期硬布线控制器_1_s_type ));
  assign bit_extender_2_out = {{20{ID_IR[31]}}, {ID_IR[31], ID_IR[7], Funct[4], ID_IR[29:26], Funct[3], ID_IR[11:8]}};  // Bit_Extender bit_extender_2
  nand nand_1 (nand_1_out, d_ff_2_q, comparator_3_eq);
  Counter #(.width(13), .max('h1fff), .ongoal("stay"), .trigger("rising"), .behavior("old")) counter_3 (
    .count(comparator_3_lt), .Q(CNT_num), .clk(clock_1_out));  // open: load, D, carry, clr, preset
  assign bit_extender_3_out = {{20{multiplexer_6_out[11]}}, multiplexer_6_out};  // Bit_Extender bit_extender_3
  assign bit_extender_4_out = {{12{ID_IR[31]}}, {ID_IR[31], ID_IR[19:15], Funct[2:0], ID_IR[20], Funct[4], ID_IR[29:26], Funct[3], ID_IR[24:21]}};  // Bit_Extender bit_extender_4
  assign CLK = nand_1_out ? clock_1_out : 1'bz;  // Controlled_Buffer controlled_buffer_1
  Regifile regifile_1 (
    .Din(RDin), .Clk(CLK), .R1(regifile_1_r1), .R2(regifile_1_r2), .WE(RegWrite), .W_num(WB_W),
    .R1_num(R1_num), .R2_num(R2_num));
  Pull_Resistor #(.pull(1)) pull_resistor_1 (.node(CLK));
  or or_3 (or_3_out, RST, DataHazzard, Branch);
  ID_EX id_ex_1 (
    .RST(or_3_out), .CLK(CLK), .AUIPC(\单周期硬布线控制器_1_auipc ), .URET(\单周期硬布线控制器_1_uret ),
    .LBU(\单周期硬布线控制器_1_lbu ), .JALR(\单周期硬布线控制器_1_jalr ), .JAL(\单周期硬布线控制器_1_jal ), .Beq(\单周期硬布线控制器_1_beq ),
    .BGE(\单周期硬布线控制器_1_bge ), .BNE(\单周期硬布线控制器_1_bne ), .Mem2Reg(\单周期硬布线控制器_1_memtoreg ),
    .MenWrite(\单周期硬布线控制器_1_memwrite ), .ALU_OP(\单周期硬布线控制器_1_alu_op ), .ALU_SRC(\单周期硬布线控制器_1_alu_src ),
    .REG_WRITE(\单周期硬布线控制器_1_regwrite ), .ECALL(ecall), .PC(ID_PC), .R1(regifile_1_r1), .R2(regifile_1_r2),
    .IS(bit_extender_3_out),
    .IR({ID_IR[31], Funct[4], ID_IR[29:26], Funct[3], ID_IR[24:15], Funct[2:0], ID_IR[11:0]}),
    .JalPc(bit_extender_4_out), .BrachPc(bit_extender_2_out), .Pc_4(ID_PC_4), .W(ID_IR[11:7]),
    .\U型 (bit_extender_1_out), .AUIPC_2(id_ex_1_auipc_2), .URET_2(URET), .LBU_2(id_ex_1_lbu_2),
    .JALR_2(Jalr), .JAL_2(Jal), .BEQ_2(id_ex_1_beq_2), .BGE_2(id_ex_1_bge_2), .BNE_2(id_ex_1_bne_2),
    .MEM2REG_2(id_ex_1_mem2reg_2), .MEMWRITE(id_ex_1_memwrite), .ALU_OP_2(id_ex_1_alu_op_2),
    .ALU_SRC_2(id_ex_1_alu_src_2), .REG_WRITE_2(EX_RegWrite), .ECALL_2(id_ex_1_ecall_2), .PC_2(EX_PC),
    .R1_2(EX_R1), .R2_2(EX_R2), .IS_2(id_ex_1_is_2), .IR_2(EX_IR), .JalPc_2(id_ex_1_jalpc_2),
    .BrachPc_2(id_ex_1_brachpc_2), .Pc_4_2(EX_PC_4), .W_2(EX_W), .\U型_2 (\id_ex_1_u型_2 ), .halt(not_3_out));  // open: R1Fwd, R2Fwd, R1Fwd_2, R2Fwd_2, PredictBranch, PredictBranch_2
  Multiplexer #(.select(1), .width(5), .disabled("Z"), .enable("false")) multiplexer_7 (
    .in0(5'b10000), .in1({5{1'b0}}), .out(multiplexer_7_out), .sel(LBU1));
  not not_3 (not_3_out, Stop);
  Shifter #(.width(32), .shift("ll")) shifter_1 (.in(Write2Reg), .\dist (multiplexer_7_out), .out(shifter_1_out));
  Multiplexer #(.select(1), .width(32), .disabled("Z"), .enable("false")) multiplexer_8 (
    .in0(EX_R2), .in1(id_ex_1_is_2), .out(multiplexer_8_out), .sel(id_ex_1_alu_src_2));
  Shifter #(.width(32), .shift("ll")) shifter_2 (.in(id_ex_1_brachpc_2), .\dist (5'b00001), .out(shifter_2_out));
  Shifter #(.width(32), .shift("ll")) shifter_3 (.in(id_ex_1_jalpc_2), .\dist (5'b00001), .out(shifter_3_out));
  Multiplexer #(.select(1), .width(5), .disabled("Z"), .enable("false")) multiplexer_9 (
    .in0(5'b01000), .in1({5{1'b0}}), .out(multiplexer_9_out), .sel(LBU0));
  ALU alu_1 (
    .X(EX_R1), .Y(multiplexer_8_out), .AluOP(id_ex_1_alu_op_2), .Equal(alu_1_equal), .Result(ALUresult),
    .out_4(alu_1_out_4));  // open: Result_2, out_6
  Adder #(.width(32)) adder_2 (.a(shifter_2_out), .b(EX_PC), .out(BranchPC));  // open: cin, cout
  Adder #(.width(32)) adder_3 (.a(shifter_3_out), .b(EX_PC), .out(JalPC));  // open: cin, cout
  Shifter #(.width(32), .shift("ll")) shifter_4 (.in(\id_ex_1_u型_2 ), .\dist (5'b01100), .out(shifter_4_out));
  Shifter #(.width(32), .shift("ll")) shifter_5 (.in(shifter_1_out), .\dist (multiplexer_9_out), .out(shifter_5_out));
  Shifter #(.width(32), .shift("lr")) shifter_6 (.in(shifter_5_out), .\dist (5'b11000), .out(LBUReasult));
  and and_7 (and_7_out, id_ex_1_beq_2, alu_1_equal);
  not not_4 (not_4_out, alu_1_equal);
  and and_8 (and_8_out, not_4_out, id_ex_1_bne_2);
  Adder #(.width(32)) adder_4 (.a(shifter_4_out), .b(EX_PC), .out(adder_4_out));  // open: cin, cout
  and and_9 (and_9_out, id_ex_1_bge_2, alu_1_out_4);
  or or_4 (Branch, Jal, Jalr, \B型 );
  or or_5 (\B型 , and_7_out, and_9_out, and_8_out);
  EX_MEM ex_mem_1 (
    .RST(RST), .CLK(CLK), .AUIPC(id_ex_1_auipc_2), .AUIPC_2(ex_mem_1_auipc_2), .LBU(id_ex_1_lbu_2),
    .LBU_2(ex_mem_1_lbu_2), .JALR(Jalr), .JALR_2(ex_mem_1_jalr_2), .JAL(Jal), .JAL_2(ex_mem_1_jal_2),
    .Mem2Reg(id_ex_1_mem2reg_2), .MEM2REG_2(ex_mem_1_mem2reg_2), .MenWrite(id_ex_1_memwrite),
    .MEMWRITE(MemWrite), .REG_WRITE(EX_RegWrite), .REG_WRITE_2(MEM_RegWrite), .ECALL(id_ex_1_ecall_2),
    .ECALL_2(ex_mem_1_ecall_2), .PC(EX_PC), .PC_2(M_PC), .R1(EX_R1), .R1_2(ex_mem_1_r1_2), .R2(EX_R2),
    .R2_2(MDin), .IR(EX_IR), .IR_2(MEM_IR), .Pc_4(EX_PC_4), .Pc_4_2(MEM_PC_4), .W(EX_W), .W_2(MEM_W),
    .\U型 (adder_4_out), .\U型_2 (\ex_mem_1_u型_2 ), .ALUResult(ALUresult),
    .ALUResult_2({ex_mem_1_aluresult_2, LBU1, LBU0}), .halt(not_5_out));
  not not_5 (not_5_out, Stop);
  RAM #(.addrWidth(10), .dataWidth(32), .bus("separate"), .Select("high")) ram_1 (
    .addr(ex_mem_1_aluresult_2[11:2]), .din(MDin), .data(ram_1_data), .str(MemWrite), .clk(CLK), .clr(RST));  // open: sel, ld
  MEM_WB mem_wb_1 (
    .RST(RST), .CLK(CLK), .AUIPC(ex_mem_1_auipc_2), .LBU(ex_mem_1_lbu_2), .JALR(ex_mem_1_jalr_2),
    .JAL(ex_mem_1_jal_2), .Mem2Reg(ex_mem_1_mem2reg_2), .REG_WRITE(MEM_RegWrite), .ECALL(ex_mem_1_ecall_2),
    .PC(M_PC), .R1(ex_mem_1_r1_2), .R2(MDin), .MemData(ram_1_data), .IR(MEM_IR),
    .ALUResult({ex_mem_1_aluresult_2, LBU1, LBU0}), .Pc_4(MEM_PC_4), .W(MEM_W), .\U型 (\ex_mem_1_u型_2 ),
    .AUIPC_2(mem_wb_1_auipc_2), .LBU_2(mem_wb_1_lbu_2), .JALR_2(mem_wb_1_jalr_2), .JAL_2(mem_wb_1_jal_2),
    .MEM2REG_2(mem_wb_1_mem2reg_2), .REG_WRITE_2(RegWrite), .ECALL_2(WB_ecall), .PC_2(WB_PC), .R1_2(WB_R1),
    .R2_2(WB_R2), .MemData_2(mem_wb_1_memdata_2), .IR_2(WB_IR), .ALUResult_2(mem_wb_1_aluresult_2),
    .Pc_4_2(mem_wb_1_pc_4_2), .W_2(WB_W), .\U型_2 (\mem_wb_1_u型_2 ), .halt(not_6_out));  // open: LBU0, LBU0_2, LBU1, LBU1_2
  not not_6 (not_6_out, Stop);
  Multiplexer #(.select(1), .width(32), .disabled("Z"), .enable("false")) multiplexer_10 (
    .in0(mem_wb_1_aluresult_2), .in1(mem_wb_1_memdata_2), .out(multiplexer_10_out), .sel(mem_wb_1_mem2reg_2));
  or or_6 (or_6_out, mem_wb_1_jal_2, mem_wb_1_jalr_2);
  Multiplexer #(.select(1), .width(32), .disabled("Z"), .enable("false")) multiplexer_11 (
    .in0(multiplexer_10_out), .in1(mem_wb_1_pc_4_2), .out(multiplexer_11_out), .sel(or_6_out));
  Multiplexer #(.select(1), .width(32), .disabled("Z"), .enable("false")) multiplexer_12 (
    .in0(multiplexer_11_out), .in1(\mem_wb_1_u型_2 ), .out(Write2Reg), .sel(mem_wb_1_auipc_2));
  Multiplexer #(.select(1), .width(32), .disabled("Z"), .enable("false")) multiplexer_13 (
    .in0(Write2Reg), .in1(LBUReasult), .out(RDin), .sel(mem_wb_1_lbu_2));

  // Other names for the same wires on the sheet: W[4:0] = ID_IR[11:7]; ID_IR (some bits) = Funct;
  //   OP[4:0] = ID_IR[6:2]; MEM_PC[31:0] = M_PC

  // Notes on the sheet:
  //   中断源
  //   时空图监测，可删除
  //   led显示a0
  //   中断等待指示
  //   ecall判断相等以及停机
  //   R1R2Used检测
  //   数码管输出
  //   ecall暂停，统计周期
  //   指令存储器
  //   contents of rom_1 (hex, n*v repeats v):
  //   13 430497 900533 2200893 73 430497 900533 2200893 73 430497 900533 2200893 73 430497 900533 2200893
  //   73 430497 900533 2200893 73 430497 900533 2200893 73 430497 900533 2200893 73 430497 900533 2200893
  //   73 a00893 73
  //   指令探针
  //   指令字
  //   ecall等待go按键
  //   jalr最低位置0
  //   控制位
  //   流水调试日志用
  //   暂停节拍，不能为0
  //   a7
  //   a0
  //   I型imm
  //   S型imm
  //   B型imm
  //   J型imm
  //   U型imm
  //   戳工具置1进入计数暂停模式，ctrl+k时钟自动运行到对应节拍暂停
  //   ctrl+k关闭时钟连续运行，将控制位置零，进入单步调试模式调试
  //   ctrl+k关闭时钟连续运行，将控制位置零，进入单步调试模式调试
  //   用这个时钟源需要去掉电路中的其他时钟源
  //   可计数暂停的时钟源
  //   lbu取字节
  //   为方便自动评测，需要输出流水线各段保存的PC值，注意是PC不是PC+4，另外ID段寄存器写入信息，Mem段内存写入信息也要输出
  //   AUIPC
  //   LBU
  //   JALR
  //   JAL
  //   ALUResult
  //   MemData
endmodule
module \重定向流水线  (
  output RegWrite,
  output MemWrite,
  output [31:0] IF_PC,
  output [31:0] ID_PC,
  output [31:0] EX_PC,
  output [31:0] M_PC,
  output [31:0] WB_PC,
  output [31:0] RDin,
  output [31:0] MDin,
  output [31:0] LedData
);

  wire alu_1_equal, alu_1_out_4, and_1_out, and_4_out, and_5_out, and_8_out, and_9_out, and_10_out,
       and_11_out, and_12_out, and_13_out, Branch, \B型 , CLK, clock_1_out, comparator_1_eq, comparator_2_eq,
       comparator_3_eq, comparator_3_lt, d_ff_1_q, ecall, ecallEq, ecallFB, EX_ecall, EX_MEM2Reg,
       ex_mem_1_ecall_2, ex_mem_1_jal_2, ex_mem_1_jalr_2, ex_mem_1_lbu_2, ex_mem_1_mem2reg_2, EX_RegWrite,
       Go, halt, id_ex_1_alu_src_2, id_ex_1_auipc_2, id_ex_1_beq_2, id_ex_1_bge_2, id_ex_1_bne_2,
       id_ex_1_lbu_2, id_ex_1_memwrite, IR1, IR2, IR3, Jal, Jalr, LBU0, LBU1, LoadUse, MEM_AUIPC,
       MEM_RegWrite, mem_wb_1_jal_2, mem_wb_1_jalr_2, mem_wb_1_lbu_2, mem_wb_1_mem2reg_2, nand_1_out,
       not_1_out, not_2_out, not_3_out, not_4_out, or_1_out, or_2_out, or_3_out, or_4_out, or_7_out, R1Used,
       R2Used, RST, URET, W1, W2, W3, WB_AUIPC, WB_ecall, WB_LBU0, WB_LBU1, \单周期硬布线控制器_1_alu_src ,
       \单周期硬布线控制器_1_auipc , \单周期硬布线控制器_1_beq , \单周期硬布线控制器_1_bge , \单周期硬布线控制器_1_bne , \单周期硬布线控制器_1_ecall ,
       \单周期硬布线控制器_1_jal , \单周期硬布线控制器_1_jalr , \单周期硬布线控制器_1_lbu , \单周期硬布线控制器_1_memtoreg ,
       \单周期硬布线控制器_1_memwrite , \单周期硬布线控制器_1_regwrite , \单周期硬布线控制器_1_s_type , \单周期硬布线控制器_1_uret ;
  wire [1:0] EX_R1Fwd, EX_R2Fwd, ID_R1Fwd, ID_R2Fwd;
  wire [3:0] id_ex_1_alu_op_2, \单周期硬布线控制器_1_alu_op ;
  wire [4:0] EX_W, Funct, MEM_W, multiplexer_7_out, multiplexer_9_out, R1_num, R2_num, WB_W;
  wire [11:0] multiplexer_4_out;
  wire [12:0] CNT_num;
  wire [15:0] \LoadUse次数 , \总周期数 , \插入气泡数 , \无条件分支数 , \条件分支成功数 ;
  wire [31:0] adder_4_out, ALUresult, bit_extender_1_out, bit_extender_2_out, bit_extender_3_out,
       bit_extender_4_out, BranchPC, EX_IR, ex_mem_1_r1_2, EX_PC_4, EX_R1, EX_R2, EX_ReR1Data, EX_ReR2Data,
       id_ex_1_brachpc_2, id_ex_1_is_2, id_ex_1_jalpc_2, \id_ex_1_u型_2 , ID_IR, ID_PC_4, IF_IR, IF_PC_4,
       JalPC, JalrPC, LBUReasult, MEM_IR, MEM_PC_4, \MEM_U型 , mem_wb_1_aluresult_2, mem_wb_1_memdata_2,
       mem_wb_1_pc_4_2, multiplexer_1_out, multiplexer_2_out, multiplexer_3_out, multiplexer_8_out,
       multiplexer_10_out, multiplexer_11_out, multiplexer_14_out, multiplexer_15_out, ram_1_data,
       regifile_1_r1, regifile_1_r2, shifter_1_out, shifter_2_out, shifter_3_out, shifter_4_out,
       shifter_5_out, WB_IR, WB_R1, WB_R2, \WB_U型 , Write2Reg;
  wire [31:2] MemData;

  Button \u_总复位  (.out(RST));
  Button _1 (.out(IR1));
  Button _2 (.out(IR2));
  Button _3 (.out(IR3));
  // Probe on \总周期数 
  // Probe on \总周期数 
  Button \u_继续运行  (.out(Go));
  LED #(.active("true")) led_1 (.in(W1));
  LED #(.active("true")) led_2 (.in(W2));
  LED #(.active("true")) led_3 (.in(W3));
  Hex_Digit_Display hex_digit_display_1 (.value(LedData[31:28]));  // open: dp
  // Probe on IF_PC[19:0]
  // RiscV_Probe riscv_probe_1: pin names not known; wires that end beside it: IF_IR
  Hex_Digit_Display hex_digit_display_2 (.value(LedData[23:20]));  // open: dp
  Hex_Digit_Display hex_digit_display_3 (.value(LedData[27:24]));  // open: dp
  // Probe on ID_PC[19:0]
  // RiscV_Probe riscv_probe_2: pin names not known; wires that end beside it: {ID_IR[31], Funct[4], ID_IR[29:26], Funct[3], ID_IR[24:15], Funct[2:0], ID_IR[11:0]}
  // Probe on ecallEq
  Hex_Digit_Display hex_digit_display_4 (.value(LedData[19:16]));  // open: dp
  Hex_Digit_Display hex_digit_display_5 (.value(LedData[15:12]));  // open: dp
  Multiplexer #(.select(1), .width(32), .disabled("Z"), .enable("false")) multiplexer_1 (
    .in0(IF_PC_4), .in1(BranchPC), .out(multiplexer_1_out), .sel(\B型 ));
  Register #(.width(32), .trigger("rising"), .Select("low")) register_1 (
    .D(EX_R2), .en(ecallEq), .Q(LedData), .clk(CLK), .clr(RST));
  \R1R2Used检测  \r1r2used检测_1  (
    .OP2(ID_IR[2]), .OP3(ID_IR[3]), .OP4(ID_IR[4]), .OP5(ID_IR[5]), .OP6(ID_IR[6]), .F12(Funct[0]),
    .F13(Funct[1]), .F14(Funct[2]), .F25(Funct[3]), .F30(Funct[4]), .R1Used(R1Used), .R2Used(R2Used));
  Hex_Digit_Display hex_digit_display_6 (.value(LedData[7:4]));  // open: dp
  Hex_Digit_Display hex_digit_display_7 (.value(LedData[11:8]));  // open: dp
  // Probe on EX_PC[19:0]
  // RiscV_Probe riscv_probe_3: pin names not known; wires that end beside it: EX_IR
  Multiplexer #(.select(1), .width(32), .disabled("Z"), .enable("false")) multiplexer_2 (
    .in0(multiplexer_1_out), .in1(JalPC), .out(multiplexer_2_out), .sel(Jal));
  Multiplexer #(.select(1), .width(32), .disabled("Z"), .enable("false")) multiplexer_3 (
    .in0(multiplexer_2_out), .in1(JalrPC), .out(multiplexer_3_out), .sel(Jalr));
  or or_1 (or_1_out, and_1_out, Go);
  and and_1 (and_1_out, not_1_out, not_2_out);
  not not_1 (not_1_out, LoadUse);
  Comparator #(.width(32), .mode("twosComplement")) comparator_1 (
    .a(EX_R1), .b(32'h22), .eq(comparator_1_eq));  // open: gt, lt
  Comparator #(.width(32), .mode("twosComplement")) comparator_2 (
    .a(EX_R1), .b(32'ha), .eq(comparator_2_eq));  // open: gt, lt
  Hex_Digit_Display hex_digit_display_8 (.value(LedData[3:0]));  // open: dp
  Register #(.width(32), .trigger("rising"), .Select("low")) PC (
    .D(multiplexer_3_out), .en(or_1_out), .Q(IF_PC), .clk(CLK), .clr(RST));
  not not_2 (not_2_out, halt);
  and and_2 (ecallEq, EX_ecall, comparator_1_eq);
  and and_3 (halt, EX_ecall, comparator_2_eq);
  not not_3 (not_3_out, halt);
  // Probe on \总周期数 
  // Probe on M_PC[19:0]
  // RiscV_Probe riscv_probe_4: pin names not known; wires that end beside it: MEM_IR
  Adder #(.width(32)) adder_1 (.a(IF_PC), .b(32'h4), .out(IF_PC_4));  // open: cin, cout
  Counter #(.width(16), .max('hffff), .ongoal("wrap"), .trigger("rising"), .behavior("new")) counter_1 (
    .count(not_3_out), .Q(\总周期数 ), .clk(CLK), .clr(RST));  // open: load, D, carry, preset, down
  // Probe on \总周期数 
  // Probe on \无条件分支数 
  // Probe on \条件分支成功数 
  // Probe on \插入气泡数 
  // Probe on \LoadUse次数 
  // Probe on IF_PC[11:0]
  // Probe on WB_PC[19:0]
  // RiscV_Probe riscv_probe_5: pin names not known; wires that end beside it: WB_IR
  // RiscV_Probe riscv_probe_6: pin names not known; wires that end beside it: IF_IR, IF_PC_4
  ROM #(.addrWidth(10), .dataWidth(32), .Select("high")) rom_1 (.addr(IF_PC[11:2]), .data(IF_IR));
  \LoadUse检测  \loaduse检测_1  (
    .R1Used(R1Used), .R2Used(R2Used), .R1_num(R1_num), .R2_num(R2_num), .EX_W(EX_W), .EX_MEM2Reg(EX_MEM2Reg),
    .LoadUse(LoadUse));
  // Probe on EX_PC[11:0]
  // Probe on ID_PC[11:0]
  or or_2 (or_2_out, RST, Branch);
  // Probe on M_PC[11:0]
  D_Flip_Flop #(.trigger("high"), .Pre_Clr_Positions("LEGACY"), .NegatePresetClear("false"), .enable("true"), .NewFFLayout("false")) d_ff_1 (.Q(d_ff_1_q));  // open: clk, D, Qn, preset, en, reset
  // Probe on 13'hc
  and and_4 (and_4_out, halt, ~Go);  // AND_Gate
  or or_3 (or_3_out, and_4_out, LoadUse);
  IF_ID if_id_1 (
    .IF_PC(IF_PC), .IF_IR(IF_IR), .IF_PC_4(IF_PC_4), .CLK(CLK), .RST(or_2_out), .ID_PC(ID_PC),
    .ID_IR({ID_IR[31], Funct[4], ID_IR[29:26], Funct[3], ID_IR[24:15], Funct[2:0], ID_IR[11:0]}),
    .ID_PC_4(ID_PC_4), .halt(or_3_out));  // open: PredictBranch, PredictBranch_2
  and and_5 (and_5_out, Go, halt);
  // Probe on WB_PC[11:0]
  Comparator #(.width(13), .mode("twosComplement")) comparator_3 (
    .a(CNT_num), .b(13'hc), .eq(comparator_3_eq), .lt(comparator_3_lt));  // open: gt
  Clock #(.highDuration(1), .lowDuration(1)) clock_1 (.out(clock_1_out));
  Counter #(.width(1), .max('h1), .ongoal("stay"), .trigger("rising"), .behavior("new")) counter_2 (
    .D(and_5_out), .Q(ecallFB), .clk(and_5_out), .clr(RST));  // open: load, count, carry, preset, down
  assign JalrPC = ALUresult & 32'hfffffffe;  // AND_Gate and_6, 32 bits wide
  nand nand_1 (nand_1_out, d_ff_1_q, comparator_3_eq);
  Counter #(.width(13), .max('h1fff), .ongoal("stay"), .trigger("rising"), .behavior("old")) counter_3 (
    .count(comparator_3_lt), .Q(CNT_num), .clk(clock_1_out));  // open: load, D, carry, clr, preset
  and and_7 (ecall, ~ecallFB, \单周期硬布线控制器_1_ecall );  // AND_Gate
  assign CLK = nand_1_out ? clock_1_out : 1'bz;  // Controlled_Buffer controlled_buffer_1
  \单周期硬布线控制器  \u_单周期硬布线控制器_1  (
    .Funct(Funct), .OP(ID_IR[6:2]), .ALU_OP(\单周期硬布线控制器_1_alu_op ), .MemToReg(\单周期硬布线控制器_1_memtoreg ),
    .MemWrite(\单周期硬布线控制器_1_memwrite ), .ALU_SRC(\单周期硬布线控制器_1_alu_src ), .RegWrite(\单周期硬布线控制器_1_regwrite ),
    .ecall(\单周期硬布线控制器_1_ecall ), .S_type(\单周期硬布线控制器_1_s_type ), .Jalr(\单周期硬布线控制器_1_jalr ),
    .Beq(\单周期硬布线控制器_1_beq ), .JAL(\单周期硬布线控制器_1_jal ), .Bne(\单周期硬布线控制器_1_bne ), .in_3(ID_IR[21]),
    .uret(\单周期硬布线控制器_1_uret ), .BGE(\单周期硬布线控制器_1_bge ), .LBU(\单周期硬布线控制器_1_lbu ), .AUIPC(\单周期硬布线控制器_1_auipc ));
  Multiplexer #(.select(1), .width(12), .disabled("Z"), .enable("false")) multiplexer_4 (
    .in0({ID_IR[31], Funct[4], ID_IR[29:26], Funct[3], ID_IR[24:20]}),
    .in1({ID_IR[31], Funct[4], ID_IR[29:26], Funct[3], ID_IR[11:7]}), .out(multiplexer_4_out),
    .sel(\单周期硬布线控制器_1_s_type ));
  assign bit_extender_1_out = {{20{ID_IR[31]}}, {ID_IR[31], ID_IR[7], Funct[4], ID_IR[29:26], Funct[3], ID_IR[11:8]}};  // Bit_Extender bit_extender_1
  assign bit_extender_2_out = {{12{ID_IR[31]}}, {ID_IR[31], Funct[4], ID_IR[29:26], Funct[3], ID_IR[24:15], Funct[2:0]}};  // Bit_Extender bit_extender_2
  Pull_Resistor #(.pull(1)) pull_resistor_1 (.node(CLK));
  Multiplexer #(.select(1), .width(5), .disabled("Z"), .enable("false")) multiplexer_5 (
    .in0(ID_IR[19:15]), .in1(5'b10001), .out(R1_num), .sel(ecall));
  Multiplexer #(.select(1), .width(5), .disabled("Z"), .enable("false")) multiplexer_6 (
    .in0(ID_IR[24:20]), .in1(5'b01010), .out(R2_num), .sel(ecall));
  assign bit_extender_3_out = {{20{multiplexer_4_out[11]}}, multiplexer_4_out};  // Bit_Extender bit_extender_3
  assign bit_extender_4_out = {{12{ID_IR[31]}}, {ID_IR[31], ID_IR[19:15], Funct[2:0], ID_IR[20], Funct[4], ID_IR[29:26], Funct[3], ID_IR[24:21]}};  // Bit_Extender bit_extender_4
  \Fwd逻辑  \fwd逻辑_1  (
    .R1Used(R1Used), .R1_num(R1_num), .EX_RegWrite(EX_RegWrite), .EX_W(EX_W), .MEM_RegWrite(MEM_RegWrite),
    .MEM_W(MEM_W), .R2Used(R2Used), .R2_num(R2_num), .R1Fwd(ID_R1Fwd), .R1Fwd_2(ID_R2Fwd));
  Regifile regifile_1 (
    .Din(RDin), .Clk(CLK), .R1(regifile_1_r1), .R2(regifile_1_r2), .WE(RegWrite), .W_num(WB_W),
    .R1_num(R1_num), .R2_num(R2_num));
  or or_4 (or_4_out, RST, LoadUse, Branch);
  ID_EX id_ex_1 (
    .RST(or_4_out), .CLK(CLK), .AUIPC(\单周期硬布线控制器_1_auipc ), .URET(\单周期硬布线控制器_1_uret ),
    .LBU(\单周期硬布线控制器_1_lbu ), .JALR(\单周期硬布线控制器_1_jalr ), .JAL(\单周期硬布线控制器_1_jal ), .Beq(\单周期硬布线控制器_1_beq ),
    .BGE(\单周期硬布线控制器_1_bge ), .BNE(\单周期硬布线控制器_1_bne ), .Mem2Reg(\单周期硬布线控制器_1_memtoreg ),
    .MenWrite(\单周期硬布线控制器_1_memwrite ), .ALU_OP(\单周期硬布线控制器_1_alu_op ), .ALU_SRC(\单周期硬布线控制器_1_alu_src ),
    .REG_WRITE(\单周期硬布线控制器_1_regwrite ), .ECALL(ecall), .PC(ID_PC), .R1(regifile_1_r1), .R2(regifile_1_r2),
    .IS(bit_extender_3_out),
    .IR({ID_IR[31], Funct[4], ID_IR[29:26], Funct[3], ID_IR[24:15], Funct[2:0], ID_IR[11:0]}),
    .JalPc(bit_extender_4_out), .BrachPc(bit_extender_1_out), .Pc_4(ID_PC_4), .W(ID_IR[11:7]),
    .\U型 (bit_extender_2_out), .AUIPC_2(id_ex_1_auipc_2), .URET_2(URET), .LBU_2(id_ex_1_lbu_2),
    .JALR_2(Jalr), .JAL_2(Jal), .BEQ_2(id_ex_1_beq_2), .BGE_2(id_ex_1_bge_2), .BNE_2(id_ex_1_bne_2),
    .MEM2REG_2(EX_MEM2Reg), .MEMWRITE(id_ex_1_memwrite), .ALU_OP_2(id_ex_1_alu_op_2),
    .ALU_SRC_2(id_ex_1_alu_src_2), .REG_WRITE_2(EX_RegWrite), .ECALL_2(EX_ecall), .PC_2(EX_PC), .R1_2(EX_R1),
    .R2_2(EX_R2), .IS_2(id_ex_1_is_2), .IR_2(EX_IR), .JalPc_2(id_ex_1_jalpc_2),
    .BrachPc_2(id_ex_1_brachpc_2), .Pc_4_2(EX_PC_4), .W_2(EX_W), .\U型_2 (\id_ex_1_u型_2 ), .halt(and_8_out),
    .R1Fwd(ID_R1Fwd), .R2Fwd(ID_R2Fwd), .R1Fwd_2(EX_R1Fwd), .R2Fwd_2(EX_R2Fwd));  // open: PredictBranch, PredictBranch_2
  and and_8 (and_8_out, halt, ~Go);  // AND_Gate
  Shifter #(.width(32), .shift("ll")) shifter_1 (.in(Write2Reg), .\dist (multiplexer_7_out), .out(shifter_1_out));
  Multiplexer #(.select(1), .width(5), .disabled("Z"), .enable("false")) multiplexer_7 (
    .in0(5'b10000), .in1({5{1'b0}}), .out(multiplexer_7_out), .sel(WB_LBU1));
  Multiplexer #(.select(1), .width(32), .disabled("Z"), .enable("false")) multiplexer_8 (
    .in0(EX_ReR2Data), .in1(id_ex_1_is_2), .out(multiplexer_8_out), .sel(id_ex_1_alu_src_2));
  Shifter #(.width(32), .shift("ll")) shifter_2 (.in(id_ex_1_brachpc_2), .\dist (5'b00001), .out(shifter_2_out));
  Multiplexer #(.select(1), .width(5), .disabled("Z"), .enable("false")) multiplexer_9 (
    .in0(5'b01000), .in1({5{1'b0}}), .out(multiplexer_9_out), .sel(WB_LBU0));
  ALU alu_1 (
    .X(EX_ReR1Data), .Y(multiplexer_8_out), .AluOP(id_ex_1_alu_op_2), .Equal(alu_1_equal),
    .Result(ALUresult), .out_4(alu_1_out_4));  // open: Result_2, out_6
  Adder #(.width(32)) adder_2 (.a(shifter_2_out), .b(EX_PC), .out(BranchPC));  // open: cin, cout
  Shifter #(.width(32), .shift("ll")) shifter_3 (.in(id_ex_1_jalpc_2), .\dist (5'b00001), .out(shifter_3_out));
  Adder #(.width(32)) adder_3 (.a(shifter_3_out), .b(EX_PC), .out(JalPC));  // open: cin, cout
  Shifter #(.width(32), .shift("ll")) shifter_4 (.in(\id_ex_1_u型_2 ), .\dist (5'b01100), .out(shifter_4_out));
  Shifter #(.width(32), .shift("ll")) shifter_5 (.in(shifter_1_out), .\dist (multiplexer_9_out), .out(shifter_5_out));
  and and_9 (and_9_out, id_ex_1_beq_2, alu_1_equal);
  not not_4 (not_4_out, alu_1_equal);
  and and_10 (and_10_out, not_4_out, id_ex_1_bne_2);
  Adder #(.width(32)) adder_4 (.a(shifter_4_out), .b(EX_PC), .out(adder_4_out));  // open: cin, cout
  Shifter #(.width(32), .shift("lr")) shifter_6 (.in(shifter_5_out), .\dist (5'b11000), .out(LBUReasult));
  and and_11 (and_11_out, id_ex_1_bge_2, alu_1_out_4);
  or or_5 (Branch, Jal, Jalr, \B型 );
  or or_6 (\B型 , and_9_out, and_11_out, and_10_out);
  EX_MEM ex_mem_1 (
    .RST(RST), .CLK(CLK), .AUIPC(id_ex_1_auipc_2), .AUIPC_2(MEM_AUIPC), .LBU(id_ex_1_lbu_2),
    .LBU_2(ex_mem_1_lbu_2), .JALR(Jalr), .JALR_2(ex_mem_1_jalr_2), .JAL(Jal), .JAL_2(ex_mem_1_jal_2),
    .Mem2Reg(EX_MEM2Reg), .MEM2REG_2(ex_mem_1_mem2reg_2), .MenWrite(id_ex_1_memwrite), .MEMWRITE(MemWrite),
    .REG_WRITE(EX_RegWrite), .REG_WRITE_2(MEM_RegWrite), .ECALL(EX_ecall), .ECALL_2(ex_mem_1_ecall_2),
    .PC(EX_PC), .PC_2(M_PC), .R1(EX_ReR1Data), .R1_2(ex_mem_1_r1_2), .R2(EX_ReR2Data), .R2_2(MDin),
    .IR(EX_IR), .IR_2(MEM_IR), .Pc_4(EX_PC_4), .Pc_4_2(MEM_PC_4), .W(EX_W), .W_2(MEM_W), .\U型 (adder_4_out),
    .\U型_2 (\MEM_U型 ), .ALUResult(ALUresult), .ALUResult_2({MemData, LBU1, LBU0}), .halt(and_12_out));
  Multiplexer #(.select(1), .width(32), .disabled("Z"), .enable("false")) multiplexer_10 (
    .in0({MemData, LBU1, LBU0}), .in1(\MEM_U型 ), .out(multiplexer_10_out), .sel(MEM_AUIPC));
  and and_12 (and_12_out, halt, ~Go);  // AND_Gate
  Multiplexer #(.select(1), .width(32), .disabled("Z"), .enable("false")) multiplexer_11 (
    .in0(RDin), .in1(\WB_U型 ), .out(multiplexer_11_out), .sel(WB_AUIPC));
  Multiplexer #(.select(2), .width(32), .disabled("Z"), .enable("false")) multiplexer_12 (
    .in0(EX_R1), .in1(multiplexer_11_out), .in2(multiplexer_10_out), .out(EX_ReR1Data), .sel(EX_R1Fwd));  // open: in3
  Multiplexer #(.select(2), .width(32), .disabled("Z"), .enable("false")) multiplexer_13 (
    .in0(EX_R2), .in1(multiplexer_11_out), .in2(multiplexer_10_out), .out(EX_ReR2Data), .sel(EX_R2Fwd));  // open: in3
  RAM #(.addrWidth(10), .dataWidth(32), .bus("separate"), .Select("high")) ram_1 (
    .addr(MemData[11:2]), .din(MDin), .data(ram_1_data), .str(MemWrite), .clk(CLK), .clr(RST));  // open: sel, ld
  and and_13 (and_13_out, halt, ~Go);  // AND_Gate
  MEM_WB mem_wb_1 (
    .RST(RST), .CLK(CLK), .AUIPC(MEM_AUIPC), .LBU(ex_mem_1_lbu_2), .JALR(ex_mem_1_jalr_2),
    .JAL(ex_mem_1_jal_2), .Mem2Reg(ex_mem_1_mem2reg_2), .REG_WRITE(MEM_RegWrite), .ECALL(ex_mem_1_ecall_2),
    .PC(M_PC), .R1(ex_mem_1_r1_2), .R2(MDin), .MemData(ram_1_data), .IR(MEM_IR),
    .ALUResult({MemData, LBU1, LBU0}), .Pc_4(MEM_PC_4), .W(MEM_W), .\U型 (\MEM_U型 ), .AUIPC_2(WB_AUIPC),
    .LBU_2(mem_wb_1_lbu_2), .JALR_2(mem_wb_1_jalr_2), .JAL_2(mem_wb_1_jal_2), .MEM2REG_2(mem_wb_1_mem2reg_2),
    .REG_WRITE_2(RegWrite), .ECALL_2(WB_ecall), .PC_2(WB_PC), .R1_2(WB_R1), .R2_2(WB_R2),
    .MemData_2(mem_wb_1_memdata_2), .IR_2(WB_IR), .ALUResult_2(mem_wb_1_aluresult_2),
    .Pc_4_2(mem_wb_1_pc_4_2), .W_2(WB_W), .\U型_2 (\WB_U型 ), .halt(and_13_out), .LBU0(LBU0), .LBU0_2(WB_LBU0),
    .LBU1(LBU1), .LBU1_2(WB_LBU1));
  Multiplexer #(.select(1), .width(32), .disabled("Z"), .enable("false")) multiplexer_14 (
    .in0(mem_wb_1_aluresult_2), .in1(mem_wb_1_memdata_2), .out(multiplexer_14_out), .sel(mem_wb_1_mem2reg_2));
  or or_7 (or_7_out, mem_wb_1_jal_2, mem_wb_1_jalr_2);
  Multiplexer #(.select(1), .width(32), .disabled("Z"), .enable("false")) multiplexer_15 (
    .in0(multiplexer_14_out), .in1(mem_wb_1_pc_4_2), .out(multiplexer_15_out), .sel(or_7_out));
  Multiplexer #(.select(1), .width(32), .disabled("Z"), .enable("false")) multiplexer_16 (
    .in0(multiplexer_15_out), .in1(\WB_U型 ), .out(Write2Reg), .sel(WB_AUIPC));
  Multiplexer #(.select(1), .width(32), .disabled("Z"), .enable("false")) multiplexer_17 (
    .in0(Write2Reg), .in1(LBUReasult), .out(RDin), .sel(mem_wb_1_lbu_2));

  // Other names for the same wires on the sheet: W[4:0] = ID_IR[11:7]; ID_IR (some bits) = Funct;
  //   OP[4:0] = ID_IR[6:2]; MEM_PC[31:0] = M_PC; MemData[1:0] = {LBU1, LBU0}

  // Notes on the sheet:
  //   中断源
  //   时空图监测，可删除
  //   中断等待指示
  //   ecall判断相等以及停机
  //   led显示a0
  //   R1R2Used检测
  //   数码管输出
  //   ecall暂停，统计周期
  //   指令存储器
  //   指令探针
  //   contents of rom_1 (hex, n*v repeats v):
  //   100493 100006f 100493 200913 300993 100006f 100493 200913 300993 100006f 100493 200913 300993
  //   100006f 100493 200913 300993 29c000ef 100413 100493 1f49493 900533 2200893 73 24d493 48463 fedff06f
  //   900533 2200893 73 100493 249493 900533 2200893 73 48463 fedff06f 100493 1f49493 900533 2200893 73
  //   4034d493 900533 2200893 73 4044d493 900533 2200893 73 4044d493 900533 2200893 73 4044d493 900533
  //   2200893 73 4044d493 900533 2200893 73 4044d493 900533 2200893 73 4044d493 900533 2200893 73 4044d493
  //   900533 2200893 73 100413 1f41993 41f9d993 433 c00913 300b13 140413 f47413 800293 100313 499993
  //   89e9b3 1300533 2200893 73 406282b3 fe0294e3 140413 f00f93 1f47433 1c41413 800293 100313 49d993
  //   89e9b3 1300533 2200893 73 406282b3 fe0294e3 1c45413 406b0b33 b0463 f95ff06f 2b3 fff2c293 829293
  //   ff2e293 500533 2200893 73 fff00413 493 84a023 140413 448493 84a023 140413 448493 84a023 140413
  //   448493 84a023 140413 448493 84a023 140413 448493 84a023 140413 448493 84a023 140413 448493 84a023
  //   140413 448493 84a023 140413 448493 84a023 140413 448493 84a023 140413 448493 84a023 140413 448493
  //   84a023 140413 448493 84a023 140413 448493 84a023 140413 448493 84a023 140413 448493 140413 433
  //   3c00493 42983 4aa03 149a2b3 28663 134a023 1442023 ffc48493 fe9412e3 800533 2200893 73 440413 3c00493
  //   fc9416e3 a00893 73 413 140413 800533 2200893 73 240413 800533 2200893 73 340413 800533 2200893 73
  //   440413 800533 2200893 73 540413 800533 2200893 73 640413 800533 2200893 73 740413 800533 2200893 73
  //   840413 800533 2200893 2200893 73 8067
  //   控制位
  //   指令字
  //   ecall等待go按键
  //   jalr最低位置0
  //   流水调试日志用
  //   暂停节拍，不能为0
  //   戳工具置1进入计数暂停模式，ctrl+k时钟自动运行到对应节拍暂停
  //   ctrl+k关闭时钟连续运行，将控制位置零，进入单步调试模式调试
  //   a7
  //   a0
  //   I型imm
  //   S型imm
  //   B型imm
  //   U型imm
  //   可计数暂停的时钟源
  //   J型imm
  //   lbu取字节
  //   为方便自动评测，需要输出流水线各段保存的PC值，注意是PC不是PC+4，另外ID段寄存器写入信息，Mem段内存写入信息也要输出
  //   JAL
  //   AUIPC
  //   LBU
  //   JALR
  //   ALUResult
  //   MemData
endmodule

module \中断按键参考电路  (
  input  \同步清零信号 ,
  output \与中断屏蔽位与 
);

  wire \_1号中断_out , and_1_out, clock_1_out, d_ff_1_q, or_1_out, or_2_out;

  Clock #(.highDuration(1), .lowDuration(1)) clock_1 (.out(clock_1_out));
  Button \_1号中断  (.out(\_1号中断_out ));
  LED #(.active("true")) \_1号中断等待指示灯  (.in(or_1_out));
  or or_1 (or_1_out, \与中断屏蔽位与 , d_ff_1_q);
  D_Flip_Flop #(.trigger("rising"), .Pre_Clr_Positions("LEGACY"), .NegatePresetClear("false"), .enable("true"), .NewFFLayout("false")) d_ff_1 (
    .clk(\_1号中断_out ), .D(1'b1), .Q(d_ff_1_q), .reset(\与中断屏蔽位与 ));  // open: Qn, preset, en
  or or_2 (or_2_out, d_ff_1_q, \与中断屏蔽位与 );
  and and_1 (and_1_out, or_2_out, ~\同步清零信号 );  // AND_Gate
  D_Flip_Flop #(.trigger("rising"), .Pre_Clr_Positions("LEGACY"), .NegatePresetClear("false"), .enable("true"), .NewFFLayout("false")) IR1 (
    .clk(clock_1_out), .D(and_1_out), .Q(\与中断屏蔽位与 ));  // open: Qn, preset, en, reset

  // Notes on the sheet:
  //   中断信号采样参考电路
  //   Reset 
endmodule

module \单周期_单级中断  (
  input  IR1,
  input  IR2,
  input  IR3,
  output RegWrite,
  output MemWrite,
  output [31:0] PC,
  output [31:0] IR,
  output [31:0] RDin,
  output [31:0] MDin,
  output [31:0] LedData
);

  wire CLK, clock_1_out, comparator_1_eq, comparator_2_eq, comparator_3_eq, comparator_4_eq, comparator_5_eq,
       comparator_5_lt, d_ff_1_q, Go, IR1_t, IR2_t, IR3_t, IRA, IRB, IRC, nand_1_out, or_1_out, W1, W2, W3;
  wire [12:0] CNT_num;
  wire [15:0] \总周期数 ;

  Button \u_继续运行  (.out(Go));
  Button _1 ();  // open: out
  Button _2 ();  // open: out
  Button _3 ();  // open: out
  LED #(.active("true")) led_1 (.in(W1));
  LED #(.active("true")) led_2 (.in(W2));
  LED #(.active("true")) led_3 (.in(W3));
  Hex_Digit_Display hex_digit_display_1 (.value(LedData[31:28]));  // open: dp
  Comparator #(.width(16), .mode("twosComplement")) comparator_1 (
    .a(16'h23b), .b(\总周期数 ), .eq(comparator_1_eq));  // open: gt, lt
  Comparator #(.width(16), .mode("twosComplement")) comparator_2 (
    .a(\总周期数 ), .b(16'h1), .eq(comparator_2_eq));  // open: gt, lt
  Comparator #(.width(16), .mode("twosComplement")) comparator_3 (
    .a(\总周期数 ), .b(16'h4), .eq(comparator_3_eq));  // open: gt, lt
  Comparator #(.width(16), .mode("twosComplement")) comparator_4 (
    .a(\总周期数 ), .b(16'h7), .eq(comparator_4_eq));  // open: gt, lt
  Hex_Digit_Display hex_digit_display_2 (.value(LedData[27:24]));  // open: dp
  Hex_Digit_Display hex_digit_display_3 (.value(LedData[23:20]));  // open: dp
  or or_1 (or_1_out, comparator_1_eq, comparator_2_eq);
  assign IRA = or_1_out ? ~CLK : 1'bz;  // Controlled_Inverter controlled_inverter_1
  assign IRB = comparator_3_eq ? ~CLK : 1'bz;  // Controlled_Inverter controlled_inverter_2
  assign IRC = comparator_4_eq ? ~CLK : 1'bz;  // Controlled_Inverter controlled_inverter_3
  Hex_Digit_Display hex_digit_display_4 (.value(LedData[15:12]));  // open: dp
  Hex_Digit_Display hex_digit_display_5 (.value(LedData[19:16]));  // open: dp
  Pull_Resistor #(.pull(0)) pull_resistor_1 (.node(IRA));
  Pull_Resistor #(.pull(0)) pull_resistor_2 (.node(IRB));
  Pull_Resistor #(.pull(0)) pull_resistor_3 (.node(IRC));
  Hex_Digit_Display hex_digit_display_6 (.value(LedData[7:4]));  // open: dp
  Hex_Digit_Display hex_digit_display_7 (.value(LedData[11:8]));  // open: dp
  // Probe on \总周期数 
  Hex_Digit_Display hex_digit_display_8 (.value(LedData[3:0]));  // open: dp
  or or_2 (IR1_t, IR1, IRA);
  or or_3 (IR2_t, IR2, IRB);
  or or_4 (IR3_t, IR3, IRC);
  D_Flip_Flop #(.trigger("high"), .Pre_Clr_Positions("LEGACY"), .NegatePresetClear("false"), .enable("true"), .NewFFLayout("false")) d_ff_1 (.Q(d_ff_1_q));  // open: clk, D, Qn, preset, en, reset
  // Probe on 13'hc
  Comparator #(.width(13), .mode("twosComplement")) comparator_5 (
    .a(CNT_num), .b(13'hc), .eq(comparator_5_eq), .lt(comparator_5_lt));  // open: gt
  Clock #(.highDuration(1), .lowDuration(1)) clock_1 (.out(clock_1_out));
  Counter #(.width(13), .max('h1fff), .ongoal("stay"), .trigger("rising"), .behavior("old")) counter_1 (
    .count(comparator_5_lt), .Q(CNT_num), .clk(clock_1_out));  // open: load, D, carry, clr, preset
  nand nand_1 (nand_1_out, d_ff_1_q, comparator_5_eq);
  assign CLK = nand_1_out ? clock_1_out : 1'bz;  // Controlled_Buffer controlled_buffer_1
  Pull_Resistor #(.pull(1)) pull_resistor_4 (.node(CLK));

  // Notes on the sheet:
  //   中断源
  //   中断等待指示
  //   总复位信号应将除ROM以外所有存储组件全部清零
  //   单级中断测试信号模拟器
  //   数码管输出
  //   数码管输出应该用寄存器锁存，否则显示数据只能一闪而过
  //   为方便自动评测，需要输出PC，IR，寄存器堆写如数据RDin
  //   RAM写使能MemWrite、RAM写入数据MDin等信号
  //   控制位
  //   暂停节拍，不能为0
  //   戳工具置1进入计数暂停模式，ctrl+k时钟自动运行到对应节拍暂停
  //   ctrl+k关闭时钟连续运行，将控制位置零，进入单步调试模式调试
  //   可计数暂停的时钟源
endmodule

module \单周期_多级中断  (
  input  IR1,
  input  IR2,
  input  IR3,
  output RegWrite,
  output MemWrite,
  output [31:0] PC,
  output [31:0] IR,
  output [31:0] RDin,
  output [31:0] MDin,
  output [31:0] LedData
);

  wire CLK, clock_1_out, comparator_1_eq, comparator_2_eq, comparator_3_eq, comparator_4_eq, comparator_5_eq,
       comparator_6_eq, comparator_6_lt, d_ff_1_q, Go, IR1_t, IR2_t, IR3_t, IRA, IRB, IRC, nand_1_out,
       or_1_out, or_2_out, W1, W2, W3;
  wire [12:0] CNT_num;
  wire [15:0] \总周期数 ;

  Button \u_继续运行  (.out(Go));
  Button _1 ();  // open: out
  Button _2 ();  // open: out
  Button _3 ();  // open: out
  LED #(.active("true")) led_1 (.in(W1));
  LED #(.active("true")) led_2 (.in(W2));
  LED #(.active("true")) led_3 (.in(W3));
  Hex_Digit_Display hex_digit_display_1 (.value(LedData[31:28]));  // open: dp
  Comparator #(.width(16), .mode("twosComplement")) comparator_1 (
    .a(\总周期数 ), .b(16'h7), .eq(comparator_1_eq));  // open: gt, lt
  Comparator #(.width(16), .mode("twosComplement")) comparator_2 (
    .a(\总周期数 ), .b(16'h241), .eq(comparator_2_eq));  // open: gt, lt
  Hex_Digit_Display hex_digit_display_2 (.value(LedData[23:20]));  // open: dp
  Hex_Digit_Display hex_digit_display_3 (.value(LedData[27:24]));  // open: dp
  Comparator #(.width(16), .mode("twosComplement")) comparator_3 (
    .a(16'h258), .b(\总周期数 ), .eq(comparator_3_eq));  // open: gt, lt
  or or_1 (or_1_out, comparator_3_eq, comparator_4_eq);
  Comparator #(.width(16), .mode("twosComplement")) comparator_4 (
    .a(\总周期数 ), .b(16'h1), .eq(comparator_4_eq));  // open: gt, lt
  Comparator #(.width(16), .mode("twosComplement")) comparator_5 (
    .a(\总周期数 ), .b(16'h4), .eq(comparator_5_eq));  // open: gt, lt
  or or_2 (or_2_out, comparator_1_eq, comparator_2_eq);
  Hex_Digit_Display hex_digit_display_4 (.value(LedData[15:12]));  // open: dp
  Hex_Digit_Display hex_digit_display_5 (.value(LedData[19:16]));  // open: dp
  Pull_Resistor #(.pull(0)) pull_resistor_1 (.node(IRA));
  assign IRA = or_1_out ? ~CLK : 1'bz;  // Controlled_Inverter controlled_inverter_1
  Pull_Resistor #(.pull(0)) pull_resistor_2 (.node(IRB));
  assign IRB = comparator_5_eq ? ~CLK : 1'bz;  // Controlled_Inverter controlled_inverter_2
  Pull_Resistor #(.pull(0)) pull_resistor_3 (.node(IRC));
  assign IRC = or_2_out ? ~CLK : 1'bz;  // Controlled_Inverter controlled_inverter_3
  Hex_Digit_Display hex_digit_display_6 (.value(LedData[7:4]));  // open: dp
  Hex_Digit_Display hex_digit_display_7 (.value(LedData[11:8]));  // open: dp
  // Probe on \总周期数 
  Hex_Digit_Display hex_digit_display_8 (.value(LedData[3:0]));  // open: dp
  or or_3 (IR1_t, IR1, IRA);
  or or_4 (IR2_t, IR2, IRB);
  or or_5 (IR3_t, IR3, IRC);
  D_Flip_Flop #(.trigger("high"), .Pre_Clr_Positions("LEGACY"), .NegatePresetClear("false"), .enable("true"), .NewFFLayout("false")) d_ff_1 (.Q(d_ff_1_q));  // open: clk, D, Qn, preset, en, reset
  // Probe on 13'hc
  Comparator #(.width(13), .mode("twosComplement")) comparator_6 (
    .a(CNT_num), .b(13'hc), .eq(comparator_6_eq), .lt(comparator_6_lt));  // open: gt
  Clock #(.highDuration(1), .lowDuration(1)) clock_1 (.out(clock_1_out));
  Counter #(.width(13), .max('h1fff), .ongoal("stay"), .trigger("rising"), .behavior("old")) counter_1 (
    .count(comparator_6_lt), .Q(CNT_num), .clk(clock_1_out));  // open: load, D, carry, clr, preset
  nand nand_1 (nand_1_out, d_ff_1_q, comparator_6_eq);
  assign CLK = nand_1_out ? clock_1_out : 1'bz;  // Controlled_Buffer controlled_buffer_1
  Pull_Resistor #(.pull(1)) pull_resistor_4 (.node(CLK));

  // Notes on the sheet:
  //   中断源
  //   中断等待指示
  //   总复位信号应将除ROM以外所有存储组件全部清零
  //   多级中断测试信号模拟器
  //   数码管输出
  //   数码管输出应该用寄存器锁存，否则显示数据只能一闪而过
  //   为方便自动评测，需要输出PC，IR，寄存器堆写如数据RDin
  //   RAM写使能MemWrite、RAM写入数据MDin等信号
  //   控制位
  //   暂停节拍，不能为0
  //   戳工具置1进入计数暂停模式，ctrl+k时钟自动运行到对应节拍暂停
  //   ctrl+k关闭时钟连续运行，将控制位置零，进入单步调试模式调试
  //   可计数暂停的时钟源
endmodule

module \封装正确性测试  (
);

  wire IR1, IR2, IR3, MemW, RegW;
  wire [31:0] EX_PC, ID_PC, IF_PC, IR, LED, MDin, MDinr, MEM_PC, PC, RDin, RDinr, WB_PC;

  \单周期RISC_V  \u_单周期risc_v_1  (
    .IR1(IR1), .IR2(IR2), .IR3(IR3), .RegWrite(RegW), .MemWrite(MemW), .PC(PC), .IR(IR), .RDin(RDin),
    .MDin(MDin), .LedData(LED));
  \气泡流水线  \u_气泡流水线_1  (
    .RegWrite(RegW), .MemWrite(MemW), .IF_PC(IF_PC), .ID_PC(ID_PC), .EX_PC(EX_PC), .M_PC(MEM_PC),
    .WB_PC(WB_PC), .RDin(RDinr), .MDin(MDinr), .LedData(LED));
  \单周期_单级中断  \u_单周期_单级中断_1  (
    .IR1(IR1), .IR2(IR2), .IR3(IR3), .RegWrite(RegW), .MemWrite(MemW), .PC(PC), .IR(IR), .RDin(RDin),
    .MDin(MDin), .LedData(LED));
  \理想流水线  \u_理想流水线_1  (
    .RegWrite(RegW), .MemWrite(MemW), .IF_PC(IF_PC), .ID_PC(ID_PC), .EX_PC(EX_PC), .M_PC(MEM_PC),
    .WB_PC(WB_PC), .RDin(RDinr), .MDin(MDinr), .LedData(LED));
  \重定向流水线  \u_重定向流水线_1  (
    .RegWrite(RegW), .MemWrite(MemW), .IF_PC(IF_PC), .ID_PC(ID_PC), .EX_PC(EX_PC), .M_PC(MEM_PC),
    .WB_PC(WB_PC), .RDin(RDinr), .MDin(MDinr), .LedData(LED));
  \单周期_多级中断  \u_单周期_多级中断_1  (
    .IR1(IR1), .IR2(IR2), .IR3(IR3), .RegWrite(RegW), .MemWrite(MemW), .PC(PC), .IR(IR), .RDin(RDin),
    .MDin(MDin), .LedData(LED));

  // Notes on the sheet:
  //   单周期封装测试
  //   气泡流水封装测试
  //   单周期+单级中断封装测试
  //   请检查上面封装有无位宽不匹配，引脚标签是否和连接的标签相对应，否则无法在educoder平台上正确测试
  //   理想流水封装测试
  //   重定向流水封装测试
  //   单周期+多级中断封装测试
endmodule

module IF_ID (
  input  halt,
  input  RST,
  input  [31:0] IF_PC,
  input  [31:0] IF_IR,
  input  [31:0] IF_PC_4,
  input  CLK,
  input  PredictBranch,
  output [31:0] ID_PC,
  output [31:0] ID_IR,
  output [31:0] ID_PC_4,
  output PredictBranch_2
);

  wire multiplexer_4_out, not_1_out;
  wire [31:0] multiplexer_1_out, multiplexer_2_out, multiplexer_3_out;

  Multiplexer #(.select(1), .width(32), .disabled("Z"), .enable("false")) multiplexer_1 (
    .in0(IF_PC), .in1({32{1'b0}}), .out(multiplexer_1_out), .sel(RST));
  Multiplexer #(.select(1), .width(32), .disabled("Z"), .enable("false")) multiplexer_2 (
    .in0(IF_IR), .in1({32{1'b0}}), .out(multiplexer_2_out), .sel(RST));
  Multiplexer #(.select(1), .width(32), .disabled("Z"), .enable("false")) multiplexer_3 (
    .in0(IF_PC_4), .in1({32{1'b0}}), .out(multiplexer_3_out), .sel(RST));
  Multiplexer #(.select(1), .width(1), .disabled("Z"), .enable("false")) multiplexer_4 (
    .in0(PredictBranch), .in1(1'b0), .out(multiplexer_4_out), .sel(RST));
  not not_1 (not_1_out, halt);
  Register #(.width(32), .trigger("rising"), .Select("low")) register_1 (
    .D(multiplexer_1_out), .en(not_1_out), .Q(ID_PC), .clk(CLK));  // open: clr
  Register #(.width(32), .trigger("rising"), .Select("low")) register_2 (
    .D(multiplexer_2_out), .en(not_1_out), .Q(ID_IR), .clk(CLK));  // open: clr
  Register #(.width(32), .trigger("rising"), .Select("low")) register_3 (
    .D(multiplexer_3_out), .en(not_1_out), .Q(ID_PC_4), .clk(CLK));  // open: clr
  Register #(.width(1), .trigger("rising"), .Select("low")) register_4 (
    .D(multiplexer_4_out), .en(not_1_out), .Q(PredictBranch_2), .clk(CLK));  // open: clr
  Pull_Resistor #(.pull(0)) pull_resistor_1 ();  // open: node
endmodule

module ID_EX (
  input  RST,
  input  halt,
  input  CLK,
  input  AUIPC,
  input  URET,
  input  LBU,
  input  JALR,
  input  JAL,
  input  Beq,
  input  BGE,
  input  BNE,
  input  Mem2Reg,
  input  MenWrite,
  input  [3:0] ALU_OP,
  input  ALU_SRC,
  input  REG_WRITE,
  input  ECALL,
  input  [31:0] PC,
  input  [31:0] R1,
  input  [31:0] R2,
  input  [31:0] IS,
  input  [31:0] IR,
  input  [31:0] JalPc,
  input  [31:0] BrachPc,
  input  [31:0] Pc_4,
  input  [4:0] W,
  input  [31:0] \U型 ,
  input  [1:0] R1Fwd,
  input  [1:0] R2Fwd,
  input  PredictBranch,
  output AUIPC_2,
  output URET_2,
  output LBU_2,
  output JALR_2,
  output JAL_2,
  output BEQ_2,
  output BGE_2,
  output BNE_2,
  output MEM2REG_2,
  output MEMWRITE,
  output [3:0] ALU_OP_2,
  output ALU_SRC_2,
  output REG_WRITE_2,
  output ECALL_2,
  output [31:0] PC_2,
  output [31:0] R1_2,
  output [31:0] R2_2,
  output [31:0] IS_2,
  output [31:0] IR_2,
  output [31:0] JalPc_2,
  output [31:0] BrachPc_2,
  output [31:0] Pc_4_2,
  output [4:0] W_2,
  output [31:0] \U型_2 ,
  output [1:0] R1Fwd_2,
  output [1:0] R2Fwd_2,
  output PredictBranch_2
);

  wire multiplexer_1_out, multiplexer_2_out, multiplexer_3_out, multiplexer_4_out, multiplexer_5_out,
       multiplexer_6_out, multiplexer_7_out, multiplexer_8_out, multiplexer_9_out, multiplexer_10_out,
       multiplexer_12_out, multiplexer_13_out, multiplexer_14_out, multiplexer_27_out, not_1_out, undriven;
  wire [1:0] multiplexer_25_out, multiplexer_26_out;
  wire [3:0] multiplexer_11_out;
  wire [4:0] multiplexer_23_out;
  wire [31:0] multiplexer_15_out, multiplexer_16_out, multiplexer_17_out, multiplexer_18_out,
       multiplexer_19_out, multiplexer_20_out, multiplexer_21_out, multiplexer_22_out, multiplexer_24_out;

  Multiplexer #(.select(1), .width(1), .disabled("Z"), .enable("false")) multiplexer_1 (
    .in0(AUIPC), .in1(1'b0), .out(multiplexer_1_out), .sel(RST));
  Multiplexer #(.select(1), .width(1), .disabled("Z"), .enable("false")) multiplexer_2 (
    .in0(URET), .in1(1'b0), .out(multiplexer_2_out), .sel(RST));
  Multiplexer #(.select(1), .width(1), .disabled("Z"), .enable("false")) multiplexer_3 (
    .in0(LBU), .in1(1'b0), .out(multiplexer_3_out), .sel(RST));
  Multiplexer #(.select(1), .width(1), .disabled("Z"), .enable("false")) multiplexer_4 (
    .in0(JALR), .in1(1'b0), .out(multiplexer_4_out), .sel(RST));
  Multiplexer #(.select(1), .width(1), .disabled("Z"), .enable("false")) multiplexer_5 (
    .in0(JAL), .in1(1'b0), .out(multiplexer_5_out), .sel(RST));
  Multiplexer #(.select(1), .width(1), .disabled("Z"), .enable("false")) multiplexer_6 (
    .in0(Beq), .in1(1'b0), .out(multiplexer_6_out), .sel(RST));
  Multiplexer #(.select(1), .width(1), .disabled("Z"), .enable("false")) multiplexer_7 (
    .in0(BGE), .in1(1'b0), .out(multiplexer_7_out), .sel(RST));
  Multiplexer #(.select(1), .width(1), .disabled("Z"), .enable("false")) multiplexer_8 (
    .in0(BNE), .in1(1'b0), .out(multiplexer_8_out), .sel(RST));
  Multiplexer #(.select(1), .width(1), .disabled("Z"), .enable("false")) multiplexer_9 (
    .in0(Mem2Reg), .in1(1'b0), .out(multiplexer_9_out), .sel(RST));
  Multiplexer #(.select(1), .width(1), .disabled("Z"), .enable("false")) multiplexer_10 (
    .in0(MenWrite), .in1(1'b0), .out(multiplexer_10_out), .sel(RST));
  Multiplexer #(.select(1), .width(4), .disabled("Z"), .enable("false")) multiplexer_11 (
    .in0(ALU_OP), .in1(4'b0000), .out(multiplexer_11_out), .sel(RST));
  Multiplexer #(.select(1), .width(1), .disabled("Z"), .enable("false")) multiplexer_12 (
    .in0(ALU_SRC), .in1(1'b0), .out(multiplexer_12_out), .sel(RST));
  Multiplexer #(.select(1), .width(1), .disabled("Z"), .enable("false")) multiplexer_13 (
    .in0(REG_WRITE), .in1(1'b0), .out(multiplexer_13_out), .sel(RST));
  Multiplexer #(.select(1), .width(1), .disabled("Z"), .enable("false")) multiplexer_14 (
    .in0(ECALL), .in1(1'b0), .out(multiplexer_14_out), .sel(RST));
  Multiplexer #(.select(1), .width(32), .disabled("Z"), .enable("false")) multiplexer_15 (
    .in0(PC), .in1({32{1'b0}}), .out(multiplexer_15_out), .sel(RST));
  Multiplexer #(.select(1), .width(32), .disabled("Z"), .enable("false")) multiplexer_16 (
    .in0(R1), .in1({32{1'b0}}), .out(multiplexer_16_out), .sel(RST));
  Multiplexer #(.select(1), .width(32), .disabled("Z"), .enable("false")) multiplexer_17 (
    .in0(R2), .in1({32{1'b0}}), .out(multiplexer_17_out), .sel(RST));
  Multiplexer #(.select(1), .width(32), .disabled("Z"), .enable("false")) multiplexer_18 (
    .in0(IS), .in1({32{1'b0}}), .out(multiplexer_18_out), .sel(RST));
  Multiplexer #(.select(1), .width(32), .disabled("Z"), .enable("false")) multiplexer_19 (
    .in0(IR), .in1({32{1'b0}}), .out(multiplexer_19_out), .sel(RST));
  Multiplexer #(.select(1), .width(32), .disabled("Z"), .enable("false")) multiplexer_20 (
    .in0(JalPc), .in1({32{1'b0}}), .out(multiplexer_20_out), .sel(RST));
  Multiplexer #(.select(1), .width(32), .disabled("Z"), .enable("false")) multiplexer_21 (
    .in0(BrachPc), .in1({32{1'b0}}), .out(multiplexer_21_out), .sel(RST));
  Multiplexer #(.select(1), .width(32), .disabled("Z"), .enable("false")) multiplexer_22 (
    .in0(Pc_4), .in1({32{1'b0}}), .out(multiplexer_22_out), .sel(RST));
  Multiplexer #(.select(1), .width(5), .disabled("Z"), .enable("false")) multiplexer_23 (
    .in0(W), .in1({5{1'b0}}), .out(multiplexer_23_out), .sel(RST));
  Multiplexer #(.select(1), .width(32), .disabled("Z"), .enable("false")) multiplexer_24 (
    .in0(\U型 ), .in1({32{1'b0}}), .out(multiplexer_24_out), .sel(RST));
  Multiplexer #(.select(1), .width(2), .disabled("Z"), .enable("false")) multiplexer_25 (
    .in0(R1Fwd), .in1(2'b00), .out(multiplexer_25_out), .sel(RST));
  Multiplexer #(.select(1), .width(2), .disabled("Z"), .enable("false")) multiplexer_26 (
    .in0(R2Fwd), .in1(2'b00), .out(multiplexer_26_out), .sel(RST));
  Multiplexer #(.select(1), .width(1), .disabled("Z"), .enable("false")) multiplexer_27 (
    .in0(PredictBranch), .in1(1'b0), .out(multiplexer_27_out), .sel(RST));
  Register #(.width(1), .trigger("rising"), .Select("low")) register_1 (
    .D(multiplexer_1_out), .en(not_1_out), .Q(AUIPC_2), .clk(CLK));  // open: clr
  Register #(.width(1), .trigger("rising"), .Select("low")) register_2 (
    .D(multiplexer_2_out), .en(not_1_out), .Q(URET_2), .clk(CLK));  // open: clr
  Register #(.width(1), .trigger("rising"), .Select("low")) register_3 (
    .D(multiplexer_3_out), .en(not_1_out), .Q(LBU_2), .clk(CLK));  // open: clr
  Register #(.width(1), .trigger("rising"), .Select("low")) register_4 (
    .D(multiplexer_4_out), .en(not_1_out), .Q(JALR_2), .clk(CLK));  // open: clr
  Register #(.width(1), .trigger("rising"), .Select("low")) register_5 (
    .D(multiplexer_5_out), .en(not_1_out), .Q(JAL_2), .clk(CLK));  // open: clr
  Register #(.width(1), .trigger("rising"), .Select("low")) register_6 (
    .D(multiplexer_6_out), .en(not_1_out), .Q(BEQ_2), .clk(CLK));  // open: clr
  Register #(.width(1), .trigger("rising"), .Select("low")) register_7 (
    .D(multiplexer_7_out), .en(not_1_out), .Q(BGE_2), .clk(CLK));  // open: clr
  Register #(.width(1), .trigger("rising"), .Select("low")) register_8 (
    .D(multiplexer_8_out), .en(not_1_out), .Q(BNE_2), .clk(CLK));  // open: clr
  Register #(.width(1), .trigger("rising"), .Select("low")) register_9 (
    .D(multiplexer_9_out), .en(not_1_out), .Q(MEM2REG_2), .clk(CLK));  // open: clr
  Register #(.width(1), .trigger("rising"), .Select("low")) register_10 (
    .D(multiplexer_10_out), .en(not_1_out), .Q(MEMWRITE), .clk(CLK));  // open: clr
  Register #(.width(4), .trigger("rising"), .Select("low")) register_11 (
    .D(multiplexer_11_out), .en(not_1_out), .Q(ALU_OP_2), .clk(CLK));  // open: clr
  Register #(.width(1), .trigger("rising"), .Select("low")) register_12 (
    .D(multiplexer_12_out), .en(not_1_out), .Q(ALU_SRC_2), .clk(CLK));  // open: clr
  Register #(.width(1), .trigger("rising"), .Select("low")) register_13 (
    .D(multiplexer_13_out), .en(not_1_out), .Q(REG_WRITE_2), .clk(CLK));  // open: clr
  Register #(.width(1), .trigger("rising"), .Select("low")) register_14 (
    .D(multiplexer_14_out), .en(not_1_out), .Q(ECALL_2), .clk(CLK));  // open: clr
  Register #(.width(32), .trigger("rising"), .Select("low")) register_15 (
    .D(multiplexer_15_out), .en(not_1_out), .Q(PC_2), .clk(CLK));  // open: clr
  Register #(.width(32), .trigger("rising"), .Select("low")) register_16 (
    .D(multiplexer_16_out), .en(not_1_out), .Q(R1_2), .clk(CLK));  // open: clr
  Register #(.width(32), .trigger("rising"), .Select("low")) register_17 (
    .D(multiplexer_17_out), .en(not_1_out), .Q(R2_2), .clk(CLK));  // open: clr
  Register #(.width(32), .trigger("rising"), .Select("low")) register_18 (
    .D(multiplexer_18_out), .en(not_1_out), .Q(IS_2), .clk(CLK), .clr(undriven));
  Register #(.width(32), .trigger("rising"), .Select("low")) register_19 (
    .D(multiplexer_19_out), .en(not_1_out), .Q(IR_2), .clk(CLK));  // open: clr
  Register #(.width(32), .trigger("rising"), .Select("low")) register_20 (
    .D(multiplexer_20_out), .en(not_1_out), .Q(JalPc_2), .clk(CLK));  // open: clr
  Register #(.width(32), .trigger("rising"), .Select("low")) register_21 (
    .D(multiplexer_21_out), .en(not_1_out), .Q(BrachPc_2), .clk(CLK));  // open: clr
  Register #(.width(32), .trigger("rising"), .Select("low")) register_22 (
    .D(multiplexer_22_out), .en(not_1_out), .Q(Pc_4_2), .clk(CLK));  // open: clr
  Register #(.width(5), .trigger("rising"), .Select("low")) register_23 (
    .D(multiplexer_23_out), .en(not_1_out), .Q(W_2), .clk(CLK));  // open: clr
  Register #(.width(32), .trigger("rising"), .Select("low")) register_24 (
    .D(multiplexer_24_out), .en(not_1_out), .Q(\U型_2 ), .clk(CLK));  // open: clr
  Register #(.width(2), .trigger("rising"), .Select("low")) register_25 (
    .D(multiplexer_25_out), .en(not_1_out), .Q(R1Fwd_2), .clk(CLK));  // open: clr
  Register #(.width(2), .trigger("rising"), .Select("low")) register_26 (
    .D(multiplexer_26_out), .en(not_1_out), .Q(R2Fwd_2), .clk(CLK));  // open: clr
  Register #(.width(1), .trigger("rising"), .Select("low")) register_27 (
    .D(multiplexer_27_out), .en(not_1_out), .Q(PredictBranch_2), .clk(CLK));  // open: clr
  Pull_Resistor #(.pull(0)) pull_resistor_1 ();  // open: node
  not not_1 (not_1_out, halt);
endmodule

module EX_MEM (
  input  halt,
  input  RST,
  input  CLK,
  input  AUIPC,
  input  LBU,
  input  JALR,
  input  JAL,
  input  Mem2Reg,
  input  MenWrite,
  input  REG_WRITE,
  input  ECALL,
  input  [31:0] PC,
  input  [31:0] R1,
  input  [31:0] R2,
  input  [31:0] IR,
  input  [31:0] ALUResult,
  input  [31:0] Pc_4,
  input  [4:0] W,
  input  [31:0] \U型 ,
  output AUIPC_2,
  output LBU_2,
  output JALR_2,
  output JAL_2,
  output MEM2REG_2,
  output MEMWRITE,
  output REG_WRITE_2,
  output ECALL_2,
  output [31:0] PC_2,
  output [31:0] R1_2,
  output [31:0] R2_2,
  output [31:0] IR_2,
  output [31:0] ALUResult_2,
  output [31:0] Pc_4_2,
  output [4:0] W_2,
  output [31:0] \U型_2 
);

  wire multiplexer_1_out, multiplexer_2_out, multiplexer_3_out, multiplexer_4_out, multiplexer_5_out,
       multiplexer_6_out, multiplexer_7_out, multiplexer_8_out, not_1_out, undriven;
  wire [4:0] multiplexer_15_out;
  wire [31:0] multiplexer_9_out, multiplexer_10_out, multiplexer_11_out, multiplexer_12_out,
       multiplexer_13_out, multiplexer_14_out, multiplexer_16_out;

  not not_1 (not_1_out, halt);
  Multiplexer #(.select(1), .width(1), .disabled("Z"), .enable("false")) multiplexer_1 (
    .in0(AUIPC), .in1(1'b0), .out(multiplexer_1_out), .sel(RST));
  Multiplexer #(.select(1), .width(1), .disabled("Z"), .enable("false")) multiplexer_2 (
    .in0(LBU), .in1(1'b0), .out(multiplexer_2_out), .sel(RST));
  Multiplexer #(.select(1), .width(1), .disabled("Z"), .enable("false")) multiplexer_3 (
    .in0(JALR), .in1(1'b0), .out(multiplexer_3_out), .sel(RST));
  Multiplexer #(.select(1), .width(1), .disabled("Z"), .enable("false")) multiplexer_4 (
    .in0(JAL), .in1(1'b0), .out(multiplexer_4_out), .sel(RST));
  Multiplexer #(.select(1), .width(1), .disabled("Z"), .enable("false")) multiplexer_5 (
    .in0(Mem2Reg), .in1(1'b0), .out(multiplexer_5_out), .sel(RST));
  Multiplexer #(.select(1), .width(1), .disabled("Z"), .enable("false")) multiplexer_6 (
    .in0(MenWrite), .in1(1'b0), .out(multiplexer_6_out), .sel(RST));
  Multiplexer #(.select(1), .width(1), .disabled("Z"), .enable("false")) multiplexer_7 (
    .in0(REG_WRITE), .in1(1'b0), .out(multiplexer_7_out), .sel(RST));
  Multiplexer #(.select(1), .width(1), .disabled("Z"), .enable("false")) multiplexer_8 (
    .in0(ECALL), .in1(1'b0), .out(multiplexer_8_out), .sel(RST));
  Multiplexer #(.select(1), .width(32), .disabled("Z"), .enable("false")) multiplexer_9 (
    .in0(PC), .in1({32{1'b0}}), .out(multiplexer_9_out), .sel(RST));
  Multiplexer #(.select(1), .width(32), .disabled("Z"), .enable("false")) multiplexer_10 (
    .in0(R1), .in1({32{1'b0}}), .out(multiplexer_10_out), .sel(RST));
  Multiplexer #(.select(1), .width(32), .disabled("Z"), .enable("false")) multiplexer_11 (
    .in0(R2), .in1({32{1'b0}}), .out(multiplexer_11_out), .sel(RST));
  Multiplexer #(.select(1), .width(32), .disabled("Z"), .enable("false")) multiplexer_12 (
    .in0(IR), .in1({32{1'b0}}), .out(multiplexer_12_out), .sel(RST));
  Multiplexer #(.select(1), .width(32), .disabled("Z"), .enable("false")) multiplexer_13 (
    .in0(ALUResult), .in1({32{1'b0}}), .out(multiplexer_13_out), .sel(RST));
  Multiplexer #(.select(1), .width(32), .disabled("Z"), .enable("false")) multiplexer_14 (
    .in0(Pc_4), .in1({32{1'b0}}), .out(multiplexer_14_out), .sel(RST));
  Multiplexer #(.select(1), .width(5), .disabled("Z"), .enable("false")) multiplexer_15 (
    .in0(W), .in1({5{1'b0}}), .out(multiplexer_15_out), .sel(RST));
  Multiplexer #(.select(1), .width(32), .disabled("Z"), .enable("false")) multiplexer_16 (
    .in0(\U型 ), .in1({32{1'b0}}), .out(multiplexer_16_out), .sel(RST));
  Pull_Resistor #(.pull(0)) pull_resistor_1 ();  // open: node
  Register #(.width(1), .trigger("rising"), .Select("low")) register_1 (
    .D(multiplexer_1_out), .en(not_1_out), .Q(AUIPC_2), .clk(CLK));  // open: clr
  Register #(.width(1), .trigger("rising"), .Select("low")) register_2 (
    .D(multiplexer_2_out), .en(not_1_out), .Q(LBU_2), .clk(CLK), .clr(undriven));
  Register #(.width(1), .trigger("rising"), .Select("low")) register_3 (
    .D(multiplexer_3_out), .en(not_1_out), .Q(JALR_2), .clk(CLK));  // open: clr
  Register #(.width(1), .trigger("rising"), .Select("low")) register_4 (
    .D(multiplexer_4_out), .en(not_1_out), .Q(JAL_2), .clk(CLK));  // open: clr
  Register #(.width(1), .trigger("rising"), .Select("low")) register_5 (
    .D(multiplexer_5_out), .en(not_1_out), .Q(MEM2REG_2), .clk(CLK));  // open: clr
  Register #(.width(1), .trigger("rising"), .Select("low")) register_6 (
    .D(multiplexer_6_out), .en(not_1_out), .Q(MEMWRITE), .clk(CLK));  // open: clr
  Register #(.width(1), .trigger("rising"), .Select("low")) register_7 (
    .D(multiplexer_7_out), .en(not_1_out), .Q(REG_WRITE_2), .clk(CLK));  // open: clr
  Register #(.width(1), .trigger("rising"), .Select("low")) register_8 (
    .D(multiplexer_8_out), .Q(ECALL_2), .clk(CLK));  // open: en, clr
  Register #(.width(32), .trigger("rising"), .Select("low")) register_9 (
    .D(multiplexer_9_out), .en(not_1_out), .Q(PC_2), .clk(CLK));  // open: clr
  Register #(.width(32), .trigger("rising"), .Select("low")) register_10 (
    .D(multiplexer_10_out), .en(not_1_out), .Q(R1_2), .clk(CLK));  // open: clr
  Register #(.width(32), .trigger("rising"), .Select("low")) register_11 (
    .D(multiplexer_11_out), .en(not_1_out), .Q(R2_2), .clk(CLK));  // open: clr
  Register #(.width(32), .trigger("rising"), .Select("low")) register_12 (
    .D(multiplexer_12_out), .en(not_1_out), .Q(IR_2), .clk(CLK));  // open: clr
  Register #(.width(32), .trigger("rising"), .Select("low")) register_13 (
    .D(multiplexer_13_out), .en(not_1_out), .Q(ALUResult_2), .clk(CLK));  // open: clr
  Register #(.width(32), .trigger("rising"), .Select("low")) register_14 (
    .D(multiplexer_14_out), .en(not_1_out), .Q(Pc_4_2), .clk(CLK));  // open: clr
  Register #(.width(5), .trigger("rising"), .Select("low")) register_15 (
    .D(multiplexer_15_out), .en(not_1_out), .Q(W_2), .clk(CLK));  // open: clr
  Register #(.width(32), .trigger("rising"), .Select("low")) register_16 (
    .D(multiplexer_16_out), .en(not_1_out), .Q(\U型_2 ), .clk(CLK));  // open: clr
endmodule

module MEM_WB (
  input  halt,
  input  RST,
  input  CLK,
  input  AUIPC,
  input  LBU,
  input  JALR,
  input  JAL,
  input  Mem2Reg,
  input  REG_WRITE,
  input  ECALL,
  input  [31:0] PC,
  input  [31:0] R1,
  input  [31:0] R2,
  input  [31:0] MemData,
  input  [31:0] IR,
  input  [31:0] ALUResult,
  input  [31:0] Pc_4,
  input  [4:0] W,
  input  [31:0] \U型 ,
  input  LBU0,
  input  LBU1,
  output AUIPC_2,
  output LBU_2,
  output JALR_2,
  output JAL_2,
  output MEM2REG_2,
  output REG_WRITE_2,
  output ECALL_2,
  output [31:0] PC_2,
  output [31:0] R1_2,
  output [31:0] R2_2,
  output [31:0] MemData_2,
  output [31:0] IR_2,
  output [31:0] ALUResult_2,
  output [31:0] Pc_4_2,
  output [4:0] W_2,
  output [31:0] \U型_2 ,
  output LBU0_2,
  output LBU1_2
);

  wire multiplexer_1_out, multiplexer_2_out, multiplexer_3_out, multiplexer_4_out, multiplexer_5_out,
       multiplexer_6_out, multiplexer_7_out, multiplexer_17_out, multiplexer_18_out, not_1_out;
  wire [4:0] multiplexer_15_out;
  wire [31:0] multiplexer_8_out, multiplexer_9_out, multiplexer_10_out, multiplexer_11_out,
       multiplexer_12_out, multiplexer_13_out, multiplexer_14_out, multiplexer_16_out;

  not not_1 (not_1_out, halt);
  Multiplexer #(.select(1), .width(1), .disabled("Z"), .enable("false")) multiplexer_1 (
    .in0(AUIPC), .in1(1'b0), .out(multiplexer_1_out), .sel(RST));
  Multiplexer #(.select(1), .width(1), .disabled("Z"), .enable("false")) multiplexer_2 (
    .in0(LBU), .in1(1'b0), .out(multiplexer_2_out), .sel(RST));
  Multiplexer #(.select(1), .width(1), .disabled("Z"), .enable("false")) multiplexer_3 (
    .in0(JALR), .in1(1'b0), .out(multiplexer_3_out), .sel(RST));
  Multiplexer #(.select(1), .width(1), .disabled("Z"), .enable("false")) multiplexer_4 (
    .in0(JAL), .in1(1'b0), .out(multiplexer_4_out), .sel(RST));
  Multiplexer #(.select(1), .width(1), .disabled("Z"), .enable("false")) multiplexer_5 (
    .in0(Mem2Reg), .in1(1'b0), .out(multiplexer_5_out), .sel(RST));
  Multiplexer #(.select(1), .width(1), .disabled("Z"), .enable("false")) multiplexer_6 (
    .in0(REG_WRITE), .in1(1'b0), .out(multiplexer_6_out), .sel(RST));
  Multiplexer #(.select(1), .width(1), .disabled("Z"), .enable("false")) multiplexer_7 (
    .in0(ECALL), .in1(1'b0), .out(multiplexer_7_out), .sel(RST));
  Multiplexer #(.select(1), .width(32), .disabled("Z"), .enable("false")) multiplexer_8 (
    .in0(PC), .in1({32{1'b0}}), .out(multiplexer_8_out), .sel(RST));
  Multiplexer #(.select(1), .width(32), .disabled("Z"), .enable("false")) multiplexer_9 (
    .in0(R1), .in1({32{1'b0}}), .out(multiplexer_9_out), .sel(RST));
  Multiplexer #(.select(1), .width(32), .disabled("Z"), .enable("false")) multiplexer_10 (
    .in0(R2), .in1({32{1'b0}}), .out(multiplexer_10_out), .sel(RST));
  Multiplexer #(.select(1), .width(32), .disabled("Z"), .enable("false")) multiplexer_11 (
    .in0(MemData), .in1({32{1'b0}}), .out(multiplexer_11_out), .sel(RST));
  Multiplexer #(.select(1), .width(32), .disabled("Z"), .enable("false")) multiplexer_12 (
    .in0(IR), .in1({32{1'b0}}), .out(multiplexer_12_out), .sel(RST));
  Multiplexer #(.select(1), .width(32), .disabled("Z"), .enable("false")) multiplexer_13 (
    .in0(ALUResult), .in1({32{1'b0}}), .out(multiplexer_13_out), .sel(RST));
  Multiplexer #(.select(1), .width(32), .disabled("Z"), .enable("false")) multiplexer_14 (
    .in0(Pc_4), .in1({32{1'b0}}), .out(multiplexer_14_out), .sel(RST));
  Multiplexer #(.select(1), .width(5), .disabled("Z"), .enable("false")) multiplexer_15 (
    .in0(W), .in1({5{1'b0}}), .out(multiplexer_15_out), .sel(RST));
  Multiplexer #(.select(1), .width(32), .disabled("Z"), .enable("false")) multiplexer_16 (
    .in0(\U型 ), .in1({32{1'b0}}), .out(multiplexer_16_out), .sel(RST));
  Multiplexer #(.select(1), .width(1), .disabled("Z"), .enable("false")) multiplexer_17 (
    .in0(LBU0), .in1(1'b0), .out(multiplexer_17_out), .sel(RST));
  Multiplexer #(.select(1), .width(1), .disabled("Z"), .enable("false")) multiplexer_18 (
    .in0(LBU1), .in1(1'b0), .out(multiplexer_18_out), .sel(RST));
  Pull_Resistor #(.pull(0)) pull_resistor_1 ();  // open: node
  Register #(.width(1), .trigger("rising"), .Select("low")) register_1 (
    .D(multiplexer_1_out), .en(not_1_out), .Q(AUIPC_2), .clk(CLK));  // open: clr
  Register #(.width(1), .trigger("rising"), .Select("low")) register_2 (
    .D(multiplexer_2_out), .en(not_1_out), .Q(LBU_2), .clk(CLK));  // open: clr
  Register #(.width(1), .trigger("rising"), .Select("low")) register_3 (
    .D(multiplexer_3_out), .en(not_1_out), .Q(JALR_2), .clk(CLK));  // open: clr
  Register #(.width(1), .trigger("rising"), .Select("low")) register_4 (
    .D(multiplexer_4_out), .en(not_1_out), .Q(JAL_2), .clk(CLK));  // open: clr
  Register #(.width(1), .trigger("rising"), .Select("low")) register_5 (
    .D(multiplexer_5_out), .en(not_1_out), .Q(MEM2REG_2), .clk(CLK));  // open: clr
  Register #(.width(1), .trigger("rising"), .Select("low")) register_6 (
    .D(multiplexer_6_out), .en(not_1_out), .Q(REG_WRITE_2), .clk(CLK));  // open: clr
  Register #(.width(1), .trigger("rising"), .Select("low")) register_7 (
    .D(multiplexer_7_out), .en(not_1_out), .Q(ECALL_2), .clk(CLK));  // open: clr
  Register #(.width(32), .trigger("rising"), .Select("low")) register_8 (
    .D(multiplexer_8_out), .en(not_1_out), .Q(PC_2), .clk(CLK));  // open: clr
  Register #(.width(32), .trigger("rising"), .Select("low")) register_9 (
    .D(multiplexer_9_out), .en(not_1_out), .Q(R1_2), .clk(CLK));  // open: clr
  Register #(.width(32), .trigger("rising"), .Select("low")) register_10 (
    .D(multiplexer_10_out), .en(not_1_out), .Q(R2_2), .clk(CLK));  // open: clr
  Register #(.width(32), .trigger("rising"), .Select("low")) register_11 (
    .D(multiplexer_11_out), .en(not_1_out), .Q(MemData_2), .clk(CLK));  // open: clr
  Register #(.width(32), .trigger("rising"), .Select("low")) register_12 (
    .D(multiplexer_12_out), .en(not_1_out), .Q(IR_2), .clk(CLK));  // open: clr
  Register #(.width(32), .trigger("rising"), .Select("low")) register_13 (
    .D(multiplexer_13_out), .en(not_1_out), .Q(ALUResult_2), .clk(CLK));  // open: clr
  Register #(.width(32), .trigger("rising"), .Select("low")) register_14 (
    .D(multiplexer_14_out), .en(not_1_out), .Q(Pc_4_2), .clk(CLK));  // open: clr
  Register #(.width(5), .trigger("rising"), .Select("low")) register_15 (
    .D(multiplexer_15_out), .en(not_1_out), .Q(W_2), .clk(CLK));  // open: clr
  Register #(.width(32), .trigger("rising"), .Select("low")) register_16 (
    .D(multiplexer_16_out), .en(not_1_out), .Q(\U型_2 ), .clk(CLK));  // open: clr
  Register #(.width(1), .trigger("rising"), .Select("low")) register_17 (
    .D(multiplexer_17_out), .en(not_1_out), .Q(LBU0_2), .clk(CLK));  // open: clr
  Register #(.width(1), .trigger("rising"), .Select("low")) register_18 (
    .D(multiplexer_18_out), .en(not_1_out), .Q(LBU1_2), .clk(CLK));  // open: clr
endmodule

module \数据相关检测  (
  input  R1Used,
  input  R2Used,
  input  [4:0] R1_num,
  input  [4:0] R2_num,
  input  [4:0] EX_W,
  input  EX_Regwrite,
  input  [4:0] MEM_W,
  input  MEM_Regwrite,
  output DataHazzard
);

  wire and_1_out, and_2_out, and_3_out, and_4_out, comparator_1_eq, comparator_2_eq, comparator_3_eq,
       comparator_4_eq, comparator_5_eq, comparator_6_eq, not_1_out, not_2_out, or_1_out, or_2_out, or_3_out;

  Comparator #(.width(5), .mode("twosComplement")) comparator_1 (
    .a(EX_W), .b(R2_num), .eq(comparator_1_eq));  // open: gt, lt
  Comparator #(.width(5), .mode("twosComplement")) comparator_2 (
    .a(R1_num), .b(MEM_W), .eq(comparator_2_eq));  // open: gt, lt
  Comparator #(.width(5), .mode("twosComplement")) comparator_3 (
    .a(MEM_W), .b(R2_num), .eq(comparator_3_eq));  // open: gt, lt
  Comparator #(.width(5), .mode("twosComplement")) comparator_4 (
    .a(R1_num), .b({5{1'b0}}), .eq(comparator_4_eq));  // open: gt, lt
  not not_1 (not_1_out, comparator_4_eq);
  not not_2 (not_2_out, comparator_5_eq);
  Comparator #(.width(5), .mode("twosComplement")) comparator_5 (
    .a(R2_num), .b({5{1'b0}}), .eq(comparator_5_eq));  // open: gt, lt
  Comparator #(.width(5), .mode("twosComplement")) comparator_6 (
    .a(EX_W), .b(R1_num), .eq(comparator_6_eq));  // open: gt, lt
  and and_1 (and_1_out, not_1_out, comparator_6_eq, EX_Regwrite);
  and and_2 (and_2_out, not_2_out, comparator_1_eq, EX_Regwrite);
  and and_3 (and_3_out, not_1_out, comparator_2_eq, MEM_Regwrite);
  and and_4 (and_4_out, not_2_out, comparator_3_eq, MEM_Regwrite);
  or or_1 (or_1_out, and_1_out, and_3_out);
  or or_2 (or_2_out, or_1_out, or_3_out);
  or or_3 (or_3_out, and_2_out, and_4_out);
  Multiplexer #(.select(2), .width(1), .disabled("Z"), .enable("false")) multiplexer_1 (
    .in0(1'b0), .in1(or_1_out), .in2(or_3_out), .in3(or_2_out), .out(DataHazzard), .sel({R2Used, R1Used}));
endmodule

module \R1R2Used检测  (
  input  OP2,
  input  OP3,
  input  OP4,
  input  OP5,
  input  OP6,
  input  F12,
  input  F13,
  input  F14,
  input  F25,
  input  F30,
  output R1Used,
  output R2Used
);

  wire and_1_out, and_2_out, and_3_out, and_4_out, and_5_out, and_6_out, and_7_out, and_8_out, and_9_out,
       and_10_out, and_11_out, and_12_out, and_13_out, and_14_out, and_15_out, and_16_out, and_17_out,
       and_18_out, and_19_out, and_20_out, and_21_out, and_22_out, and_23_out, and_24_out, and_25_out,
       and_26_out, and_27_out, and_28_out, and_29_out, and_30_out, and_31_out, and_32_out, and_33_out,
       and_34_out, not_1_out, not_2_out, not_3_out, not_4_out, not_5_out, not_6_out, not_7_out, not_8_out,
       not_9_out, not_10_out, not_11_out, not_12_out, not_13_out, not_14_out, not_15_out, not_16_out,
       not_17_out, not_18_out, not_19_out, not_20_out, not_21_out, not_22_out, not_23_out, not_24_out,
       not_25_out, not_26_out, not_27_out, not_28_out, not_29_out, not_30_out, not_31_out, not_32_out,
       not_33_out, not_34_out, not_35_out, not_36_out, not_37_out, not_38_out, not_39_out, not_40_out,
       not_41_out, not_42_out, not_43_out, not_44_out, not_45_out, not_46_out, not_47_out, not_48_out,
       not_49_out, not_50_out, not_51_out, not_52_out, not_53_out, not_54_out, not_55_out, not_56_out,
       not_57_out, not_58_out, not_59_out, not_60_out, not_61_out, not_62_out, not_63_out, not_64_out,
       not_65_out, not_66_out, not_67_out, not_68_out, not_69_out, not_70_out, not_71_out, not_72_out,
       not_73_out, not_74_out, not_75_out, not_76_out, not_77_out, not_78_out, not_79_out, not_80_out,
       not_81_out, not_82_out, not_83_out, not_84_out, not_85_out, not_86_out, not_87_out, not_88_out,
       not_89_out, not_90_out, not_91_out, not_92_out, not_93_out, not_94_out, not_95_out, not_96_out,
       not_97_out, not_98_out, not_99_out, not_100_out, not_101_out, not_102_out, not_103_out, not_104_out,
       not_105_out, not_106_out, not_107_out, not_108_out, not_109_out, not_110_out, not_111_out,
       not_112_out, not_113_out, not_114_out, not_115_out, not_116_out, not_117_out, not_118_out,
       not_119_out, not_120_out, not_121_out, not_122_out, not_123_out, not_124_out, not_125_out,
       not_126_out, not_127_out, not_128_out, not_129_out, not_130_out, not_131_out, not_132_out,
       not_133_out, not_134_out, not_135_out, not_136_out, not_137_out, not_138_out, not_139_out,
       not_140_out, not_141_out, not_142_out, not_143_out, not_144_out, not_145_out, not_146_out,
       not_147_out, not_148_out, not_149_out, not_150_out, not_151_out, not_152_out, not_153_out,
       not_154_out, not_155_out, not_156_out, not_157_out, not_158_out, not_159_out, not_160_out,
       not_161_out, not_162_out, not_163_out, not_164_out, not_165_out, not_166_out, not_167_out,
       not_168_out, not_169_out, not_170_out, not_171_out, not_172_out, not_173_out, not_174_out,
       not_175_out, not_176_out, not_177_out, not_178_out, not_179_out, not_180_out, not_181_out,
       not_182_out, not_183_out, not_184_out, not_185_out, not_186_out, not_187_out, not_188_out,
       not_189_out, not_190_out, not_191_out, not_192_out, not_193_out, not_194_out, not_195_out,
       not_196_out, not_197_out, not_198_out, not_199_out, not_200_out, not_201_out, not_202_out,
       not_203_out, not_204_out, not_205_out, not_206_out, not_207_out;

  not not_1 (not_1_out, F30);
  not not_2 (not_2_out, F25);
  not not_3 (not_3_out, F14);
  not not_4 (not_4_out, F13);
  not not_5 (not_5_out, F12);
  not not_6 (not_6_out, OP6);
  not not_7 (not_7_out, OP3);
  not not_8 (not_8_out, OP2);
  not not_9 (not_9_out, F25);
  not not_10 (not_10_out, F14);
  not not_11 (not_11_out, F13);
  not not_12 (not_12_out, F12);
  not not_13 (not_13_out, OP6);
  not not_14 (not_14_out, OP3);
  not not_15 (not_15_out, OP2);
  not not_16 (not_16_out, F30);
  not not_17 (not_17_out, F25);
  not not_18 (not_18_out, OP6);
  not not_19 (not_19_out, OP3);
  not not_20 (not_20_out, OP2);
  not not_21 (not_21_out, F30);
  not not_22 (not_22_out, F25);
  not not_23 (not_23_out, F12);
  not not_24 (not_24_out, OP6);
  not not_25 (not_25_out, OP3);
  not not_26 (not_26_out, OP2);
  not not_27 (not_27_out, F30);
  not not_28 (not_28_out, F25);
  not not_29 (not_29_out, F14);
  not not_30 (not_30_out, F12);
  not not_31 (not_31_out, OP6);
  not not_32 (not_32_out, OP3);
  not not_33 (not_33_out, OP2);
  not not_34 (not_34_out, F30);
  not not_35 (not_35_out, F25);
  not not_36 (not_36_out, F14);
  not not_37 (not_37_out, OP6);
  not not_38 (not_38_out, OP3);
  not not_39 (not_39_out, OP2);
  not not_40 (not_40_out, F14);
  not not_41 (not_41_out, F13);
  not not_42 (not_42_out, F12);
  not not_43 (not_43_out, OP6);
  not not_44 (not_44_out, OP5);
  not not_45 (not_45_out, OP3);
  not not_46 (not_46_out, OP2);
  not not_47 (not_47_out, OP6);
  not not_48 (not_48_out, OP5);
  not not_49 (not_49_out, OP3);
  not not_50 (not_50_out, OP2);
  not not_51 (not_51_out, F12);
  not not_52 (not_52_out, OP6);
  not not_53 (not_53_out, OP5);
  not not_54 (not_54_out, OP3);
  not not_55 (not_55_out, OP2);
  not not_56 (not_56_out, F13);
  not not_57 (not_57_out, F12);
  not not_58 (not_58_out, OP6);
  not not_59 (not_59_out, OP5);
  not not_60 (not_60_out, OP3);
  not not_61 (not_61_out, OP2);
  not not_62 (not_62_out, F14);
  not not_63 (not_63_out, F12);
  not not_64 (not_64_out, OP6);
  not not_65 (not_65_out, OP5);
  not not_66 (not_66_out, OP3);
  not not_67 (not_67_out, OP2);
  not not_68 (not_68_out, F30);
  not not_69 (not_69_out, F25);
  not not_70 (not_70_out, F14);
  not not_71 (not_71_out, F13);
  not not_72 (not_72_out, OP6);
  not not_73 (not_73_out, OP5);
  not not_74 (not_74_out, OP3);
  not not_75 (not_75_out, OP2);
  not not_76 (not_76_out, F30);
  not not_77 (not_77_out, F25);
  not not_78 (not_78_out, F13);
  not not_79 (not_79_out, OP6);
  not not_80 (not_80_out, OP5);
  not not_81 (not_81_out, OP3);
  not not_82 (not_82_out, OP2);
  not not_83 (not_83_out, F25);
  not not_84 (not_84_out, F13);
  not not_85 (not_85_out, OP6);
  not not_86 (not_86_out, OP5);
  not not_87 (not_87_out, OP3);
  not not_88 (not_88_out, OP2);
  not not_89 (not_89_out, F14);
  not not_90 (not_90_out, F12);
  not not_91 (not_91_out, OP6);
  not not_92 (not_92_out, OP5);
  not not_93 (not_93_out, OP4);
  not not_94 (not_94_out, OP3);
  not not_95 (not_95_out, OP2);
  not not_96 (not_96_out, F14);
  not not_97 (not_97_out, F12);
  not not_98 (not_98_out, OP6);
  not not_99 (not_99_out, OP4);
  not not_100 (not_100_out, OP3);
  not not_101 (not_101_out, OP2);
  not not_102 (not_102_out, F30);
  not not_103 (not_103_out, F25);
  not not_104 (not_104_out, F14);
  not not_105 (not_105_out, F13);
  not not_106 (not_106_out, F12);
  not not_107 (not_107_out, OP3);
  not not_108 (not_108_out, OP2);
  not not_109 (not_109_out, F14);
  not not_110 (not_110_out, F13);
  not not_111 (not_111_out, F12);
  not not_112 (not_112_out, OP4);
  not not_113 (not_113_out, OP3);
  not not_114 (not_114_out, OP2);
  not not_115 (not_115_out, F14);
  not not_116 (not_116_out, F13);
  not not_117 (not_117_out, OP4);
  not not_118 (not_118_out, OP3);
  not not_119 (not_119_out, OP2);
  not not_120 (not_120_out, F14);
  not not_121 (not_121_out, F13);
  not not_122 (not_122_out, F12);
  not not_123 (not_123_out, OP4);
  not not_124 (not_124_out, OP3);
  not not_125 (not_125_out, F30);
  not not_126 (not_126_out, F25);
  not not_127 (not_127_out, F13);
  not not_128 (not_128_out, OP6);
  not not_129 (not_129_out, OP3);
  not not_130 (not_130_out, OP2);
  not not_131 (not_131_out, F13);
  not not_132 (not_132_out, F12);
  not not_133 (not_133_out, OP6);
  not not_134 (not_134_out, OP5);
  not not_135 (not_135_out, OP4);
  not not_136 (not_136_out, OP3);
  not not_137 (not_137_out, OP2);
  not not_138 (not_138_out, F13);
  not not_139 (not_139_out, OP4);
  not not_140 (not_140_out, OP3);
  not not_141 (not_141_out, OP2);
  not not_142 (not_142_out, F30);
  not not_143 (not_143_out, F25);
  not not_144 (not_144_out, F14);
  not not_145 (not_145_out, F13);
  not not_146 (not_146_out, F12);
  not not_147 (not_147_out, OP6);
  not not_148 (not_148_out, OP3);
  not not_149 (not_149_out, OP2);
  not not_150 (not_150_out, F25);
  not not_151 (not_151_out, F14);
  not not_152 (not_152_out, F13);
  not not_153 (not_153_out, F12);
  not not_154 (not_154_out, OP6);
  not not_155 (not_155_out, OP3);
  not not_156 (not_156_out, OP2);
  not not_157 (not_157_out, F30);
  not not_158 (not_158_out, F25);
  not not_159 (not_159_out, OP6);
  not not_160 (not_160_out, OP3);
  not not_161 (not_161_out, OP2);
  not not_162 (not_162_out, F30);
  not not_163 (not_163_out, F25);
  not not_164 (not_164_out, F12);
  not not_165 (not_165_out, OP6);
  not not_166 (not_166_out, OP3);
  not not_167 (not_167_out, OP2);
  not not_168 (not_168_out, F30);
  not not_169 (not_169_out, F25);
  not not_170 (not_170_out, F14);
  not not_171 (not_171_out, F12);
  not not_172 (not_172_out, OP6);
  not not_173 (not_173_out, OP3);
  not not_174 (not_174_out, OP2);
  not not_175 (not_175_out, F30);
  not not_176 (not_176_out, F25);
  not not_177 (not_177_out, F14);
  not not_178 (not_178_out, OP6);
  not not_179 (not_179_out, OP3);
  not not_180 (not_180_out, OP2);
  not not_181 (not_181_out, F14);
  not not_182 (not_182_out, F12);
  not not_183 (not_183_out, OP6);
  not not_184 (not_184_out, OP4);
  not not_185 (not_185_out, OP3);
  not not_186 (not_186_out, OP2);
  not not_187 (not_187_out, F14);
  not not_188 (not_188_out, F13);
  not not_189 (not_189_out, F12);
  not not_190 (not_190_out, OP4);
  not not_191 (not_191_out, OP3);
  not not_192 (not_192_out, OP2);
  not not_193 (not_193_out, F14);
  not not_194 (not_194_out, F13);
  not not_195 (not_195_out, OP4);
  not not_196 (not_196_out, OP3);
  not not_197 (not_197_out, OP2);
  not not_198 (not_198_out, F30);
  not not_199 (not_199_out, F25);
  not not_200 (not_200_out, F13);
  not not_201 (not_201_out, OP6);
  not not_202 (not_202_out, OP3);
  not not_203 (not_203_out, OP2);
  not not_204 (not_204_out, F13);
  not not_205 (not_205_out, OP4);
  not not_206 (not_206_out, OP3);
  not not_207 (not_207_out, OP2);
  and and_1 (and_1_out, not_1_out, not_2_out, not_3_out, not_4_out, not_5_out, not_6_out, OP5, OP4, not_7_out, not_8_out);
  and and_2 (and_2_out, F30, not_9_out, not_10_out, not_11_out, not_12_out, not_13_out, OP5, OP4, not_14_out, not_15_out);
  and and_3 (and_3_out, not_16_out, not_17_out, F14, F13, F12, not_18_out, OP5, OP4, not_19_out, not_20_out);
  and and_4 (and_4_out, not_21_out, not_22_out, F14, F13, not_23_out, not_24_out, OP5, OP4, not_25_out, not_26_out);
  and and_5 (and_5_out, not_27_out, not_28_out, not_29_out, F13, not_30_out, not_31_out, OP5, OP4, not_32_out, not_33_out);
  and and_6 (and_6_out, not_34_out, not_35_out, not_36_out, F13, F12, not_37_out, OP5, OP4, not_38_out, not_39_out);
  and and_7 (and_7_out, not_40_out, not_41_out, not_42_out, not_43_out, not_44_out, OP4, not_45_out, not_46_out);
  and and_8 (and_8_out, F14, F13, F12, not_47_out, not_48_out, OP4, not_49_out, not_50_out);
  and and_9 (and_9_out, F14, F13, not_51_out, not_52_out, not_53_out, OP4, not_54_out, not_55_out);
  and and_10 (and_10_out, F14, not_56_out, not_57_out, not_58_out, not_59_out, OP4, not_60_out, not_61_out);
  and and_11 (and_11_out, not_62_out, F13, not_63_out, not_64_out, not_65_out, OP4, not_66_out, not_67_out);
  and and_12 (and_12_out, not_68_out, not_69_out, not_70_out, not_71_out, F12, not_72_out, not_73_out, OP4, not_74_out, not_75_out);
  and and_13 (and_13_out, not_76_out, not_77_out, F14, not_78_out, F12, not_79_out, not_80_out, OP4, not_81_out, not_82_out);
  and and_14 (and_14_out, F30, not_83_out, F14, not_84_out, F12, not_85_out, not_86_out, OP4, not_87_out, not_88_out);
  and and_15 (and_15_out, not_89_out, F13, not_90_out, not_91_out, not_92_out, not_93_out, not_94_out, not_95_out);
  and and_16 (and_16_out, not_96_out, F13, not_97_out, not_98_out, OP5, not_99_out, not_100_out, not_101_out);
  and and_17 (and_17_out, not_102_out, not_103_out, not_104_out, not_105_out, not_106_out, OP6, OP5, OP4, not_107_out, not_108_out);
  and and_18 (and_18_out, not_109_out, not_110_out, not_111_out, OP6, OP5, not_112_out, not_113_out, not_114_out);
  and and_19 (and_19_out, not_115_out, not_116_out, F12, OP6, OP5, not_117_out, not_118_out, not_119_out);
  and and_20 (and_20_out, not_120_out, not_121_out, not_122_out, OP6, OP5, not_123_out, not_124_out, OP2);
  and and_21 (and_21_out, not_125_out, not_126_out, F14, not_127_out, F12, not_128_out, OP5, OP4, not_129_out, not_130_out);
  and and_22 (and_22_out, F14, not_131_out, not_132_out, not_133_out, not_134_out, not_135_out, not_136_out, not_137_out);
  and and_23 (and_23_out, F14, not_138_out, F12, OP6, OP5, not_139_out, not_140_out, not_141_out);
  and and_24 (and_24_out, not_142_out, not_143_out, not_144_out, not_145_out, not_146_out, not_147_out, OP5, OP4, not_148_out, not_149_out);
  and and_25 (and_25_out, F30, not_150_out, not_151_out, not_152_out, not_153_out, not_154_out, OP5, OP4, not_155_out, not_156_out);
  and and_26 (and_26_out, not_157_out, not_158_out, F14, F13, F12, not_159_out, OP5, OP4, not_160_out, not_161_out);
  and and_27 (and_27_out, not_162_out, not_163_out, F14, F13, not_164_out, not_165_out, OP5, OP4, not_166_out, not_167_out);
  and and_28 (and_28_out, not_168_out, not_169_out, not_170_out, F13, not_171_out, not_172_out, OP5, OP4, not_173_out, not_174_out);
  and and_29 (and_29_out, not_175_out, not_176_out, not_177_out, F13, F12, not_178_out, OP5, OP4, not_179_out, not_180_out);
  and and_30 (and_30_out, not_181_out, F13, not_182_out, not_183_out, OP5, not_184_out, not_185_out, not_186_out);
  and and_31 (and_31_out, not_187_out, not_188_out, not_189_out, OP6, OP5, not_190_out, not_191_out, not_192_out);
  and and_32 (and_32_out, not_193_out, not_194_out, F12, OP6, OP5, not_195_out, not_196_out, not_197_out);
  and and_33 (and_33_out, not_198_out, not_199_out, F14, not_200_out, F12, not_201_out, OP5, OP4, not_202_out, not_203_out);
  and and_34 (and_34_out, F14, not_204_out, F12, OP6, OP5, not_205_out, not_206_out, not_207_out);
  or or_1 (R2Used, and_24_out, and_25_out, and_26_out, and_27_out, and_28_out, and_29_out, and_30_out, and_31_out, and_32_out, and_33_out, and_34_out);
  or or_2 (R1Used, and_1_out, and_2_out, and_3_out, and_4_out, and_5_out, and_6_out, and_7_out, and_8_out, and_9_out, and_10_out, and_11_out, and_12_out, and_13_out, and_14_out, and_15_out, and_16_out, and_17_out, and_18_out, and_19_out, and_20_out, and_21_out, and_22_out, and_23_out);
endmodule

module \LoadUse检测  (
  input  R1Used,
  input  R2Used,
  input  [4:0] R1_num,
  input  [4:0] R2_num,
  input  [4:0] EX_W,
  input  EX_MEM2Reg,
  output LoadUse
);

  wire and_1_out, and_2_out, comparator_1_eq, comparator_2_eq, comparator_3_eq, comparator_4_eq, not_1_out,
       not_2_out;

  Comparator #(.width(5), .mode("twosComplement")) comparator_1 (
    .a(R1_num), .b({5{1'b0}}), .eq(comparator_1_eq));  // open: gt, lt
  Comparator #(.width(5), .mode("twosComplement")) comparator_2 (
    .a(R2_num), .b({5{1'b0}}), .eq(comparator_2_eq));  // open: gt, lt
  Comparator #(.width(5), .mode("twosComplement")) comparator_3 (
    .a(EX_W), .b(R1_num), .eq(comparator_3_eq));  // open: gt, lt
  Comparator #(.width(5), .mode("twosComplement")) comparator_4 (
    .a(EX_W), .b(R2_num), .eq(comparator_4_eq));  // open: gt, lt
  not not_1 (not_1_out, comparator_1_eq);
  not not_2 (not_2_out, comparator_2_eq);
  and and_1 (and_1_out, R1Used, not_1_out, comparator_3_eq, EX_MEM2Reg);
  and and_2 (and_2_out, R2Used, not_2_out, EX_MEM2Reg, comparator_4_eq);
  or or_1 (LoadUse, and_1_out, and_2_out);
endmodule

module \Fwd逻辑  (
  input  R1Used,
  input  [4:0] R1_num,
  input  EX_RegWrite,
  input  [4:0] EX_W,
  input  MEM_RegWrite,
  input  [4:0] MEM_W,
  input  R2Used,
  input  [4:0] R2_num,
  output [1:0] R1Fwd,
  output [1:0] R1Fwd_2
);

  wire comparator_1_eq, comparator_2_eq, comparator_3_eq, comparator_4_eq, comparator_5_eq, comparator_6_eq,
       not_1_out, not_2_out;
  wire [1:0] and_1_out, and_3_out;

  not not_1 (not_1_out, comparator_1_eq);
  Comparator #(.width(5), .mode("twosComplement")) comparator_1 (
    .a(R1_num), .b({5{1'b0}}), .eq(comparator_1_eq));  // open: gt, lt
  Comparator #(.width(5), .mode("twosComplement")) comparator_2 (
    .a(R1_num), .b(EX_W), .eq(comparator_2_eq));  // open: gt, lt
  Comparator #(.width(5), .mode("twosComplement")) comparator_3 (
    .a(R1_num), .b(MEM_W), .eq(comparator_3_eq));  // open: gt, lt
  Comparator #(.width(5), .mode("twosComplement")) comparator_4 (
    .a(R2_num), .b({5{1'b0}}), .eq(comparator_4_eq));  // open: gt, lt
  not not_2 (not_2_out, comparator_4_eq);
  Comparator #(.width(5), .mode("twosComplement")) comparator_5 (
    .a(EX_W), .b(R2_num), .eq(comparator_5_eq));  // open: gt, lt
  Comparator #(.width(5), .mode("twosComplement")) comparator_6 (
    .a(MEM_W), .b(R2_num), .eq(comparator_6_eq));  // open: gt, lt
  and and_1 (and_1_out[0], R1Used, not_1_out, EX_RegWrite, comparator_2_eq);
  and and_2 (and_1_out[1], not_1_out, R1Used, MEM_RegWrite, comparator_3_eq);
  and and_3 (and_3_out[0], R2Used, not_2_out, EX_RegWrite, comparator_5_eq);
  and and_4 (and_3_out[1], not_2_out, R2Used, MEM_RegWrite, comparator_6_eq);
  Multiplexer #(.select(2), .width(2), .disabled("Z"), .enable("false")) multiplexer_1 (
    .in0(2'b00), .in1(2'b10), .in2(2'b01), .in3(2'b10), .out(R1Fwd), .sel(and_1_out));
  Multiplexer #(.select(2), .width(2), .disabled("Z"), .enable("false")) multiplexer_2 (
    .in0(2'b00), .in1(2'b10), .in2(2'b01), .in3(2'b10), .out(R1Fwd_2), .sel(and_3_out));
endmodule
module \重定向分支预测  (
  output RegWrite,
  output MemWrite,
  output [31:0] IF_PC,
  output [31:0] ID_PC,
  output [31:0] EX_PC,
  output [31:0] M_PC,
  output [31:0] WB_PC,
  output [31:0] RDin,
  output [31:0] MDin,
  output [31:0] LedData
);

  wire alu_1_equal, alu_1_out_4, and_1_out, and_3_out, and_6_out, and_7_out, and_8_out, and_9_out,
       and_10_out, and_11_out, and_12_out, and_13_out, and_14_out, and_15_out, and_16_out, and_21_out,
       and_22_out, and_23_out, and_24_out, beq, bge, bne, Branch, \B型 , ClearA, ClearB, ClearC, CLK,
       clock_1_out, comparator_1_eq, comparator_2_eq, comparator_3_eq, comparator_4_eq, comparator_5_eq,
       comparator_6_eq, comparator_7_eq, comparator_7_lt, comparator_8_eq, d_ff_1_q, decoder_1_out1,
       decoder_1_out2, decoder_1_out3, ecall, ecallEq, EX_ecall, EX_MEM2Reg, ex_mem_1_ecall_2,
       ex_mem_1_jal_2, ex_mem_1_jalr_2, ex_mem_1_lbu_2, ex_mem_1_mem2reg_2, EX_predictBranch, EX_RegWrite,
       Go, halt, id_ex_1_alu_src_2, id_ex_1_auipc_2, id_ex_1_lbu_2, id_ex_1_memwrite, ID_predictBranch, IE,
       IF_predictBranch, INT, IR1, IR2, IR3, IRA, IRB, IRC, Jal, Jalr, LBU0, LBU1, LoadUse, MEM_AUIPC,
       MEM_RegWrite, mem_wb_1_jal_2, mem_wb_1_jalr_2, mem_wb_1_lbu_2, mem_wb_1_mem2reg_2, multiplexer_19_out,
       nand_1_out, not_1_out, not_2_out, not_3_out, not_4_out, not_6_out, not_7_out, not_8_out, not_9_out,
       not_10_out, not_11_out, not_12_out, not_13_out, not_14_out, or_1_out, or_3_out, or_5_out, or_6_out,
       or_8_out, or_11_out, or_12_out, or_16_out, or_17_out, or_18_out, or_19_out, or_20_out, or_21_out,
       predictError, R1Used, R2Used, register_4_q, register_5_q, register_6_q, register_7_q, register_8_q,
       register_9_q, RST, URET, W1, W2, W3, WB_AUIPC, WB_ecall, WB_LBU0, WB_LBU1, \中断信号 , \分支出现 ,
       \单周期硬布线控制器_1_alu_src , \单周期硬布线控制器_1_auipc , \单周期硬布线控制器_1_beq , \单周期硬布线控制器_1_bge , \单周期硬布线控制器_1_bne ,
       \单周期硬布线控制器_1_jal , \单周期硬布线控制器_1_jalr , \单周期硬布线控制器_1_lbu , \单周期硬布线控制器_1_memtoreg ,
       \单周期硬布线控制器_1_memwrite , \单周期硬布线控制器_1_regwrite , \单周期硬布线控制器_1_s_type , \单周期硬布线控制器_1_uret , \无条件分支跳转 ,
       \条件分支出现 ;
  wire [1:0] EX_R1Fwd, EX_R2Fwd, ID_R1Fwd, ID_R2Fwd, register_3_q, \中断号 ;
  wire [3:0] id_ex_1_alu_op_2, \单周期硬布线控制器_1_alu_op ;
  wire [4:0] EX_W, Funct, MEM_W, multiplexer_14_out, multiplexer_16_out, R1_num, R2_num, WB_W;
  wire [11:0] multiplexer_10_out;
  wire [12:0] CNT_num;
  wire [15:0] \LoadUse次数 , \总周期数 , \插入气泡数 , \无条件分支数 , \条件分支成功数 ;
  wire [31:0] adder_4_out, ALUresult, bit_extender_1_out, bit_extender_2_out, bit_extender_3_out,
       bit_extender_4_out, BranchPC, btb_1_btb_jumpaddr, EX_IR, ex_mem_1_r1_2, EX_PC_4, EX_R1, EX_R2,
       EX_ReR1Data, EX_ReR2Data, \EX_分支PC , id_ex_1_brachpc_2, id_ex_1_is_2, id_ex_1_jalpc_2, \id_ex_1_u型_2 ,
       ID_IR, ID_PC_4, IF_IR, IF_PC_4, INTPC, JalPC, JalrPC, LBUReasult, LocalPC, MEM_IR, MEM_PC_4, \MEM_U型 ,
       mem_wb_1_aluresult_2, mem_wb_1_memdata_2, mem_wb_1_pc_4_2, multiplexer_1_out, multiplexer_2_out,
       multiplexer_3_out, multiplexer_4_out, multiplexer_6_out, multiplexer_8_out, multiplexer_15_out,
       multiplexer_18_out, multiplexer_20_out, multiplexer_24_out, multiplexer_25_out, PredictPC, ram_1_data,
       regifile_1_r1, regifile_1_r2, RETPC, shifter_1_out, shifter_2_out, shifter_3_out, shifter_4_out,
       shifter_5_out, WB_IR, WB_R1, WB_R2, \WB_U型 , Write2Reg;
  wire [31:2] MemData;

  Button \u_总复位  (.out(RST));
  Button _1 (.out(IR1));
  Button _2 (.out(IR2));
  Button _3 (.out(IR3));
  // Probe on \总周期数 
  // Probe on \总周期数 
  Button \u_继续运行  (.out(Go));
  LED #(.active("true")) led_1 (.in(W1));
  LED #(.active("true")) led_2 (.in(W2));
  LED #(.active("true")) led_3 (.in(W3));
  Hex_Digit_Display hex_digit_display_1 (.value(LedData[31:28]));  // open: dp
  // Probe on IF_PC[19:0]
  // RiscV_Probe riscv_probe_1: pin names not known; wires that end beside it: IF_IR
  Comparator #(.width(16), .mode("twosComplement")) comparator_1 (
    .a(16'h23b), .b(\总周期数 ), .eq(comparator_1_eq));  // open: gt, lt
  Comparator #(.width(16), .mode("twosComplement")) comparator_2 (
    .a(\总周期数 ), .b(16'h1), .eq(comparator_2_eq));  // open: gt, lt
  Comparator #(.width(16), .mode("twosComplement")) comparator_3 (
    .a(\总周期数 ), .b(16'h4), .eq(comparator_3_eq));  // open: gt, lt
  Comparator #(.width(16), .mode("twosComplement")) comparator_4 (
    .a(\总周期数 ), .b(16'h7), .eq(comparator_4_eq));  // open: gt, lt
  Multiplexer #(.select(1), .width(32), .disabled("Z"), .enable("false")) multiplexer_1 (
    .in0(EX_PC_4), .in1(BranchPC), .out(multiplexer_1_out), .sel(\B型 ));
  Hex_Digit_Display hex_digit_display_2 (.value(LedData[23:20]));  // open: dp
  Hex_Digit_Display hex_digit_display_3 (.value(LedData[27:24]));  // open: dp
  // Probe on ID_PC[19:0]
  // RiscV_Probe riscv_probe_2: pin names not known; wires that end beside it: {ID_IR[31], Funct[4], ID_IR[29:26], Funct[3], ID_IR[24:15], Funct[2:0], ID_IR[11:0]}
  or or_1 (or_1_out, comparator_1_eq, comparator_2_eq);
  assign IRA = or_1_out ? ~CLK : 1'bz;  // Controlled_Inverter controlled_inverter_1
  assign IRB = comparator_3_eq ? ~CLK : 1'bz;  // Controlled_Inverter controlled_inverter_2
  assign IRC = comparator_4_eq ? ~CLK : 1'bz;  // Controlled_Inverter controlled_inverter_3
  Multiplexer #(.select(1), .width(32), .disabled("Z"), .enable("false")) multiplexer_2 (
    .in0(multiplexer_1_out), .in1(JalPC), .out(multiplexer_2_out), .sel(Jal));
  Multiplexer #(.select(1), .width(32), .disabled("Z"), .enable("false")) multiplexer_3 (
    .in0(multiplexer_2_out), .in1(JalrPC), .out(multiplexer_3_out), .sel(Jalr));
  Multiplexer #(.select(1), .width(32), .disabled("Z"), .enable("false")) multiplexer_4 (
    .in0({32{1'b0}}), .in1(EX_ReR2Data), .out(multiplexer_4_out), .sel(ecallEq));
  // Probe on ecallEq
  Hex_Digit_Display hex_digit_display_4 (.value(LedData[19:16]));  // open: dp
  Hex_Digit_Display hex_digit_display_5 (.value(LedData[15:12]));  // open: dp
  Pull_Resistor #(.pull(0)) pull_resistor_1 (.node(IRA));
  Pull_Resistor #(.pull(0)) pull_resistor_2 (.node(IRB));
  Pull_Resistor #(.pull(0)) pull_resistor_3 (.node(IRC));
  Multiplexer #(.select(1), .width(32), .disabled("Z"), .enable("false")) multiplexer_5 (
    .in0(PredictPC), .in1(multiplexer_3_out), .out(LocalPC), .sel(predictError));
  Register #(.width(32), .trigger("rising"), .Select("low")) register_1 (
    .D(multiplexer_4_out), .en(ecallEq), .Q(LedData), .clk(CLK), .clr(RST));
  \R1R2Used检测  \r1r2used检测_1  (
    .OP2(ID_IR[2]), .OP3(ID_IR[3]), .OP4(ID_IR[4]), .OP5(ID_IR[5]), .OP6(ID_IR[6]), .F12(Funct[0]),
    .F13(Funct[1]), .F14(Funct[2]), .F25(Funct[3]), .F30(Funct[4]), .R1Used(R1Used), .R2Used(R2Used));
  or or_2 (\条件分支出现 , bge, beq, bne);
  Hex_Digit_Display hex_digit_display_6 (.value(LedData[7:4]));  // open: dp
  Hex_Digit_Display hex_digit_display_7 (.value(LedData[11:8]));  // open: dp
  // Probe on EX_PC[19:0]
  // RiscV_Probe riscv_probe_3: pin names not known; wires that end beside it: EX_IR
  Multiplexer #(.select(1), .width(32), .disabled("Z"), .enable("false")) multiplexer_6 (
    .in0(LocalPC), .in1(RETPC), .out(multiplexer_6_out), .sel(URET));
  or or_3 (or_3_out, and_1_out, Go);
  and and_1 (and_1_out, not_1_out, not_3_out);
  not not_1 (not_1_out, LoadUse);
  Comparator #(.width(32), .mode("twosComplement")) comparator_5 (
    .a(WB_R1), .b(32'h22), .eq(comparator_5_eq));  // open: gt, lt
  not not_2 (not_2_out, comparator_5_eq);
  // Probe on {\条件分支出现 , Jal, Jalr}
  Multiplexer #(.select(3), .width(32), .disabled("Z"), .enable("false")) multiplexer_7 (
    .in0(IF_PC), .in1(ALUresult), .in2(JalPC), .in4(BranchPC), .out(\EX_分支PC ), .sel({\条件分支出现 , Jal, Jalr}));  // open: in3, in5, in6, in7
  Hex_Digit_Display hex_digit_display_8 (.value(LedData[3:0]));  // open: dp
  Multiplexer #(.select(1), .width(32), .disabled("Z"), .enable("false")) multiplexer_8 (
    .in0(multiplexer_6_out), .in1(INTPC), .out(multiplexer_8_out), .sel(INT));
  Register #(.width(32), .trigger("rising"), .Select("low")) PC (
    .D(multiplexer_8_out), .en(or_3_out), .Q(IF_PC), .clk(CLK), .clr(RST));
  not not_3 (not_3_out, halt);
  and and_2 (halt, WB_ecall, not_2_out);
  not not_4 (not_4_out, halt);
  // Probe on \总周期数 
  // Probe on M_PC[19:0]
  // RiscV_Probe riscv_probe_4: pin names not known; wires that end beside it: MEM_IR
  Adder #(.width(32)) adder_1 (.a(IF_PC), .b(32'h4), .out(IF_PC_4));  // open: cin, cout
  Counter #(.width(16), .max('hffff), .ongoal("wrap"), .trigger("rising"), .behavior("new")) counter_1 (
    .count(not_4_out), .Q(\总周期数 ), .clk(CLK), .clr(RST));  // open: load, D, carry, preset, down
  // Probe on \总周期数 
  // Probe on \无条件分支数 
  // Probe on \条件分支成功数 
  // Probe on \插入气泡数 
  // Probe on \LoadUse次数 
  or or_4 (\分支出现 , bge, beq, bne, Jalr, Jal);
  // Probe on IF_PC[11:0]
  // Probe on WB_PC[19:0]
  // RiscV_Probe riscv_probe_5: pin names not known; wires that end beside it: WB_IR
  // RiscV_Probe riscv_probe_6: pin names not known; wires that end beside it: IF_IR, IF_PC_4
  ROM #(.addrWidth(10), .dataWidth(32), .Select("high")) rom_1 (.addr(IF_PC[11:2]), .data(IF_IR));
  \LoadUse检测  \loaduse检测_1  (
    .R1Used(R1Used), .R2Used(R2Used), .R1_num(R1_num), .R2_num(R2_num), .EX_W(EX_W), .EX_MEM2Reg(EX_MEM2Reg),
    .LoadUse(LoadUse));
  // Probe on EX_PC[11:0]
  // Probe on ID_PC[11:0]
  or or_5 (or_5_out, RST, Branch);
  Comparator #(.width(32), .mode("twosComplement")) comparator_6 (
    .a(EX_ReR1Data), .b(32'h22), .eq(comparator_6_eq));  // open: gt, lt
  // Probe on M_PC[11:0]
  D_Flip_Flop #(.trigger("high"), .Pre_Clr_Positions("LEGACY"), .NegatePresetClear("false"), .enable("true"), .NewFFLayout("false")) d_ff_1 (.Q(d_ff_1_q));  // open: clk, D, Qn, preset, en, reset
  // Probe on 13'hc
  and and_3 (and_3_out, halt, ~Go);  // AND_Gate
  or or_6 (or_6_out, and_3_out, LoadUse);
  IF_ID if_id_1 (
    .IF_PC(IF_PC), .IF_IR(IF_IR), .IF_PC_4(IF_PC_4), .CLK(CLK), .RST(or_5_out), .ID_PC(ID_PC),
    .ID_IR({ID_IR[31], Funct[4], ID_IR[29:26], Funct[3], ID_IR[24:15], Funct[2:0], ID_IR[11:0]}),
    .ID_PC_4(ID_PC_4), .halt(or_6_out), .PredictBranch(IF_predictBranch), .PredictBranch_2(ID_predictBranch));
  and and_4 (ecallEq, EX_ecall, comparator_6_eq);
  BTB btb_1 (
    .PC(IF_PC), .EX_PC(EX_PC), .EX_BranchAddr(\EX_分支PC ), .EX_Branch(\分支出现 ), .EX_Branched(Branch),
    .in_6(CLK), .ID_PredictJump(IF_predictBranch), .BTB_JumpAddr(btb_1_btb_jumpaddr));
  // Probe on WB_PC[11:0]
  Comparator #(.width(13), .mode("twosComplement")) comparator_7 (
    .a(CNT_num), .b(13'hc), .eq(comparator_7_eq), .lt(comparator_7_lt));  // open: gt
  Clock #(.highDuration(1), .lowDuration(1)) clock_1 (.out(clock_1_out));
  assign JalrPC = ALUresult & 32'hfffffffe;  // AND_Gate and_5, 32 bits wide
  nand nand_1 (nand_1_out, d_ff_1_q, comparator_7_eq);
  Counter #(.width(13), .max('h1fff), .ongoal("stay"), .trigger("rising"), .behavior("old")) counter_2 (
    .count(comparator_7_lt), .Q(CNT_num), .clk(clock_1_out));  // open: load, D, carry, clr, preset
  Multiplexer #(.select(1), .width(32), .disabled("Z"), .enable("false")) multiplexer_9 (
    .in0(IF_PC_4), .in1(btb_1_btb_jumpaddr), .out(PredictPC), .sel(IF_predictBranch));
  not not_5 (predictError, comparator_8_eq);
  Comparator #(.width(1), .mode("twosComplement")) comparator_8 (
    .a(Branch), .b(EX_predictBranch), .eq(comparator_8_eq));  // open: gt, lt
  assign CLK = nand_1_out ? clock_1_out : 1'bz;  // Controlled_Buffer controlled_buffer_1
  \单周期硬布线控制器  \u_单周期硬布线控制器_1  (
    .Funct(Funct), .OP(ID_IR[6:2]), .ALU_OP(\单周期硬布线控制器_1_alu_op ), .MemToReg(\单周期硬布线控制器_1_memtoreg ),
    .MemWrite(\单周期硬布线控制器_1_memwrite ), .ALU_SRC(\单周期硬布线控制器_1_alu_src ), .RegWrite(\单周期硬布线控制器_1_regwrite ),
    .ecall(ecall), .S_type(\单周期硬布线控制器_1_s_type ), .Jalr(\单周期硬布线控制器_1_jalr ), .Beq(\单周期硬布线控制器_1_beq ),
    .JAL(\单周期硬布线控制器_1_jal ), .Bne(\单周期硬布线控制器_1_bne ), .in_3(ID_IR[21]), .uret(\单周期硬布线控制器_1_uret ),
    .BGE(\单周期硬布线控制器_1_bge ), .LBU(\单周期硬布线控制器_1_lbu ), .AUIPC(\单周期硬布线控制器_1_auipc ));
  Multiplexer #(.select(1), .width(12), .disabled("Z"), .enable("false")) multiplexer_10 (
    .in0({ID_IR[31], Funct[4], ID_IR[29:26], Funct[3], ID_IR[24:20]}),
    .in1({ID_IR[31], Funct[4], ID_IR[29:26], Funct[3], ID_IR[11:7]}), .out(multiplexer_10_out),
    .sel(\单周期硬布线控制器_1_s_type ));
  assign bit_extender_1_out = {{20{ID_IR[31]}}, {ID_IR[31], ID_IR[7], Funct[4], ID_IR[29:26], Funct[3], ID_IR[11:8]}};  // Bit_Extender bit_extender_1
  assign bit_extender_2_out = {{12{ID_IR[31]}}, {ID_IR[31], Funct[4], ID_IR[29:26], Funct[3], ID_IR[24:15], Funct[2:0]}};  // Bit_Extender bit_extender_2
  Pull_Resistor #(.pull(1)) pull_resistor_4 (.node(CLK));
  or or_7 (\无条件分支跳转 , Jalr, Jal);
  Multiplexer #(.select(1), .width(5), .disabled("Z"), .enable("false")) multiplexer_11 (
    .in0(ID_IR[19:15]), .in1(5'b10001), .out(R1_num), .sel(ecall));
  Multiplexer #(.select(1), .width(5), .disabled("Z"), .enable("false")) multiplexer_12 (
    .in0(ID_IR[24:20]), .in1(5'b01010), .out(R2_num), .sel(ecall));
  assign bit_extender_3_out = {{20{multiplexer_10_out[11]}}, multiplexer_10_out};  // Bit_Extender bit_extender_3
  assign bit_extender_4_out = {{12{ID_IR[31]}}, {ID_IR[31], ID_IR[19:15], Funct[2:0], ID_IR[20], Funct[4], ID_IR[29:26], Funct[3], ID_IR[24:21]}};  // Bit_Extender bit_extender_4
  \Fwd逻辑  \fwd逻辑_1  (
    .R1Used(R1Used), .R1_num(R1_num), .EX_RegWrite(EX_RegWrite), .EX_W(EX_W), .MEM_RegWrite(MEM_RegWrite),
    .MEM_W(MEM_W), .R2Used(R2Used), .R2_num(R2_num), .R1Fwd(ID_R1Fwd), .R1Fwd_2(ID_R2Fwd));
  Regifile regifile_1 (
    .Din(RDin), .Clk(CLK), .R1(regifile_1_r1), .R2(regifile_1_r2), .WE(RegWrite), .W_num(WB_W),
    .R1_num(R1_num), .R2_num(R2_num));
  Counter #(.width(16), .max('hffff), .ongoal("wrap"), .trigger("rising"), .behavior("old")) counter_3 (
    .count(1'b0), .Q(\无条件分支数 ), .clk(RST), .clr(RST));  // open: load, D, carry, preset
  Multiplexer #(.select(1), .width(1), .disabled("Z"), .enable("false")) multiplexer_13 (
    .in0(and_6_out), .in1(1'b0), .out(RST), .sel(not_6_out));
  not not_6 (not_6_out, not_7_out);
  and and_6 (and_6_out, \无条件分支跳转 , CLK);
  or or_8 (or_8_out, RST, LoadUse, Branch);
  ID_EX id_ex_1 (
    .RST(or_8_out), .CLK(CLK), .AUIPC(\单周期硬布线控制器_1_auipc ), .URET(\单周期硬布线控制器_1_uret ),
    .LBU(\单周期硬布线控制器_1_lbu ), .JALR(\单周期硬布线控制器_1_jalr ), .JAL(\单周期硬布线控制器_1_jal ), .Beq(\单周期硬布线控制器_1_beq ),
    .BGE(\单周期硬布线控制器_1_bge ), .BNE(\单周期硬布线控制器_1_bne ), .Mem2Reg(\单周期硬布线控制器_1_memtoreg ),
    .MenWrite(\单周期硬布线控制器_1_memwrite ), .ALU_OP(\单周期硬布线控制器_1_alu_op ), .ALU_SRC(\单周期硬布线控制器_1_alu_src ),
    .REG_WRITE(\单周期硬布线控制器_1_regwrite ), .ECALL(ecall), .PC(ID_PC), .R1(regifile_1_r1), .R2(regifile_1_r2),
    .IS(bit_extender_3_out),
    .IR({ID_IR[31], Funct[4], ID_IR[29:26], Funct[3], ID_IR[24:15], Funct[2:0], ID_IR[11:0]}),
    .JalPc(bit_extender_4_out), .BrachPc(bit_extender_1_out), .Pc_4(ID_PC_4), .W(ID_IR[11:7]),
    .\U型 (bit_extender_2_out), .AUIPC_2(id_ex_1_auipc_2), .URET_2(URET), .LBU_2(id_ex_1_lbu_2),
    .JALR_2(Jalr), .JAL_2(Jal), .BEQ_2(beq), .BGE_2(bge), .BNE_2(bne), .MEM2REG_2(EX_MEM2Reg),
    .MEMWRITE(id_ex_1_memwrite), .ALU_OP_2(id_ex_1_alu_op_2), .ALU_SRC_2(id_ex_1_alu_src_2),
    .REG_WRITE_2(EX_RegWrite), .ECALL_2(EX_ecall), .PC_2(EX_PC), .R1_2(EX_R1), .R2_2(EX_R2),
    .IS_2(id_ex_1_is_2), .IR_2(EX_IR), .JalPc_2(id_ex_1_jalpc_2), .BrachPc_2(id_ex_1_brachpc_2),
    .Pc_4_2(EX_PC_4), .W_2(EX_W), .\U型_2 (\id_ex_1_u型_2 ), .halt(and_7_out), .R1Fwd(ID_R1Fwd),
    .R2Fwd(ID_R2Fwd), .R1Fwd_2(EX_R1Fwd), .R2Fwd_2(EX_R2Fwd), .PredictBranch(ID_predictBranch),
    .PredictBranch_2(EX_predictBranch));
  not not_7 (not_7_out, CLK);
  and and_7 (and_7_out, halt, ~Go);  // AND_Gate
  Shifter #(.width(32), .shift("ll")) shifter_1 (.in(Write2Reg), .\dist (multiplexer_14_out), .out(shifter_1_out));
  Multiplexer #(.select(1), .width(5), .disabled("Z"), .enable("false")) multiplexer_14 (
    .in0(5'b10000), .in1({5{1'b0}}), .out(multiplexer_14_out), .sel(WB_LBU1));
  Multiplexer #(.select(1), .width(32), .disabled("Z"), .enable("false")) multiplexer_15 (
    .in0(EX_ReR2Data), .in1(id_ex_1_is_2), .out(multiplexer_15_out), .sel(id_ex_1_alu_src_2));
  Shifter #(.width(32), .shift("ll")) shifter_2 (.in(id_ex_1_brachpc_2), .\dist (5'b00001), .out(shifter_2_out));
  Multiplexer #(.select(1), .width(5), .disabled("Z"), .enable("false")) multiplexer_16 (
    .in0(5'b01000), .in1({5{1'b0}}), .out(multiplexer_16_out), .sel(WB_LBU0));
  and and_8 (and_8_out, \B型 , CLK);
  ALU alu_1 (
    .X(EX_ReR1Data), .Y(multiplexer_15_out), .AluOP(id_ex_1_alu_op_2), .Equal(alu_1_equal),
    .Result(ALUresult), .out_4(alu_1_out_4));  // open: Result_2, out_6
  Adder #(.width(32)) adder_2 (.a(shifter_2_out), .b(EX_PC), .out(BranchPC));  // open: cin, cout
  Shifter #(.width(32), .shift("ll")) shifter_3 (.in(id_ex_1_jalpc_2), .\dist (5'b00001), .out(shifter_3_out));
  Adder #(.width(32)) adder_3 (.a(shifter_3_out), .b(EX_PC), .out(JalPC));  // open: cin, cout
  Shifter #(.width(32), .shift("ll")) shifter_4 (.in(\id_ex_1_u型_2 ), .\dist (5'b01100), .out(shifter_4_out));
  Shifter #(.width(32), .shift("ll")) shifter_5 (.in(shifter_1_out), .\dist (multiplexer_16_out), .out(shifter_5_out));
  Counter #(.width(16), .max('hffff), .ongoal("wrap"), .trigger("rising"), .behavior("old")) counter_4 (
    .count(1'b0), .Q(\条件分支成功数 ), .clk(RST), .clr(RST));  // open: load, D, carry, preset
  Multiplexer #(.select(1), .width(1), .disabled("Z"), .enable("false")) multiplexer_17 (
    .in0(and_8_out), .in1(1'b0), .out(RST), .sel(not_9_out));
  not not_8 (not_8_out, CLK);
  not not_9 (not_9_out, not_8_out);
  and and_9 (and_9_out, beq, alu_1_equal);
  not not_10 (not_10_out, alu_1_equal);
  and and_10 (and_10_out, not_10_out, bne);
  Adder #(.width(32)) adder_4 (.a(shifter_4_out), .b(EX_PC), .out(adder_4_out));  // open: cin, cout
  Shifter #(.width(32), .shift("lr")) shifter_6 (.in(shifter_5_out), .\dist (5'b11000), .out(LBUReasult));
  and and_11 (and_11_out, bge, alu_1_out_4);
  or or_9 (Branch, Jal, Jalr, \B型 );
  or or_10 (\B型 , and_9_out, and_11_out, and_10_out);
  or or_11 (or_11_out, LoadUse, predictError);
  EX_MEM ex_mem_1 (
    .RST(RST), .CLK(CLK), .AUIPC(id_ex_1_auipc_2), .AUIPC_2(MEM_AUIPC), .LBU(id_ex_1_lbu_2),
    .LBU_2(ex_mem_1_lbu_2), .JALR(Jalr), .JALR_2(ex_mem_1_jalr_2), .JAL(Jal), .JAL_2(ex_mem_1_jal_2),
    .Mem2Reg(EX_MEM2Reg), .MEM2REG_2(ex_mem_1_mem2reg_2), .MenWrite(id_ex_1_memwrite), .MEMWRITE(MemWrite),
    .REG_WRITE(EX_RegWrite), .REG_WRITE_2(MEM_RegWrite), .ECALL(EX_ecall), .ECALL_2(ex_mem_1_ecall_2),
    .PC(EX_PC), .PC_2(M_PC), .R1(EX_ReR1Data), .R1_2(ex_mem_1_r1_2), .R2(EX_ReR2Data), .R2_2(MDin),
    .IR(EX_IR), .IR_2(MEM_IR), .Pc_4(EX_PC_4), .Pc_4_2(MEM_PC_4), .W(EX_W), .W_2(MEM_W), .\U型 (adder_4_out),
    .\U型_2 (\MEM_U型 ), .ALUResult(ALUresult), .ALUResult_2({MemData, LBU1, LBU0}), .halt(and_14_out));
  Multiplexer #(.select(1), .width(32), .disabled("Z"), .enable("false")) multiplexer_18 (
    .in0({MemData, LBU1, LBU0}), .in1(\MEM_U型 ), .out(multiplexer_18_out), .sel(MEM_AUIPC));
  Counter #(.width(16), .max('hffff), .ongoal("wrap"), .trigger("rising"), .behavior("old")) counter_5 (
    .count(1'b1), .Q(\插入气泡数 ), .clk(multiplexer_19_out), .clr(RST));  // open: load, D, carry, preset
  Multiplexer #(.select(1), .width(1), .disabled("Z"), .enable("false")) multiplexer_19 (
    .in0(and_12_out), .in1(1'b0), .out(multiplexer_19_out), .sel(not_11_out));
  not not_11 (not_11_out, not_12_out);
  not not_12 (not_12_out, CLK);
  and and_12 (and_12_out, and_13_out, CLK);
  and and_13 (and_13_out, ~halt, or_11_out);  // AND_Gate
  and and_14 (and_14_out, halt, ~Go);  // AND_Gate
  Multiplexer #(.select(1), .width(32), .disabled("Z"), .enable("false")) multiplexer_20 (
    .in0(RDin), .in1(\WB_U型 ), .out(multiplexer_20_out), .sel(WB_AUIPC));
  Multiplexer #(.select(2), .width(32), .disabled("Z"), .enable("false")) multiplexer_21 (
    .in0(EX_R1), .in1(multiplexer_20_out), .in2(multiplexer_18_out), .out(EX_ReR1Data), .sel(EX_R1Fwd));  // open: in3
  Multiplexer #(.select(2), .width(32), .disabled("Z"), .enable("false")) multiplexer_22 (
    .in0(EX_R2), .in1(multiplexer_20_out), .in2(multiplexer_18_out), .out(EX_ReR2Data), .sel(EX_R2Fwd));  // open: in3
  Counter #(.width(16), .max('hffff), .ongoal("wrap"), .trigger("rising"), .behavior("old")) counter_6 (
    .count(1'b0), .Q(\LoadUse次数 ), .clk(RST), .clr(RST));  // open: load, D, carry, preset
  Multiplexer #(.select(1), .width(1), .disabled("Z"), .enable("false")) multiplexer_23 (
    .in0(and_15_out), .in1(1'b0), .out(RST), .sel(not_13_out));
  not not_13 (not_13_out, not_14_out);
  and and_15 (and_15_out, LoadUse, CLK);
  RAM #(.addrWidth(10), .dataWidth(32), .bus("separate"), .Select("high")) ram_1 (
    .addr(MemData[11:2]), .din(MDin), .data(ram_1_data), .str(MemWrite), .clk(CLK), .clr(RST));  // open: sel, ld
  not not_14 (not_14_out, CLK);
  and and_16 (and_16_out, halt, ~Go);  // AND_Gate
  MEM_WB mem_wb_1 (
    .RST(RST), .CLK(CLK), .AUIPC(MEM_AUIPC), .LBU(ex_mem_1_lbu_2), .JALR(ex_mem_1_jalr_2),
    .JAL(ex_mem_1_jal_2), .Mem2Reg(ex_mem_1_mem2reg_2), .REG_WRITE(MEM_RegWrite), .ECALL(ex_mem_1_ecall_2),
    .PC(M_PC), .R1(ex_mem_1_r1_2), .R2(MDin), .MemData(ram_1_data), .IR(MEM_IR),
    .ALUResult({MemData, LBU1, LBU0}), .Pc_4(MEM_PC_4), .W(MEM_W), .\U型 (\MEM_U型 ), .AUIPC_2(WB_AUIPC),
    .LBU_2(mem_wb_1_lbu_2), .JALR_2(mem_wb_1_jalr_2), .JAL_2(mem_wb_1_jal_2), .MEM2REG_2(mem_wb_1_mem2reg_2),
    .REG_WRITE_2(RegWrite), .ECALL_2(WB_ecall), .PC_2(WB_PC), .R1_2(WB_R1), .R2_2(WB_R2),
    .MemData_2(mem_wb_1_memdata_2), .IR_2(WB_IR), .ALUResult_2(mem_wb_1_aluresult_2),
    .Pc_4_2(mem_wb_1_pc_4_2), .W_2(WB_W), .\U型_2 (\WB_U型 ), .halt(and_16_out), .LBU0(LBU0), .LBU0_2(WB_LBU0),
    .LBU1(LBU1), .LBU1_2(WB_LBU1));
  Multiplexer #(.select(1), .width(32), .disabled("Z"), .enable("false")) multiplexer_24 (
    .in0(mem_wb_1_aluresult_2), .in1(mem_wb_1_memdata_2), .out(multiplexer_24_out), .sel(mem_wb_1_mem2reg_2));
  or or_12 (or_12_out, mem_wb_1_jal_2, mem_wb_1_jalr_2);
  Multiplexer #(.select(1), .width(32), .disabled("Z"), .enable("false")) multiplexer_25 (
    .in0(multiplexer_24_out), .in1(mem_wb_1_pc_4_2), .out(multiplexer_25_out), .sel(or_12_out));
  Multiplexer #(.select(1), .width(32), .disabled("Z"), .enable("false")) multiplexer_26 (
    .in0(multiplexer_25_out), .in1(\WB_U型 ), .out(Write2Reg), .sel(WB_AUIPC));
  Multiplexer #(.select(1), .width(32), .disabled("Z"), .enable("false")) multiplexer_27 (
    .in0(Write2Reg), .in1(LBUReasult), .out(RDin), .sel(mem_wb_1_lbu_2));
  or or_13 (W1, register_7_q, register_4_q);
  or or_14 (W2, register_8_q, register_5_q);
  or or_15 (W3, register_9_q, register_6_q);
  and and_17 (INT, \中断信号 , IE);
  Register #(.width(32), .trigger("falling"), .Select("low")) register_2 (
    .D(LocalPC), .en(INT), .Q(RETPC), .clk(CLK), .clr(RST));
  Register #(.width(2), .trigger("rising"), .Select("low")) register_3 (
    .D(\中断号 ), .en(INT), .Q(register_3_q), .clk(CLK), .clr(RST));
  Decoder #(.select(2), .tristate("false"), .disabled("Z"), .enable("false")) decoder_1 (
    .out1(decoder_1_out1), .out2(decoder_1_out2), .out3(decoder_1_out3), .sel(register_3_q));  // open: out0
  Register #(.width(1), .trigger("rising"), .Select("low")) register_4 (
    .D(1'b1), .Q(register_4_q), .clk(IRA), .clr(or_16_out));  // open: en
  or or_16 (or_16_out, register_7_q, RST);
  Register #(.width(1), .trigger("rising"), .Select("low")) register_5 (
    .D(1'b1), .Q(register_5_q), .clk(IRB), .clr(or_17_out));  // open: en
  or or_17 (or_17_out, register_8_q, RST);
  Register #(.width(1), .trigger("rising"), .Select("low")) register_6 (
    .D(1'b1), .Q(register_6_q), .clk(IRC), .clr(or_18_out));  // open: en
  or or_18 (or_18_out, register_9_q, RST);
  Multiplexer #(.select(2), .width(32), .disabled("Z"), .enable("false")) multiplexer_28 (
    .in1(32'h30ac), .in2(32'h3150), .in3(32'h31f4), .out(INTPC), .sel(\中断号 ));  // open: in0
  and and_18 (ClearA, URET, decoder_1_out1);
  and and_19 (ClearB, decoder_1_out2, URET);
  and and_20 (ClearC, decoder_1_out3, URET);
  or or_19 (or_19_out, register_4_q, register_7_q);
  or or_20 (or_20_out, register_5_q, register_8_q);
  or or_21 (or_21_out, register_6_q, register_9_q);
  and and_21 (and_21_out, or_19_out, ~ClearA);  // AND_Gate
  and and_22 (and_22_out, or_20_out, ~ClearB);  // AND_Gate
  and and_23 (and_23_out, or_21_out, ~ClearC);  // AND_Gate
  Register #(.width(1), .trigger("rising"), .Select("low")) register_7 (
    .D(and_21_out), .Q(register_7_q), .clk(CLK), .clr(RST));  // open: en
  Register #(.width(1), .trigger("rising"), .Select("low")) register_8 (
    .D(and_22_out), .Q(register_8_q), .clk(CLK), .clr(RST));  // open: en
  Register #(.width(1), .trigger("rising"), .Select("low")) register_9 (
    .D(and_23_out), .Q(register_9_q), .clk(CLK), .clr(RST));  // open: en
  and and_24 (and_24_out, \中断信号 , ~URET);  // AND_Gate
  Priority_Encoder #(.select(2), .disabled("Z")) priority_encoder_1 (
    .in1(register_7_q), .in2(register_8_q), .in3(register_9_q), .out(\中断号 ), .gs(\中断信号 ));  // open: in0, en_out, en_in
  D_Flip_Flop #(.trigger("rising"), .Pre_Clr_Positions("ABOVE_BELOW"), .NegatePresetClear("false"), .enable("false"), .NewFFLayout("true")) d_ff_2 (
    .clk(CLK), .D(and_24_out), .Qn(IE), .reset(RST));  // open: Q, preset

  // Other names for the same wires on the sheet: W[4:0] = ID_IR[11:7]; ID_IR (some bits) = Funct;
  //   OP[4:0] = ID_IR[6:2]; MEM_PC[31:0] = M_PC; MemData[1:0] = {LBU1, LBU0}

  // Notes on the sheet:
  //   中断源
  //   时空图监测，可删除
  //   中断等待指示
  //   单级中断测试信号模拟器
  //   ecall判断相等以及停机
  //   led显示a0
  //   R1R2Used检测
  //   分支信号类型及对应跳转地址
  //   数码管输出
  //   ecall暂停，统计周期
  //   分支检测
  //   指令存储器
  //   指令探针
  //   contents of rom_1 (hex, n*v repeats v):
  //   100493 100006f 100493 200913 300993 100006f 100493 200913 300993 100006f 100493 200913 300993
  //   100006f 100493 200913 300993 414000ef 100413 100493 1f49493 900533 2200893 73 24d493 48463 fedff06f
  //   900533 2200893 73 100493 249493 900533 2200893 73 48463 fedff06f 100493 1f49493 900533 2200893 73
  //   4034d493 900533 2200893 73 4044d493 900533 2200893 73 4044d493 900533 2200893 73 4044d493 900533
  //   2200893 73 4044d493 900533 2200893 73 4044d493 900533 2200893 73 4044d493 900533 2200893 73 4044d493
  //   900533 2200893 73 100413 1f41993 41f9d993 433 c00913 300b13 140413 f47413 800293 100313 499993
  //   89e9b3 1300533 2200893 73 406282b3 fe0294e3 140413 f00f93 1f47433 1c41413 800293 100313 49d993
  //   89e9b3 1300533 2200893 73 406282b3 fe0294e3 1c45413 406b0b33 b0463 f95ff06f 2b3 fff2c293 829293
  //   ff2e293 500533 2200893 73 fff00413 493 84a023 140413 448493 84a023 140413 448493 84a023 140413
  //   448493 84a023 140413 448493 84a023 140413 448493 84a023 140413 448493 84a023 140413 448493 84a023
  //   140413 448493 84a023 140413 448493 84a023 140413 448493 84a023 140413 448493 84a023 140413 448493
  //   84a023 140413 448493 84a023 140413 448493 84a023 140413 448493 84a023 140413 448493 140413 433
  //   3c00493 42983 4aa03 149a2b3 28663 134a023 1442023 ffc48493 fe9412e3 800533 2200893 73 440413 3c00493
  //   fc9416e3 a00893 73 100293 300313 800493 849493 7648493 1449493 900533 2200893 73 800e13 54d4b3
  //   64d4b3 900533 2200893 73 fffe0e13 fe0e14e3 a00893 73 13 430497 900533 2200893 73 430497 900533
  //   2200893 73 430497 900533 2200893 73 430497 900533 2200893 73 430497 900533 2200893 73 430497 900533
  //   2200893 73 430497 900533 2200893 73 430497 900533 2200893 73 a00893 73 313 1000e13 8400493 849493
  //   8348493 400913 891913 490913 849493 8248493 849493 8148493 891913 490913 891913 490913 932023
  //   12484b3 430313 fffe0e13 fe0e18e3 2000e13 313 34483 900533 2200893 73 130313 fffe0e13 fe0e14e3 a00893
  //   73 f00493 900533 2200893 73 fff48493 fe04d8e3 a00893 73 413 140413 800533 2200893 73 240413 800533
  //   2200893 73 340413 800533 2200893 73 440413 800533 2200893 73 540413 800533 2200893 73 640413 800533
  //   2200893 73 740413 800533 2200893 73 840413 800533 2200893 2200893 73 8067
  //   控制位
  //   指令字
  //   jalr最低位置0
  //   BTB表构建
  //   预测结果比对
  //   流水调试日志用
  //   暂停节拍，不能为0
  //   戳工具置1进入计数暂停模式，ctrl+k时钟自动运行到对应节拍暂停
  //   ctrl+k关闭时钟连续运行，将控制位置零，进入单步调试模式调试
  //   a7
  //   a0
  //   I型imm
  //   S型imm
  //   B型imm
  //   U型imm
  //   可计数暂停的时钟源
  //   J型imm
  //   lbu取字节
  //   为方便自动评测，需要输出流水线各段保存的PC值，注意是PC不是PC+4，另外ID段寄存器写入信息，Mem段内存写入信息也要输出
  //   JAL
  //   AUIPC
  //   LBU
  //   JALR
  //   ALUResult
  //   MemData
  //   允许中断情况下产生中断
  //   保护现场，保护返回地址
  //   生成清零信号
  //   中断使能寄存器IE
endmodule

module BTB (
  input  [31:0] PC,
  input  [31:0] EX_PC,
  input  [31:0] EX_BranchAddr,
  input  EX_Branch,
  input  EX_Branched,
  input  in_6,
  output ID_PredictJump,
  output [31:0] BTB_JumpAddr
);

  wire and_17_out, and_26_out, and_27_out, and_28_out, and_29_out, and_30_out, and_31_out, and_32_out,
       and_33_out, comparator_1_eq, comparator_2_eq, comparator_3_eq, comparator_4_eq, comparator_5_eq,
       comparator_6_eq, comparator_7_eq, comparator_8_eq, comparator_9_eq, comparator_10_eq,
       comparator_11_eq, comparator_12_eq, comparator_13_eq, comparator_14_eq, comparator_15_eq,
       comparator_16_eq, d_ff_1_q, d_ff_2_q, d_ff_3_q, d_ff_4_q, d_ff_5_q, d_ff_6_q, d_ff_7_q, d_ff_8_q,
       decoder_1_out0, decoder_1_out1, decoder_1_out2, decoder_1_out3, decoder_1_out4, decoder_1_out5,
       decoder_1_out6, decoder_1_out7, decoder_2_out0, decoder_2_out1, decoder_2_out2, decoder_2_out3,
       decoder_2_out4, decoder_2_out5, decoder_2_out6, decoder_2_out7, EX_Hit, EX_Miss, L0, L1, L2, L3, L4,
       L5, L6, L7, M0, M1, M2, M3, M4, M5, M6, M7, max_1_p5, max_1_p6, max_2_p5, max_2_p6, max_3_p5,
       max_3_p6, max_4_p6, max_4_p7, max_5_p3, max_5_p4, max_6_p3, max_6_p4, not_1_out, not_2_out, not_3_out,
       not_4_out, not_5_out, not_6_out, not_7_out, not_8_out, or_1_out, or_2_out, or_3_out, or_4_out,
       or_5_out, or_6_out, or_7_out, or_8_out, or_10_out, or_11_out, or_12_out, or_13_out, or_14_out,
       or_15_out, or_16_out, or_17_out, priority_encoder_1_gs, v0, v1, v2, v3, v4, v5, v6, v7, write0,
       write1, write2, write3, write4, write5, write6, write7;
  wire [0:0] controlled_buffer_9_out, controlled_buffer_10_out, controlled_buffer_11_out,
       controlled_buffer_12_out, controlled_buffer_13_out, controlled_buffer_14_out,
       controlled_buffer_15_out, controlled_buffer_16_out;
  wire [1:0] fsm_1_p5, fsm_2_p5, fsm_3_p5, fsm_4_p5, fsm_5_p5, fsm_6_p5, fsm_7_p5, fsm_8_p5, predict0,
       predict1, predict2, predict3, predict4, predict5, predict6, predict7;
  wire [2:0] max_7_p5, priority_encoder_1_out;
  wire [15:0] c0, c1, c2, c3, c4, c5, c6, c7;
  wire [31:0] register_17_q, register_18_q, register_19_q, register_20_q, register_21_q, register_22_q,
       register_23_q, register_24_q, tag0, tag1, tag2, tag3, tag4, tag5, tag6, tag7;

  LED #(.active("true")) led_1 (.in(v0));
  Register #(.width(1), .trigger("rising"), .Select("low")) register_1 (
    .D(1'b1), .en(write0), .Q(v0), .clk(in_6));  // open: clr
  LED #(.active("true")) led_2 (.in(v1));
  Register #(.width(1), .trigger("rising"), .Select("low")) register_2 (
    .D(1'b1), .en(write1), .Q(v1), .clk(in_6));  // open: clr
  LED #(.active("true")) led_3 (.in(v2));
  Register #(.width(1), .trigger("rising"), .Select("low")) register_3 (
    .D(1'b1), .en(write2), .Q(v2), .clk(in_6));  // open: clr
  LED #(.active("true")) led_4 (.in(v3));
  Register #(.width(1), .trigger("rising"), .Select("low")) register_4 (
    .D(1'b1), .en(write3), .Q(v3), .clk(in_6));  // open: clr
  LED #(.active("true")) led_5 (.in(v4));
  Register #(.width(1), .trigger("rising"), .Select("low")) register_5 (
    .D(1'b1), .en(write4), .Q(v4), .clk(in_6));  // open: clr
  LED #(.active("true")) led_6 (.in(v5));
  Register #(.width(1), .trigger("rising"), .Select("low")) register_6 (
    .D(1'b1), .en(write5), .Q(v5), .clk(in_6));  // open: clr
  LED #(.active("true")) led_7 (.in(v6));
  Register #(.width(1), .trigger("rising"), .Select("low")) register_7 (
    .D(1'b1), .en(write6), .Q(v6), .clk(in_6));  // open: clr
  Register #(.width(1), .trigger("rising"), .Select("low")) register_8 (
    .D(1'b1), .en(write7), .Q(v7), .clk(in_6));  // open: clr
  LED #(.active("true")) led_8 (.in(v7));
  // Probe on tag0
  Register #(.width(32), .trigger("rising"), .Select("low")) register_9 (
    .D(EX_PC), .en(write0), .Q(tag0), .clk(in_6));  // open: clr
  // Probe on tag1
  Register #(.width(32), .trigger("rising"), .Select("low")) register_10 (
    .D(EX_PC), .en(write1), .Q(tag1), .clk(in_6));  // open: clr
  // Probe on tag2
  Register #(.width(32), .trigger("rising"), .Select("low")) register_11 (
    .D(EX_PC), .en(write2), .Q(tag2), .clk(in_6));  // open: clr
  // Probe on tag3
  Register #(.width(32), .trigger("rising"), .Select("low")) register_12 (
    .D(EX_PC), .en(write3), .Q(tag3), .clk(in_6));  // open: clr
  // Probe on tag4
  Register #(.width(32), .trigger("rising"), .Select("low")) register_13 (
    .D(EX_PC), .en(write4), .Q(tag4), .clk(in_6));  // open: clr
  // Probe on tag5
  Register #(.width(32), .trigger("rising"), .Select("low")) register_14 (
    .D(EX_PC), .en(write5), .Q(tag5), .clk(in_6));  // open: clr
  Register #(.width(32), .trigger("rising"), .Select("low")) register_15 (
    .D(EX_PC), .en(write6), .Q(tag6), .clk(in_6));  // open: clr
  // Probe on tag7
  Register #(.width(32), .trigger("rising"), .Select("low")) register_16 (
    .D(EX_PC), .en(write7), .Q(tag7), .clk(in_6));  // open: clr
  // Probe on tag6
  Counter #(.width(16), .max('hffff), .ongoal("wrap"), .trigger("rising"), .behavior("new")) counter_1 (
    .Q(c0), .clk(in_6), .clr(d_ff_3_q));  // open: load, D, count, carry, preset, down
  or or_1 (or_1_out, write0, L0);
  Counter #(.width(16), .max('hffff), .ongoal("wrap"), .trigger("rising"), .behavior("new")) counter_2 (
    .Q(c1), .clk(in_6), .clr(d_ff_4_q));  // open: load, D, count, carry, preset, down
  or or_2 (or_2_out, write1, L1);
  Counter #(.width(16), .max('hffff), .ongoal("wrap"), .trigger("rising"), .behavior("new")) counter_3 (
    .Q(c2), .clk(in_6), .clr(d_ff_5_q));  // open: load, D, count, carry, preset, down
  or or_3 (or_3_out, write2, L2);
  Counter #(.width(16), .max('hffff), .ongoal("wrap"), .trigger("rising"), .behavior("new")) counter_4 (
    .Q(c3), .clk(in_6), .clr(d_ff_6_q));  // open: load, D, count, carry, preset, down
  or or_4 (or_4_out, write3, L3);
  Counter #(.width(16), .max('hffff), .ongoal("wrap"), .trigger("rising"), .behavior("new")) counter_5 (
    .Q(c4), .clk(in_6), .clr(d_ff_1_q));  // open: load, D, count, carry, preset, down
  D_Flip_Flop #(.trigger("rising"), .Pre_Clr_Positions("ABOVE_BELOW"), .NegatePresetClear("false"), .enable("false"), .NewFFLayout("false")) d_ff_1 (
    .clk(in_6), .D(or_5_out), .Q(d_ff_1_q));  // open: Qn, preset, reset
  or or_5 (or_5_out, write4, L4);
  Counter #(.width(16), .max('hffff), .ongoal("wrap"), .trigger("rising"), .behavior("new")) counter_6 (
    .Q(c5), .clk(in_6), .clr(d_ff_7_q));  // open: load, D, count, carry, preset, down
  or or_6 (or_6_out, write5, L5);
  Counter #(.width(16), .max('hffff), .ongoal("wrap"), .trigger("rising"), .behavior("new")) counter_7 (
    .Q(c6), .clk(in_6), .clr(d_ff_8_q));  // open: load, D, count, carry, preset, down
  or or_7 (or_7_out, write6, L6);
  Counter #(.width(16), .max('hffff), .ongoal("wrap"), .trigger("rising"), .behavior("new")) counter_8 (
    .Q(c7), .clk(in_6), .clr(d_ff_2_q));  // open: load, D, count, carry, preset, down
  D_Flip_Flop #(.trigger("rising"), .Pre_Clr_Positions("LEGACY"), .NegatePresetClear("false"), .enable("true"), .NewFFLayout("false")) d_ff_2 (
    .clk(in_6), .D(or_8_out), .Q(d_ff_2_q));  // open: Qn, preset, en, reset
  or or_8 (or_8_out, write7, L7);
  D_Flip_Flop #(.trigger("rising"), .Pre_Clr_Positions("ABOVE_BELOW"), .NegatePresetClear("false"), .enable("false"), .NewFFLayout("false")) d_ff_3 (
    .clk(in_6), .D(or_1_out), .Q(d_ff_3_q));  // open: Qn, preset, reset
  D_Flip_Flop #(.trigger("rising"), .Pre_Clr_Positions("ABOVE_BELOW"), .NegatePresetClear("false"), .enable("false"), .NewFFLayout("false")) d_ff_4 (
    .clk(in_6), .D(or_2_out), .Q(d_ff_4_q));  // open: Qn, preset, reset
  D_Flip_Flop #(.trigger("rising"), .Pre_Clr_Positions("ABOVE_BELOW"), .NegatePresetClear("false"), .enable("false"), .NewFFLayout("false")) d_ff_5 (
    .clk(in_6), .D(or_3_out), .Q(d_ff_5_q));  // open: Qn, preset, reset
  D_Flip_Flop #(.trigger("rising"), .Pre_Clr_Positions("ABOVE_BELOW"), .NegatePresetClear("false"), .enable("false"), .NewFFLayout("false")) d_ff_6 (
    .clk(in_6), .D(or_4_out), .Q(d_ff_6_q));  // open: Qn, preset, reset
  D_Flip_Flop #(.trigger("rising"), .Pre_Clr_Positions("ABOVE_BELOW"), .NegatePresetClear("false"), .enable("false"), .NewFFLayout("false")) d_ff_7 (
    .clk(in_6), .D(or_6_out), .Q(d_ff_7_q));  // open: Qn, preset, reset
  D_Flip_Flop #(.trigger("rising"), .Pre_Clr_Positions("LEGACY"), .NegatePresetClear("false"), .enable("true"), .NewFFLayout("false")) d_ff_8 (
    .clk(in_6), .D(or_7_out), .Q(d_ff_8_q));  // open: Qn, preset, en, reset
  Register #(.width(32), .trigger("rising"), .Select("low")) register_17 (
    .D(EX_BranchAddr), .en(write0), .Q(register_17_q), .clk(in_6));  // open: clr
  Register #(.width(32), .trigger("rising"), .Select("low")) register_18 (
    .D(EX_BranchAddr), .en(write1), .Q(register_18_q), .clk(in_6));  // open: clr
  Register #(.width(32), .trigger("rising"), .Select("low")) register_19 (
    .D(EX_BranchAddr), .en(write2), .Q(register_19_q), .clk(in_6));  // open: clr
  Register #(.width(32), .trigger("rising"), .Select("low")) register_20 (
    .D(EX_BranchAddr), .en(write3), .Q(register_20_q), .clk(in_6));  // open: clr
  Register #(.width(32), .trigger("rising"), .Select("low")) register_21 (
    .D(EX_BranchAddr), .en(write4), .Q(register_21_q), .clk(in_6));  // open: clr
  Register #(.width(32), .trigger("rising"), .Select("low")) register_22 (
    .D(EX_BranchAddr), .en(write5), .Q(register_22_q), .clk(in_6));  // open: clr
  Register #(.width(32), .trigger("rising"), .Select("low")) register_23 (
    .D(EX_BranchAddr), .en(write6), .Q(register_23_q), .clk(in_6));  // open: clr
  Register #(.width(32), .trigger("rising"), .Select("low")) register_24 (
    .D(EX_BranchAddr), .en(write7), .Q(register_24_q), .clk(in_6));  // open: clr
  assign BTB_JumpAddr = L0 ? register_17_q : 32'bz;  // Controlled_Buffer controlled_buffer_1
  assign BTB_JumpAddr = L1 ? register_18_q : 32'bz;  // Controlled_Buffer controlled_buffer_2
  assign BTB_JumpAddr = L2 ? register_19_q : 32'bz;  // Controlled_Buffer controlled_buffer_3
  assign BTB_JumpAddr = L3 ? register_20_q : 32'bz;  // Controlled_Buffer controlled_buffer_4
  assign BTB_JumpAddr = L4 ? register_21_q : 32'bz;  // Controlled_Buffer controlled_buffer_5
  assign BTB_JumpAddr = L5 ? register_22_q : 32'bz;  // Controlled_Buffer controlled_buffer_6
  assign BTB_JumpAddr = L6 ? register_23_q : 32'bz;  // Controlled_Buffer controlled_buffer_7
  assign BTB_JumpAddr = L7 ? register_24_q : 32'bz;  // Controlled_Buffer controlled_buffer_8
  Comparator #(.width(32), .mode("twosComplement")) comparator_1 (
    .a(tag0), .b(PC), .eq(comparator_1_eq));  // open: gt, lt
  Comparator #(.width(32), .mode("twosComplement")) comparator_2 (
    .a(tag1), .b(PC), .eq(comparator_2_eq));  // open: gt, lt
  Comparator #(.width(32), .mode("twosComplement")) comparator_3 (
    .a(tag2), .b(PC), .eq(comparator_3_eq));  // open: gt, lt
  Comparator #(.width(32), .mode("twosComplement")) comparator_4 (
    .a(tag3), .b(PC), .eq(comparator_4_eq));  // open: gt, lt
  Comparator #(.width(32), .mode("twosComplement")) comparator_5 (
    .a(tag4), .b(PC), .eq(comparator_5_eq));  // open: gt, lt
  Comparator #(.width(32), .mode("twosComplement")) comparator_6 (
    .a(tag5), .b(PC), .eq(comparator_6_eq));  // open: gt, lt
  Comparator #(.width(32), .mode("twosComplement")) comparator_7 (
    .a(tag6), .b(PC), .eq(comparator_7_eq));  // open: gt, lt
  Comparator #(.width(32), .mode("twosComplement")) comparator_8 (
    .a(tag7), .b(PC), .eq(comparator_8_eq));  // open: gt, lt
  and and_1 (L0, v0, comparator_1_eq);
  and and_2 (L1, v1, comparator_2_eq);
  and and_3 (L2, v2, comparator_3_eq);
  and and_4 (L3, v3, comparator_4_eq);
  and and_5 (L4, v4, comparator_5_eq);
  and and_6 (L5, v5, comparator_6_eq);
  and and_7 (L6, v6, comparator_7_eq);
  and and_8 (L7, v7, comparator_8_eq);
  Comparator #(.width(32), .mode("twosComplement")) comparator_9 (
    .a(tag0), .b(EX_PC), .eq(comparator_9_eq));  // open: gt, lt
  Comparator #(.width(32), .mode("twosComplement")) comparator_10 (
    .a(tag1), .b(EX_PC), .eq(comparator_10_eq));  // open: gt, lt
  Comparator #(.width(32), .mode("twosComplement")) comparator_11 (
    .a(tag2), .b(EX_PC), .eq(comparator_11_eq));  // open: gt, lt
  Comparator #(.width(32), .mode("twosComplement")) comparator_12 (
    .a(tag3), .b(EX_PC), .eq(comparator_12_eq));  // open: gt, lt
  Comparator #(.width(32), .mode("twosComplement")) comparator_13 (
    .a(tag4), .b(EX_PC), .eq(comparator_13_eq));  // open: gt, lt
  Comparator #(.width(32), .mode("twosComplement")) comparator_14 (
    .a(tag5), .b(EX_PC), .eq(comparator_14_eq));  // open: gt, lt
  Comparator #(.width(32), .mode("twosComplement")) comparator_15 (
    .a(tag6), .b(EX_PC), .eq(comparator_15_eq));  // open: gt, lt
  Comparator #(.width(32), .mode("twosComplement")) comparator_16 (
    .a(tag7), .b(EX_PC), .eq(comparator_16_eq));  // open: gt, lt
  and and_9 (M0, v0, comparator_9_eq);
  and and_10 (M1, v1, comparator_10_eq);
  and and_11 (M2, v2, comparator_11_eq);
  and and_12 (M3, v3, comparator_12_eq);
  and and_13 (M4, v4, comparator_13_eq);
  and and_14 (M5, v5, comparator_14_eq);
  and and_15 (M6, v6, comparator_15_eq);
  and and_16 (M7, v7, comparator_16_eq);
  not not_1 (not_1_out, v0);
  not not_2 (not_2_out, v1);
  not not_3 (not_3_out, v2);
  not not_4 (not_4_out, v3);
  not not_5 (not_5_out, v4);
  not not_6 (not_6_out, v5);
  not not_7 (not_7_out, v6);
  not not_8 (not_8_out, v7);
  // 重定向流水线ccab_MAX max_1: pin names not known; wires that end beside it: c0, 3'b000, c1, 3'b001, max_1_p5, max_1_p6
  // 重定向流水线ccab_MAX max_2: pin names not known; wires that end beside it: c2, 3'b010, c3, 3'b011, max_2_p5, max_2_p6, max_2_p5, max_2_p6
  // 重定向流水线ccab_MAX max_3: pin names not known; wires that end beside it: c4, 3'b100, c5, 3'b101, max_3_p5, max_3_p6
  // 重定向流水线ccab_MAX max_4: pin names not known; wires that end beside it: v4, c6, 3'b110, c7, 3'b111, max_4_p6, max_4_p7, max_4_p6, max_4_p7
  or or_9 (EX_Hit, M0, M1, M2, M3, M4, M5, M6, M7);
  not not_9 (EX_Miss, EX_Hit);
  Priority_Encoder #(.select(3), .disabled("Z")) priority_encoder_1 (
    .in0(not_1_out), .in1(not_2_out), .in2(not_3_out), .in3(not_4_out), .in4(not_5_out), .in5(not_6_out),
    .in6(not_7_out), .in7(not_8_out), .out(priority_encoder_1_out), .gs(priority_encoder_1_gs));  // open: en_out, en_in
  // 重定向流水线ccab_MAX max_5: pin names not known; wires that end beside it: max_1_p5, max_1_p6, max_5_p3, max_5_p4
  // 重定向流水线ccab_MAX max_6: pin names not known; wires that end beside it: max_3_p5, max_3_p6, max_6_p3, max_6_p4
  and and_17 (and_17_out, v0, v1, v2, v3, v4, v5, v6, v7);
  Decoder #(.select(3), .tristate("false"), .disabled(0), .enable("true")) decoder_1 (
    .out0(decoder_1_out0), .out1(decoder_1_out1), .out2(decoder_1_out2), .out3(decoder_1_out3),
    .out4(decoder_1_out4), .out5(decoder_1_out5), .out6(decoder_1_out6), .out7(decoder_1_out7),
    .sel(priority_encoder_1_out), .en(priority_encoder_1_gs));
  Decoder #(.select(3), .tristate("false"), .disabled(0), .enable("true")) decoder_2 (
    .out0(decoder_2_out0), .out1(decoder_2_out1), .out2(decoder_2_out2), .out3(decoder_2_out3),
    .out4(decoder_2_out4), .out5(decoder_2_out5), .out6(decoder_2_out6), .out7(decoder_2_out7),
    .sel(max_7_p5), .en(and_17_out));
  // 重定向流水线ccab_MAX max_7: pin names not known; wires that end beside it: max_5_p3, max_5_p4, max_6_p3, max_6_p4, max_7_p5
  or or_10 (or_10_out, decoder_1_out0, decoder_2_out0);
  or or_11 (or_11_out, decoder_1_out1, decoder_2_out1);
  or or_12 (or_12_out, decoder_1_out2, decoder_2_out2);
  or or_13 (or_13_out, decoder_1_out3, decoder_2_out3);
  or or_14 (or_14_out, decoder_1_out4, decoder_2_out4);
  or or_15 (or_15_out, decoder_1_out5, decoder_2_out5);
  or or_16 (or_16_out, decoder_1_out6, decoder_2_out6);
  or or_17 (or_17_out, decoder_1_out7, decoder_2_out7);
  and and_18 (write0, or_10_out, EX_Miss, EX_Branch);
  and and_19 (write1, or_11_out, EX_Miss, EX_Branch);
  and and_20 (write2, or_12_out, EX_Miss, EX_Branch);
  and and_21 (write3, or_13_out, EX_Miss, EX_Branch);
  and and_22 (write4, or_14_out, EX_Miss, EX_Branch);
  and and_23 (write5, or_15_out, EX_Miss, EX_Branch);
  and and_24 (write6, or_16_out, EX_Miss, EX_Branch);
  and and_25 (write7, or_17_out, EX_Miss, EX_Branch);
  assign {ID_PredictJump, controlled_buffer_9_out[0]} = L0 ? predict0 : 2'bz;  // Controlled_Buffer controlled_buffer_9
  assign {ID_PredictJump, controlled_buffer_10_out[0]} = L1 ? predict1 : 2'bz;  // Controlled_Buffer controlled_buffer_10
  assign {ID_PredictJump, controlled_buffer_11_out[0]} = L2 ? predict2 : 2'bz;  // Controlled_Buffer controlled_buffer_11
  assign {ID_PredictJump, controlled_buffer_12_out[0]} = L3 ? predict3 : 2'bz;  // Controlled_Buffer controlled_buffer_12
  assign {ID_PredictJump, controlled_buffer_13_out[0]} = L4 ? predict4 : 2'bz;  // Controlled_Buffer controlled_buffer_13
  assign {ID_PredictJump, controlled_buffer_14_out[0]} = L5 ? predict5 : 2'bz;  // Controlled_Buffer controlled_buffer_14
  assign {ID_PredictJump, controlled_buffer_15_out[0]} = L6 ? predict6 : 2'bz;  // Controlled_Buffer controlled_buffer_15
  assign {ID_PredictJump, controlled_buffer_16_out[0]} = L7 ? predict7 : 2'bz;  // Controlled_Buffer controlled_buffer_16
  Pull_Resistor #(.pull(0)) pull_resistor_1 (.node(ID_PredictJump));
  // 重定向流水线ccab_FSM fsm_1: pin names not known; wires that end beside it: predict0[1], predict0[0], EX_Branched, fsm_1_p5[1], fsm_1_p5[0]
  // 重定向流水线ccab_FSM fsm_2: pin names not known; wires that end beside it: predict1[1], predict1[0], EX_Branched, fsm_2_p5[1], fsm_2_p5[0]
  // 重定向流水线ccab_FSM fsm_3: pin names not known; wires that end beside it: predict2[1], predict2[0], EX_Branched, fsm_3_p5[1], fsm_3_p5[0]
  // 重定向流水线ccab_FSM fsm_4: pin names not known; wires that end beside it: predict3[1], predict3[0], EX_Branched, fsm_4_p5[1], fsm_4_p5[0]
  // 重定向流水线ccab_FSM fsm_5: pin names not known; wires that end beside it: predict4[1], predict4[0], EX_Branched, fsm_5_p5[1], fsm_5_p5[0]
  // 重定向流水线ccab_FSM fsm_6: pin names not known; wires that end beside it: predict5[1], predict5[0], EX_Branched, fsm_6_p5[1], fsm_6_p5[0]
  // 重定向流水线ccab_FSM fsm_7: pin names not known; wires that end beside it: predict6[1], predict6[0], EX_Branched, fsm_7_p5[1], fsm_7_p5[0]
  // 重定向流水线ccab_FSM fsm_8: pin names not known; wires that end beside it: predict7[1], predict7[0], EX_Branched, fsm_8_p5[1], fsm_8_p5[0]
  and and_26 (and_26_out, EX_Branch, M0);
  Register #(.width(2), .trigger("rising"), .Select("low")) register_25 (
    .D(fsm_1_p5), .en(and_26_out), .Q(predict0), .clk(in_6));  // open: clr
  and and_27 (and_27_out, EX_Branch, M1);
  Register #(.width(2), .trigger("rising"), .Select("low")) register_26 (
    .D(fsm_2_p5), .en(and_27_out), .Q(predict1), .clk(in_6));  // open: clr
  and and_28 (and_28_out, EX_Branch, M2);
  Register #(.width(2), .trigger("rising"), .Select("low")) register_27 (
    .D(fsm_3_p5), .en(and_28_out), .Q(predict2), .clk(in_6));  // open: clr
  and and_29 (and_29_out, EX_Branch, M3);
  Register #(.width(2), .trigger("rising"), .Select("low")) register_28 (
    .D(fsm_4_p5), .en(and_29_out), .Q(predict3), .clk(in_6));  // open: clr
  and and_30 (and_30_out, EX_Branch, M4);
  Register #(.width(2), .trigger("rising"), .Select("low")) register_29 (
    .D(fsm_5_p5), .en(and_30_out), .Q(predict4), .clk(in_6));  // open: clr
  and and_31 (and_31_out, EX_Branch, M5);
  Register #(.width(2), .trigger("rising"), .Select("low")) register_30 (
    .D(fsm_6_p5), .en(and_31_out), .Q(predict5), .clk(in_6));  // open: clr
  and and_32 (and_32_out, EX_Branch, M6);
  Register #(.width(2), .trigger("rising"), .Select("low")) register_31 (
    .D(fsm_7_p5), .en(and_32_out), .Q(predict6), .clk(in_6));  // open: clr
  and and_33 (and_33_out, EX_Branch, M7);
  Register #(.width(2), .trigger("rising"), .Select("low")) register_32 (
    .D(fsm_8_p5), .en(and_33_out), .Q(predict7), .clk(in_6));  // open: clr

  // Other names for the same wires on the sheet: CLK = in_6; Tag[31:0] = EX_PC

  // Notes on the sheet:
  //   EX写入逻辑
  //   历史预测位
  //   与PC比较数据命中  选择L而不是M
  //   EX.PC如果数据命中，需要根据EX.Branched的值依据预测位状态机更新分支预测历史位的值
endmodule

module FSM (
  input  high,
  input  low,
  input  jump,
  output NextHigh,
  output NextLow
);

  wire and_1_out, and_2_out, and_3_out, and_4_out, not_1_out, not_2_out, not_3_out, not_4_out, not_5_out;

  not not_1 (not_1_out, low);
  not not_2 (not_2_out, high);
  not not_3 (not_3_out, low);
  not not_4 (not_4_out, low);
  not not_5 (not_5_out, jump);
  and and_1 (and_1_out, low, jump);
  and and_2 (and_2_out, high, not_1_out);
  and and_3 (and_3_out, not_2_out, not_3_out, jump);
  and and_4 (and_4_out, high, not_4_out, not_5_out);
  or or_1 (NextHigh, and_1_out, and_2_out);
  or or_2 (NextLow, and_3_out, and_4_out);
endmodule

module MAX (
  input  [15:0] Y,
  input  [15:0] X,
  input  [2:0] Y_num,
  input  [2:0] X_num,
  output [15:0] MAX,
  output [2:0] Max_num
);

  wire comparator_1_eq, comparator_1_gt, or_1_out;

  Comparator #(.width(16), .mode("unsigned")) comparator_1 (
    .a(X), .b(Y), .gt(comparator_1_gt), .eq(comparator_1_eq));  // open: lt
  Multiplexer #(.select(1), .width(16), .disabled("Z"), .enable("false")) multiplexer_1 (
    .in0(Y), .in1(X), .out(MAX), .sel(or_1_out));
  or or_1 (or_1_out, comparator_1_gt, comparator_1_eq);
  Multiplexer #(.select(1), .width(3), .disabled("Z"), .enable("false")) multiplexer_2 (
    .in0(Y_num), .in1(X_num), .out(Max_num), .sel(or_1_out));

  // Notes on the sheet:
  //   输出两个输入中的较大值，并输出较大值的3位编号
endmodule
