// Logisim project 团队任务.circ as structural Verilog
module \单周期RISC_V  (
  input  IR1,
  input  IR2,
  input  IR3,
  output RegWrite,
  output MemWrite,
  output [31:0] PC,
  output [31:0] IR,
  output [31:0] RDin,
  output [31:0] MDin,
  output [31:0] LedData,
  output [31:0] \行1 ,
  output [31:0] \行2 ,
  output [31:0] \行3 ,
  output [31:0] \行4 ,
  output [31:0] \行5 ,
  output [31:0] \行6 ,
  output [31:0] \行7 ,
  output [31:0] \行8 ,
  output [31:0] \行9 ,
  output [31:0] \行10 ,
  output [31:0] \行11 ,
  output [31:0] \行12 ,
  output [31:0] \行13 ,
  output [31:0] \行14 ,
  output [31:0] \行15 ,
  output [31:0] \行16 ,
  output [31:0] \行17 ,
  output [31:0] \行18 ,
  output [31:0] \行19 ,
  output [31:0] \行20 ,
  output [31:0] \行21 ,
  output [31:0] \行22 ,
  output [31:0] \行23 ,
  output [31:0] \行24 ,
  output [31:0] \行25 ,
  output [31:0] \行26 ,
  output [31:0] \行27 ,
  output [31:0] \行28 ,
  output [31:0] \行29 ,
  output [31:0] \行30 ,
  output [31:0] \行31 ,
  output [31:0] \行32 
);

  wire AluSrcB, and_2_out, and_3_out, and_5_out, and_6_out, and_7_out, and_8_out, and_9_out, beq, bgeu, bne,
       Branch, CLK, clock_1_out, comparator_1_eq, comparator_2_eq, comparator_2_lt, comparator_3_lt,
       comparator_4_eq, d_ff_1_q, ecall, equal, gae, Go, halt, high, IR1_t, IR2_t, IR3_t, IRA, IRB, IRC, jal,
       jalr, JAMP, less, lhu, MemToReg, nand_1_out, not_1_out, not_2_out, not_3_out, not_4_out, not_5_out,
       or_1_out, or_2_out, RST, S_type, sltiu, uret, W1, W2, W3;
  wire [3:0] AluOP;
  wire [4:0] multiplexer_4_out, multiplexer_7_out;
  wire [9:0] ADDR;
  wire [11:0] imm12_B;
  wire [12:0] CNT_num;
  wire [15:0] multiplexer_12_out, \分支成功数 , \总周期数 ;
  wire [19:0] imm20_J;
  wire [31:0] adder_1_out, adder_3_out, and_1_out, Bin, bit_extender_1_out, bit_extender_2_out,
       bit_extender_3_out, bit_extender_4_out, bit_extender_5_out, bit_extender_6_out, bit_extender_7_out,
       MDout, multiplexer_2_out, multiplexer_3_out, multiplexer_5_out, multiplexer_6_out, multiplexer_9_out,
       multiplexer_10_out, PC_4, PCin, R1, ram_1_data, Result, \地图_1_行1 , \地图_1_行2 , \地图_1_行3 , \地图_1_行4 ,
       \地图_1_行5 , \地图_1_行6 , \地图_1_行7 , \地图_1_行8 , \地图_1_行9 , \地图_1_行10 , \地图_1_行11 , \地图_1_行12 , \地图_1_行13 ,
       \地图_1_行14 , \地图_1_行15 , \地图_1_行16 , \地图_1_行17 , \地图_1_行18 , \地图_1_行19 , \地图_1_行20 , \地图_1_行21 ,
       \地图_1_行22 , \地图_1_行23 , \地图_1_行24 , \地图_1_行25 , \地图_1_行26 , \地图_1_行27 , \地图_1_行28 , \地图_1_行29 ,
       \地图_1_行30 , \地图_1_行31 , \地图_1_行32 , \点阵_1__3_2 , \点阵_1__4_2 , \点阵_1__5_2 , \点阵_1__6_2 , \点阵_1__7_2 ,
       \点阵_1__8_2 , \点阵_1__9_2 , \点阵_1__10_2 , \点阵_1__11_2 , \点阵_1__12_2 , \点阵_1__13_2 , \点阵_1__14_2 ,
       \点阵_1__15_2 , \点阵_1__16_2 , \点阵_1__17_2 , \点阵_1__18_2 , \点阵_1__19_2 , \点阵_1__20_2 , \点阵_1__21_2 ,
       \点阵_1__22_2 , \点阵_1__23_2 , \点阵_1__24_2 , \点阵_1__25_2 , \点阵_1__26_2 , \点阵_1__27_2 , \点阵_1__28_2 ,
       \点阵_1__29_2 , \点阵_1__30_2 ;

  Button \u_继续运行  (.out(Go));
  Button _1 (.out(IRA));
  Button _2 (.out(IRB));
  Button _3 (.out(IRC));
  Button button_1 (.out(RST));
  LED led_1 (.in(W1));
  LED led_2 (.in(W2));
  LED led_3 (.in(W3));
  or or_1 (or_1_out, Go, not_1_out);
  Hex_Digit_Display hex_digit_display_1 (.value(LedData[31:28]));  // open: dp
  Register #(.width(32), .Select("low")) u_PC (.D(PCin), .en(or_1_out), .Q(PC), .clk(CLK), .clr(RST));
  not not_1 (not_1_out, halt);
  not not_2 (not_2_out, halt);
  Multiplexer #(.width(32), .enable("false")) multiplexer_1 (
    .in0(multiplexer_2_out), .in1(adder_1_out), .out(PCin), .sel(Branch));
  assign bit_extender_1_out = {{20{imm12_B[11]}}, imm12_B};  // Bit_Extender bit_extender_1
  Hex_Digit_Display hex_digit_display_2 (.value(LedData[27:24]));  // open: dp
  Hex_Digit_Display hex_digit_display_3 (.value(LedData[23:20]));  // open: dp
  Counter #(.width(16), .max('hffff)) counter_1 (
    .count(or_2_out), .Q(\总周期数 ), .clk(CLK), .clr(RST));  // open: load, D, carry, preset, down
  or or_2 (or_2_out, not_2_out, Go);
  or or_3 (JAMP, jal, jalr);
  Multiplexer #(.width(32), .enable("false")) multiplexer_2 (
    .in0(multiplexer_3_out), .in1(and_1_out), .out(multiplexer_2_out), .sel(jalr));
  Adder #(.width(32)) adder_1 (.a(bit_extender_1_out), .b(PC), .out(adder_1_out));  // open: cin, cout
  Hex_Digit_Display hex_digit_display_4 (.value(LedData[19:16]));  // open: dp
  Hex_Digit_Display hex_digit_display_5 (.value(LedData[15:12]));  // open: dp
  // RiscV_Probe riscv_probe_1: pin names not known; wires that end beside it: IR, IR[19:15], IR[11:7]
  Adder #(.width(32)) adder_2 (.a(PC), .b(32'h4), .out(PC_4));  // open: cin, cout
  Multiplexer #(.width(32), .enable("false")) multiplexer_3 (
    .in0(PC_4), .in1(adder_3_out), .out(multiplexer_3_out), .sel(jal));
  assign and_1_out = {Result[31:12], ADDR, high, Result[0]} & 32'hfffffffe;  // AND_Gate and_1, 32 bits wide
  assign bit_extender_2_out = {{12{imm20_J[19]}}, imm20_J};  // Bit_Extender bit_extender_2
  Adder #(.width(32)) adder_3 (.a(bit_extender_2_out), .b(PC), .out(adder_3_out));  // open: cin, cout
  Hex_Digit_Display hex_digit_display_6 (.value(LedData[7:4]));  // open: dp
  Hex_Digit_Display hex_digit_display_7 (.value(LedData[11:8]));  // open: dp
  // Probe on \总周期数 
  ROM #(.addrWidth(10), .dataWidth(32), .Select("high")) rom_1 (.addr(PC[11:2]), .data(IR));
  Hex_Digit_Display hex_digit_display_8 (.value(LedData[3:0]));  // open: dp
  \单周期硬布线控制器  \u_单周期硬布线控制器_1  (
    .Funct({IR[30], IR[25], IR[14:12]}), .OP(IR[6:2]), .ALU_OP(AluOP), .MemToReg(MemToReg),
    .MemWrite(MemWrite), .ALU_SRC(AluSrcB), .RegWrite(RegWrite), .ecall(ecall), .S_type(S_type), .Jalr(jalr),
    .Beq(beq), .JAL(jal), .Bne(bne), .in_3(IR[21]), .uret(uret), .sltiu(sltiu), .lhu(lhu), .bgeu(bgeu));  // open: CSRRSI, CSRRCI
  Multiplexer #(.width(5), .enable("false")) multiplexer_4 (
    .in0(IR[24:20]), .in1(5'b01010), .out(multiplexer_4_out), .sel(ecall));
  Multiplexer #(.width(32), .enable("false")) multiplexer_5 (
    .in0({Result[31:12], ADDR, high, Result[0]}), .in1(MDout), .out(multiplexer_5_out), .sel(MemToReg));
  Multiplexer #(.width(32), .enable("false")) multiplexer_6 (
    .in0(multiplexer_5_out), .in1(PC_4), .out(multiplexer_6_out), .sel(JAMP));
  assign bit_extender_3_out = {{31{1'b0}}, less};  // Bit_Extender bit_extender_3
  or or_4 (IR1_t, IR1, IRA);
  Multiplexer #(.width(5), .enable("false")) multiplexer_7 (
    .in0(IR[19:15]), .in1(5'b10001), .out(multiplexer_7_out), .sel(ecall));
  Shifter #(.width(12)) shifter_1 (.in({IR[31], IR[7], IR[30:25], IR[11:8]}), .\dist (4'b0001), .out(imm12_B));
  Shifter #(.width(20)) shifter_2 (.in({IR[31], IR[19:12], IR[20], IR[30:21]}), .\dist (5'b00001), .out(imm20_J));
  Multiplexer #(.width(32), .enable("false")) multiplexer_8 (
    .in0(multiplexer_6_out), .in1(bit_extender_3_out), .out(RDin), .sel(sltiu));
  Comparator #(.width(32)) comparator_1 (.a(R1), .b(32'h22), .eq(comparator_1_eq));  // open: gt, lt
  and and_2 (and_2_out, ecall, comparator_1_eq);
  or or_5 (IR2_t, IR2, IRB);
  Regifile regifile_1 (
    .Din(RDin), .Clk(CLK), .R1(R1), .R2(MDin), .WE(RegWrite), .W_num(IR[11:7]), .R1_num(multiplexer_7_out),
    .R2_num(multiplexer_4_out));
  not not_3 (not_3_out, comparator_1_eq);
  and and_3 (and_3_out, not_3_out, ecall);
  not not_4 (not_4_out, Go);
  Register #(.width(32), .Select("low")) register_1 (.D(MDin), .en(and_2_out), .Q(LedData), .clk(CLK), .clr(RST));
  or or_6 (IR3_t, IR3, IRC);
  Multiplexer #(.width(32), .enable("false")) multiplexer_9 (
    .in0(MDin), .in1(Bin), .out(multiplexer_9_out), .sel(AluSrcB));
  assign bit_extender_4_out = {{20{1'b0}}, IR[31:20]};  // Bit_Extender bit_extender_4
  and and_4 (halt, and_3_out, not_4_out);
  ALU alu_1 (
    .X(R1), .Y(multiplexer_9_out), .AluOP(AluOP), .Equal(equal),
    .Result({Result[31:12], ADDR, high, Result[0]}), .out_4(gae), .out_6(less));  // open: Result_2
  assign bit_extender_5_out = {{20{IR[31]}}, IR[31:20]};  // Bit_Extender bit_extender_5
  assign bit_extender_6_out = {{20{IR[31]}}, {IR[31:25], IR[11:7]}};  // Bit_Extender bit_extender_6
  not not_5 (not_5_out, equal);
  Multiplexer #(.width(32), .enable("false")) multiplexer_10 (
    .in0(bit_extender_5_out), .in1(bit_extender_4_out), .out(multiplexer_10_out), .sel(sltiu));
  and and_5 (and_5_out, beq, equal);
  and and_6 (and_6_out, not_5_out, bne);
  Multiplexer #(.width(32), .enable("false")) multiplexer_11 (
    .in0(multiplexer_10_out), .in1(bit_extender_6_out), .out(Bin), .sel(S_type));
  and and_7 (and_7_out, gae, bgeu);
  or or_7 (Branch, and_5_out, and_6_out, and_7_out);
  Counter #(.width(16), .max('hffff)) counter_2 (
    .count(Branch), .Q(\分支成功数 ), .clk(CLK), .clr(RST));  // open: load, D, carry, preset, down
  RAM #(.addrWidth(10), .dataWidth(32), .bus("separate"), .Select("high"), .simpleMode("false")) ram_1 (
    .addr(ADDR), .din(MDin), .data(ram_1_data), .str(MemWrite), .clk(CLK), .ld(MemToReg), .clr(RST));  // open: sel
  D_Flip_Flop #(.trigger("high"), .Pre_Clr_Positions("LEGACY"), .enable("true"), .NewFFLayout("false")) d_ff_1 (.Q(d_ff_1_q));  // open: clk, D, Qn, preset, en, reset
  // Probe on 13'hc
  Comparator #(.width(13)) comparator_2 (
    .a(CNT_num), .b(13'hc), .eq(comparator_2_eq), .lt(comparator_2_lt));  // open: gt
  Clock clock_1 (.out(clock_1_out));
  Multiplexer #(.width(16), .enable("false")) multiplexer_12 (
    .in0(ram_1_data[15:0]), .in1(ram_1_data[31:16]), .out(multiplexer_12_out), .sel(high));
  Counter #(.width(13), .max('h1fff), .ongoal("stay"), .behavior("old")) counter_3 (
    .count(comparator_2_lt), .Q(CNT_num), .clk(clock_1_out));  // open: load, D, carry, clr, preset
  assign bit_extender_7_out = {{16{1'b0}}, multiplexer_12_out};  // Bit_Extender bit_extender_7
  nand nand_1 (nand_1_out, d_ff_1_q, comparator_2_eq);
  Multiplexer #(.width(32), .enable("false")) multiplexer_13 (
    .in0(ram_1_data), .in1(bit_extender_7_out), .out(MDout), .sel(lhu));
  assign CLK = nand_1_out ? clock_1_out : 1'bz;  // Controlled_Buffer controlled_buffer_1
  Pull_Resistor #(.pull(1)) pull_resistor_1 (.node(CLK));
  Comparator #(.width(10), .mode("unsigned")) comparator_3 (
    .a(ADDR), .b(10'h20), .lt(comparator_3_lt));  // open: gt, eq
  and and_8 (and_8_out, MemWrite, comparator_3_lt);
  Comparator #(.width(32)) comparator_4 (.a(R1), .b(32'h22), .eq(comparator_4_eq));  // open: gt, lt
  and and_9 (and_9_out, comparator_4_eq, ecall);
  \地图  \u_地图_1  (
    .\写使能 (and_8_out), .Addr(ADDR), .CLK(CLK), .Data(MDin), .\行1 (\地图_1_行1 ), .\行9 (\地图_1_行9 ),
    .\行17 (\地图_1_行17 ), .\行25 (\地图_1_行25 ), .\行2 (\地图_1_行2 ), .\行10 (\地图_1_行10 ), .\行18 (\地图_1_行18 ),
    .\行26 (\地图_1_行26 ), .\行3 (\地图_1_行3 ), .\行11 (\地图_1_行11 ), .\行19 (\地图_1_行19 ), .\行27 (\地图_1_行27 ),
    .\行4 (\地图_1_行4 ), .\行12 (\地图_1_行12 ), .\行20 (\地图_1_行20 ), .\行28 (\地图_1_行28 ), .\行5 (\地图_1_行5 ),
    .\行13 (\地图_1_行13 ), .\行21 (\地图_1_行21 ), .\行29 (\地图_1_行29 ), .\行6 (\地图_1_行6 ), .\行14 (\地图_1_行14 ),
    .\行22 (\地图_1_行22 ), .\行30 (\地图_1_行30 ), .\行7 (\地图_1_行7 ), .\行15 (\地图_1_行15 ), .\行23 (\地图_1_行23 ),
    .\行31 (\地图_1_行31 ), .\行8 (\地图_1_行8 ), .\行16 (\地图_1_行16 ), .\行24 (\地图_1_行24 ), .\行32 (\地图_1_行32 ),
    .RST(RST));
  \点阵  \u_点阵_1  (
    .\写使能 (and_9_out), ._1(\地图_1_行1 ), ._2(\地图_1_行2 ), ._3(\地图_1_行3 ), ._4(\地图_1_行4 ), ._5(\地图_1_行5 ),
    ._6(\地图_1_行6 ), ._7(\地图_1_行7 ), ._8(\地图_1_行8 ), ._9(\地图_1_行9 ), ._10(\地图_1_行10 ), ._11(\地图_1_行11 ),
    ._12(\地图_1_行12 ), ._13(\地图_1_行13 ), ._14(\地图_1_行14 ), ._15(\地图_1_行15 ), ._16(\地图_1_行16 ),
    ._17(\地图_1_行17 ), ._18(\地图_1_行18 ), ._19(\地图_1_行19 ), ._20(\地图_1_行20 ), ._21(\地图_1_行21 ),
    ._22(\地图_1_行22 ), ._23(\地图_1_行23 ), ._24(\地图_1_行24 ), ._25(\地图_1_行25 ), ._26(\地图_1_行26 ),
    ._27(\地图_1_行27 ), ._28(\地图_1_行28 ), ._29(\地图_1_行29 ), ._30(\地图_1_行30 ), ._31(\地图_1_行31 ),
    ._32(\地图_1_行32 ), .CLK(CLK), ._1_2(\行1 ), ._2_2(\行2 ), ._3_2(\点阵_1__3_2 ), ._4_2(\点阵_1__4_2 ),
    ._5_2(\点阵_1__5_2 ), ._6_2(\点阵_1__6_2 ), ._7_2(\点阵_1__7_2 ), ._8_2(\点阵_1__8_2 ), ._9_2(\点阵_1__9_2 ),
    ._10_2(\点阵_1__10_2 ), ._11_2(\点阵_1__11_2 ), ._12_2(\点阵_1__12_2 ), ._13_2(\点阵_1__13_2 ),
    ._14_2(\点阵_1__14_2 ), ._15_2(\点阵_1__15_2 ), ._16_2(\点阵_1__16_2 ), ._17_2(\点阵_1__17_2 ),
    ._18_2(\点阵_1__18_2 ), ._19_2(\点阵_1__19_2 ), ._20_2(\点阵_1__20_2 ), ._21_2(\点阵_1__21_2 ),
    ._22_2(\点阵_1__22_2 ), ._23_2(\点阵_1__23_2 ), ._24_2(\点阵_1__24_2 ), ._25_2(\点阵_1__25_2 ),
    ._26_2(\点阵_1__26_2 ), ._27_2(\点阵_1__27_2 ), ._28_2(\点阵_1__28_2 ), ._29_2(\点阵_1__29_2 ),
    ._30_2(\点阵_1__30_2 ), ._31_2(\行31 ), ._32_2(\行32 ), .RST(RST));
  assign \行3  = \点阵_1__3_2  | 32'h60;  // OR_Gate or_8, 32 bits wide
  assign \行4  = \点阵_1__4_2  | 32'h1e0;  // OR_Gate or_9, 32 bits wide
  assign \行5  = \点阵_1__5_2  | 32'h7e0;  // OR_Gate or_10, 32 bits wide
  assign \行6  = \点阵_1__6_2  | 32'h1e0;  // OR_Gate or_11, 32 bits wide
  assign \行7  = \点阵_1__7_2  | 32'h3e0;  // OR_Gate or_12, 32 bits wide
  assign \行8  = \点阵_1__8_2  | 32'h1e0;  // OR_Gate or_13, 32 bits wide
  assign \行9  = \点阵_1__9_2  | 32'h7e0;  // OR_Gate or_14, 32 bits wide
  assign \行10  = \点阵_1__10_2  | 32'h1fe0;  // OR_Gate or_15, 32 bits wide
  assign \行11  = \点阵_1__11_2  | 32'h7e0;  // OR_Gate or_16, 32 bits wide
  assign \行12  = \点阵_1__12_2  | 32'hfe2;  // OR_Gate or_17, 32 bits wide
  assign \行13  = \点阵_1__13_2  | 32'h7e2;  // OR_Gate or_18, 32 bits wide
  assign \行14  = \点阵_1__14_2  | 32'h7e2;  // OR_Gate or_19, 32 bits wide
  assign \行15  = \点阵_1__15_2  | 32'h3ffe;  // OR_Gate or_20, 32 bits wide
  assign \行16  = \点阵_1__16_2  | 32'h1fffe;  // OR_Gate or_21, 32 bits wide
  assign \行17  = \点阵_1__17_2  | 32'h3ffe;  // OR_Gate or_22, 32 bits wide
  assign \行18  = \点阵_1__18_2  | 32'h7e2;  // OR_Gate or_23, 32 bits wide
  assign \行19  = \点阵_1__19_2  | 32'h7e2;  // OR_Gate or_24, 32 bits wide
  assign \行20  = \点阵_1__20_2  | 32'hfe2;  // OR_Gate or_25, 32 bits wide
  assign \行21  = \点阵_1__21_2  | 32'h7e0;  // OR_Gate or_26, 32 bits wide
  assign \行22  = \点阵_1__22_2  | 32'h7e0;  // OR_Gate or_27, 32 bits wide
  assign \行23  = \点阵_1__23_2  | 32'h1fe0;  // OR_Gate or_28, 32 bits wide
  assign \行24  = \点阵_1__24_2  | 32'h7e0;  // OR_Gate or_29, 32 bits wide
  assign \行25  = \点阵_1__25_2  | 32'h1e0;  // OR_Gate or_30, 32 bits wide
  assign \行26  = \点阵_1__26_2  | 32'h3e0;  // OR_Gate or_31, 32 bits wide
  assign \行27  = \点阵_1__27_2  | 32'h1e0;  // OR_Gate or_32, 32 bits wide
  assign \行28  = \点阵_1__28_2  | 32'h7e0;  // OR_Gate or_33, 32 bits wide
  assign \行29  = \点阵_1__29_2  | 32'h1e0;  // OR_Gate or_34, 32 bits wide
  assign \行30  = \点阵_1__30_2  | 32'h60;  // OR_Gate or_35, 32 bits wide

  // Other names for the same wires on the sheet: imm12_S[11:0] = {IR[31:25], IR[11:7]}; imm12_I[11:0] = IR[31:20];
  //   R2[31:0] = MDin; Result[11:1] = {ADDR, high}

  // Notes on the sheet:
  //   中断源
  //   中断等待指示
  //   数码管输出应该用寄存器锁存，否则显示数据只能一闪而过
  //   数码管输出
  //   指令存储器
  //   指令探针
  //   指令字
  //   contents of rom_1 (hex, n*v repeats v):
  //   413 493 913 993 400513 a00613 693 168693 20040413 100c13 bc1c13 18484b3 593 158593 141413 149493
  //   802c23 6802223 2902623 4902623 191913 199993 1202823 7202623 3302223 5302c23 2200893 73 fcb512e3
  //   40090913 100c13 cc1c13 18989b3 593 158593 191913 199993 1202823 7202623 3302223 5302c23 141413
  //   149493 802c23 6802223 2902623 4902623 2200893 73 fcb512e3 f4d61ae3 693 168693 30040413 300c13 ac1c13
  //   18484b3 593 158593 141413 149493 802c23 6802223 2902623 4902623 191913 199993 1202823 7202623
  //   3302223 5302c23 2200893 73 fcb512e3 60090913 300c13 bc1c13 18989b3 593 158593 191913 199993 1202823
  //   7202623 3302223 5302c23 141413 149493 802c23 6802223 2902623 4902623 2200893 73 fcb512e3 f4d61ae3
  //   300c13 10c1c13 18a0a33 3402c23 3402e23 5402023 30040413 300c13 ac1c13 18484b3 593 158593 141413
  //   149493 802c23 6802223 2902623 4902623 191913 199993 1202823 7202623 3302223 5302c23 1a1a13 3402c23
  //   3402e23 5402023 2200893 73 fab51ae3 300c13 10c1c13 18a0a33 60090913 300c13 bc1c13 18989b3 593 158593
  //   191913 199993 1202823 7202623 3302223 5302c23 141413 149493 802c23 6802223 2902623 4902623 1a1a13
  //   3402c23 3402e23 5402023 2200893 73 fab51ae3 f15ff06f
  //   JAL
  //   JALR
  //   URET
  //   Beq
  //   Bne
  //   MemToReg
  //   MemWrite
  //   AluOP
  //   AluSrcB
  //   RegWrite
  //   为方便自动评测，需要输出PC，IR，寄存器堆写如数据RDin
  //   RAM写使能MemWrite、RAM写入数据MDin等信号
  //   数据存储器
  //   控制位
  //   暂停节拍，不能为0
  //   戳工具置1进入计数暂停模式，ctrl+k时钟自动运行到对应节拍暂停
  //   ctrl+k关闭时钟连续运行，将控制位置零，进入单步调试模式调试
  //   用这个时钟源需要去掉电路中的其他时钟源
  //   可计数暂停的时钟源
endmodule

// 单周期硬布线控制器
module \单周期硬布线控制器  (
  input  [4:0] OP,
  input  [4:0] Funct,
  input  in_3,
  output [3:0] ALU_OP,
  output uret,
  output MemToReg,
  output ecall,
  output MemWrite,
  output ALU_SRC,
  output RegWrite,
  output S_type,
  output Beq,
  output Bne,
  output Jalr,
  output JAL,
  output sltiu,
  output lhu,
  output bgeu,
  output CSRRSI,
  output CSRRCI
);

  wire \控制信号自动生成_1_ecall ;

  \运算控制器自动生成  \u_运算控制器自动生成_1  (
    .OP2(OP[0]), .OP3(OP[1]), .OP4(OP[2]), .OP5(OP[3]), .OP6(OP[4]), .F12(Funct[0]), .F13(Funct[1]),
    .F14(Funct[2]), .F25(Funct[3]), .F30(Funct[4]), .S0(ALU_OP[0]), .S1(ALU_OP[1]), .S2(ALU_OP[2]),
    .S3(ALU_OP[3]));
  \控制信号自动生成  \u_控制信号自动生成_1  (
    .OP2(OP[0]), .OP3(OP[1]), .OP4(OP[2]), .OP5(OP[3]), .OP6(OP[4]), .MemToReg(MemToReg), .F12(Funct[0]),
    .F13(Funct[1]), .F14(Funct[2]), .F25(Funct[3]), .F30(Funct[4]), .MemWrite(MemWrite), .ALU_SRC(ALU_SRC),
    .RegWrite(RegWrite), .ecall(\控制信号自动生成_1_ecall ), .S_Type(S_type), .BEQ(Beq), .BNE(Bne), .JALR(Jalr),
    .JAL(JAL), .sltiu(sltiu), .lhu(lhu), .bgeu(bgeu), .CSRRSI(CSRRSI), .CSRRCI(CSRRCI));
  and and_1 (uret, in_3, \控制信号自动生成_1_ecall );
  and and_2 (ecall, ~in_3, \控制信号自动生成_1_ecall );  // AND_Gate

  // Other names for the same wires on the sheet: IR21 = in_3; OP_CODE[4:0] = OP

  // Notes on the sheet:
  //   运算器控制器，根据指令生成运算器功能选择信号
  //   控制信号生成，产生数据通路需要的其他控制信号
endmodule

// 运算器控制器
module \运算控制器自动生成  (
  input  OP2,
  input  OP3,
  input  OP4,
  input  OP5,
  input  OP6,
  input  F12,
  input  F13,
  input  F14,
  input  F25,
  input  F30,
  output S0,
  output S1,
  output S2,
  output S3
);

  wire and_1_out, and_2_out, and_3_out, and_4_out, and_5_out, and_6_out, and_7_out, and_8_out, and_9_out,
       and_10_out, and_11_out, and_12_out, and_13_out, and_14_out, and_15_out, and_16_out, and_17_out,
       and_18_out, and_19_out, and_20_out, and_21_out, and_22_out, and_23_out, and_24_out, and_25_out,
       and_26_out, and_27_out, and_28_out, and_29_out, and_30_out, and_31_out, and_32_out, not_1_out,
       not_2_out, not_3_out, not_4_out, not_5_out, not_6_out, not_7_out, not_8_out, not_9_out, not_10_out,
       not_11_out, not_12_out, not_13_out, not_14_out, not_15_out, not_16_out, not_17_out, not_18_out,
       not_19_out, not_20_out, not_21_out, not_22_out, not_23_out, not_24_out, not_25_out, not_26_out,
       not_27_out, not_28_out, not_29_out, not_30_out, not_31_out, not_32_out, not_33_out, not_34_out,
       not_35_out, not_36_out, not_37_out, not_38_out, not_39_out, not_40_out, not_41_out, not_42_out,
       not_43_out, not_44_out, not_45_out, not_46_out, not_47_out, not_48_out, not_49_out, not_50_out,
       not_51_out, not_52_out, not_53_out, not_54_out, not_55_out, not_56_out, not_57_out, not_58_out,
       not_59_out, not_60_out, not_61_out, not_62_out, not_63_out, not_64_out, not_65_out, not_66_out,
       not_67_out, not_68_out, not_69_out, not_70_out, not_71_out, not_72_out, not_73_out, not_74_out,
       not_75_out, not_76_out, not_77_out, not_78_out, not_79_out, not_80_out, not_81_out, not_82_out,
       not_83_out, not_84_out, not_85_out, not_86_out, not_87_out, not_88_out, not_89_out, not_90_out,
       not_91_out, not_92_out, not_93_out, not_94_out, not_95_out, not_96_out, not_97_out, not_98_out,
       not_99_out, not_100_out, not_101_out, not_102_out, not_103_out, not_104_out, not_105_out, not_106_out,
       not_107_out, not_108_out, not_109_out, not_110_out, not_111_out, not_112_out, not_113_out,
       not_114_out, not_115_out, not_116_out, not_117_out, not_118_out, not_119_out, not_120_out,
       not_121_out, not_122_out, not_123_out, not_124_out, not_125_out, not_126_out, not_127_out,
       not_128_out, not_129_out, not_130_out, not_131_out, not_132_out, not_133_out, not_134_out,
       not_135_out, not_136_out, not_137_out, not_138_out, not_139_out, not_140_out, not_141_out,
       not_142_out, not_143_out, not_144_out, not_145_out, not_146_out, not_147_out, not_148_out,
       not_149_out, not_150_out, not_151_out, not_152_out, not_153_out, not_154_out, not_155_out,
       not_156_out, not_157_out, not_158_out, not_159_out, not_160_out, not_161_out, not_162_out,
       not_163_out, not_164_out, not_165_out, not_166_out, not_167_out;

  not not_1 (not_1_out, OP2);
  not not_2 (not_2_out, OP3);
  not not_3 (not_3_out, OP4);
  not not_4 (not_4_out, OP6);
  not not_5 (not_5_out, F12);
  not not_6 (not_6_out, F14);
  not not_7 (not_7_out, OP2);
  not not_8 (not_8_out, OP3);
  not not_9 (not_9_out, OP4);
  not not_10 (not_10_out, OP5);
  not not_11 (not_11_out, OP6);
  not not_12 (not_12_out, F13);
  not not_13 (not_13_out, OP2);
  not not_14 (not_14_out, OP3);
  not not_15 (not_15_out, OP5);
  not not_16 (not_16_out, OP6);
  not not_17 (not_17_out, F12);
  not not_18 (not_18_out, F13);
  not not_19 (not_19_out, OP2);
  not not_20 (not_20_out, OP3);
  not not_21 (not_21_out, OP5);
  not not_22 (not_22_out, OP6);
  not not_23 (not_23_out, F12);
  not not_24 (not_24_out, F14);
  not not_25 (not_25_out, OP2);
  not not_26 (not_26_out, OP3);
  not not_27 (not_27_out, OP6);
  not not_28 (not_28_out, F12);
  not not_29 (not_29_out, F13);
  not not_30 (not_30_out, F25);
  not not_31 (not_31_out, F30);
  not not_32 (not_32_out, OP2);
  not not_33 (not_33_out, OP3);
  not not_34 (not_34_out, OP6);
  not not_35 (not_35_out, F12);
  not not_36 (not_36_out, F14);
  not not_37 (not_37_out, F25);
  not not_38 (not_38_out, F30);
  not not_39 (not_39_out, OP2);
  not not_40 (not_40_out, OP3);
  not not_41 (not_41_out, OP5);
  not not_42 (not_42_out, OP6);
  not not_43 (not_43_out, F13);
  not not_44 (not_44_out, F25);
  not not_45 (not_45_out, OP2);
  not not_46 (not_46_out, OP3);
  not not_47 (not_47_out, OP5);
  not not_48 (not_48_out, OP6);
  not not_49 (not_49_out, OP2);
  not not_50 (not_50_out, OP3);
  not not_51 (not_51_out, OP6);
  not not_52 (not_52_out, F25);
  not not_53 (not_53_out, F30);
  not not_54 (not_54_out, OP2);
  not not_55 (not_55_out, OP3);
  not not_56 (not_56_out, OP3);
  not not_57 (not_57_out, OP4);
  not not_58 (not_58_out, F12);
  not not_59 (not_59_out, F13);
  not not_60 (not_60_out, F14);
  not not_61 (not_61_out, OP2);
  not not_62 (not_62_out, OP3);
  not not_63 (not_63_out, OP5);
  not not_64 (not_64_out, OP6);
  not not_65 (not_65_out, F12);
  not not_66 (not_66_out, F14);
  not not_67 (not_67_out, OP2);
  not not_68 (not_68_out, OP3);
  not not_69 (not_69_out, OP6);
  not not_70 (not_70_out, F12);
  not not_71 (not_71_out, F14);
  not not_72 (not_72_out, F25);
  not not_73 (not_73_out, F30);
  not not_74 (not_74_out, OP2);
  not not_75 (not_75_out, OP3);
  not not_76 (not_76_out, OP5);
  not not_77 (not_77_out, OP6);
  not not_78 (not_78_out, F25);
  not not_79 (not_79_out, F30);
  not not_80 (not_80_out, OP2);
  not not_81 (not_81_out, OP3);
  not not_82 (not_82_out, OP5);
  not not_83 (not_83_out, OP6);
  not not_84 (not_84_out, OP2);
  not not_85 (not_85_out, OP3);
  not not_86 (not_86_out, OP6);
  not not_87 (not_87_out, F25);
  not not_88 (not_88_out, F30);
  not not_89 (not_89_out, OP2);
  not not_90 (not_90_out, OP3);
  not not_91 (not_91_out, OP6);
  not not_92 (not_92_out, F12);
  not not_93 (not_93_out, F13);
  not not_94 (not_94_out, F14);
  not not_95 (not_95_out, F25);
  not not_96 (not_96_out, OP2);
  not not_97 (not_97_out, OP3);
  not not_98 (not_98_out, OP2);
  not not_99 (not_99_out, OP3);
  not not_100 (not_100_out, OP4);
  not not_101 (not_101_out, OP6);
  not not_102 (not_102_out, F12);
  not not_103 (not_103_out, F14);
  not not_104 (not_104_out, OP2);
  not not_105 (not_105_out, OP3);
  not not_106 (not_106_out, OP4);
  not not_107 (not_107_out, OP5);
  not not_108 (not_108_out, OP6);
  not not_109 (not_109_out, F13);
  not not_110 (not_110_out, OP2);
  not not_111 (not_111_out, OP3);
  not not_112 (not_112_out, OP2);
  not not_113 (not_113_out, OP3);
  not not_114 (not_114_out, OP5);
  not not_115 (not_115_out, OP6);
  not not_116 (not_116_out, F12);
  not not_117 (not_117_out, F13);
  not not_118 (not_118_out, F14);
  not not_119 (not_119_out, OP2);
  not not_120 (not_120_out, OP3);
  not not_121 (not_121_out, OP6);
  not not_122 (not_122_out, F12);
  not not_123 (not_123_out, F13);
  not not_124 (not_124_out, F14);
  not not_125 (not_125_out, F25);
  not not_126 (not_126_out, OP2);
  not not_127 (not_127_out, OP3);
  not not_128 (not_128_out, OP5);
  not not_129 (not_129_out, OP6);
  not not_130 (not_130_out, OP2);
  not not_131 (not_131_out, OP3);
  not not_132 (not_132_out, OP6);
  not not_133 (not_133_out, F25);
  not not_134 (not_134_out, F30);
  not not_135 (not_135_out, OP3);
  not not_136 (not_136_out, OP4);
  not not_137 (not_137_out, F12);
  not not_138 (not_138_out, F13);
  not not_139 (not_139_out, F14);
  not not_140 (not_140_out, OP2);
  not not_141 (not_141_out, OP3);
  not not_142 (not_142_out, OP4);
  not not_143 (not_143_out, OP2);
  not not_144 (not_144_out, OP3);
  not not_145 (not_145_out, OP5);
  not not_146 (not_146_out, OP6);
  not not_147 (not_147_out, F12);
  not not_148 (not_148_out, OP2);
  not not_149 (not_149_out, OP3);
  not not_150 (not_150_out, OP6);
  not not_151 (not_151_out, F12);
  not not_152 (not_152_out, F25);
  not not_153 (not_153_out, F30);
  not not_154 (not_154_out, OP2);
  not not_155 (not_155_out, OP3);
  not not_156 (not_156_out, OP5);
  not not_157 (not_157_out, OP6);
  not not_158 (not_158_out, F14);
  not not_159 (not_159_out, OP2);
  not not_160 (not_160_out, OP3);
  not not_161 (not_161_out, OP6);
  not not_162 (not_162_out, F14);
  not not_163 (not_163_out, F25);
  not not_164 (not_164_out, F30);
  not not_165 (not_165_out, OP2);
  not not_166 (not_166_out, OP3);
  not not_167 (not_167_out, F12);
  and and_1 (and_1_out, not_1_out, not_2_out, not_3_out, not_4_out, not_5_out, F13, not_6_out);
  and and_2 (and_2_out, not_7_out, not_8_out, not_9_out, not_10_out, not_11_out, F12, not_12_out, F14);
  and and_3 (and_3_out, not_13_out, not_14_out, OP4, not_15_out, not_16_out, not_17_out, not_18_out);
  and and_4 (and_4_out, not_19_out, not_20_out, OP4, not_21_out, not_22_out, not_23_out, not_24_out);
  and and_5 (and_5_out, not_25_out, not_26_out, OP4, not_27_out, not_28_out, not_29_out, not_30_out, not_31_out);
  and and_6 (and_6_out, not_32_out, not_33_out, OP4, not_34_out, not_35_out, not_36_out, not_37_out, not_38_out);
  and and_7 (and_7_out, not_39_out, not_40_out, OP4, not_41_out, not_42_out, not_43_out, F14, not_44_out, F30);
  and and_8 (and_8_out, not_45_out, not_46_out, OP4, not_47_out, not_48_out, F12, F13, F14);
  and and_9 (and_9_out, not_49_out, not_50_out, OP4, not_51_out, F12, F13, F14, not_52_out, not_53_out);
  and and_10 (and_10_out, not_54_out, not_55_out, OP4, OP5, OP6, F12, F13, F14);
  and and_11 (and_11_out, OP2, not_56_out, not_57_out, OP5, OP6, not_58_out, not_59_out, not_60_out);
  and and_12 (and_12_out, not_61_out, not_62_out, OP4, not_63_out, not_64_out, not_65_out, F13, not_66_out);
  and and_13 (and_13_out, not_67_out, not_68_out, OP4, not_69_out, not_70_out, F13, not_71_out, not_72_out, not_73_out);
  and and_14 (and_14_out, not_74_out, not_75_out, OP4, not_76_out, not_77_out, F12, F14, not_78_out, not_79_out);
  and and_15 (and_15_out, not_80_out, not_81_out, OP4, not_82_out, not_83_out, F12, F13, F14);
  and and_16 (and_16_out, not_84_out, not_85_out, OP4, not_86_out, F12, F13, F14, not_87_out, not_88_out);
  and and_17 (and_17_out, not_89_out, not_90_out, OP4, OP5, not_91_out, not_92_out, not_93_out, not_94_out, not_95_out, F30);
  and and_18 (and_18_out, not_96_out, not_97_out, OP4, OP5, OP6, F12, F13, F14);
  and and_19 (and_19_out, not_98_out, not_99_out, not_100_out, not_101_out, not_102_out, F13, not_103_out);
  and and_20 (and_20_out, not_104_out, not_105_out, not_106_out, not_107_out, not_108_out, F12, not_109_out, F14);
  and and_21 (and_21_out, not_110_out, not_111_out, OP5, OP6, F12, F13, F14);
  and and_22 (and_22_out, not_112_out, not_113_out, OP4, not_114_out, not_115_out, not_116_out, not_117_out, not_118_out);
  and and_23 (and_23_out, not_119_out, not_120_out, OP4, not_121_out, not_122_out, not_123_out, not_124_out, not_125_out);
  and and_24 (and_24_out, not_126_out, not_127_out, OP4, not_128_out, not_129_out, F12, F13);
  and and_25 (and_25_out, not_130_out, not_131_out, OP4, not_132_out, F12, F13, not_133_out, not_134_out);
  and and_26 (and_26_out, OP2, not_135_out, not_136_out, OP5, OP6, not_137_out, not_138_out, not_139_out);
  and and_27 (and_27_out, not_140_out, not_141_out, not_142_out, OP5, OP6, F12, F13, F14);
  and and_28 (and_28_out, not_143_out, not_144_out, OP4, not_145_out, not_146_out, not_147_out, F14);
  and and_29 (and_29_out, not_148_out, not_149_out, OP4, not_150_out, not_151_out, F14, not_152_out, not_153_out);
  and and_30 (and_30_out, not_154_out, not_155_out, OP4, not_156_out, not_157_out, F13, not_158_out);
  and and_31 (and_31_out, not_159_out, not_160_out, OP4, not_161_out, F13, not_162_out, not_163_out, not_164_out);
  and and_32 (and_32_out, not_165_out, not_166_out, OP4, OP5, OP6, not_167_out, F13, F14);
  or or_1 (S3, and_27_out, and_28_out, and_29_out, and_30_out, and_31_out, and_32_out);
  or or_2 (S0, and_1_out, and_2_out, and_3_out, and_4_out, and_5_out, and_6_out, and_7_out, and_8_out, and_9_out, and_10_out, and_11_out);
  or or_3 (S1, and_12_out, and_13_out, and_14_out, and_15_out, and_16_out, and_17_out, and_18_out);
  or or_4 (S2, and_19_out, and_20_out, and_21_out, and_22_out, and_23_out, and_24_out, and_25_out, and_26_out);
endmodule

// 控制信号生成
module \控制信号自动生成  (
  input  OP2,
  input  OP3,
  input  OP4,
  input  OP5,
  input  OP6,
  input  F12,
  input  F13,
  input  F14,
  input  F25,
  input  F30,
  output MemToReg,
  output MemWrite,
  output ALU_SRC,
  output RegWrite,
  output ecall,
  output S_Type,
  output BEQ,
  output BNE,
  output JALR,
  output JAL,
  output sltiu,
  output lhu,
  output bgeu,
  output CSRRSI,
  output CSRRCI
);

  wire and_1_out, and_2_out, and_4_out, and_5_out, and_6_out, and_7_out, and_8_out, and_9_out, and_10_out,
       and_11_out, and_12_out, and_13_out, and_14_out, and_15_out, and_16_out, and_17_out, and_18_out,
       and_19_out, and_20_out, and_21_out, and_22_out, not_1_out, not_2_out, not_3_out, not_4_out, not_5_out,
       not_6_out, not_7_out, not_8_out, not_9_out, not_10_out, not_11_out, not_12_out, not_13_out,
       not_14_out, not_15_out, not_16_out, not_17_out, not_18_out, not_19_out, not_20_out, not_21_out,
       not_22_out, not_23_out, not_24_out, not_25_out, not_26_out, not_27_out, not_28_out, not_29_out,
       not_30_out, not_31_out, not_32_out, not_33_out, not_34_out, not_35_out, not_36_out, not_37_out,
       not_38_out, not_39_out, not_40_out, not_41_out, not_42_out, not_43_out, not_44_out, not_45_out,
       not_46_out, not_47_out, not_48_out, not_49_out, not_50_out, not_51_out, not_52_out, not_53_out,
       not_54_out, not_55_out, not_56_out, not_57_out, not_58_out, not_59_out, not_60_out, not_61_out,
       not_62_out, not_63_out, not_64_out, not_65_out, not_66_out, not_67_out, not_68_out, not_69_out,
       not_70_out, not_71_out, not_72_out, not_73_out, not_74_out, not_75_out, not_76_out, not_77_out,
       not_78_out, not_79_out, not_80_out, not_81_out, not_82_out, not_83_out, not_84_out, not_85_out,
       not_86_out, not_87_out, not_88_out, not_89_out, not_90_out, not_91_out, not_92_out, not_93_out,
       not_94_out, not_95_out, not_96_out, not_97_out, not_98_out, not_99_out, not_100_out, not_101_out,
       not_102_out, not_103_out, not_104_out, not_105_out, not_106_out, not_107_out, not_108_out,
       not_109_out, not_110_out, not_111_out, not_112_out, not_113_out, not_114_out, not_115_out,
       not_116_out, not_117_out, not_118_out, not_119_out, not_120_out, not_121_out, not_122_out,
       not_123_out, not_124_out, not_125_out, not_126_out, not_127_out, not_128_out, not_129_out,
       not_130_out, not_131_out, not_132_out, not_133_out, not_134_out, not_135_out, not_136_out,
       not_137_out, not_138_out, not_139_out, not_140_out, not_141_out, not_142_out, not_143_out,
       not_144_out, not_145_out, not_146_out, not_147_out, not_148_out, not_149_out, not_150_out,
       not_151_out, not_152_out, not_153_out, not_154_out, not_155_out, not_156_out, not_157_out,
       not_158_out, not_159_out, not_160_out;

  not not_1 (not_1_out, OP2);
  not not_2 (not_2_out, OP3);
  not not_3 (not_3_out, OP4);
  not not_4 (not_4_out, OP5);
  not not_5 (not_5_out, OP6);
  not not_6 (not_6_out, F12);
  not not_7 (not_7_out, F14);
  not not_8 (not_8_out, OP2);
  not not_9 (not_9_out, OP3);
  not not_10 (not_10_out, OP4);
  not not_11 (not_11_out, OP5);
  not not_12 (not_12_out, OP6);
  not not_13 (not_13_out, F13);
  not not_14 (not_14_out, OP2);
  not not_15 (not_15_out, OP3);
  not not_16 (not_16_out, OP4);
  not not_17 (not_17_out, OP6);
  not not_18 (not_18_out, F12);
  not not_19 (not_19_out, F14);
  not not_20 (not_20_out, OP2);
  not not_21 (not_21_out, OP3);
  not not_22 (not_22_out, OP4);
  not not_23 (not_23_out, OP6);
  not not_24 (not_24_out, F12);
  not not_25 (not_25_out, F14);
  not not_26 (not_26_out, OP2);
  not not_27 (not_27_out, OP3);
  not not_28 (not_28_out, OP4);
  not not_29 (not_29_out, OP5);
  not not_30 (not_30_out, OP6);
  not not_31 (not_31_out, F13);
  not not_32 (not_32_out, OP2);
  not not_33 (not_33_out, OP3);
  not not_34 (not_34_out, OP5);
  not not_35 (not_35_out, OP6);
  not not_36 (not_36_out, F12);
  not not_37 (not_37_out, OP2);
  not not_38 (not_38_out, OP3);
  not not_39 (not_39_out, OP5);
  not not_40 (not_40_out, OP6);
  not not_41 (not_41_out, F25);
  not not_42 (not_42_out, F30);
  not not_43 (not_43_out, OP2);
  not not_44 (not_44_out, OP3);
  not not_45 (not_45_out, OP5);
  not not_46 (not_46_out, OP6);
  not not_47 (not_47_out, F25);
  not not_48 (not_48_out, OP2);
  not not_49 (not_49_out, OP3);
  not not_50 (not_50_out, OP5);
  not not_51 (not_51_out, OP6);
  not not_52 (not_52_out, OP2);
  not not_53 (not_53_out, OP3);
  not not_54 (not_54_out, OP3);
  not not_55 (not_55_out, OP4);
  not not_56 (not_56_out, F12);
  not not_57 (not_57_out, F13);
  not not_58 (not_58_out, F14);
  not not_59 (not_59_out, OP2);
  not not_60 (not_60_out, OP3);
  not not_61 (not_61_out, OP5);
  not not_62 (not_62_out, OP6);
  not not_63 (not_63_out, F12);
  not not_64 (not_64_out, F14);
  not not_65 (not_65_out, OP2);
  not not_66 (not_66_out, OP3);
  not not_67 (not_67_out, OP4);
  not not_68 (not_68_out, OP5);
  not not_69 (not_69_out, OP6);
  not not_70 (not_70_out, F13);
  not not_71 (not_71_out, OP2);
  not not_72 (not_72_out, OP3);
  not not_73 (not_73_out, OP5);
  not not_74 (not_74_out, OP6);
  not not_75 (not_75_out, F12);
  not not_76 (not_76_out, OP2);
  not not_77 (not_77_out, OP3);
  not not_78 (not_78_out, OP5);
  not not_79 (not_79_out, OP6);
  not not_80 (not_80_out, F25);
  not not_81 (not_81_out, F30);
  not not_82 (not_82_out, OP2);
  not not_83 (not_83_out, OP3);
  not not_84 (not_84_out, OP6);
  not not_85 (not_85_out, F12);
  not not_86 (not_86_out, F13);
  not not_87 (not_87_out, F14);
  not not_88 (not_88_out, F25);
  not not_89 (not_89_out, OP2);
  not not_90 (not_90_out, OP3);
  not not_91 (not_91_out, OP6);
  not not_92 (not_92_out, F12);
  not not_93 (not_93_out, F25);
  not not_94 (not_94_out, F30);
  not not_95 (not_95_out, OP2);
  not not_96 (not_96_out, OP3);
  not not_97 (not_97_out, OP5);
  not not_98 (not_98_out, OP6);
  not not_99 (not_99_out, F25);
  not not_100 (not_100_out, OP2);
  not not_101 (not_101_out, OP3);
  not not_102 (not_102_out, OP5);
  not not_103 (not_103_out, OP6);
  not not_104 (not_104_out, OP2);
  not not_105 (not_105_out, OP3);
  not not_106 (not_106_out, OP6);
  not not_107 (not_107_out, F25);
  not not_108 (not_108_out, F30);
  not not_109 (not_109_out, OP4);
  not not_110 (not_110_out, F12);
  not not_111 (not_111_out, F13);
  not not_112 (not_112_out, F14);
  not not_113 (not_113_out, OP4);
  not not_114 (not_114_out, OP2);
  not not_115 (not_115_out, OP3);
  not not_116 (not_116_out, F12);
  not not_117 (not_117_out, F13);
  not not_118 (not_118_out, F14);
  not not_119 (not_119_out, OP2);
  not not_120 (not_120_out, OP3);
  not not_121 (not_121_out, OP4);
  not not_122 (not_122_out, OP6);
  not not_123 (not_123_out, F12);
  not not_124 (not_124_out, F14);
  not not_125 (not_125_out, OP2);
  not not_126 (not_126_out, OP3);
  not not_127 (not_127_out, OP4);
  not not_128 (not_128_out, F12);
  not not_129 (not_129_out, F13);
  not not_130 (not_130_out, F14);
  not not_131 (not_131_out, OP2);
  not not_132 (not_132_out, OP3);
  not not_133 (not_133_out, OP4);
  not not_134 (not_134_out, F13);
  not not_135 (not_135_out, F14);
  not not_136 (not_136_out, OP3);
  not not_137 (not_137_out, OP4);
  not not_138 (not_138_out, F12);
  not not_139 (not_139_out, F13);
  not not_140 (not_140_out, F14);
  not not_141 (not_141_out, OP4);
  not not_142 (not_142_out, OP2);
  not not_143 (not_143_out, OP3);
  not not_144 (not_144_out, OP5);
  not not_145 (not_145_out, OP6);
  not not_146 (not_146_out, F14);
  not not_147 (not_147_out, OP2);
  not not_148 (not_148_out, OP3);
  not not_149 (not_149_out, OP4);
  not not_150 (not_150_out, OP5);
  not not_151 (not_151_out, OP6);
  not not_152 (not_152_out, F13);
  not not_153 (not_153_out, OP2);
  not not_154 (not_154_out, OP3);
  not not_155 (not_155_out, OP4);
  not not_156 (not_156_out, OP2);
  not not_157 (not_157_out, OP3);
  not not_158 (not_158_out, F12);
  not not_159 (not_159_out, OP3);
  not not_160 (not_160_out, OP2);
  and and_1 (and_1_out, not_1_out, not_2_out, not_3_out, not_4_out, not_5_out, not_6_out, F13, not_7_out);
  and and_2 (and_2_out, not_8_out, not_9_out, not_10_out, not_11_out, not_12_out, F12, not_13_out, F14);
  and and_3 (MemWrite, not_14_out, not_15_out, not_16_out, OP5, not_17_out, not_18_out, F13, not_19_out);
  and and_4 (and_4_out, not_20_out, not_21_out, not_22_out, not_23_out, not_24_out, F13, not_25_out);
  and and_5 (and_5_out, not_26_out, not_27_out, not_28_out, not_29_out, not_30_out, F12, not_31_out, F14);
  and and_6 (and_6_out, not_32_out, not_33_out, OP4, not_34_out, not_35_out, not_36_out);
  and and_7 (and_7_out, not_37_out, not_38_out, OP4, not_39_out, not_40_out, not_41_out, not_42_out);
  and and_8 (and_8_out, not_43_out, not_44_out, OP4, not_45_out, not_46_out, F14, not_47_out);
  and and_9 (and_9_out, not_48_out, not_49_out, OP4, not_50_out, not_51_out, F13);
  and and_10 (and_10_out, not_52_out, not_53_out, OP4, OP5, OP6, F13, F14);
  and and_11 (and_11_out, OP2, not_54_out, not_55_out, OP5, OP6, not_56_out, not_57_out, not_58_out);
  and and_12 (and_12_out, not_59_out, not_60_out, not_61_out, not_62_out, not_63_out, F13, not_64_out);
  and and_13 (and_13_out, not_65_out, not_66_out, not_67_out, not_68_out, not_69_out, F12, not_70_out, F14);
  and and_14 (and_14_out, not_71_out, not_72_out, OP4, not_73_out, not_74_out, not_75_out);
  and and_15 (and_15_out, not_76_out, not_77_out, OP4, not_78_out, not_79_out, not_80_out, not_81_out);
  and and_16 (and_16_out, not_82_out, not_83_out, OP4, not_84_out, not_85_out, not_86_out, not_87_out, not_88_out);
  and and_17 (and_17_out, not_89_out, not_90_out, OP4, not_91_out, not_92_out, not_93_out, not_94_out);
  and and_18 (and_18_out, not_95_out, not_96_out, OP4, not_97_out, not_98_out, F14, not_99_out);
  and and_19 (and_19_out, not_100_out, not_101_out, OP4, not_102_out, not_103_out, F13);
  and and_20 (and_20_out, not_104_out, not_105_out, OP4, not_106_out, F13, not_107_out, not_108_out);
  and and_21 (and_21_out, OP2, not_109_out, OP5, OP6, not_110_out, not_111_out, not_112_out);
  and and_22 (and_22_out, OP2, OP3, not_113_out, OP5, OP6);
  and and_23 (ecall, not_114_out, not_115_out, OP4, OP5, OP6, not_116_out, not_117_out, not_118_out);
  and and_24 (S_Type, not_119_out, not_120_out, not_121_out, OP5, not_122_out, not_123_out, F13, not_124_out);
  and and_25 (BEQ, not_125_out, not_126_out, not_127_out, OP5, OP6, not_128_out, not_129_out, not_130_out);
  and and_26 (BNE, not_131_out, not_132_out, not_133_out, OP5, OP6, F12, not_134_out, not_135_out);
  and and_27 (JALR, OP2, not_136_out, not_137_out, OP5, OP6, not_138_out, not_139_out, not_140_out);
  and and_28 (JAL, OP2, OP3, not_141_out, OP5, OP6);
  and and_29 (sltiu, not_142_out, not_143_out, OP4, not_144_out, not_145_out, F12, F13, not_146_out);
  and and_30 (lhu, not_147_out, not_148_out, not_149_out, not_150_out, not_151_out, F12, not_152_out, F14);
  and and_31 (bgeu, not_153_out, not_154_out, not_155_out, OP5, OP6, F12, F13, F14);
  and and_32 (CSRRSI, not_156_out, not_157_out, OP4, OP5, OP6, not_158_out, F13, F14);
  and and_33 (CSRRCI, F14, F13, F12, OP6, OP5, OP4, not_159_out, not_160_out);
  or or_1 (MemToReg, and_1_out, and_2_out);
  or or_2 (ALU_SRC, and_4_out, and_5_out, and_6_out, and_7_out, and_8_out, and_9_out, and_10_out, and_11_out);
  or or_3 (RegWrite, and_12_out, and_13_out, and_14_out, and_15_out, and_16_out, and_17_out, and_18_out, and_19_out, and_20_out, and_21_out, and_22_out);
endmodule

module \理想流水线  (
  output RegWrite,
  output MemWrite,
  output [31:0] IF_PC,
  output [31:0] ID_PC,
  output [31:0] EX_PC,
  output [31:0] M_PC,
  output [31:0] WB_PC,
  output [31:0] RDin,
  output [31:0] MDin,
  output [31:0] LedData
);

  wire AluSrcB, and_2_out, and_3_out, and_4_out, and_5_out, and_6_out, and_7_out, beq, bgeu, bne, Branch,
       CLK, clock_1_out, comparator_1_eq, comparator_1_lt, comparator_2_eq, d_ff_1_q, ecall, en, equal,
       ex_mem_1_haltout, ex_mem_1_jampout, ex_mem_1_memtoregout, ex_mem_1_regwriteout, gae, Go, halt, high,
       id_ex_1_alusrcbout, id_ex_1_haltout, id_ex_1_memtoregout, id_ex_1_memwriteout, id_ex_1_regwriteout,
       id_ex_1_s_typeout, IR1, IR2, IR3, jal, jalr, JAMP, less, lhu, mem_wb_1_jampout, mem_wb_1_memtoregout,
       MemToReg, nand_1_out, not_1_out, not_2_out, not_3_out, not_4_out, not_5_out, not_6_out, or_2_out, RST,
       S_type, sltiu, uret, W1, W2, W3, \单周期硬布线控制器_1_alu_src , \单周期硬布线控制器_1_beq , \单周期硬布线控制器_1_bne ,
       \单周期硬布线控制器_1_jal , \单周期硬布线控制器_1_jalr , \单周期硬布线控制器_1_memtoreg , \单周期硬布线控制器_1_memwrite ,
       \单周期硬布线控制器_1_regwrite , \单周期硬布线控制器_1_s_type ;
  wire [3:0] id_ex_1_aluopout, \单周期硬布线控制器_1_alu_op ;
  wire [4:0] ex_mem_1_w_out, id_ex_1_w_out, multiplexer_4_out, multiplexer_5_out, W_num;
  wire [11:0] imm12_I, imm12_S, shifter_1_out;
  wire [12:0] CNT_num;
  wire [15:0] \LoadUse次数 , multiplexer_14_out, \分支成功数 , \总周期数 , \插入气泡数 , \无条件分支数 , \条件分支成功数 ;
  wire [19:0] shifter_2_out;
  wire [31:0] adder_1_out, adder_2_out, adder_4_out, and_1_out, Bin, bit_extender_1_out, bit_extender_2_out,
       bit_extender_3_out, bit_extender_4_out, bit_extender_5_out, bit_extender_6_out, bit_extender_7_out,
       bit_extender_8_out, bit_extender_9_out, EX_IR, ex_mem_1_resultout, id_ex_1_imm_i_out,
       id_ex_1_imm_s_out, id_ex_1_r1out, id_ex_1_r2out, ID_IR, IF_IR, imm_B, imm_J, MDout, MEM_IR,
       mem_wb_1_resultout, mem_wb_1_rmdataout, multiplexer_2_out, multiplexer_3_out, multiplexer_6_out,
       multiplexer_8_out, multiplexer_9_out, multiplexer_10_out, multiplexer_11_out, multiplexer_12_out,
       multiplexer_15_out, PC_4, PCin, R1, R2, ram_1_data, Result, undriven, WB_IR;

  Button \u_总复位  (.out(RST));
  Button _1 (.out(IR1));
  Button _2 (.out(IR2));
  Button _3 (.out(IR3));
  // Probe on \总周期数 
  // Probe on \总周期数 
  Button \u_继续运行  (.out(Go));
  LED led_1 (.in(W1));
  LED led_2 (.in(W2));
  LED led_3 (.in(W3));
  Hex_Digit_Display hex_digit_display_1 (.value(LedData[31:28]));  // open: dp
  // Probe on IF_PC[19:0]
  // RiscV_Probe riscv_probe_1: pin names not known; wires that end beside it: IF_IR
  Multiplexer #(.width(32), .enable("false")) multiplexer_1 (
    .in0(multiplexer_2_out), .in1(adder_1_out), .out(PCin), .sel(Branch));
  Hex_Digit_Display hex_digit_display_2 (.value(LedData[23:20]));  // open: dp
  Hex_Digit_Display hex_digit_display_3 (.value(LedData[27:24]));  // open: dp
  // Probe on ID_PC[19:0]
  // RiscV_Probe riscv_probe_2: pin names not known; wires that end beside it: ID_IR
  not not_1 (not_1_out, halt);
  Multiplexer #(.width(32), .enable("false")) multiplexer_2 (
    .in0(multiplexer_3_out), .in1(and_1_out), .out(multiplexer_2_out), .sel(jalr));
  Adder #(.width(32)) adder_1 (.a(imm_B), .b(EX_PC), .out(adder_1_out));  // open: cin, cout
  Hex_Digit_Display hex_digit_display_4 (.value(LedData[19:16]));  // open: dp
  Hex_Digit_Display hex_digit_display_5 (.value(LedData[15:12]));  // open: dp
  Counter #(.width(16), .max('hffff)) counter_1 (
    .count(not_1_out), .Q(\总周期数 ), .clk(CLK), .clr(RST));  // open: load, D, carry, preset, down
  not not_2 (not_2_out, halt);
  Multiplexer #(.width(32), .enable("false")) multiplexer_3 (
    .in0(PC_4), .in1(adder_2_out), .out(multiplexer_3_out), .sel(jal));
  assign and_1_out = Result & 32'hfffffffe;  // AND_Gate and_1, 32 bits wide
  Adder #(.width(32)) adder_2 (.a(imm_J), .b(EX_PC), .out(adder_2_out));  // open: cin, cout
  Hex_Digit_Display hex_digit_display_6 (.value(LedData[7:4]));  // open: dp
  Hex_Digit_Display hex_digit_display_7 (.value(LedData[11:8]));  // open: dp
  // Probe on EX_PC[19:0]
  // RiscV_Probe riscv_probe_3: pin names not known; wires that end beside it: EX_IR
  Register #(.width(32), .Select("low")) PC (.D(PCin), .en(not_2_out), .Q(IF_PC), .clk(CLK), .clr(RST));
  Hex_Digit_Display hex_digit_display_8 (.value(LedData[3:0]));  // open: dp
  Adder #(.width(32)) adder_3 (.a(IF_PC), .b(32'h4), .out(PC_4));  // open: cin, cout
  // Probe on \总周期数 
  // Probe on M_PC[19:0]
  // RiscV_Probe riscv_probe_4: pin names not known; wires that end beside it: MEM_IR
  // Probe on \总周期数 
  // Probe on \无条件分支数 
  // Probe on \条件分支成功数 
  // Probe on \插入气泡数 
  // Probe on \LoadUse次数 
  ROM #(.addrWidth(10), .dataWidth(32), .Select("high")) rom_1 (.addr(IF_PC[11:2]), .data(IF_IR));
  // Probe on IF_PC[11:0]
  // Probe on WB_PC[19:0]
  // RiscV_Probe riscv_probe_5: pin names not known; wires that end beside it: WB_IR
  IF_ID if_id_1 (
    .PCin(IF_PC), .IRin(IF_IR), .PCout(ID_PC), .IRout(ID_IR), .RST(RST), .EN_H(en), .CLK(CLK));  // open: Predictin, Predictout
  // Probe on ID_PC[11:0]
  // Probe on EX_PC[11:0]
  // Probe on M_PC[11:0]
  D_Flip_Flop #(.trigger("high"), .Pre_Clr_Positions("LEGACY"), .enable("true"), .NewFFLayout("false")) d_ff_1 (.Q(d_ff_1_q));  // open: clk, D, Qn, preset, en, reset
  // Probe on 13'hc
  // RiscV_Probe riscv_probe_6: pin names not known; wires that end beside it: ID_IR, ID_IR[19:15], ID_IR[11:7]
  // Probe on WB_PC[11:0]
  Comparator #(.width(13)) comparator_1 (
    .a(CNT_num), .b(13'hc), .eq(comparator_1_eq), .lt(comparator_1_lt));  // open: gt
  Clock clock_1 (.out(clock_1_out));
  nand nand_1 (nand_1_out, d_ff_1_q, comparator_1_eq);
  Counter #(.width(13), .max('h1fff), .ongoal("stay"), .behavior("old")) counter_2 (
    .count(comparator_1_lt), .Q(CNT_num), .clk(clock_1_out));  // open: load, D, carry, clr, preset
  assign CLK = nand_1_out ? clock_1_out : 1'bz;  // Controlled_Buffer controlled_buffer_1
  \单周期硬布线控制器  \u_单周期硬布线控制器_1  (
    .Funct({ID_IR[30], ID_IR[25], ID_IR[14:12]}), .OP(ID_IR[6:2]), .ALU_OP(\单周期硬布线控制器_1_alu_op ),
    .MemToReg(\单周期硬布线控制器_1_memtoreg ), .MemWrite(\单周期硬布线控制器_1_memwrite ), .ALU_SRC(\单周期硬布线控制器_1_alu_src ),
    .RegWrite(\单周期硬布线控制器_1_regwrite ), .ecall(ecall), .S_type(\单周期硬布线控制器_1_s_type ),
    .Jalr(\单周期硬布线控制器_1_jalr ), .Beq(\单周期硬布线控制器_1_beq ), .JAL(\单周期硬布线控制器_1_jal ), .Bne(\单周期硬布线控制器_1_bne ),
    .in_3(ID_IR[21]), .uret(uret), .sltiu(sltiu), .lhu(lhu), .bgeu(bgeu));  // open: CSRRSI, CSRRCI
  Multiplexer #(.width(5), .enable("false")) multiplexer_4 (
    .in0(ID_IR[19:15]), .in1(5'b10001), .out(multiplexer_4_out), .sel(ecall));
  Multiplexer #(.width(5), .enable("false")) multiplexer_5 (
    .in0(ID_IR[24:20]), .in1(5'b01010), .out(multiplexer_5_out), .sel(ecall));
  Shifter #(.width(12)) shifter_1 (
    .in({ID_IR[31], ID_IR[7], ID_IR[30:25], ID_IR[11:8]}), .\dist (4'b0001), .out(shifter_1_out));
  Shifter #(.width(20)) shifter_2 (
    .in({ID_IR[31], ID_IR[19:12], ID_IR[20], ID_IR[30:21]}), .\dist (5'b00001), .out(shifter_2_out));
  assign bit_extender_1_out = {{20{1'b0}}, imm12_I};  // Bit_Extender bit_extender_1
  Pull_Resistor #(.pull(1)) pull_resistor_1 (.node(CLK));
  assign bit_extender_2_out = {{20{ID_IR[31]}}, {ID_IR[31:25], ID_IR[11:7]}};  // Bit_Extender bit_extender_2
  assign bit_extender_3_out = {{20{shifter_1_out[11]}}, shifter_1_out};  // Bit_Extender bit_extender_3
  assign bit_extender_4_out = {{12{shifter_2_out[19]}}, shifter_2_out};  // Bit_Extender bit_extender_4
  assign bit_extender_5_out = {{20{imm12_I[11]}}, imm12_I};  // Bit_Extender bit_extender_5
  Regifile regifile_1 (
    .Din(RDin), .Clk(CLK), .R1(R1), .R2(R2), .WE(RegWrite), .W_num(W_num), .R1_num(multiplexer_4_out),
    .R2_num(multiplexer_5_out));
  assign bit_extender_6_out = {{20{ID_IR[31]}}, ID_IR[31:20]};  // Bit_Extender bit_extender_6
  Comparator #(.width(32)) comparator_2 (.a(R1), .b(32'h22), .eq(comparator_2_eq));  // open: gt, lt
  and and_2 (and_2_out, ecall, comparator_2_eq);
  Multiplexer #(.width(32), .enable("false")) multiplexer_6 (
    .in0(bit_extender_5_out), .in1(bit_extender_1_out), .out(multiplexer_6_out), .sel(sltiu));
  assign bit_extender_7_out = {{20{imm12_S[11]}}, imm12_S};  // Bit_Extender bit_extender_7
  not not_3 (not_3_out, comparator_2_eq);
  and and_3 (and_3_out, not_3_out, ecall);
  Multiplexer #(.width(32), .enable("false")) multiplexer_7 (
    .in0(multiplexer_6_out), .in1(bit_extender_7_out), .out(Bin), .sel(S_type));
  and and_4 (and_4_out, and_3_out, not_4_out);
  not not_4 (not_4_out, Go);
  Register #(.width(32), .Select("low")) register_1 (.D(R2), .en(and_2_out), .Q(LedData), .clk(CLK), .clr(RST));
  ID_EX id_ex_1 (
    .PCin(ID_PC), .Beqin(\单周期硬布线控制器_1_beq ), .Bnein(\单周期硬布线控制器_1_bne ), .IRin(ID_IR),
    .MemToRegin(\单周期硬布线控制器_1_memtoreg ), .Imm_I_in(bit_extender_6_out), .MemWritein(\单周期硬布线控制器_1_memwrite ),
    .AluSrcBin(\单周期硬布线控制器_1_alu_src ), .Imm_S_in(bit_extender_2_out), .RegWritein(\单周期硬布线控制器_1_regwrite ),
    .S_typein(\单周期硬布线控制器_1_s_type ), .Imm_B_in(bit_extender_3_out), .Jalin(\单周期硬布线控制器_1_jal ),
    .Jalrin(\单周期硬布线控制器_1_jalr ), .Imm_J_in(bit_extender_4_out), .AluOpin(\单周期硬布线控制器_1_alu_op ),
    .Haltin(and_4_out), .W_in(ID_IR[11:7]), .R1in(R1), .R2in(R2), .PCout(EX_PC), .Beqout(beq), .Bneout(bne),
    .IRout(EX_IR), .MemToRegout(id_ex_1_memtoregout), .Imm_I_out(id_ex_1_imm_i_out),
    .MemWriteout(id_ex_1_memwriteout), .AluSrcBout(id_ex_1_alusrcbout), .Imm_S_out(id_ex_1_imm_s_out),
    .RegWriteout(id_ex_1_regwriteout), .S_Typeout(id_ex_1_s_typeout), .Imm_B_out(imm_B), .Jalout(jal),
    .Jalrout(jalr), .Imm_J_out(imm_J), .AluOpout(id_ex_1_aluopout), .Haltout(id_ex_1_haltout),
    .W_out(id_ex_1_w_out), .R1out(id_ex_1_r1out), .R2out(id_ex_1_r2out), .RST(RST), .EN_H(en), .CLK(CLK));  // open: sltiuin, sltiuout, lhuin, lhuout, bgeuin, bgeuout, R1Forwardin, R1Forwardout, R2Forwardin, R2Forwardout, uretin, uretout, Predictin, Predictou9t, callin, callout
  not not_5 (not_5_out, equal);
  Multiplexer #(.width(32), .enable("false")) multiplexer_8 (
    .in0(id_ex_1_imm_i_out), .in1(id_ex_1_imm_s_out), .out(multiplexer_8_out), .sel(id_ex_1_s_typeout));
  Multiplexer #(.width(32), .enable("false")) multiplexer_9 (
    .in1(Bin), .out(multiplexer_9_out), .sel(AluSrcB));  // open: in0
  Multiplexer #(.width(32), .enable("false")) multiplexer_10 (
    .in0(Result), .in1(MDout), .out(multiplexer_10_out), .sel(MemToReg));
  Multiplexer #(.width(32), .enable("false")) multiplexer_11 (
    .in0(multiplexer_10_out), .in1(PC_4), .out(multiplexer_11_out), .sel(JAMP));
  assign bit_extender_8_out = {{31{1'b0}}, less};  // Bit_Extender bit_extender_8
  and and_5 (and_5_out, beq, equal);
  and and_6 (and_6_out, not_5_out, bne);
  and and_7 (and_7_out, gae, bgeu);
  Multiplexer #(.width(32), .enable("false")) multiplexer_12 (
    .in0(id_ex_1_r2out), .in1(multiplexer_8_out), .out(multiplexer_12_out), .sel(id_ex_1_alusrcbout));
  Multiplexer #(.width(32), .enable("false")) multiplexer_13 (
    .in0(multiplexer_11_out), .in1(bit_extender_8_out), .out(RDin), .sel(sltiu));
  ALU alu_1 (
    .X(id_ex_1_r1out), .Y(multiplexer_12_out), .AluOP(id_ex_1_aluopout), .Equal(equal), .Result(Result),
    .out_4(gae), .out_6(less));  // open: Result_2
  or or_1 (Branch, and_5_out, and_6_out, and_7_out);
  Counter #(.width(16), .max('hffff)) counter_3 (
    .count(Branch), .Q(\分支成功数 ), .clk(CLK), .clr(RST));  // open: load, D, carry, preset, down
  or or_2 (or_2_out, jal, jalr);
  EX_MEM ex_mem_1 (
    .MemToRegin(id_ex_1_memtoregout), .PCin(EX_PC), .MemWritein(id_ex_1_memwriteout), .IRin(EX_IR),
    .JAMPin(or_2_out), .RegWritein(id_ex_1_regwriteout), .Resultin(Result), .Haltin(id_ex_1_haltout),
    .MDatain(id_ex_1_r2out), .W_in(id_ex_1_w_out), .MemToRegout(ex_mem_1_memtoregout), .PCout(M_PC),
    .MemWriteout(MemWrite), .IRout(MEM_IR), .JAMPout(ex_mem_1_jampout), .RegWriteout(ex_mem_1_regwriteout),
    .Resultout({ex_mem_1_resultout[31:2], high, ex_mem_1_resultout[0]}), .Haltout(ex_mem_1_haltout),
    .Mdataout(MDin), .W_out(ex_mem_1_w_out), .RST(RST), .EN_H(en), .CLK(CLK));  // open: lessin, lessout, sltiuin, sltiuout, lhuin, lhuout
  RAM #(.addrWidth(10), .dataWidth(32), .bus("separate"), .Select("high"), .simpleMode("false")) ram_1 (
    .addr(ex_mem_1_resultout[11:2]), .din(MDin), .data(ram_1_data), .str(MemWrite), .clk(CLK),
    .ld(ex_mem_1_memtoregout), .clr(RST));  // open: sel
  MEM_WB mem_wb_1 (
    .PCin(M_PC), .MemToRegin(ex_mem_1_memtoregout), .IRin(MEM_IR), .JAMPin(ex_mem_1_jampout),
    .RegWritein(ex_mem_1_regwriteout), .Resultin({ex_mem_1_resultout[31:2], high, ex_mem_1_resultout[0]}),
    .Haltin(ex_mem_1_haltout), .RMDatain(ram_1_data), .W_in(ex_mem_1_w_out), .PCout(WB_PC),
    .MemToRegout(mem_wb_1_memtoregout), .IRout(WB_IR), .JAMPout(mem_wb_1_jampout), .RegWriteout(RegWrite),
    .Resultout(mem_wb_1_resultout), .Haltout(halt), .RMdataout(mem_wb_1_rmdataout), .W_out(W_num), .RST(RST),
    .EN_H(en), .CLK(CLK));  // open: lessin, lessout, sltiuin, sltiuout, lhuin, lhuout, highin, highout
  Multiplexer #(.width(16), .enable("false")) multiplexer_14 (
    .in0(undriven[15:0]), .in1(undriven[31:16]), .out(multiplexer_14_out), .sel(high));
  Adder #(.width(32)) adder_4 (.a(32'h4), .b(WB_PC), .out(adder_4_out));  // open: cin, cout
  Multiplexer #(.width(32), .enable("false")) multiplexer_15 (
    .in0(mem_wb_1_resultout), .in1(mem_wb_1_rmdataout), .out(multiplexer_15_out), .sel(mem_wb_1_memtoregout));
  not not_6 (not_6_out, halt);
  or or_3 (en, not_6_out, Go);
  assign bit_extender_9_out = {{16{1'b0}}, multiplexer_14_out};  // Bit_Extender bit_extender_9
  Multiplexer #(.width(32), .enable("false")) multiplexer_16 (
    .in0(multiplexer_15_out), .in1(adder_4_out), .out(RDin), .sel(mem_wb_1_jampout));
  Multiplexer #(.width(32), .enable("false")) multiplexer_17 (
    .in0(undriven), .in1(bit_extender_9_out), .out(MDout), .sel(lhu));

  // Other names for the same wires on the sheet: IR[31:0] = ID_IR; RD_num[4:0] = ID_IR[11:7]; MEM_PC[31:0] = M_PC;
  //   MEMWB[31:0] = RDin

  // Notes on the sheet:
  //   中断源
  //   时空图监测，可删除
  //   中断等待指示
  //   数码管输出
  //   指令存储器
  //   contents of rom_1 (hex, n*v repeats v):
  //   100493 100006f 100493 200913 300993 100006f 100493 200913 300993 100006f 100493 200913 300993
  //   100006f 100493 200913 300993 29c000ef 100413 100493 1f49493 900533 2200893 73 24d493 48463 fedff06f
  //   900533 2200893 73 100493 249493 900533 2200893 73 48463 fedff06f 100493 1f49493 900533 2200893 73
  //   4034d493 900533 2200893 73 4044d493 900533 2200893 73 4044d493 900533 2200893 73 4044d493 900533
  //   2200893 73 4044d493 900533 2200893 73 4044d493 900533 2200893 73 4044d493 900533 2200893 73 4044d493
  //   900533 2200893 73 100413 1f41993 41f9d993 433 c00913 300b13 140413 f47413 800293 100313 499993
  //   89e9b3 1300533 2200893 73 406282b3 fe0294e3 140413 f00f93 1f47433 1c41413 800293 100313 49d993
  //   89e9b3 1300533 2200893 73 406282b3 fe0294e3 1c45413 406b0b33 b0463 f95ff06f 2b3 fff2c293 829293
  //   ff2e293 500533 2200893 73 fff00413 493 84a023 140413 448493 84a023 140413 448493 84a023 140413
  //   448493 84a023 140413 448493 84a023 140413 448493 84a023 140413 448493 84a023 140413 448493 84a023
  //   140413 448493 84a023 140413 448493 84a023 140413 448493 84a023 140413 448493 84a023 140413 448493
  //   84a023 140413 448493 84a023 140413 448493 84a023 140413 448493 84a023 140413 448493 140413 433
  //   3c00493 42983 4aa03 149a2b3 28663 134a023 1442023 ffc48493 fe9412e3 800533 2200893 73 440413 3c00493
  //   fc9416e3 a00893 73 413 140413 800533 2200893 73 240413 800533 2200893 73 340413 800533 2200893 73
  //   440413 800533 2200893 73 540413 800533 2200893 73 640413 800533 2200893 73 740413 800533 2200893 73
  //   840413 800533 2200893 2200893 73 8067
  //   控制位
  //   流水调试日志用
  //   暂停节拍，不能为0
  //   指令探针
  //   戳工具置1进入计数暂停模式，ctrl+k时钟自动运行到对应节拍暂停
  //   ctrl+k关闭时钟连续运行，将控制位置零，进入单步调试模式调试
  //   用这个时钟源需要去掉电路中的其他时钟源
  //   指令字
  //   JAL
  //   JALR
  //   URET
  //   可计数暂停的时钟源
  //   Beq
  //   Bne
  //   MemToReg
  //   MemWrite
  //   AluOP
  //   AluSrcB
  //   RegWrite
  //   为方便自动评测，需要输出流水线各段保存的PC值，注意是PC不是PC+4，另外ID段寄存器写入信息，Mem段内存写入信息也要输出
  //   数据存储器
endmodule

// ALU
module ALU (
  input  [31:0] X,
  input  [31:0] Y,
  input  [3:0] AluOP,
  output out_4,
  output Equal,
  output out_6,
  output [31:0] Result,
  output [31:0] Result_2
);

  wire [0:0] comparator_1_lt, comparator_2_lt;
  wire [31:0] adder_1_out, AND_out, divider_1_out, divider_1_rem, multiplier_1_cout, multiplier_1_out,
       NOR_out, OR_out, shifter_1_out, shifter_2_out, shifter_3_out, subtractor_1_out, XOR_out;

  assign AND_out = X & Y;  // AND_Gate AND, 32 bits wide
  assign OR_out = X | Y;  // OR_Gate OR, 32 bits wide
  Shifter #(.width(32)) shifter_1 (.in(X), .\dist (Y[4:0]), .out(shifter_1_out));
  Shifter #(.width(32), .shift("ar")) shifter_2 (.in(X), .\dist (Y[4:0]), .out(shifter_2_out));
  Shifter #(.width(32), .shift("lr")) shifter_3 (.in(X), .\dist (Y[4:0]), .out(shifter_3_out));
  Multiplier #(.width(32)) multiplier_1 (.a(X), .b(Y), .out(multiplier_1_out), .cout(multiplier_1_cout));  // open: cin
  Divider #(.width(32)) divider_1 (.a(X), .b(Y), .out(divider_1_out), .rem(divider_1_rem));  // open: upper
  Adder #(.width(32)) adder_1 (.a(X), .b(Y), .out(adder_1_out));  // open: cin, cout
  Subtractor #(.width(32)) subtractor_1 (.a(X), .b(Y), .out(subtractor_1_out));  // open: bin, bout
  assign XOR_out = X ^ Y;  // XOR_Gate XOR, 32 bits wide
  assign NOR_out = ~(X | Y);  // NOR_Gate NOR, 32 bits wide
  Comparator #(.width(32)) comparator_1 (.a(X), .b(Y), .eq(Equal), .lt(comparator_1_lt[0]));  // open: gt
  Comparator #(.width(32), .mode("unsigned")) comparator_2 (.a(X), .b(Y), .lt(comparator_2_lt[0]));  // open: gt, eq
  Multiplexer #(.select(4), .width(32), .enable("false")) multiplexer_1 (
    .in0(shifter_1_out), .in1(shifter_2_out), .in2(shifter_3_out), .in3(multiplier_1_out),
    .in4(divider_1_out), .in5(adder_1_out), .in6(subtractor_1_out), .in7(AND_out), .in8(OR_out),
    .in9(XOR_out), .in10(NOR_out), .in11({{31{1'b0}}, comparator_1_lt[0]}),
    .in12({{31{1'b0}}, comparator_2_lt[0]}), .in13({32{1'b0}}), .in14({32{1'b0}}), .in15({32{1'b0}}),
    .out(Result), .sel(AluOP));
  Multiplexer #(.select(4), .width(32), .enable("false")) multiplexer_2 (
    .in0({32{1'b0}}), .in1({32{1'b0}}), .in2({32{1'b0}}), .in3(multiplier_1_cout), .in4(divider_1_rem),
    .in5({32{1'b0}}), .in6({32{1'b0}}), .in7({32{1'b0}}), .in8({32{1'b0}}), .in9({32{1'b0}}),
    .in10({32{1'b0}}), .in11({32{1'b0}}), .in12({32{1'b0}}), .in13({32{1'b0}}), .in14({32{1'b0}}),
    .in15({32{1'b0}}), .out(Result_2), .sel(AluOP));
  Multiplexer #(.select(4), .enable("false")) multiplexer_3 (
    .in0(1'b0), .in1(1'b0), .in2(1'b0), .in3(1'b0), .in4(1'b0), .in5(1'b0), .in6(1'b0), .in7(1'b0),
    .in8(1'b0), .in9(1'b0), .in10(1'b0), .in11(comparator_1_lt[0]), .in12(comparator_2_lt[0]), .in13(1'b0),
    .in14(1'b0), .in15(1'b0), .out(out_6), .sel(AluOP));
  not not_1 (out_4, out_6);

  // Other names for the same wires on the sheet: Result2[31:0] = Result_2; S[3:0] = AluOP; tunnel = out_6;
  //   tunnel_t = out_4

  // Notes on the sheet:
  //   不要改变此引脚区域内容，也不要改变ALU封装形式
  //   输入引脚
  //   输出引脚
endmodule

module Regifile (
  input  [31:0] Din,
  input  Clk,
  input  WE,
  input  [4:0] R1_num,
  input  [4:0] W_num,
  input  [4:0] R2_num,
  output [31:0] R1,
  output [31:0] R2
);

  // RegisterFile registerfile_1: pin names not known; wires that end beside it: Din, Clk, WE, W_num, R1_num, R2_num, R1, R2
endmodule

module \寄存器有关判断  (
  input  OP2,
  input  OP3,
  input  OP4,
  input  OP5,
  input  OP6,
  input  F12,
  input  F13,
  input  F14,
  input  F25,
  input  F30,
  output R1,
  output R2
);

  wire and_1_out, and_2_out, and_3_out, and_4_out, and_5_out, and_6_out, and_7_out, and_8_out, and_9_out,
       and_10_out, and_11_out, and_12_out, and_13_out, and_14_out, and_15_out, and_16_out, and_17_out,
       and_18_out, and_19_out, and_20_out, and_21_out, and_22_out, and_23_out, and_24_out, and_25_out,
       and_26_out, and_27_out, and_28_out, and_29_out, and_30_out, and_31_out, and_32_out, and_33_out,
       and_34_out, and_35_out, and_36_out, not_1_out, not_2_out, not_3_out, not_4_out, not_5_out, not_6_out,
       not_7_out, not_8_out, not_9_out, not_10_out, not_11_out, not_12_out, not_13_out, not_14_out,
       not_15_out, not_16_out, not_17_out, not_18_out, not_19_out, not_20_out, not_21_out, not_22_out,
       not_23_out, not_24_out, not_25_out, not_26_out, not_27_out, not_28_out, not_29_out, not_30_out,
       not_31_out, not_32_out, not_33_out, not_34_out, not_35_out, not_36_out, not_37_out, not_38_out,
       not_39_out, not_40_out, not_41_out, not_42_out, not_43_out, not_44_out, not_45_out, not_46_out,
       not_47_out, not_48_out, not_49_out, not_50_out, not_51_out, not_52_out, not_53_out, not_54_out,
       not_55_out, not_56_out, not_57_out, not_58_out, not_59_out, not_60_out, not_61_out, not_62_out,
       not_63_out, not_64_out, not_65_out, not_66_out, not_67_out, not_68_out, not_69_out, not_70_out,
       not_71_out, not_72_out, not_73_out, not_74_out, not_75_out, not_76_out, not_77_out, not_78_out,
       not_79_out, not_80_out, not_81_out, not_82_out, not_83_out, not_84_out, not_85_out, not_86_out,
       not_87_out, not_88_out, not_89_out, not_90_out, not_91_out, not_92_out, not_93_out, not_94_out,
       not_95_out, not_96_out, not_97_out, not_98_out, not_99_out, not_100_out, not_101_out, not_102_out,
       not_103_out, not_104_out, not_105_out, not_106_out, not_107_out, not_108_out, not_109_out,
       not_110_out, not_111_out, not_112_out, not_113_out, not_114_out, not_115_out, not_116_out,
       not_117_out, not_118_out, not_119_out, not_120_out, not_121_out, not_122_out, not_123_out,
       not_124_out, not_125_out, not_126_out, not_127_out, not_128_out, not_129_out, not_130_out,
       not_131_out, not_132_out, not_133_out, not_134_out, not_135_out, not_136_out, not_137_out,
       not_138_out, not_139_out, not_140_out, not_141_out, not_142_out, not_143_out, not_144_out,
       not_145_out, not_146_out, not_147_out, not_148_out, not_149_out, not_150_out, not_151_out,
       not_152_out, not_153_out, not_154_out, not_155_out, not_156_out, not_157_out, not_158_out,
       not_159_out, not_160_out, not_161_out, not_162_out, not_163_out, not_164_out, not_165_out,
       not_166_out, not_167_out, not_168_out, not_169_out, not_170_out, not_171_out, not_172_out,
       not_173_out, not_174_out, not_175_out, not_176_out, not_177_out, not_178_out, not_179_out,
       not_180_out, not_181_out, not_182_out, not_183_out, not_184_out, not_185_out, not_186_out,
       not_187_out, not_188_out, not_189_out, not_190_out, not_191_out, not_192_out, not_193_out,
       not_194_out, not_195_out, not_196_out, not_197_out, not_198_out, not_199_out, not_200_out,
       not_201_out, not_202_out, not_203_out, not_204_out, not_205_out, not_206_out, not_207_out,
       not_208_out, not_209_out, not_210_out, not_211_out, not_212_out, not_213_out, not_214_out,
       not_215_out, not_216_out, not_217_out, not_218_out;

  not not_1 (not_1_out, F30);
  not not_2 (not_2_out, F25);
  not not_3 (not_3_out, F14);
  not not_4 (not_4_out, F13);
  not not_5 (not_5_out, F12);
  not not_6 (not_6_out, OP6);
  not not_7 (not_7_out, OP3);
  not not_8 (not_8_out, OP2);
  not not_9 (not_9_out, F25);
  not not_10 (not_10_out, F14);
  not not_11 (not_11_out, F13);
  not not_12 (not_12_out, F12);
  not not_13 (not_13_out, OP6);
  not not_14 (not_14_out, OP3);
  not not_15 (not_15_out, OP2);
  not not_16 (not_16_out, F30);
  not not_17 (not_17_out, F25);
  not not_18 (not_18_out, OP6);
  not not_19 (not_19_out, OP3);
  not not_20 (not_20_out, OP2);
  not not_21 (not_21_out, F30);
  not not_22 (not_22_out, F25);
  not not_23 (not_23_out, F12);
  not not_24 (not_24_out, OP6);
  not not_25 (not_25_out, OP3);
  not not_26 (not_26_out, OP2);
  not not_27 (not_27_out, F30);
  not not_28 (not_28_out, F25);
  not not_29 (not_29_out, F14);
  not not_30 (not_30_out, F12);
  not not_31 (not_31_out, OP6);
  not not_32 (not_32_out, OP3);
  not not_33 (not_33_out, OP2);
  not not_34 (not_34_out, F30);
  not not_35 (not_35_out, F25);
  not not_36 (not_36_out, F14);
  not not_37 (not_37_out, OP6);
  not not_38 (not_38_out, OP3);
  not not_39 (not_39_out, OP2);
  not not_40 (not_40_out, F14);
  not not_41 (not_41_out, F13);
  not not_42 (not_42_out, F12);
  not not_43 (not_43_out, OP6);
  not not_44 (not_44_out, OP5);
  not not_45 (not_45_out, OP3);
  not not_46 (not_46_out, OP2);
  not not_47 (not_47_out, OP6);
  not not_48 (not_48_out, OP5);
  not not_49 (not_49_out, OP3);
  not not_50 (not_50_out, OP2);
  not not_51 (not_51_out, F12);
  not not_52 (not_52_out, OP6);
  not not_53 (not_53_out, OP5);
  not not_54 (not_54_out, OP3);
  not not_55 (not_55_out, OP2);
  not not_56 (not_56_out, F13);
  not not_57 (not_57_out, F12);
  not not_58 (not_58_out, OP6);
  not not_59 (not_59_out, OP5);
  not not_60 (not_60_out, OP3);
  not not_61 (not_61_out, OP2);
  not not_62 (not_62_out, F14);
  not not_63 (not_63_out, F12);
  not not_64 (not_64_out, OP6);
  not not_65 (not_65_out, OP5);
  not not_66 (not_66_out, OP3);
  not not_67 (not_67_out, OP2);
  not not_68 (not_68_out, F30);
  not not_69 (not_69_out, F25);
  not not_70 (not_70_out, F14);
  not not_71 (not_71_out, F13);
  not not_72 (not_72_out, OP6);
  not not_73 (not_73_out, OP5);
  not not_74 (not_74_out, OP3);
  not not_75 (not_75_out, OP2);
  not not_76 (not_76_out, F30);
  not not_77 (not_77_out, F25);
  not not_78 (not_78_out, F13);
  not not_79 (not_79_out, OP6);
  not not_80 (not_80_out, OP5);
  not not_81 (not_81_out, OP3);
  not not_82 (not_82_out, OP2);
  not not_83 (not_83_out, F25);
  not not_84 (not_84_out, F13);
  not not_85 (not_85_out, OP6);
  not not_86 (not_86_out, OP5);
  not not_87 (not_87_out, OP3);
  not not_88 (not_88_out, OP2);
  not not_89 (not_89_out, F14);
  not not_90 (not_90_out, F12);
  not not_91 (not_91_out, OP6);
  not not_92 (not_92_out, OP5);
  not not_93 (not_93_out, OP4);
  not not_94 (not_94_out, OP3);
  not not_95 (not_95_out, OP2);
  not not_96 (not_96_out, F14);
  not not_97 (not_97_out, F12);
  not not_98 (not_98_out, OP6);
  not not_99 (not_99_out, OP4);
  not not_100 (not_100_out, OP3);
  not not_101 (not_101_out, OP2);
  not not_102 (not_102_out, F30);
  not not_103 (not_103_out, F25);
  not not_104 (not_104_out, F14);
  not not_105 (not_105_out, F13);
  not not_106 (not_106_out, F12);
  not not_107 (not_107_out, OP3);
  not not_108 (not_108_out, OP2);
  not not_109 (not_109_out, F14);
  not not_110 (not_110_out, F13);
  not not_111 (not_111_out, F12);
  not not_112 (not_112_out, OP4);
  not not_113 (not_113_out, OP3);
  not not_114 (not_114_out, OP2);
  not not_115 (not_115_out, F14);
  not not_116 (not_116_out, F13);
  not not_117 (not_117_out, OP4);
  not not_118 (not_118_out, OP3);
  not not_119 (not_119_out, OP2);
  not not_120 (not_120_out, F14);
  not not_121 (not_121_out, F13);
  not not_122 (not_122_out, F12);
  not not_123 (not_123_out, OP4);
  not not_124 (not_124_out, OP3);
  not not_125 (not_125_out, F30);
  not not_126 (not_126_out, F25);
  not not_127 (not_127_out, F13);
  not not_128 (not_128_out, F12);
  not not_129 (not_129_out, OP6);
  not not_130 (not_130_out, OP3);
  not not_131 (not_131_out, OP2);
  not not_132 (not_132_out, F14);
  not not_133 (not_133_out, OP6);
  not not_134 (not_134_out, OP5);
  not not_135 (not_135_out, OP3);
  not not_136 (not_136_out, OP2);
  not not_137 (not_137_out, F13);
  not not_138 (not_138_out, OP6);
  not not_139 (not_139_out, OP5);
  not not_140 (not_140_out, OP4);
  not not_141 (not_141_out, OP3);
  not not_142 (not_142_out, OP2);
  not not_143 (not_143_out, OP4);
  not not_144 (not_144_out, OP3);
  not not_145 (not_145_out, OP2);
  not not_146 (not_146_out, F30);
  not not_147 (not_147_out, F25);
  not not_148 (not_148_out, F14);
  not not_149 (not_149_out, F13);
  not not_150 (not_150_out, F12);
  not not_151 (not_151_out, OP6);
  not not_152 (not_152_out, OP3);
  not not_153 (not_153_out, OP2);
  not not_154 (not_154_out, F25);
  not not_155 (not_155_out, F14);
  not not_156 (not_156_out, F13);
  not not_157 (not_157_out, F12);
  not not_158 (not_158_out, OP6);
  not not_159 (not_159_out, OP3);
  not not_160 (not_160_out, OP2);
  not not_161 (not_161_out, F30);
  not not_162 (not_162_out, F25);
  not not_163 (not_163_out, OP6);
  not not_164 (not_164_out, OP3);
  not not_165 (not_165_out, OP2);
  not not_166 (not_166_out, F30);
  not not_167 (not_167_out, F25);
  not not_168 (not_168_out, F12);
  not not_169 (not_169_out, OP6);
  not not_170 (not_170_out, OP3);
  not not_171 (not_171_out, OP2);
  not not_172 (not_172_out, F30);
  not not_173 (not_173_out, F25);
  not not_174 (not_174_out, F14);
  not not_175 (not_175_out, F12);
  not not_176 (not_176_out, OP6);
  not not_177 (not_177_out, OP3);
  not not_178 (not_178_out, OP2);
  not not_179 (not_179_out, F30);
  not not_180 (not_180_out, F25);
  not not_181 (not_181_out, F14);
  not not_182 (not_182_out, OP6);
  not not_183 (not_183_out, OP3);
  not not_184 (not_184_out, OP2);
  not not_185 (not_185_out, F14);
  not not_186 (not_186_out, F12);
  not not_187 (not_187_out, OP6);
  not not_188 (not_188_out, OP4);
  not not_189 (not_189_out, OP3);
  not not_190 (not_190_out, OP2);
  not not_191 (not_191_out, F30);
  not not_192 (not_192_out, F25);
  not not_193 (not_193_out, F14);
  not not_194 (not_194_out, F13);
  not not_195 (not_195_out, F12);
  not not_196 (not_196_out, OP3);
  not not_197 (not_197_out, OP2);
  not not_198 (not_198_out, F14);
  not not_199 (not_199_out, F13);
  not not_200 (not_200_out, F12);
  not not_201 (not_201_out, OP4);
  not not_202 (not_202_out, OP3);
  not not_203 (not_203_out, OP2);
  not not_204 (not_204_out, F14);
  not not_205 (not_205_out, F13);
  not not_206 (not_206_out, OP4);
  not not_207 (not_207_out, OP3);
  not not_208 (not_208_out, OP2);
  not not_209 (not_209_out, F30);
  not not_210 (not_210_out, F25);
  not not_211 (not_211_out, F13);
  not not_212 (not_212_out, F12);
  not not_213 (not_213_out, OP6);
  not not_214 (not_214_out, OP3);
  not not_215 (not_215_out, OP2);
  not not_216 (not_216_out, OP4);
  not not_217 (not_217_out, OP3);
  not not_218 (not_218_out, OP2);
  and and_1 (and_1_out, not_1_out, not_2_out, not_3_out, not_4_out, not_5_out, not_6_out, OP5, OP4, not_7_out, not_8_out);
  and and_2 (and_2_out, F30, not_9_out, not_10_out, not_11_out, not_12_out, not_13_out, OP5, OP4, not_14_out, not_15_out);
  and and_3 (and_3_out, not_16_out, not_17_out, F14, F13, F12, not_18_out, OP5, OP4, not_19_out, not_20_out);
  and and_4 (and_4_out, not_21_out, not_22_out, F14, F13, not_23_out, not_24_out, OP5, OP4, not_25_out, not_26_out);
  and and_5 (and_5_out, not_27_out, not_28_out, not_29_out, F13, not_30_out, not_31_out, OP5, OP4, not_32_out, not_33_out);
  and and_6 (and_6_out, not_34_out, not_35_out, not_36_out, F13, F12, not_37_out, OP5, OP4, not_38_out, not_39_out);
  and and_7 (and_7_out, not_40_out, not_41_out, not_42_out, not_43_out, not_44_out, OP4, not_45_out, not_46_out);
  and and_8 (and_8_out, F14, F13, F12, not_47_out, not_48_out, OP4, not_49_out, not_50_out);
  and and_9 (and_9_out, F14, F13, not_51_out, not_52_out, not_53_out, OP4, not_54_out, not_55_out);
  and and_10 (and_10_out, F14, not_56_out, not_57_out, not_58_out, not_59_out, OP4, not_60_out, not_61_out);
  and and_11 (and_11_out, not_62_out, F13, not_63_out, not_64_out, not_65_out, OP4, not_66_out, not_67_out);
  and and_12 (and_12_out, not_68_out, not_69_out, not_70_out, not_71_out, F12, not_72_out, not_73_out, OP4, not_74_out, not_75_out);
  and and_13 (and_13_out, not_76_out, not_77_out, F14, not_78_out, F12, not_79_out, not_80_out, OP4, not_81_out, not_82_out);
  and and_14 (and_14_out, F30, not_83_out, F14, not_84_out, F12, not_85_out, not_86_out, OP4, not_87_out, not_88_out);
  and and_15 (and_15_out, not_89_out, F13, not_90_out, not_91_out, not_92_out, not_93_out, not_94_out, not_95_out);
  and and_16 (and_16_out, not_96_out, F13, not_97_out, not_98_out, OP5, not_99_out, not_100_out, not_101_out);
  and and_17 (and_17_out, not_102_out, not_103_out, not_104_out, not_105_out, not_106_out, OP6, OP5, OP4, not_107_out, not_108_out);
  and and_18 (and_18_out, not_109_out, not_110_out, not_111_out, OP6, OP5, not_112_out, not_113_out, not_114_out);
  and and_19 (and_19_out, not_115_out, not_116_out, F12, OP6, OP5, not_117_out, not_118_out, not_119_out);
  and and_20 (and_20_out, not_120_out, not_121_out, not_122_out, OP6, OP5, not_123_out, not_124_out, OP2);
  and and_21 (and_21_out, not_125_out, not_126_out, F14, not_127_out, not_128_out, not_129_out, OP5, OP4, not_130_out, not_131_out);
  and and_22 (and_22_out, not_132_out, F13, F12, not_133_out, not_134_out, OP4, not_135_out, not_136_out);
  and and_23 (and_23_out, F14, not_137_out, F12, not_138_out, not_139_out, not_140_out, not_141_out, not_142_out);
  and and_24 (and_24_out, F14, F13, F12, OP6, OP5, not_143_out, not_144_out, not_145_out);
  and and_25 (and_25_out, not_146_out, not_147_out, not_148_out, not_149_out, not_150_out, not_151_out, OP5, OP4, not_152_out, not_153_out);
  and and_26 (and_26_out, F30, not_154_out, not_155_out, not_156_out, not_157_out, not_158_out, OP5, OP4, not_159_out, not_160_out);
  and and_27 (and_27_out, not_161_out, not_162_out, F14, F13, F12, not_163_out, OP5, OP4, not_164_out, not_165_out);
  and and_28 (and_28_out, not_166_out, not_167_out, F14, F13, not_168_out, not_169_out, OP5, OP4, not_170_out, not_171_out);
  and and_29 (and_29_out, not_172_out, not_173_out, not_174_out, F13, not_175_out, not_176_out, OP5, OP4, not_177_out, not_178_out);
  and and_30 (and_30_out, not_179_out, not_180_out, not_181_out, F13, F12, not_182_out, OP5, OP4, not_183_out, not_184_out);
  and and_31 (and_31_out, not_185_out, F13, not_186_out, not_187_out, OP5, not_188_out, not_189_out, not_190_out);
  and and_32 (and_32_out, not_191_out, not_192_out, not_193_out, not_194_out, not_195_out, OP6, OP5, OP4, not_196_out, not_197_out);
  and and_33 (and_33_out, not_198_out, not_199_out, not_200_out, OP6, OP5, not_201_out, not_202_out, not_203_out);
  and and_34 (and_34_out, not_204_out, not_205_out, F12, OP6, OP5, not_206_out, not_207_out, not_208_out);
  and and_35 (and_35_out, not_209_out, not_210_out, F14, not_211_out, not_212_out, not_213_out, OP5, OP4, not_214_out, not_215_out);
  and and_36 (and_36_out, F14, F13, F12, OP6, OP5, not_216_out, not_217_out, not_218_out);
  or or_1 (R2, and_25_out, and_26_out, and_27_out, and_28_out, and_29_out, and_30_out, and_31_out, and_32_out, and_33_out, and_34_out, and_35_out, and_36_out);
  or or_2 (R1, and_1_out, and_2_out, and_3_out, and_4_out, and_5_out, and_6_out, and_7_out, and_8_out, and_9_out, and_10_out, and_11_out, and_12_out, and_13_out, and_14_out, and_15_out, and_16_out, and_17_out, and_18_out, and_19_out, and_20_out, and_21_out, and_22_out, and_23_out, and_24_out);
endmodule

module \数据冲突判断  (
  input  [4:0] ID_R1_num,
  input  [4:0] EX_W_num,
  input  EX_RegWrite,
  input  [4:0] ID_R2_num,
  input  [4:0] MEM_W_num,
  input  MEM_RegWrite,
  input  [4:0] OP,
  input  [4:0] Funct,
  output \数据相关 
);

  wire and_1_out, and_2_out, and_3_out, and_4_out, and_5_out, and_6_out, comparator_1_eq, comparator_2_eq,
       comparator_3_eq, comparator_4_eq, comparator_5_eq, comparator_6_eq, comparator_7_eq, comparator_8_eq,
       or_1_out, or_2_out, \寄存器有关判断_1_r1 , \寄存器有关判断_1_r2 ;

  \寄存器有关判断  \u_寄存器有关判断_1  (
    .OP2(OP[0]), .OP3(OP[1]), .OP4(OP[2]), .OP5(OP[3]), .OP6(OP[4]), .F12(Funct[0]), .F13(Funct[1]),
    .F14(Funct[2]), .F25(Funct[3]), .F30(Funct[4]), .R1(\寄存器有关判断_1_r1 ), .R2(\寄存器有关判断_1_r2 ));
  Comparator #(.width(5)) comparator_1 (.a(ID_R1_num), .b(EX_W_num), .eq(comparator_1_eq));  // open: gt, lt
  Comparator #(.width(5)) comparator_2 (.a(EX_W_num), .b({5{1'b0}}), .eq(comparator_2_eq));  // open: gt, lt
  Comparator #(.width(5)) comparator_3 (.a(ID_R2_num), .b(EX_W_num), .eq(comparator_3_eq));  // open: gt, lt
  Comparator #(.width(5)) comparator_4 (.a(EX_W_num), .b({5{1'b0}}), .eq(comparator_4_eq));  // open: gt, lt
  and and_1 (and_1_out, comparator_1_eq, EX_RegWrite, ~comparator_2_eq);  // AND_Gate
  and and_2 (and_2_out, comparator_3_eq, EX_RegWrite, ~comparator_4_eq);  // AND_Gate
  Comparator #(.width(5)) comparator_5 (.a(ID_R1_num), .b(MEM_W_num), .eq(comparator_5_eq));  // open: gt, lt
  Comparator #(.width(5)) comparator_6 (.a(MEM_W_num), .b({5{1'b0}}), .eq(comparator_6_eq));  // open: gt, lt
  Comparator #(.width(5)) comparator_7 (.a(ID_R2_num), .b(MEM_W_num), .eq(comparator_7_eq));  // open: gt, lt
  Comparator #(.width(5)) comparator_8 (.a(MEM_W_num), .b({5{1'b0}}), .eq(comparator_8_eq));  // open: gt, lt
  and and_3 (and_3_out, comparator_5_eq, MEM_RegWrite, ~comparator_6_eq);  // AND_Gate
  and and_4 (and_4_out, comparator_7_eq, MEM_RegWrite, ~comparator_8_eq);  // AND_Gate
  or or_1 (or_1_out, and_3_out, and_1_out);
  or or_2 (or_2_out, and_2_out, and_4_out);
  and and_5 (and_5_out, or_1_out, \寄存器有关判断_1_r1 );
  and and_6 (and_6_out, \寄存器有关判断_1_r2 , or_2_out);
  or or_3 (\数据相关 , and_5_out, and_6_out);
endmodule

module \气泡流水线  (
  output RegWrite,
  output MemWrite,
  output [31:0] IF_PC,
  output [31:0] ID_PC,
  output [31:0] EX_PC,
  output [31:0] M_PC,
  output [31:0] WB_PC,
  output [31:0] RDin,
  output [31:0] MDin,
  output [31:0] LedData
);

  wire and_1_out, and_3_out, and_4_out, and_5_out, and_6_out, and_7_out, and_8_out, and_9_out, and_10_out,
       and_11_out, beq, bgeu, bne, Branch, CLK, clock_1_out, comparator_1_eq, comparator_1_lt,
       comparator_2_eq, d_ff_1_q, ecall, en, equal, ex_mem_1_haltout, ex_mem_1_jampout, ex_mem_1_lessout,
       ex_mem_1_lhuout, ex_mem_1_memtoregout, ex_mem_1_sltiuout, EX_RegWrite, gae, Go, halt, high,
       id_ex_1_alusrcbout, id_ex_1_bgeuout, id_ex_1_haltout, id_ex_1_lhuout, id_ex_1_memtoregout,
       id_ex_1_memwriteout, id_ex_1_s_typeout, id_ex_1_sltiuout, IR1, IR2, IR3, jal, jalr, less, lhu,
       MEM_RegWrite, mem_wb_1_highout, mem_wb_1_jampout, mem_wb_1_lessout, mem_wb_1_lhuout,
       mem_wb_1_memtoregout, mem_wb_1_sltiuout, nand_1_out, not_1_out, not_2_out, not_3_out, not_4_out,
       not_5_out, not_6_out, not_7_out, not_8_out, not_9_out, not_10_out, or_1_out, or_2_out, or_3_out,
       or_4_out, or_6_out, or_7_out, RST, sltiu, uret, W1, W2, W3, \单周期硬布线控制器_1_alu_src , \单周期硬布线控制器_1_beq ,
       \单周期硬布线控制器_1_bne , \单周期硬布线控制器_1_jal , \单周期硬布线控制器_1_jalr , \单周期硬布线控制器_1_memtoreg ,
       \单周期硬布线控制器_1_memwrite , \单周期硬布线控制器_1_regwrite , \单周期硬布线控制器_1_s_type , \数据相关 ;
  wire [3:0] id_ex_1_aluopout, \单周期硬布线控制器_1_alu_op ;
  wire [4:0] EX_W_num, ID_Funct, ID_R1_num, ID_R2_num, MEM_W_num, W_num;
  wire [11:0] shifter_1_out;
  wire [12:0] CNT_num;
  wire [15:0] adder_5_out, counter_6_q, \LoadUse次数 , multiplexer_9_out, shifter_3_out, \分支成功数 , \总周期数 ,
       \插入气泡数 , \无条件分支数 , \条件分支成功数 ;
  wire [19:0] shifter_2_out;
  wire [31:0] adder_1_out, adder_2_out, adder_4_out, and_2_out, bit_extender_1_out, bit_extender_2_out,
       bit_extender_3_out, bit_extender_4_out, bit_extender_5_out, bit_extender_6_out, bit_extender_7_out,
       EX_IR, ex_mem_1_resultout, id_ex_1_imm_i_out, id_ex_1_imm_s_out, id_ex_1_r1out, id_ex_1_r2out, ID_IR,
       IF_IR, imm_B, imm_J, MEM_IR, mem_wb_1_resultout, mem_wb_1_rmdataout, multiplexer_2_out,
       multiplexer_3_out, multiplexer_6_out, multiplexer_7_out, multiplexer_8_out, multiplexer_10_out,
       multiplexer_11_out, multiplexer_12_out, PC_4, PCin, R1, R2, ram_1_data, Result, WB_IR;

  Button \u_总复位  (.out(RST));
  Button _1 (.out(IR1));
  Button _2 (.out(IR2));
  Button _3 (.out(IR3));
  // Probe on \总周期数 
  // Probe on \总周期数 
  Button \u_继续运行  (.out(Go));
  LED led_1 (.in(W1));
  LED led_2 (.in(W2));
  LED led_3 (.in(W3));
  Hex_Digit_Display hex_digit_display_1 (.value(LedData[31:28]));  // open: dp
  // Probe on IF_PC[19:0]
  // RiscV_Probe riscv_probe_1: pin names not known; wires that end beside it: IF_IR
  Hex_Digit_Display hex_digit_display_2 (.value(LedData[27:24]));  // open: dp
  Hex_Digit_Display hex_digit_display_3 (.value(LedData[23:20]));  // open: dp
  // Probe on ID_PC[19:0]
  // RiscV_Probe riscv_probe_2: pin names not known; wires that end beside it: {ID_IR[31], ID_Funct[4], ID_IR[29:26], ID_Funct[3], ID_IR[24:15], ID_Funct[2:0], ID_IR[11:0]}
  Hex_Digit_Display hex_digit_display_4 (.value(LedData[19:16]));  // open: dp
  Hex_Digit_Display hex_digit_display_5 (.value(LedData[15:12]));  // open: dp
  and and_1 (and_1_out, not_2_out, not_1_out);
  not not_1 (not_1_out, halt);
  not not_2 (not_2_out, \数据相关 );
  Multiplexer #(.width(32), .enable("false")) multiplexer_1 (
    .in0(multiplexer_2_out), .in1(adder_1_out), .out(PCin), .sel(Branch));
  Adder #(.width(32)) adder_1 (.a(imm_B), .b(EX_PC), .out(adder_1_out));  // open: cin, cout
  Hex_Digit_Display hex_digit_display_6 (.value(LedData[7:4]));  // open: dp
  Hex_Digit_Display hex_digit_display_7 (.value(LedData[11:8]));  // open: dp
  // Probe on EX_PC[19:0]
  // RiscV_Probe riscv_probe_3: pin names not known; wires that end beside it: EX_IR
  \数据冲突判断  \u_数据冲突判断_1  (
    .ID_R1_num(ID_R1_num), .EX_W_num(EX_W_num), .EX_RegWrite(EX_RegWrite), .ID_R2_num(ID_R2_num),
    .MEM_W_num(MEM_W_num), .MEM_RegWrite(MEM_RegWrite), .OP(ID_IR[6:2]), .Funct(ID_Funct), .\数据相关 (\数据相关 ));
  or or_1 (or_1_out, and_1_out, Go);
  Multiplexer #(.width(32), .enable("false")) multiplexer_2 (
    .in0(multiplexer_3_out), .in1(and_2_out), .out(multiplexer_2_out), .sel(jalr));
  assign and_2_out = Result & 32'hfffffffe;  // AND_Gate and_2, 32 bits wide
  Hex_Digit_Display hex_digit_display_8 (.value(LedData[3:0]));  // open: dp
  and and_3 (and_3_out, or_1_out, not_2_out);
  Register #(.width(32), .Select("low")) PC (.D(PCin), .en(and_3_out), .Q(IF_PC), .clk(CLK), .clr(RST));
  Multiplexer #(.width(32), .enable("false")) multiplexer_3 (
    .in0(PC_4), .in1(adder_2_out), .out(multiplexer_3_out), .sel(jal));
  Adder #(.width(32)) adder_2 (.a(imm_J), .b(EX_PC), .out(adder_2_out));  // open: cin, cout
  // Probe on \总周期数 
  // Probe on M_PC[19:0]
  // RiscV_Probe riscv_probe_4: pin names not known; wires that end beside it: MEM_IR
  not not_3 (not_3_out, halt);
  // Probe on \总周期数 
  // Probe on \无条件分支数 
  // Probe on \条件分支成功数 
  // Probe on \插入气泡数 
  // Probe on \LoadUse次数 
  Counter #(.width(16), .max('hffff)) counter_1 (
    .count(not_3_out), .Q(\总周期数 ), .clk(CLK), .clr(RST));  // open: load, D, carry, preset, down
  Adder #(.width(32)) adder_3 (.a(IF_PC), .b(32'h4), .out(PC_4));  // open: cin, cout
  // Probe on IF_PC[11:0]
  // Probe on WB_PC[19:0]
  // RiscV_Probe riscv_probe_5: pin names not known; wires that end beside it: WB_IR
  // Probe on EX_PC[11:0]
  // Probe on ID_PC[11:0]
  or or_2 (or_2_out, RST, or_3_out);
  or or_3 (or_3_out, jal, jalr, Branch);
  ROM #(.addrWidth(10), .dataWidth(32), .Select("high")) rom_1 (.addr(IF_PC[11:2]), .data(IF_IR));
  and and_4 (and_4_out, en, not_4_out);
  not not_4 (not_4_out, \数据相关 );
  // Probe on M_PC[11:0]
  D_Flip_Flop #(.trigger("high"), .Pre_Clr_Positions("LEGACY"), .enable("true"), .NewFFLayout("false")) d_ff_1 (.Q(d_ff_1_q));  // open: clk, D, Qn, preset, en, reset
  // Probe on 13'hc
  // Probe on Result
  IF_ID if_id_1 (
    .PCin(IF_PC), .IRin(IF_IR), .PCout(ID_PC),
    .IRout({ID_IR[31], ID_Funct[4], ID_IR[29:26], ID_Funct[3], ID_IR[24:15], ID_Funct[2:0], ID_IR[11:0]}),
    .RST(or_2_out), .EN_H(and_4_out), .CLK(CLK));  // open: Predictin, Predictout
  // Probe on WB_PC[11:0]
  Comparator #(.width(13)) comparator_1 (
    .a(CNT_num), .b(13'hc), .eq(comparator_1_eq), .lt(comparator_1_lt));  // open: gt
  Clock clock_1 (.out(clock_1_out));
  nand nand_1 (nand_1_out, d_ff_1_q, comparator_1_eq);
  Counter #(.width(13), .max('h1fff), .ongoal("stay"), .behavior("old")) counter_2 (
    .count(comparator_1_lt), .Q(CNT_num), .clk(clock_1_out));  // open: load, D, carry, clr, preset
  // RiscV_Probe riscv_probe_6: pin names not known; wires that end beside it: {ID_IR[31], ID_Funct[4], ID_IR[29:26], ID_Funct[3], ID_IR[24:15], ID_Funct[2:0], ID_IR[11:0]}, ID_IR[19:15], ID_IR[11:7]
  assign CLK = nand_1_out ? clock_1_out : 1'bz;  // Controlled_Buffer controlled_buffer_1
  Pull_Resistor #(.pull(1)) pull_resistor_1 (.node(CLK));
  \单周期硬布线控制器  \u_单周期硬布线控制器_1  (
    .Funct(ID_Funct), .OP(ID_IR[6:2]), .ALU_OP(\单周期硬布线控制器_1_alu_op ), .MemToReg(\单周期硬布线控制器_1_memtoreg ),
    .MemWrite(\单周期硬布线控制器_1_memwrite ), .ALU_SRC(\单周期硬布线控制器_1_alu_src ), .RegWrite(\单周期硬布线控制器_1_regwrite ),
    .ecall(ecall), .S_type(\单周期硬布线控制器_1_s_type ), .Jalr(\单周期硬布线控制器_1_jalr ), .Beq(\单周期硬布线控制器_1_beq ),
    .JAL(\单周期硬布线控制器_1_jal ), .Bne(\单周期硬布线控制器_1_bne ), .in_3(ID_IR[21]), .uret(uret), .sltiu(sltiu),
    .lhu(lhu), .bgeu(bgeu));  // open: CSRRSI, CSRRCI
  Multiplexer #(.width(5), .enable("false")) multiplexer_4 (
    .in0(ID_IR[24:20]), .in1(5'b01010), .out(ID_R2_num), .sel(ecall));
  Multiplexer #(.width(5), .enable("false")) multiplexer_5 (
    .in0(ID_IR[19:15]), .in1(5'b10001), .out(ID_R1_num), .sel(ecall));
  Shifter #(.width(12)) shifter_1 (
    .in({ID_IR[31], ID_IR[7], ID_Funct[4], ID_IR[29:26], ID_Funct[3], ID_IR[11:8]}), .\dist (4'b0001),
    .out(shifter_1_out));
  Shifter #(.width(20)) shifter_2 (
    .in({ID_IR[31], ID_IR[19:15], ID_Funct[2:0], ID_IR[20], ID_Funct[4], ID_IR[29:26], ID_Funct[3], ID_IR[24:21]}),
    .\dist (5'b00001), .out(shifter_2_out));
  not not_5 (not_5_out, CLK);
  assign bit_extender_1_out = {{20{ID_IR[31]}}, {ID_IR[31], ID_Funct[4], ID_IR[29:26], ID_Funct[3], ID_IR[11:7]}};  // Bit_Extender bit_extender_1
  assign bit_extender_2_out = {{20{shifter_1_out[11]}}, shifter_1_out};  // Bit_Extender bit_extender_2
  assign bit_extender_3_out = {{12{shifter_2_out[19]}}, shifter_2_out};  // Bit_Extender bit_extender_3
  Regifile regifile_1 (
    .Din(RDin), .Clk(not_5_out), .R1(R1), .R2(R2), .WE(RegWrite), .W_num(W_num), .R1_num(ID_R1_num),
    .R2_num(ID_R2_num));
  assign bit_extender_4_out = {{20{ID_IR[31]}}, {ID_IR[31], ID_Funct[4], ID_IR[29:26], ID_Funct[3], ID_IR[24:20]}};  // Bit_Extender bit_extender_4
  assign bit_extender_5_out = {{20{1'b0}}, {ID_IR[31], ID_Funct[4], ID_IR[29:26], ID_Funct[3], ID_IR[24:20]}};  // Bit_Extender bit_extender_5
  not not_6 (not_6_out, comparator_2_eq);
  Comparator #(.width(32)) comparator_2 (.a(R1), .b(32'h22), .eq(comparator_2_eq));  // open: gt, lt
  and and_5 (and_5_out, ecall, comparator_2_eq);
  Multiplexer #(.width(32), .enable("false")) multiplexer_6 (
    .in0(bit_extender_4_out), .in1(bit_extender_5_out), .out(multiplexer_6_out), .sel(sltiu));
  and and_6 (and_6_out, not_6_out, ecall);
  and and_7 (and_7_out, and_6_out, not_7_out);
  not not_7 (not_7_out, Go);
  Register #(.width(32), .Select("low")) register_1 (.D(R2), .en(and_5_out), .Q(LedData), .clk(CLK), .clr(RST));
  or or_4 (or_4_out, or_2_out, \数据相关 );
  ID_EX id_ex_1 (
    .PCin(ID_PC), .Beqin(\单周期硬布线控制器_1_beq ), .Bnein(\单周期硬布线控制器_1_bne ),
    .IRin({ID_IR[31], ID_Funct[4], ID_IR[29:26], ID_Funct[3], ID_IR[24:15], ID_Funct[2:0], ID_IR[11:0]}),
    .MemToRegin(\单周期硬布线控制器_1_memtoreg ), .Imm_I_in(multiplexer_6_out), .MemWritein(\单周期硬布线控制器_1_memwrite ),
    .AluSrcBin(\单周期硬布线控制器_1_alu_src ), .Imm_S_in(bit_extender_1_out), .RegWritein(\单周期硬布线控制器_1_regwrite ),
    .S_typein(\单周期硬布线控制器_1_s_type ), .Imm_B_in(bit_extender_2_out), .Jalin(\单周期硬布线控制器_1_jal ),
    .Jalrin(\单周期硬布线控制器_1_jalr ), .Imm_J_in(bit_extender_3_out), .AluOpin(\单周期硬布线控制器_1_alu_op ),
    .Haltin(and_7_out), .W_in(ID_IR[11:7]), .R1in(R1), .R2in(R2), .PCout(EX_PC), .Beqout(beq), .Bneout(bne),
    .IRout(EX_IR), .MemToRegout(id_ex_1_memtoregout), .Imm_I_out(id_ex_1_imm_i_out),
    .MemWriteout(id_ex_1_memwriteout), .AluSrcBout(id_ex_1_alusrcbout), .Imm_S_out(id_ex_1_imm_s_out),
    .RegWriteout(EX_RegWrite), .S_Typeout(id_ex_1_s_typeout), .Imm_B_out(imm_B), .Jalout(jal),
    .Jalrout(jalr), .Imm_J_out(imm_J), .AluOpout(id_ex_1_aluopout), .Haltout(id_ex_1_haltout),
    .W_out(EX_W_num), .R1out(id_ex_1_r1out), .R2out(id_ex_1_r2out), .RST(or_4_out), .EN_H(en), .CLK(CLK),
    .sltiuin(sltiu), .sltiuout(id_ex_1_sltiuout), .lhuin(lhu), .lhuout(id_ex_1_lhuout), .bgeuin(bgeu),
    .bgeuout(id_ex_1_bgeuout));  // open: R1Forwardin, R1Forwardout, R2Forwardin, R2Forwardout, uretin, uretout, Predictin, Predictou9t, callin, callout
  not not_8 (not_8_out, equal);
  Multiplexer #(.width(32), .enable("false")) multiplexer_7 (
    .in0(id_ex_1_r2out), .in1(multiplexer_8_out), .out(multiplexer_7_out), .sel(id_ex_1_alusrcbout));
  Multiplexer #(.width(32), .enable("false")) multiplexer_8 (
    .in0(id_ex_1_imm_i_out), .in1(id_ex_1_imm_s_out), .out(multiplexer_8_out), .sel(id_ex_1_s_typeout));
  and and_8 (and_8_out, beq, equal);
  and and_9 (and_9_out, not_8_out, bne);
  and and_10 (and_10_out, gae, id_ex_1_bgeuout);
  or or_5 (Branch, and_8_out, and_9_out, and_10_out);
  ALU alu_1 (
    .X(id_ex_1_r1out), .Y(multiplexer_7_out), .AluOP(id_ex_1_aluopout), .Equal(equal), .Result(Result),
    .out_4(gae), .out_6(less));  // open: Result_2
  Counter #(.width(16), .max('hffff)) counter_3 (
    .count(Branch), .Q(\分支成功数 ), .clk(CLK), .clr(RST));  // open: load, D, carry, preset, down
  or or_6 (or_6_out, jal, jalr);
  EX_MEM ex_mem_1 (
    .MemToRegin(id_ex_1_memtoregout), .PCin(EX_PC), .MemWritein(id_ex_1_memwriteout), .IRin(EX_IR),
    .JAMPin(or_6_out), .RegWritein(EX_RegWrite), .Resultin(Result), .Haltin(id_ex_1_haltout),
    .MDatain(id_ex_1_r2out), .W_in(EX_W_num), .MemToRegout(ex_mem_1_memtoregout), .PCout(M_PC),
    .MemWriteout(MemWrite), .IRout(MEM_IR), .JAMPout(ex_mem_1_jampout), .RegWriteout(MEM_RegWrite),
    .Resultout({ex_mem_1_resultout[31:2], high, ex_mem_1_resultout[0]}), .Haltout(ex_mem_1_haltout),
    .Mdataout(MDin), .W_out(MEM_W_num), .RST(RST), .EN_H(en), .CLK(CLK), .lessin(less),
    .lessout(ex_mem_1_lessout), .sltiuin(id_ex_1_sltiuout), .sltiuout(ex_mem_1_sltiuout),
    .lhuin(id_ex_1_lhuout), .lhuout(ex_mem_1_lhuout));
  Counter #(.width(16), .max('hffff)) counter_4 (
    .count(Branch), .Q(\条件分支成功数 ), .clk(CLK), .clr(RST));  // open: load, D, carry, preset, down
  or or_7 (or_7_out, jal, jalr);
  Counter #(.width(16), .max('hffff)) counter_5 (
    .count(or_7_out), .Q(\无条件分支数 ), .clk(CLK), .clr(RST));  // open: load, D, carry, preset, down
  RAM #(.addrWidth(10), .dataWidth(32), .bus("separate"), .Select("high"), .simpleMode("false")) ram_1 (
    .addr(ex_mem_1_resultout[11:2]), .din(MDin), .data(ram_1_data), .str(MemWrite), .clk(CLK),
    .ld(ex_mem_1_memtoregout), .clr(RST));  // open: sel
  MEM_WB mem_wb_1 (
    .PCin(M_PC), .MemToRegin(ex_mem_1_memtoregout), .IRin(MEM_IR), .JAMPin(ex_mem_1_jampout),
    .RegWritein(MEM_RegWrite), .Resultin({ex_mem_1_resultout[31:2], high, ex_mem_1_resultout[0]}),
    .Haltin(ex_mem_1_haltout), .RMDatain(ram_1_data), .W_in(MEM_W_num), .PCout(WB_PC),
    .MemToRegout(mem_wb_1_memtoregout), .IRout(WB_IR), .JAMPout(mem_wb_1_jampout), .RegWriteout(RegWrite),
    .Resultout(mem_wb_1_resultout), .Haltout(halt), .RMdataout(mem_wb_1_rmdataout), .W_out(W_num), .RST(RST),
    .EN_H(en), .CLK(CLK), .lessin(ex_mem_1_lessout), .lessout(mem_wb_1_lessout), .sltiuin(ex_mem_1_sltiuout),
    .sltiuout(mem_wb_1_sltiuout), .lhuin(ex_mem_1_lhuout), .lhuout(mem_wb_1_lhuout), .highin(high),
    .highout(mem_wb_1_highout));
  not not_9 (not_9_out, halt);
  Adder #(.width(32)) adder_4 (.a(32'h4), .b(WB_PC), .out(adder_4_out));  // open: cin, cout
  Multiplexer #(.width(16), .enable("false")) multiplexer_9 (
    .in0(mem_wb_1_rmdataout[15:0]), .in1(mem_wb_1_rmdataout[31:16]), .out(multiplexer_9_out),
    .sel(mem_wb_1_highout));
  not not_10 (not_10_out, halt);
  or or_8 (en, not_10_out, Go);
  Adder #(.width(16)) adder_5 (.a(\条件分支成功数 ), .b(\无条件分支数 ), .out(adder_5_out));  // open: cin, cout
  and and_11 (and_11_out, \数据相关 , not_9_out);
  assign bit_extender_6_out = {{16{1'b0}}, multiplexer_9_out};  // Bit_Extender bit_extender_6
  Shifter #(.width(16)) shifter_3 (.in(adder_5_out), .\dist (4'b0001), .out(shifter_3_out));
  Counter #(.width(16), .max('hffff)) counter_6 (
    .count(and_11_out), .Q(counter_6_q), .clk(CLK), .clr(RST));  // open: load, D, carry, preset, down
  Adder #(.width(16)) adder_6 (.a(shifter_3_out), .b(counter_6_q), .out(\插入气泡数 ));  // open: cin, cout
  Multiplexer #(.width(32), .enable("false")) multiplexer_10 (
    .in0(mem_wb_1_rmdataout), .in1(bit_extender_6_out), .out(multiplexer_10_out), .sel(mem_wb_1_lhuout));
  Multiplexer #(.width(32), .enable("false")) multiplexer_11 (
    .in0(mem_wb_1_resultout), .in1(multiplexer_10_out), .out(multiplexer_11_out), .sel(mem_wb_1_memtoregout));
  Multiplexer #(.width(32), .enable("false")) multiplexer_12 (
    .in0(multiplexer_11_out), .in1(adder_4_out), .out(multiplexer_12_out), .sel(mem_wb_1_jampout));
  assign bit_extender_7_out = {{31{1'b0}}, mem_wb_1_lessout};  // Bit_Extender bit_extender_7
  Multiplexer #(.width(32), .enable("false")) multiplexer_13 (
    .in0(multiplexer_12_out), .in1(bit_extender_7_out), .out(RDin), .sel(mem_wb_1_sltiuout));

  // Other names for the same wires on the sheet: IR[31:0] = {ID_IR[31], ID_Funct[4], ID_IR[29:26], ID_Funct[3], ID_IR[24:15], ID_Funct[2:0], ID_IR[11:0]};
  //   RD_num[4:0] = ID_IR[11:7]; ID_IR (some bits) = ID_Funct; ID_OP[4:0] = ID_IR[6:2]; MEM_PC[31:0] = M_PC;
  //   MEMWB[31:0] = RDin

  // Notes on the sheet:
  //   中断源
  //   时空图监测，可删除
  //   中断等待指示
  //   数码管输出
  //   指令存储器
  //   控制位
  //   contents of rom_1 (hex, n*v repeats v):
  //   100493 100006f 100493 200913 300993 100006f 100493 200913 300993 100006f 100493 200913 300993
  //   100006f 100493 200913 300993 3c0000ef 100413 100493 1f49493 900533 2200893 73 24d493 48463 fedff06f
  //   900533 2200893 73 100493 249493 900533 2200893 73 48463 fedff06f 100493 1f49493 900533 2200893 73
  //   4034d493 900533 2200893 73 4044d493 900533 2200893 73 4044d493 900533 2200893 73 4044d493 900533
  //   2200893 73 4044d493 900533 2200893 73 4044d493 900533 2200893 73 4044d493 900533 2200893 73 4044d493
  //   900533 2200893 73 100413 1f41993 41f9d993 433 c00913 300b13 140413 f47413 800293 100313 499993
  //   89e9b3 1300533 2200893 73 406282b3 fe0294e3 140413 f00f93 1f47433 1c41413 800293 100313 49d993
  //   89e9b3 1300533 2200893 73 406282b3 fe0294e3 1c45413 406b0b33 b0463 f95ff06f 2b3 fff2c293 829293
  //   ff2e293 500533 2200893 73 fff00413 493 84a023 140413 448493 84a023 140413 448493 84a023 140413
  //   448493 84a023 140413 448493 84a023 140413 448493 84a023 140413 448493 84a023 140413 448493 84a023
  //   140413 448493 84a023 140413 448493 84a023 140413 448493 84a023 140413 448493 84a023 140413 448493
  //   84a023 140413 448493 84a023 140413 448493 84a023 140413 448493 84a023 140413 448493 140413 433
  //   3c00493 42983 4aa03 149a2b3 28663 134a023 1442023 ffc48493 fe9412e3 800533 2200893 73 440413 3c00493
  //   fc9416e3 3200893 73 fff00293 7700493 849493 7748493 900533 2200893 73 1000e13 54c4b3 900533 2200893
  //   73 fffe0e13 fe0e16e3 a00893 73 fff00293 313 1900413 841413 9700493 940533 2200893 73 5484b3 494b313
  //   fe0306e3 a00893 73 313 1000e13 8400493 849493 8348493 400913 891913 490913 849493 8248493 849493
  //   8148493 891913 490913 891913 490913 932023 12484b3 430313 fffe0e13 fe0e18e3 2000e13 313 35483 900533
  //   2200893 73 230313 fffe0e13 fe0e14e3 a00893 73 f00493 100913 409909b3 900533 2200893 73 fff48493
  //   ff29f6e3 a00893 73 a00893 73 413 140413 800533 2200893 73 240413 800533 2200893 73 340413 800533
  //   2200893 73 440413 800533 2200893 73 540413 800533 2200893 73 640413 800533 2200893 73 740413 800533
  //   2200893 73 840413 800533 2200893 2200893 73 8067
  //   流水调试日志用
  //   暂停节拍，不能为0
  //   戳工具置1进入计数暂停模式，ctrl+k时钟自动运行到对应节拍暂停
  //   ctrl+k关闭时钟连续运行，将控制位置零，进入单步调试模式调试
  //   用这个时钟源需要去掉电路中的其他时钟源
  //   指令探针
  //   可计数暂停的时钟源
  //   ctrl+k关闭时钟连续运行，将控制位置零，进入单步调试模式调试
  //   指令字
  //   JAL
  //   JALR
  //   URET
  //   Beq
  //   Bne
  //   MemToReg
  //   MemWrite
  //   AluOP
  //   AluSrcB
  //   RegWrite
  //   为方便自动评测，需要输出流水线各段保存的PC值，注意是PC不是PC+4，另外ID段寄存器写入信息，Mem段内存写入信息也要输出
  //   数据存储器
endmodule
module \重定向组合逻辑  (
  input  [4:0] ID_R1_num,
  input  [4:0] EX_W_num,
  input  EX_RegWrite,
  input  [4:0] EX_OP,
  input  [4:0] ID_R2_num,
  input  [4:0] MEM_W_num,
  input  MEM_RegWrite,
  input  [4:0] ID_OP,
  input  [4:0] ID_Funct,
  output \数据相关 ,
  output [1:0] R1Forward,
  output Load_Use,
  output [1:0] R2Forward
);

  wire and_3_out, and_4_out, and_5_out, and_6_out, and_9_out, and_10_out, and_11_out, and_12_out,
       comparator_1_eq, comparator_2_eq, comparator_3_eq, comparator_4_eq, comparator_5_eq, comparator_6_eq,
       comparator_7_eq, comparator_8_eq, comparator_9_eq, comparator_10_eq, \EX_R1冲突 , \EX_R2冲突 , \MEM_R1冲突 ,
       \MEM_R2冲突 , or_1_out, or_2_out, or_4_out, or_5_out, \R1使用 , \R2使用 ;

  \寄存器有关判断  \u_寄存器有关判断_1  (
    .OP2(ID_OP[0]), .OP3(ID_OP[1]), .OP4(ID_OP[2]), .OP5(ID_OP[3]), .OP6(ID_OP[4]), .F12(ID_Funct[0]),
    .F13(ID_Funct[1]), .F14(ID_Funct[2]), .F25(ID_Funct[3]), .F30(ID_Funct[4]), .R1(\R1使用 ), .R2(\R2使用 ));
  Comparator #(.width(5)) comparator_1 (.a(ID_R1_num), .b(EX_W_num), .eq(comparator_1_eq));  // open: gt, lt
  Comparator #(.width(5)) comparator_2 (.a(EX_W_num), .b({5{1'b0}}), .eq(comparator_2_eq));  // open: gt, lt
  Comparator #(.width(5)) comparator_3 (.a(ID_R2_num), .b(EX_W_num), .eq(comparator_3_eq));  // open: gt, lt
  Comparator #(.width(5)) comparator_4 (.a(EX_W_num), .b({5{1'b0}}), .eq(comparator_4_eq));  // open: gt, lt
  and and_1 (\EX_R1冲突 , comparator_1_eq, EX_RegWrite, ~comparator_2_eq);  // AND_Gate
  and and_2 (\EX_R2冲突 , comparator_3_eq, EX_RegWrite, ~comparator_4_eq);  // AND_Gate
  and and_3 (and_3_out, \R1使用 , \MEM_R1冲突 );
  and and_4 (and_4_out, \R1使用 , \EX_R1冲突 );
  and and_5 (and_5_out, \R2使用 , \MEM_R2冲突 );
  and and_6 (and_6_out, \R2使用 , \EX_R2冲突 );
  Priority_Encoder #(.select(2)) priority_encoder_1 (
    .in0(1'b1), .in1(and_3_out), .in2(and_4_out), .out(R1Forward));  // open: in3, gs, en_out, en_in
  Priority_Encoder #(.select(2)) priority_encoder_2 (
    .in0(1'b1), .in1(and_5_out), .in2(and_6_out), .out(R2Forward));  // open: in3, gs, en_out, en_in
  Comparator #(.width(5)) comparator_5 (.a(ID_R1_num), .b(MEM_W_num), .eq(comparator_5_eq));  // open: gt, lt
  Comparator #(.width(5)) comparator_6 (.a(MEM_W_num), .b({5{1'b0}}), .eq(comparator_6_eq));  // open: gt, lt
  Comparator #(.width(5)) comparator_7 (.a(ID_R2_num), .b(MEM_W_num), .eq(comparator_7_eq));  // open: gt, lt
  Comparator #(.width(5)) comparator_8 (.a(MEM_W_num), .b({5{1'b0}}), .eq(comparator_8_eq));  // open: gt, lt
  and and_7 (\MEM_R1冲突 , comparator_5_eq, MEM_RegWrite, ~comparator_6_eq);  // AND_Gate
  and and_8 (\MEM_R2冲突 , comparator_7_eq, MEM_RegWrite, ~comparator_8_eq);  // AND_Gate
  or or_1 (or_1_out, \MEM_R1冲突 , \EX_R1冲突 );
  or or_2 (or_2_out, \EX_R2冲突 , \MEM_R2冲突 );
  and and_9 (and_9_out, or_1_out, \R1使用 );
  or or_3 (\数据相关 , and_9_out, and_10_out);
  and and_10 (and_10_out, \R2使用 , or_2_out);
  and and_11 (and_11_out, \R1使用 , \EX_R1冲突 );
  and and_12 (and_12_out, \EX_R2冲突 , \R2使用 );
  Comparator #(.width(5)) comparator_9 (.a(EX_OP), .b({5{1'b0}}), .eq(comparator_9_eq));  // open: gt, lt
  Comparator #(.width(5)) comparator_10 (.a(EX_OP), .b(5'b00101), .eq(comparator_10_eq));  // open: gt, lt
  or or_4 (or_4_out, and_11_out, and_12_out);
  and and_13 (Load_Use, or_4_out, or_5_out);
  or or_5 (or_5_out, comparator_9_eq, comparator_10_eq);

  // Notes on the sheet:
  //   lw、lhu
endmodule

module \重定向流水线  (
  output RegWrite,
  output MemWrite,
  output [31:0] IF_PC,
  output [31:0] ID_PC,
  output [31:0] EX_PC,
  output [31:0] M_PC,
  output [31:0] WB_PC,
  output [31:0] RDin,
  output [31:0] MDin,
  output [31:0] LedData
);

  wire and_1_out, and_2_out, and_4_out, and_5_out, and_6_out, and_7_out, and_8_out, and_9_out, and_10_out,
       and_11_out, and_12_out, beq, bgeu, bne, Branch, CLK, clock_1_out, comparator_1_eq, comparator_1_lt,
       comparator_2_eq, d_ff_1_q, ecall, en, equal, EX_ecall, ex_mem_1_haltout, ex_mem_1_jampout,
       ex_mem_1_lessout, ex_mem_1_lhuout, ex_mem_1_memtoregout, ex_mem_1_sltiuout, EX_RegWrite_num, gae, Go,
       halt, id_ex_1_alusrcbout, id_ex_1_bgeuout, id_ex_1_lhuout, id_ex_1_memtoregout, id_ex_1_memwriteout,
       id_ex_1_s_typeout, id_ex_1_sltiuout, IR1, IR2, IR3, jal, jalr, less, lhu, Load_Use, MEM_RegWrite_num,
       mem_wb_1_highout, mem_wb_1_jampout, mem_wb_1_lessout, mem_wb_1_lhuout, mem_wb_1_memtoregout,
       mem_wb_1_sltiuout, nand_1_out, not_1_out, not_2_out, not_3_out, not_4_out, not_5_out, not_6_out,
       not_7_out, not_8_out, not_9_out, not_10_out, not_11_out, or_1_out, or_2_out, or_3_out, or_4_out,
       or_5_out, or_7_out, RST, sltiu, uret, W1, W2, W3, \单周期硬布线控制器_1_alu_src , \单周期硬布线控制器_1_beq ,
       \单周期硬布线控制器_1_bne , \单周期硬布线控制器_1_jal , \单周期硬布线控制器_1_jalr , \单周期硬布线控制器_1_memtoreg ,
       \单周期硬布线控制器_1_memwrite , \单周期硬布线控制器_1_regwrite , \单周期硬布线控制器_1_s_type , \数据相关 ;
  wire [1:0] id_ex_1_r1forwardout, id_ex_1_r2forwardout, R1Forward, R2Forward;
  wire [3:0] id_ex_1_aluopout, \单周期硬布线控制器_1_alu_op ;
  wire [4:0] EX_W_num, ID_Funct, ID_R1_num, ID_R2_num, MEM_W_num, W_num;
  wire [11:0] shifter_1_out;
  wire [12:0] CNT_num;
  wire [15:0] adder_4_out, \LoadUse次数 , multiplexer_11_out, shifter_3_out, \分支成功数 , \总周期数 , \插入气泡数 ,
       \无条件分支数 , \条件分支成功数 ;
  wire [19:0] shifter_2_out;
  wire [31:0] adder_1_out, adder_2_out, adder_6_out, ALUResult, and_3_out, bit_extender_1_out,
       bit_extender_2_out, bit_extender_3_out, bit_extender_4_out, bit_extender_5_out, bit_extender_6_out,
       bit_extender_7_out, EX_IR, EX_R1, EX_R2, id_ex_1_imm_i_out, id_ex_1_imm_s_out, id_ex_1_r1out,
       id_ex_1_r2out, ID_IR, IF_IR, imm_B, imm_J, MEM_IR, mem_wb_1_resultout, mem_wb_1_rmdataout,
       multiplexer_1_out, multiplexer_3_out, multiplexer_6_out, multiplexer_7_out, multiplexer_10_out,
       multiplexer_12_out, multiplexer_13_out, multiplexer_14_out, PC_4, PCin, R1, R2, ram_1_data, Result,
       WB_IR;

  Button \u_总复位  (.out(RST));
  Button _1 (.out(IR1));
  Button _2 (.out(IR2));
  Button _3 (.out(IR3));
  // Probe on \总周期数 
  // Probe on \总周期数 
  Button \u_继续运行  (.out(Go));
  LED led_1 (.in(W1));
  LED led_2 (.in(W2));
  LED led_3 (.in(W3));
  not not_1 (not_1_out, halt);
  not not_2 (not_2_out, Load_Use);
  Hex_Digit_Display hex_digit_display_1 (.value(LedData[31:28]));  // open: dp
  // Probe on IF_PC[19:0]
  // RiscV_Probe riscv_probe_1: pin names not known; wires that end beside it: IF_IR
  and and_1 (and_1_out, not_1_out, not_2_out);
  Hex_Digit_Display hex_digit_display_2 (.value(LedData[23:20]));  // open: dp
  Hex_Digit_Display hex_digit_display_3 (.value(LedData[27:24]));  // open: dp
  // Probe on ID_PC[19:0]
  // RiscV_Probe riscv_probe_2: pin names not known; wires that end beside it: {ID_IR[31], ID_Funct[4], ID_IR[29:26], ID_Funct[3], ID_IR[24:15], ID_Funct[2:0], ID_IR[11:0]}
  \重定向组合逻辑  \u_重定向组合逻辑_1  (
    .ID_R1_num(ID_R1_num), .EX_W_num(EX_W_num), .EX_RegWrite(EX_RegWrite_num), .EX_OP(EX_IR[6:2]),
    .ID_R2_num(ID_R2_num), .MEM_W_num(MEM_W_num), .MEM_RegWrite(MEM_RegWrite_num), .ID_OP(ID_IR[6:2]),
    .ID_Funct(ID_Funct), .\数据相关 (\数据相关 ), .R1Forward(R1Forward), .Load_Use(Load_Use), .R2Forward(R2Forward));
  Hex_Digit_Display hex_digit_display_4 (.value(LedData[19:16]));  // open: dp
  Hex_Digit_Display hex_digit_display_5 (.value(LedData[15:12]));  // open: dp
  or or_1 (or_1_out, Go, and_1_out);
  Hex_Digit_Display hex_digit_display_6 (.value(LedData[11:8]));  // open: dp
  Hex_Digit_Display hex_digit_display_7 (.value(LedData[7:4]));  // open: dp
  // Probe on EX_PC[19:0]
  // RiscV_Probe riscv_probe_3: pin names not known; wires that end beside it: EX_IR
  and and_2 (and_2_out, or_1_out, not_2_out);
  Multiplexer #(.width(32), .enable("false")) multiplexer_1 (
    .in0(multiplexer_3_out), .in1(and_3_out), .out(multiplexer_1_out), .sel(jalr));
  Multiplexer #(.width(32), .enable("false")) multiplexer_2 (
    .in0(multiplexer_1_out), .in1(adder_1_out), .out(PCin), .sel(Branch));
  Adder #(.width(32)) adder_1 (.a(imm_B), .b(EX_PC), .out(adder_1_out));  // open: cin, cout
  Hex_Digit_Display hex_digit_display_8 (.value(LedData[3:0]));  // open: dp
  Multiplexer #(.width(32), .enable("false")) multiplexer_3 (
    .in0(PC_4), .in1(adder_2_out), .out(multiplexer_3_out), .sel(jal));
  assign and_3_out = Result & 32'hfffffffe;  // AND_Gate and_3, 32 bits wide
  // Probe on \总周期数 
  // Probe on M_PC[19:0]
  // RiscV_Probe riscv_probe_4: pin names not known; wires that end beside it: MEM_IR
  Register #(.width(32), .Select("low")) PC (.D(PCin), .en(and_2_out), .Q(IF_PC), .clk(CLK), .clr(RST));
  Adder #(.width(32)) adder_2 (.a(imm_J), .b(EX_PC), .out(adder_2_out));  // open: cin, cout
  // Probe on \总周期数 
  // Probe on \无条件分支数 
  // Probe on \条件分支成功数 
  // Probe on \插入气泡数 
  // Probe on \LoadUse次数 
  not not_3 (not_3_out, halt);
  // Probe on IF_PC[11:0]
  // Probe on WB_PC[19:0]
  // RiscV_Probe riscv_probe_5: pin names not known; wires that end beside it: WB_IR
  Counter #(.width(16), .max('hffff)) counter_1 (
    .count(not_3_out), .Q(\总周期数 ), .clk(CLK), .clr(RST));  // open: load, D, carry, preset, down
  Adder #(.width(32)) adder_3 (.a(IF_PC), .b(32'h4), .out(PC_4));  // open: cin, cout
  // Probe on EX_PC[11:0]
  // Probe on ID_PC[11:0]
  or or_2 (or_2_out, jal, jalr, Branch);
  ROM #(.addrWidth(10), .dataWidth(32), .Select("high")) rom_1 (.addr(IF_PC[11:2]), .data(IF_IR));
  not not_4 (not_4_out, Load_Use);
  // Probe on M_PC[11:0]
  D_Flip_Flop #(.trigger("high"), .Pre_Clr_Positions("LEGACY"), .enable("true"), .NewFFLayout("false")) d_ff_1 (.Q(d_ff_1_q));  // open: clk, D, Qn, preset, en, reset
  // Probe on 13'h8f7
  or or_3 (or_3_out, RST, or_2_out);
  IF_ID if_id_1 (
    .PCin(IF_PC), .IRin(IF_IR), .PCout(ID_PC),
    .IRout({ID_IR[31], ID_Funct[4], ID_IR[29:26], ID_Funct[3], ID_IR[24:15], ID_Funct[2:0], ID_IR[11:0]}),
    .RST(or_3_out), .EN_H(and_4_out), .CLK(CLK));  // open: Predictin, Predictout
  and and_4 (and_4_out, en, not_4_out);
  // Probe on WB_PC[11:0]
  Comparator #(.width(13)) comparator_1 (
    .a(CNT_num), .b(13'h8f7), .eq(comparator_1_eq), .lt(comparator_1_lt));  // open: gt
  Clock clock_1 (.out(clock_1_out));
  // Probe on Result
  nand nand_1 (nand_1_out, d_ff_1_q, comparator_1_eq);
  Counter #(.width(13), .max('h1fff), .ongoal("stay"), .behavior("old")) counter_2 (
    .count(comparator_1_lt), .Q(CNT_num), .clk(clock_1_out));  // open: load, D, carry, clr, preset
  // RiscV_Probe riscv_probe_6: pin names not known; wires that end beside it: {ID_IR[31], ID_Funct[4], ID_IR[29:26], ID_Funct[3], ID_IR[24:15], ID_Funct[2:0], ID_IR[11:0]}, ID_IR[19:15], ID_IR[11:7]
  assign CLK = nand_1_out ? clock_1_out : 1'bz;  // Controlled_Buffer controlled_buffer_1
  Pull_Resistor #(.pull(1)) pull_resistor_1 (.node(CLK));
  \中断按键参考电路  \u_中断按键参考电路_1  (.\与中断屏蔽位与 (RST), .\同步清零信号 (RST));
  \单周期硬布线控制器  \u_单周期硬布线控制器_1  (
    .Funct(ID_Funct), .OP(ID_IR[6:2]), .ALU_OP(\单周期硬布线控制器_1_alu_op ), .MemToReg(\单周期硬布线控制器_1_memtoreg ),
    .MemWrite(\单周期硬布线控制器_1_memwrite ), .ALU_SRC(\单周期硬布线控制器_1_alu_src ), .RegWrite(\单周期硬布线控制器_1_regwrite ),
    .ecall(ecall), .S_type(\单周期硬布线控制器_1_s_type ), .Jalr(\单周期硬布线控制器_1_jalr ), .Beq(\单周期硬布线控制器_1_beq ),
    .JAL(\单周期硬布线控制器_1_jal ), .Bne(\单周期硬布线控制器_1_bne ), .in_3(ID_IR[21]), .uret(uret), .sltiu(sltiu),
    .lhu(lhu), .bgeu(bgeu));  // open: CSRRSI, CSRRCI
  Multiplexer #(.width(5), .enable("false")) multiplexer_4 (
    .in0(ID_IR[19:15]), .in1(5'b10001), .out(ID_R1_num), .sel(ecall));
  Multiplexer #(.width(5), .enable("false")) multiplexer_5 (
    .in0(ID_IR[24:20]), .in1(5'b01010), .out(ID_R2_num), .sel(ecall));
  Shifter #(.width(12)) shifter_1 (
    .in({ID_IR[31], ID_IR[7], ID_Funct[4], ID_IR[29:26], ID_Funct[3], ID_IR[11:8]}), .\dist (4'b0001),
    .out(shifter_1_out));
  Shifter #(.width(20)) shifter_2 (
    .in({ID_IR[31], ID_IR[19:15], ID_Funct[2:0], ID_IR[20], ID_Funct[4], ID_IR[29:26], ID_Funct[3], ID_IR[24:21]}),
    .\dist (5'b00001), .out(shifter_2_out));
  not not_5 (not_5_out, CLK);
  Regifile regifile_1 (
    .Din(RDin), .Clk(not_5_out), .R1(R1), .R2(R2), .WE(RegWrite), .W_num(W_num), .R1_num(ID_R1_num),
    .R2_num(ID_R2_num));
  assign bit_extender_1_out = {{20{ID_IR[31]}}, {ID_IR[31], ID_Funct[4], ID_IR[29:26], ID_Funct[3], ID_IR[11:7]}};  // Bit_Extender bit_extender_1
  assign bit_extender_2_out = {{20{shifter_1_out[11]}}, shifter_1_out};  // Bit_Extender bit_extender_2
  assign bit_extender_3_out = {{12{shifter_2_out[19]}}, shifter_2_out};  // Bit_Extender bit_extender_3
  assign bit_extender_4_out = {{20{ID_IR[31]}}, {ID_IR[31], ID_Funct[4], ID_IR[29:26], ID_Funct[3], ID_IR[24:20]}};  // Bit_Extender bit_extender_4
  assign bit_extender_5_out = {{20{1'b0}}, {ID_IR[31], ID_Funct[4], ID_IR[29:26], ID_Funct[3], ID_IR[24:20]}};  // Bit_Extender bit_extender_5
  Multiplexer #(.width(32), .enable("false")) multiplexer_6 (
    .in0(bit_extender_4_out), .in1(bit_extender_5_out), .out(multiplexer_6_out), .sel(sltiu));
  Counter #(.width(16), .max('hffff)) counter_3 (
    .count(Branch), .Q(\条件分支成功数 ), .clk(CLK), .clr(RST));  // open: load, D, carry, preset, down
  or or_4 (or_4_out, or_3_out, Load_Use);
  ID_EX id_ex_1 (
    .PCin(ID_PC), .Beqin(\单周期硬布线控制器_1_beq ), .Bnein(\单周期硬布线控制器_1_bne ),
    .IRin({ID_IR[31], ID_Funct[4], ID_IR[29:26], ID_Funct[3], ID_IR[24:15], ID_Funct[2:0], ID_IR[11:0]}),
    .MemToRegin(\单周期硬布线控制器_1_memtoreg ), .Imm_I_in(multiplexer_6_out), .MemWritein(\单周期硬布线控制器_1_memwrite ),
    .AluSrcBin(\单周期硬布线控制器_1_alu_src ), .Imm_S_in(bit_extender_1_out), .RegWritein(\单周期硬布线控制器_1_regwrite ),
    .S_typein(\单周期硬布线控制器_1_s_type ), .Imm_B_in(bit_extender_2_out), .Jalin(\单周期硬布线控制器_1_jal ),
    .Jalrin(\单周期硬布线控制器_1_jalr ), .Imm_J_in(bit_extender_3_out), .AluOpin(\单周期硬布线控制器_1_alu_op ),
    .Haltin(ecall), .W_in(ID_IR[11:7]), .R1in(R1), .R2in(R2), .PCout(EX_PC), .Beqout(beq), .Bneout(bne),
    .IRout(EX_IR), .MemToRegout(id_ex_1_memtoregout), .Imm_I_out(id_ex_1_imm_i_out),
    .MemWriteout(id_ex_1_memwriteout), .AluSrcBout(id_ex_1_alusrcbout), .Imm_S_out(id_ex_1_imm_s_out),
    .RegWriteout(EX_RegWrite_num), .S_Typeout(id_ex_1_s_typeout), .Imm_B_out(imm_B), .Jalout(jal),
    .Jalrout(jalr), .Imm_J_out(imm_J), .AluOpout(id_ex_1_aluopout), .Haltout(EX_ecall), .W_out(EX_W_num),
    .R1out(id_ex_1_r1out), .R2out(id_ex_1_r2out), .RST(or_4_out), .EN_H(en), .CLK(CLK), .sltiuin(sltiu),
    .sltiuout(id_ex_1_sltiuout), .lhuin(lhu), .lhuout(id_ex_1_lhuout), .bgeuin(bgeu),
    .bgeuout(id_ex_1_bgeuout), .R1Forwardin(R1Forward), .R1Forwardout(id_ex_1_r1forwardout),
    .R2Forwardin(R2Forward), .R2Forwardout(id_ex_1_r2forwardout));  // open: uretin, uretout, Predictin, Predictou9t, callin, callout
  or or_5 (or_5_out, jal, jalr);
  Multiplexer #(.width(32), .enable("false")) multiplexer_7 (
    .in0(id_ex_1_imm_i_out), .in1(id_ex_1_imm_s_out), .out(multiplexer_7_out), .sel(id_ex_1_s_typeout));
  Counter #(.width(16), .max('hffff)) counter_4 (
    .count(or_5_out), .Q(\无条件分支数 ), .clk(CLK), .clr(RST));  // open: load, D, carry, preset, down
  not not_6 (not_6_out, equal);
  and and_5 (and_5_out, beq, equal);
  and and_6 (and_6_out, not_6_out, bne);
  and and_7 (and_7_out, gae, id_ex_1_bgeuout);
  Multiplexer #(.select(2), .width(32), .enable("false")) multiplexer_8 (
    .in0(id_ex_1_r2out), .in1(RDin), .in2(ALUResult), .out(EX_R2), .sel(id_ex_1_r2forwardout));  // open: in3
  or or_6 (Branch, and_5_out, and_6_out, and_7_out);
  Counter #(.width(16), .max('hffff)) counter_5 (
    .count(Branch), .Q(\分支成功数 ), .clk(CLK), .clr(RST));  // open: load, D, carry, preset, down
  not not_7 (not_7_out, halt);
  Multiplexer #(.select(2), .width(32), .enable("false")) multiplexer_9 (
    .in0(id_ex_1_r1out), .in1(RDin), .in2(ALUResult), .out(EX_R1), .sel(id_ex_1_r1forwardout));  // open: in3
  Adder #(.width(16)) adder_4 (.a(\条件分支成功数 ), .b(\无条件分支数 ), .out(adder_4_out));  // open: cin, cout
  and and_8 (and_8_out, Load_Use, not_7_out);
  Multiplexer #(.width(32), .enable("false")) multiplexer_10 (
    .in0(EX_R2), .in1(multiplexer_7_out), .out(multiplexer_10_out), .sel(id_ex_1_alusrcbout));
  Shifter #(.width(16)) shifter_3 (.in(adder_4_out), .\dist (4'b0001), .out(shifter_3_out));
  Counter #(.width(16), .max('hffff)) counter_6 (
    .count(and_8_out), .Q(\LoadUse次数 ), .clk(CLK), .clr(RST));  // open: load, D, carry, preset, down
  ALU alu_1 (
    .X(EX_R1), .Y(multiplexer_10_out), .AluOP(id_ex_1_aluopout), .Equal(equal), .Result(Result), .out_4(gae),
    .out_6(less));  // open: Result_2
  Comparator #(.width(32)) comparator_2 (.a(EX_R1), .b(32'h22), .eq(comparator_2_eq));  // open: gt, lt
  and and_9 (and_9_out, EX_ecall, comparator_2_eq);
  Adder #(.width(16)) adder_5 (.a(shifter_3_out), .b(\LoadUse次数 ), .out(\插入气泡数 ));  // open: cin, cout
  not not_8 (not_8_out, comparator_2_eq);
  and and_10 (and_10_out, not_8_out, EX_ecall);
  not not_9 (not_9_out, Go);
  Register #(.width(32), .Select("low")) register_1 (.D(EX_R2), .en(and_9_out), .Q(LedData), .clk(CLK), .clr(RST));
  or or_7 (or_7_out, jal, jalr);
  and and_11 (and_11_out, and_10_out, not_9_out);
  EX_MEM ex_mem_1 (
    .MemToRegin(id_ex_1_memtoregout), .PCin(EX_PC), .MemWritein(id_ex_1_memwriteout), .IRin(EX_IR),
    .JAMPin(or_7_out), .RegWritein(EX_RegWrite_num), .Resultin(Result), .Haltin(and_11_out), .MDatain(EX_R2),
    .W_in(EX_W_num), .MemToRegout(ex_mem_1_memtoregout), .PCout(M_PC), .MemWriteout(MemWrite),
    .IRout(MEM_IR), .JAMPout(ex_mem_1_jampout), .RegWriteout(MEM_RegWrite_num), .Resultout(ALUResult),
    .Haltout(ex_mem_1_haltout), .Mdataout(MDin), .W_out(MEM_W_num), .RST(RST), .EN_H(en), .CLK(CLK),
    .lessin(less), .lessout(ex_mem_1_lessout), .sltiuin(id_ex_1_sltiuout), .sltiuout(ex_mem_1_sltiuout),
    .lhuin(id_ex_1_lhuout), .lhuout(ex_mem_1_lhuout));
  RAM #(.addrWidth(10), .dataWidth(32), .bus("separate"), .Select("high"), .simpleMode("false")) ram_1 (
    .addr(ALUResult[11:2]), .din(MDin), .data(ram_1_data), .str(MemWrite), .clk(CLK),
    .ld(ex_mem_1_memtoregout), .clr(RST));  // open: sel
  MEM_WB mem_wb_1 (
    .PCin(M_PC), .MemToRegin(ex_mem_1_memtoregout), .IRin(MEM_IR), .JAMPin(ex_mem_1_jampout),
    .RegWritein(MEM_RegWrite_num), .Resultin(ALUResult), .Haltin(ex_mem_1_haltout), .RMDatain(ram_1_data),
    .W_in(MEM_W_num), .PCout(WB_PC), .MemToRegout(mem_wb_1_memtoregout), .IRout(WB_IR),
    .JAMPout(mem_wb_1_jampout), .RegWriteout(RegWrite), .Resultout(mem_wb_1_resultout), .Haltout(halt),
    .RMdataout(mem_wb_1_rmdataout), .W_out(W_num), .RST(RST), .EN_H(en), .CLK(CLK),
    .lessin(ex_mem_1_lessout), .lessout(mem_wb_1_lessout), .sltiuin(ex_mem_1_sltiuout),
    .sltiuout(mem_wb_1_sltiuout), .lhuin(ex_mem_1_lhuout), .lhuout(mem_wb_1_lhuout), .highin(ALUResult[1]),
    .highout(mem_wb_1_highout));
  Adder #(.width(32)) adder_6 (.a(32'h4), .b(WB_PC), .out(adder_6_out));  // open: cin, cout
  Multiplexer #(.width(16), .enable("false")) multiplexer_11 (
    .in0(mem_wb_1_rmdataout[15:0]), .in1(mem_wb_1_rmdataout[31:16]), .out(multiplexer_11_out),
    .sel(mem_wb_1_highout));
  assign bit_extender_6_out = {{16{1'b0}}, multiplexer_11_out};  // Bit_Extender bit_extender_6
  and and_12 (and_12_out, halt, ~Go);  // AND_Gate
  not not_10 (not_10_out, and_12_out);
  not not_11 (not_11_out, halt);
  or or_8 (en, not_11_out, Go);
  Multiplexer #(.width(32), .enable("false")) multiplexer_12 (
    .in0(mem_wb_1_rmdataout), .in1(bit_extender_6_out), .out(multiplexer_12_out), .sel(mem_wb_1_lhuout));
  Multiplexer #(.width(32), .enable("false")) multiplexer_13 (
    .in0(mem_wb_1_resultout), .in1(multiplexer_12_out), .out(multiplexer_13_out), .sel(mem_wb_1_memtoregout));
  Multiplexer #(.width(32), .enable("false")) multiplexer_14 (
    .in0(multiplexer_13_out), .in1(adder_6_out), .out(multiplexer_14_out), .sel(mem_wb_1_jampout));
  assign bit_extender_7_out = {{31{1'b0}}, mem_wb_1_lessout};  // Bit_Extender bit_extender_7
  Multiplexer #(.width(32), .enable("false")) multiplexer_15 (
    .in0(multiplexer_14_out), .in1(bit_extender_7_out), .out(RDin), .sel(mem_wb_1_sltiuout));

  // Other names for the same wires on the sheet: IR[31:0] = {ID_IR[31], ID_Funct[4], ID_IR[29:26], ID_Funct[3], ID_IR[24:15], ID_Funct[2:0], ID_IR[11:0]};
  //   RD_num[4:0] = ID_IR[11:7]; ID_IR (some bits) = ID_Funct; high = ALUResult[1]; ID_OP[4:0] = ID_IR[6:2];
  //   MEM_PC[31:0] = M_PC; MEMWB[31:0] = RDin

  // Notes on the sheet:
  //   中断源
  //   时空图监测，可删除
  //   中断等待指示
  //   数码管输出
  //   控制位
  //   contents of rom_1 (hex, n*v repeats v):
  //   100493 100006f 100493 200913 300993 100006f 100493 200913 300993 100006f 100493 200913 300993
  //   100006f 100493 200913 300993 29c000ef 100413 100493 1f49493 900533 2200893 73 24d493 48463 fedff06f
  //   900533 2200893 73 100493 249493 900533 2200893 73 48463 fedff06f 100493 1f49493 900533 2200893 73
  //   4034d493 900533 2200893 73 4044d493 900533 2200893 73 4044d493 900533 2200893 73 4044d493 900533
  //   2200893 73 4044d493 900533 2200893 73 4044d493 900533 2200893 73 4044d493 900533 2200893 73 4044d493
  //   900533 2200893 73 100413 1f41993 41f9d993 433 c00913 300b13 140413 f47413 800293 100313 499993
  //   89e9b3 1300533 2200893 73 406282b3 fe0294e3 140413 f00f93 1f47433 1c41413 800293 100313 49d993
  //   89e9b3 1300533 2200893 73 406282b3 fe0294e3 1c45413 406b0b33 b0463 f95ff06f 2b3 fff2c293 829293
  //   ff2e293 500533 2200893 73 fff00413 493 84a023 140413 448493 84a023 140413 448493 84a023 140413
  //   448493 84a023 140413 448493 84a023 140413 448493 84a023 140413 448493 84a023 140413 448493 84a023
  //   140413 448493 84a023 140413 448493 84a023 140413 448493 84a023 140413 448493 84a023 140413 448493
  //   84a023 140413 448493 84a023 140413 448493 84a023 140413 448493 84a023 140413 448493 140413 433
  //   3c00493 42983 4aa03 149a2b3 28663 134a023 1442023 ffc48493 fe9412e3 800533 2200893 73 440413 3c00493
  //   fc9416e3 a00893 73 413 140413 800533 2200893 73 240413 800533 2200893 73 340413 800533 2200893 73
  //   440413 800533 2200893 73 540413 800533 2200893 73 640413 800533 2200893 73 740413 800533 2200893 73
  //   840413 800533 2200893 2200893 73 8067
  //   指令存储器
  //   流水调试日志用
  //   暂停节拍，不能为0
  //   戳工具置1进入计数暂停模式，ctrl+k时钟自动运行到对应节拍暂停
  //   ctrl+k关闭时钟连续运行，将控制位置零，进入单步调试模式调试
  //   可计数暂停的时钟源
  //   指令探针
  //   指令字
  //   JAL
  //   JALR
  //   URET
  //   Beq
  //   Bne
  //   MemToReg
  //   MemWrite
  //   AluOP
  //   AluSrcB
  //   RegWrite
  //   为方便自动评测，需要输出流水线各段保存的PC值，注意是PC不是PC+4，另外ID段寄存器写入信息，Mem段内存写入信息也要输出
  //   数据存储器
endmodule

module \中断按键参考电路  (
  input  \同步清零信号 ,
  output \与中断屏蔽位与 
);

  wire \_1号中断_out , and_1_out, clock_1_out, d_ff_1_q, or_1_out, or_2_out;

  Clock clock_1 (.out(clock_1_out));
  Button \_1号中断  (.out(\_1号中断_out ));
  or or_1 (or_1_out, \与中断屏蔽位与 , d_ff_1_q);
  LED \_1号中断等待指示灯  (.in(or_1_out));
  D_Flip_Flop #(.Pre_Clr_Positions("LEGACY"), .enable("true"), .NewFFLayout("false")) d_ff_1 (
    .clk(\_1号中断_out ), .D(1'b1), .Q(d_ff_1_q), .reset(\与中断屏蔽位与 ));  // open: Qn, preset, en
  or or_2 (or_2_out, d_ff_1_q, \与中断屏蔽位与 );
  and and_1 (and_1_out, or_2_out, ~\同步清零信号 );  // AND_Gate
  D_Flip_Flop #(.Pre_Clr_Positions("LEGACY"), .enable("true"), .NewFFLayout("false")) IR1 (
    .clk(clock_1_out), .D(and_1_out), .Q(\与中断屏蔽位与 ));  // open: Qn, preset, en, reset

  // Notes on the sheet:
  //   中断信号采样参考电路
  //   Reset 
endmodule

module \单周期_多级中断  (
  input  IR1,
  input  IR2,
  input  IR3,
  output RegWrite,
  output MemWrite,
  output [31:0] PC,
  output [31:0] IR,
  output [31:0] RDin,
  output [31:0] MDin,
  output [31:0] LedData
);

  wire _1_out, _2_out, _3_out, AluSrcB, and_1_out, and_2_out, and_3_out, and_4_out, and_7_out, and_8_out,
       and_10_out, and_11_out, and_12_out, beq, bgeu, bne, Branch, CLK, clock_1_out, CLR1, CLR2, CLR3,
       comparator_1_eq, comparator_2_eq, comparator_3_eq, comparator_4_eq, comparator_5_eq, comparator_6_lt,
       comparator_7_eq, comparator_7_lt, comparator_8_eq, CSRRCI, CSRRSI, d_ff_1_q, d_ff_2_q, d_ff_3_q,
       d_ff_5_q, ecall, equal, gae, Go, halt, high, IE, INTR, INTR1, INTR2, INTR3, IR1_t, IR2_t, IR3_t, IRA,
       IRB, IRC, jal, jalr, JAMP, less, lhu, MemToReg, nand_1_out, not_1_out, not_2_out, not_3_out,
       not_4_out, not_5_out, not_6_out, or_4_out, or_5_out, or_6_out, or_7_out, or_8_out, or_9_out,
       or_11_out, or_13_out, or_15_out, or_16_out, or_18_out, RST, S_type, sltiu, uret, W1, W2, W3;
  wire [1:0] CUR_INTR, multiplexer_11_out, multiplexer_14_out, multiplexer_17_out, priority_encoder_1_out,
       priority_encoder_2_out, priority_encoder_3_out, priority_encoder_4_out, register_5_q, register_7_q;
  wire [3:0] AluOP;
  wire [4:0] multiplexer_8_out, multiplexer_10_out;
  wire [11:0] imm12_B;
  wire [12:0] CNT_num;
  wire [15:0] multiplexer_20_out, \分支成功数 , \总周期数 ;
  wire [19:0] imm20_J;
  wire [31:0] adder_2_out, adder_3_out, and_6_out, Bin, bit_extender_1_out, bit_extender_2_out,
       bit_extender_3_out, bit_extender_4_out, bit_extender_5_out, bit_extender_6_out, bit_extender_7_out,
       IR_PC, MDout, MEPC, multiplexer_2_out, multiplexer_3_out, multiplexer_4_out, multiplexer_5_out,
       multiplexer_7_out, multiplexer_9_out, multiplexer_12_out, multiplexer_13_out, multiplexer_15_out,
       multiplexer_18_out, PC_4, PCin, R1, ram_1_data, register_2_q, register_3_q, Result;

  Button \u_继续运行  (.out(Go));
  Button _1 (.out(_1_out));
  Button _2 (.out(_2_out));
  Button _3 (.out(_3_out));
  LED led_1 (.in(W1));
  LED led_2 (.in(W2));
  LED led_3 (.in(W3));
  or or_1 (W1, INTR1, d_ff_1_q);
  or or_2 (W2, INTR2, d_ff_2_q);
  or or_3 (W3, INTR3, d_ff_3_q);
  Hex_Digit_Display hex_digit_display_1 (.value(LedData[31:28]));  // open: dp
  Comparator #(.width(16)) comparator_1 (.a(\总周期数 ), .b(16'h7), .eq(comparator_1_eq));  // open: gt, lt
  Comparator #(.width(16)) comparator_2 (.a(\总周期数 ), .b(16'h241), .eq(comparator_2_eq));  // open: gt, lt
  D_Flip_Flop #(.Pre_Clr_Positions("LEGACY"), .enable("true"), .NewFFLayout("false")) d_ff_1 (
    .clk(IRA), .D(1'b1), .Q(d_ff_1_q), .reset(INTR1));  // open: Qn, preset, en
  D_Flip_Flop #(.Pre_Clr_Positions("LEGACY"), .enable("true"), .NewFFLayout("false")) d_ff_2 (
    .clk(IRB), .D(1'b1), .Q(d_ff_2_q), .reset(INTR2));  // open: Qn, preset, en
  D_Flip_Flop #(.Pre_Clr_Positions("LEGACY"), .enable("true"), .NewFFLayout("false")) d_ff_3 (
    .clk(IRC), .D(1'b1), .Q(d_ff_3_q), .reset(INTR3));  // open: Qn, preset, en
  Demultiplexer #(.select(2), .enable("false")) demultiplexer_1 (
    .out1(CLR1), .out2(CLR2), .out3(CLR3), .in(uret), .sel(CUR_INTR));  // open: out0
  Hex_Digit_Display hex_digit_display_2 (.value(LedData[23:20]));  // open: dp
  Hex_Digit_Display hex_digit_display_3 (.value(LedData[27:24]));  // open: dp
  Comparator #(.width(16)) comparator_3 (.a(16'h258), .b(\总周期数 ), .eq(comparator_3_eq));  // open: gt, lt
  or or_4 (or_4_out, comparator_3_eq, comparator_4_eq);
  Comparator #(.width(16)) comparator_4 (.a(\总周期数 ), .b(16'h1), .eq(comparator_4_eq));  // open: gt, lt
  Comparator #(.width(16)) comparator_5 (.a(\总周期数 ), .b(16'h4), .eq(comparator_5_eq));  // open: gt, lt
  or or_5 (or_5_out, comparator_1_eq, comparator_2_eq);
  or or_6 (or_6_out, d_ff_1_q, INTR1);
  or or_7 (or_7_out, d_ff_2_q, INTR2);
  or or_8 (or_8_out, d_ff_3_q, INTR3);
  Multiplexer #(.select(2), .width(32), .enable("false")) multiplexer_1 (
    .in1(32'h30ac), .in2(32'h3158), .in3(32'h3204), .out(IR_PC), .sel(priority_encoder_1_out));  // open: in0
  Priority_Encoder #(.select(2)) priority_encoder_1 (
    .in0(1'b1), .in1(INTR1), .in2(INTR2), .in3(INTR3), .out(priority_encoder_1_out));  // open: gs, en_out, en_in
  Hex_Digit_Display hex_digit_display_4 (.value(LedData[15:12]));  // open: dp
  Hex_Digit_Display hex_digit_display_5 (.value(LedData[19:16]));  // open: dp
  Button button_1 (.out(RST));
  Pull_Resistor pull_resistor_1 (.node(IRA));
  assign IRA = or_4_out ? ~CLK : 1'bz;  // Controlled_Inverter controlled_inverter_1
  Pull_Resistor pull_resistor_2 (.node(IRB));
  assign IRB = comparator_5_eq ? ~CLK : 1'bz;  // Controlled_Inverter controlled_inverter_2
  Pull_Resistor pull_resistor_3 (.node(IRC));
  assign IRC = or_5_out ? ~CLK : 1'bz;  // Controlled_Inverter controlled_inverter_3
  and and_1 (and_1_out, or_6_out, ~CLR1);  // AND_Gate
  and and_2 (and_2_out, or_7_out, ~CLR2);  // AND_Gate
  and and_3 (and_3_out, or_8_out, ~CLR3);  // AND_Gate
  Hex_Digit_Display hex_digit_display_6 (.value(LedData[7:4]));  // open: dp
  Hex_Digit_Display hex_digit_display_7 (.value(LedData[11:8]));  // open: dp
  // Probe on \总周期数 
  D_Flip_Flop #(.Pre_Clr_Positions("LEGACY"), .enable("true"), .NewFFLayout("false")) u_IR1 (
    .clk(CLK), .D(and_1_out), .Q(INTR1));  // open: Qn, preset, en, reset
  D_Flip_Flop #(.Pre_Clr_Positions("LEGACY"), .enable("true"), .NewFFLayout("false")) IR1_2 (
    .clk(CLK), .D(and_2_out), .Q(INTR2));  // open: Qn, preset, en, reset
  D_Flip_Flop #(.Pre_Clr_Positions("LEGACY"), .enable("true"), .NewFFLayout("false")) IR1_3 (
    .clk(CLK), .D(and_3_out), .Q(INTR3));  // open: Qn, preset, en, reset
  Hex_Digit_Display hex_digit_display_8 (.value(LedData[3:0]));  // open: dp
  Priority_Encoder #(.select(2)) priority_encoder_2 (
    .in0(1'b1), .in1(INTR1), .in2(INTR2), .in3(INTR3), .out(priority_encoder_2_out));  // open: gs, en_out, en_in
  or or_9 (or_9_out, INTR1, INTR2, INTR3);
  Multiplexer #(.select(2), .width(32), .enable("false")) multiplexer_2 (
    .in0(PCin), .in1(IR_PC), .in2(MEPC), .out(multiplexer_2_out), .sel(priority_encoder_3_out));  // open: in3
  Multiplexer #(.width(32), .enable("false")) multiplexer_3 (
    .in0(PCin), .in1(register_2_q), .out(multiplexer_3_out), .sel(uret));
  or or_10 (IR1_t, IR1, IRA);
  Priority_Encoder #(.select(2)) priority_encoder_3 (
    .in0(1'b1), .in1(INTR), .in2(uret), .out(priority_encoder_3_out));  // open: in3, gs, en_out, en_in
  Register #(.width(32), .Select("low")) register_1 (
    .D(multiplexer_3_out), .en(or_11_out), .Q(MEPC), .clk(CLK));  // open: clr
  or or_11 (or_11_out, uret, INTR);
  or or_12 (IR2_t, IR2, IRB);
  Comparator #(.width(2), .mode("unsigned")) comparator_6 (
    .a(CUR_INTR), .b(priority_encoder_2_out), .lt(comparator_6_lt));  // open: gt, eq
  or or_13 (or_13_out, ~or_9_out, CSRRSI, uret);  // OR_Gate
  and and_4 (and_4_out, or_13_out, not_1_out);
  not not_1 (not_1_out, CSRRCI);
  Multiplexer #(.width(32), .enable("false")) multiplexer_4 (
    .in0(MEPC), .in1(register_3_q), .out(multiplexer_4_out), .sel(uret));
  D_Flip_Flop #(.Pre_Clr_Positions("LEGACY"), .enable("true")) d_ff_4 (
    .clk(CLK), .D(and_4_out), .Q(IE));  // open: Qn, preset, en, reset
  Register #(.width(32), .Select("low")) register_2 (
    .D(multiplexer_4_out), .en(or_11_out), .Q(register_2_q), .clk(CLK));  // open: clr
  or or_14 (IR3_t, IR3, IRC);
  and and_5 (INTR, comparator_6_lt, IE);
  or or_15 (or_15_out, Go, not_2_out);
  not not_2 (not_2_out, halt);
  not not_3 (not_3_out, halt);
  Multiplexer #(.width(32), .enable("false")) multiplexer_5 (
    .in0(register_2_q), .in1({32{1'b0}}), .out(multiplexer_5_out), .sel(uret));
  Register #(.width(32), .Select("low")) u_PC (.D(multiplexer_2_out), .en(or_15_out), .Q(PC), .clk(CLK), .clr(RST));
  or or_16 (or_16_out, not_3_out, Go);
  or or_17 (JAMP, jal, jalr);
  Register #(.width(32), .Select("low")) register_3 (
    .D(multiplexer_5_out), .en(or_11_out), .Q(register_3_q), .clk(CLK));  // open: clr
  Adder #(.width(32)) adder_1 (.a(PC), .b(32'h4), .out(PC_4));  // open: cin, cout
  Counter #(.width(16), .max('hffff)) counter_1 (
    .count(or_16_out), .Q(\总周期数 ), .clk(CLK), .clr(RST));  // open: load, D, carry, preset, down
  // RiscV_Probe riscv_probe_1: pin names not known; wires that end beside it: IR, IR[19:15], IR[11:7]
  ROM #(.addrWidth(10), .dataWidth(32), .Select("high")) rom_1 (.addr(PC[11:2]), .data(IR));
  Multiplexer #(.width(32), .enable("false")) multiplexer_6 (
    .in0(multiplexer_7_out), .in1(adder_2_out), .out(PCin), .sel(Branch));
  assign bit_extender_1_out = {{20{imm12_B[11]}}, imm12_B};  // Bit_Extender bit_extender_1
  Multiplexer #(.width(32), .enable("false")) multiplexer_7 (
    .in0(multiplexer_9_out), .in1(and_6_out), .out(multiplexer_7_out), .sel(jalr));
  Adder #(.width(32)) adder_2 (.a(bit_extender_1_out), .b(PC), .out(adder_2_out));  // open: cin, cout
  Priority_Encoder #(.select(2)) priority_encoder_4 (
    .in0(1'b1), .in1(INTR1), .in2(INTR2), .in3(INTR3), .out(priority_encoder_4_out));  // open: gs, en_out, en_in
  \单周期硬布线控制器  \u_单周期硬布线控制器_1  (
    .Funct({IR[30], IR[25], IR[14:12]}), .OP(IR[6:2]), .ALU_OP(AluOP), .MemToReg(MemToReg),
    .MemWrite(MemWrite), .ALU_SRC(AluSrcB), .RegWrite(RegWrite), .ecall(ecall), .S_type(S_type), .Jalr(jalr),
    .Beq(beq), .JAL(jal), .Bne(bne), .in_3(IR[21]), .uret(uret), .sltiu(sltiu), .lhu(lhu), .bgeu(bgeu),
    .CSRRSI(CSRRSI), .CSRRCI(CSRRCI));
  Multiplexer #(.width(5), .enable("false")) multiplexer_8 (
    .in0(IR[24:20]), .in1(5'b01010), .out(multiplexer_8_out), .sel(ecall));
  Multiplexer #(.width(32), .enable("false")) multiplexer_9 (
    .in0(PC_4), .in1(adder_3_out), .out(multiplexer_9_out), .sel(jal));
  assign and_6_out = {Result[31:2], high, Result[0]} & 32'hfffffffe;  // AND_Gate and_6, 32 bits wide
  assign bit_extender_2_out = {{12{imm20_J[19]}}, imm20_J};  // Bit_Extender bit_extender_2
  Adder #(.width(32)) adder_3 (.a(bit_extender_2_out), .b(PC), .out(adder_3_out));  // open: cin, cout
  Multiplexer #(.width(5), .enable("false")) multiplexer_10 (
    .in0(IR[19:15]), .in1(5'b10001), .out(multiplexer_10_out), .sel(ecall));
  Shifter #(.width(12)) shifter_1 (.in({IR[31], IR[7], IR[30:25], IR[11:8]}), .\dist (4'b0001), .out(imm12_B));
  Shifter #(.width(20)) shifter_2 (.in({IR[31], IR[19:12], IR[20], IR[30:21]}), .\dist (5'b00001), .out(imm20_J));
  Multiplexer #(.width(2), .enable("false")) multiplexer_11 (
    .in0(priority_encoder_4_out), .in1(register_5_q), .out(multiplexer_11_out), .sel(uret));
  D_Flip_Flop #(.trigger("high"), .Pre_Clr_Positions("LEGACY"), .enable("true"), .NewFFLayout("false")) d_ff_5 (.Q(d_ff_5_q));  // open: clk, D, Qn, preset, en, reset
  // Probe on 13'hc
  Multiplexer #(.width(32), .enable("false")) multiplexer_12 (
    .in0({Result[31:2], high, Result[0]}), .in1(MDout), .out(multiplexer_12_out), .sel(MemToReg));
  Register #(.width(2), .Select("low")) register_4 (
    .D(multiplexer_11_out), .en(or_18_out), .Q(CUR_INTR), .clk(CLK));  // open: clr
  or or_18 (or_18_out, uret, INTR);
  Comparator #(.width(13)) comparator_7 (
    .a(CNT_num), .b(13'hc), .eq(comparator_7_eq), .lt(comparator_7_lt));  // open: gt
  Clock clock_1 (.out(clock_1_out));
  Regifile regifile_1 (
    .Din(RDin), .Clk(CLK), .R1(R1), .R2(MDin), .WE(RegWrite), .W_num(IR[11:7]), .R1_num(multiplexer_10_out),
    .R2_num(multiplexer_8_out));
  Multiplexer #(.width(32), .enable("false")) multiplexer_13 (
    .in0(multiplexer_12_out), .in1(PC_4), .out(multiplexer_13_out), .sel(JAMP));
  assign bit_extender_3_out = {{31{1'b0}}, less};  // Bit_Extender bit_extender_3
  Comparator #(.width(32)) comparator_8 (.a(R1), .b(32'h22), .eq(comparator_8_eq));  // open: gt, lt
  Multiplexer #(.width(2), .enable("false")) multiplexer_14 (
    .in0(CUR_INTR), .in1(register_7_q), .out(multiplexer_14_out), .sel(uret));
  Counter #(.width(13), .max('h1fff), .ongoal("stay"), .behavior("old")) counter_2 (
    .count(comparator_7_lt), .Q(CNT_num), .clk(clock_1_out));  // open: load, D, carry, clr, preset
  Multiplexer #(.width(32), .enable("false")) multiplexer_15 (
    .in0(MDin), .in1(Bin), .out(multiplexer_15_out), .sel(AluSrcB));
  assign bit_extender_4_out = {{20{1'b0}}, IR[31:20]};  // Bit_Extender bit_extender_4
  Multiplexer #(.width(32), .enable("false")) multiplexer_16 (
    .in0(multiplexer_13_out), .in1(bit_extender_3_out), .out(RDin), .sel(sltiu));
  not not_4 (not_4_out, comparator_8_eq);
  and and_7 (and_7_out, ecall, comparator_8_eq);
  Register #(.width(2), .Select("low")) register_5 (
    .D(multiplexer_14_out), .en(or_18_out), .Q(register_5_q), .clk(CLK));  // open: clr
  nand nand_1 (nand_1_out, d_ff_5_q, comparator_7_eq);
  ALU alu_1 (
    .X(R1), .Y(multiplexer_15_out), .AluOP(AluOP), .Equal(equal), .Result({Result[31:2], high, Result[0]}),
    .out_4(gae), .out_6(less));  // open: Result_2
  assign bit_extender_5_out = {{20{IR[31]}}, IR[31:20]};  // Bit_Extender bit_extender_5
  and and_8 (and_8_out, not_4_out, ecall);
  not not_5 (not_5_out, Go);
  Multiplexer #(.width(2), .enable("false")) multiplexer_17 (
    .in0(register_5_q), .in1(2'b00), .out(multiplexer_17_out), .sel(uret));
  assign CLK = nand_1_out ? clock_1_out : 1'bz;  // Controlled_Buffer controlled_buffer_1
  Pull_Resistor #(.pull(1)) pull_resistor_4 (.node(CLK));
  Multiplexer #(.width(32), .enable("false")) multiplexer_18 (
    .in0(bit_extender_5_out), .in1(bit_extender_4_out), .out(multiplexer_18_out), .sel(sltiu));
  assign bit_extender_6_out = {{20{IR[31]}}, {IR[31:25], IR[11:7]}};  // Bit_Extender bit_extender_6
  and and_9 (halt, and_8_out, not_5_out);
  Register #(.width(32), .Select("low")) register_6 (.D(MDin), .en(and_7_out), .Q(LedData), .clk(CLK), .clr(RST));
  Register #(.width(2), .Select("low")) register_7 (
    .D(multiplexer_17_out), .en(or_18_out), .Q(register_7_q), .clk(CLK));  // open: clr
  Multiplexer #(.width(32), .enable("false")) multiplexer_19 (
    .in0(multiplexer_18_out), .in1(bit_extender_6_out), .out(Bin), .sel(S_type));
  not not_6 (not_6_out, equal);
  and and_10 (and_10_out, beq, equal);
  and and_11 (and_11_out, not_6_out, bne);
  RAM #(.addrWidth(10), .dataWidth(32), .bus("separate"), .Select("high"), .simpleMode("false")) ram_1 (
    .addr(Result[11:2]), .din(MDin), .data(ram_1_data), .str(MemWrite), .clk(CLK), .ld(MemToReg), .clr(RST));  // open: sel
  or or_19 (Branch, and_10_out, and_11_out, and_12_out);
  and and_12 (and_12_out, gae, bgeu);
  Counter #(.width(16), .max('hffff)) counter_3 (
    .count(Branch), .Q(\分支成功数 ), .clk(CLK), .clr(RST));  // open: load, D, carry, preset, down
  Multiplexer #(.width(16), .enable("false")) multiplexer_20 (
    .in0(ram_1_data[15:0]), .in1(ram_1_data[31:16]), .out(multiplexer_20_out), .sel(high));
  assign bit_extender_7_out = {{16{1'b0}}, multiplexer_20_out};  // Bit_Extender bit_extender_7
  Multiplexer #(.width(32), .enable("false")) multiplexer_21 (
    .in0(ram_1_data), .in1(bit_extender_7_out), .out(MDout), .sel(lhu));

  // Other names for the same wires on the sheet: imm12_S[11:0] = {IR[31:25], IR[11:7]}; imm12_I[11:0] = IR[31:20];
  //   R2[31:0] = MDin; Result[1] = high

  // Notes on the sheet:
  //   中断源
  //   中断等待指示
  //   总复位信号应将除ROM以外所有存储组件全部清零
  //   多级中断测试信号模拟器
  //   清除中断
  //   数码管输出
  //   Reset 
  //   Reset 
  //   Reset 
  //   数码管输出应该用寄存器锁存，否则显示数据只能一闪而过
  //   中断响应阶段
  //   保存断点地址
  //   中断响应
  //   中断使能位(用于开关中断)
  //   指令存储器
  //   为方便自动评测，需要输出PC，IR，寄存器堆写如数据RDin
  //   指令探针
  //   contents of rom_1 (hex, n*v repeats v):
  //   7d000113 100413 1f41993 41f9d993 433 c00913 800b13 140413 f47413 800293 100313 499993 89e9b3 1300533
  //   2200893 73 406282b3 fe0294e3 140413 f00f93 1f47433 1c41413 800293 100313 49d993 89e9b3 1300533
  //   2200893 73 406282b3 fe0294e3 1c45413 406b0b33 b0463 f95ff06f 2b3 fff2c293 1029293 fff2e293 500533
  //   2200893 73 f5dff06f 1112023 410113 a12023 410113 812023 410113 1312023 410113 1412023 410113 1512023
  //   410113 1612023 410113 40e073 100b13 300a13 100a93 1600433 441413 14469b3 1300533 2200893 73 fe0416e3
  //   415a0a33 fe0a10e3 40f073 ffc10113 12b03 ffc10113 12a83 ffc10113 12a03 ffc10113 12983 ffc10113 12403
  //   ffc10113 12503 ffc10113 12883 200073 1112023 410113 a12023 410113 812023 410113 1312023 410113
  //   1412023 410113 1512023 410113 1612023 410113 40e073 200b13 300a13 100a93 1600433 441413 14469b3
  //   1300533 2200893 73 fe0416e3 415a0a33 fe0a10e3 40f073 ffc10113 12b03 ffc10113 12a83 ffc10113 12a03
  //   ffc10113 12983 ffc10113 12403 ffc10113 12503 ffc10113 12883 200073 1112023 410113 a12023 410113
  //   812023 410113 1312023 410113 1412023 410113 1512023 410113 1612023 410113 40e073 300b13 300a13
  //   100a93 1600433 441413 14469b3 1300533 2200893 73 fe0416e3 415a0a33 fe0a10e3 40f073 ffc10113 12b03
  //   ffc10113 12a83 ffc10113 12a03 ffc10113 12983 ffc10113 12403 ffc10113 12503 ffc10113 12883 200073
  //   RAM写使能MemWrite、RAM写入数据MDin等信号
  //   JAL
  //   JALR
  //   指令字
  //   Beq
  //   Bne
  //   URET
  //   MemToReg
  //   MemWrite
  //   AluOP
  //   AluSrcB
  //   RegWrite
  //   控制位
  //   暂停节拍，不能为0
  //   保存中断号
  //   戳工具置1进入计数暂停模式，ctrl+k时钟自动运行到对应节拍暂停
  //   ctrl+k关闭时钟连续运行，将控制位置零，进入单步调试模式调试
  //   可计数暂停的时钟源
  //   数据存储器
endmodule

module \封装正确性测试  (
);

  wire IR1, IR2, IR3, MemW, RegW;
  wire [31:0] EX_PC, ID_PC, IF_PC, IR, LED, MDin, MDinr, MEM_PC, PC, RDin, RDinr, WB_PC;

  // 单周期RISC_V 单周期risc_v_1: pin names not known; wires that end beside it: IR3, IR1, IR2, IR3, RegW, MemW, PC, IR, RDin, MDin, LED, RegW, MemW, IF_PC, ID_PC, EX_PC, MEM_PC, WB_PC, RDinr, MDinr, LED
  \气泡流水线  \u_气泡流水线_1  (
    .RegWrite(RegW), .MemWrite(MemW), .IF_PC(IF_PC), .ID_PC(ID_PC), .EX_PC(EX_PC), .M_PC(MEM_PC),
    .WB_PC(WB_PC), .RDin(RDinr), .MDin(MDinr), .LedData(LED));
  \单周期_单级中断  \u_单周期_单级中断_1  ();
  \理想流水线  \u_理想流水线_1  (
    .RegWrite(RegW), .MemWrite(MemW), .IF_PC(IF_PC), .ID_PC(ID_PC), .EX_PC(EX_PC), .M_PC(MEM_PC),
    .WB_PC(WB_PC), .RDin(RDinr), .MDin(MDinr), .LedData(LED));
  \重定向流水线  \u_重定向流水线_1  (
    .RegWrite(RegW), .MemWrite(MemW), .IF_PC(IF_PC), .ID_PC(ID_PC), .EX_PC(EX_PC), .M_PC(MEM_PC),
    .WB_PC(WB_PC), .RDin(RDinr), .MDin(MDinr), .LedData(LED));
  \单周期_多级中断  \u_单周期_多级中断_1  (
    .IR1(IR1), .IR2(IR2), .IR3(IR3), .RegWrite(RegW), .MemWrite(MemW), .PC(PC), .IR(IR), .RDin(RDin),
    .MDin(MDin), .LedData(LED));

  // Notes on the sheet:
  //   单周期封装测试
  //   气泡流水封装测试
  //   单周期+单级中断封装测试
  //   请检查上面封装有无位宽不匹配，引脚标签是否和连接的标签相对应，否则无法在educoder平台上正确测试
  //   理想流水封装测试
  //   重定向流水封装测试
  //   单周期+多级中断封装测试
endmodule

module \流水线中断  (
  input  GO,
  input  RST,
  input  CLK,
  output [31:0] \行1 ,
  output [31:0] \行2 ,
  output [31:0] \行3 ,
  output [31:0] \行4 ,
  output [31:0] \行5 ,
  output [31:0] \行6 ,
  output [31:0] \行7 ,
  output [31:0] \行8 ,
  output [31:0] \行9 ,
  output [31:0] \行10 ,
  output [31:0] \行11 ,
  output [31:0] \行12 ,
  output [31:0] \行13 ,
  output [31:0] \行14 ,
  output [31:0] \行15 ,
  output [31:0] \行16 ,
  output [31:0] \行17 ,
  output [31:0] \行18 ,
  output [31:0] \行19 ,
  output [31:0] \行20 ,
  output [31:0] \行21 ,
  output [31:0] \行22 ,
  output [31:0] \行23 ,
  output [31:0] \行24 ,
  output [31:0] \行25 ,
  output [31:0] \行26 ,
  output [31:0] \行27 ,
  output [31:0] \行28 ,
  output [31:0] \行29 ,
  output [31:0] \行30 ,
  output [31:0] \行31 ,
  output [31:0] \行32 
);

  wire and_1_out, and_2_out, and_3_out, and_5_out, and_6_out, and_8_out, and_9_out, and_10_out, and_11_out,
       and_12_out, and_13_out, and_15_out, and_16_out, and_17_out, beq, bgeu, bne, Branch, call, CLR1, CLR2,
       CLR3, comparator_1_eq, comparator_2_eq, comparator_3_eq, comparator_4_eq, comparator_5_lt, d_ff_1_q,
       d_ff_2_q, d_ff_3_q, d_ff_4_q, ecall, en, equal, EX_call, EX_ecall, ex_mem_1_haltout, ex_mem_1_jampout,
       ex_mem_1_lessout, ex_mem_1_lhuout, ex_mem_1_memtoregout, ex_mem_1_sltiuout, EX_RegWrite_num, EX_URET,
       gae, halt, id_ex_1_alusrcbout, id_ex_1_bgeuout, id_ex_1_lhuout, id_ex_1_memtoregout,
       id_ex_1_memwriteout, id_ex_1_s_typeout, id_ex_1_sltiuout, IE, INTR, INTR1, INTR2, INTR3, IR1, IR2,
       IR3, IRHAVE, jal, jalr, less, lhu, Load_Use, MEM_RegWrite_num, mem_wb_1_highout, mem_wb_1_jampout,
       mem_wb_1_lessout, mem_wb_1_lhuout, mem_wb_1_memtoregout, mem_wb_1_sltiuout, MemWrite, not_1_out,
       not_2_out, not_3_out, not_4_out, not_5_out, not_6_out, not_7_out, not_8_out, not_9_out, not_10_out,
       or_1_out, or_6_out, or_7_out, or_8_out, or_9_out, or_10_out, or_11_out, or_12_out, or_13_out,
       or_15_out, or_17_out, RegWrite, sltiu, uret, W1, W2, W3, \单周期硬布线控制器_1_alu_src , \单周期硬布线控制器_1_beq ,
       \单周期硬布线控制器_1_bne , \单周期硬布线控制器_1_jal , \单周期硬布线控制器_1_jalr , \单周期硬布线控制器_1_memtoreg ,
       \单周期硬布线控制器_1_memwrite , \单周期硬布线控制器_1_regwrite , \单周期硬布线控制器_1_s_type , \数据相关 ;
  wire [1:0] id_ex_1_r1forwardout, id_ex_1_r2forwardout, priority_encoder_1_out, priority_encoder_2_out,
       R1Forward, R2Forward, register_2_q, register_4_q, register_5_q;
  wire [3:0] id_ex_1_aluopout, \单周期硬布线控制器_1_alu_op ;
  wire [4:0] EX_W_num, ID_Funct, ID_R1_num, ID_R2_num, MEM_W_num, W_num;
  wire [11:0] shifter_1_out;
  wire [15:0] multiplexer_15_out, \分支成功数 , \总周期数 ;
  wire [19:0] shifter_2_out;
  wire [31:0] adder_1_out, adder_2_out, adder_4_out, ALUResult, and_7_out, bit_extender_1_out,
       bit_extender_2_out, bit_extender_3_out, bit_extender_4_out, bit_extender_5_out, bit_extender_6_out,
       bit_extender_7_out, EX_IR, EX_PC, EX_R1, EX_R2, id_ex_1_imm_i_out, id_ex_1_imm_s_out, id_ex_1_r1out,
       id_ex_1_r2out, ID_IR, ID_PC, IF_IR, IF_PC, imm_B, imm_J, IR_PC, LedData, MDin, MEM_IR, MEM_PC,
       mem_wb_1_resultout, mem_wb_1_rmdataout, MEMWB, MEPC, multiplexer_2_out, multiplexer_3_out,
       multiplexer_5_out, multiplexer_6_out, multiplexer_7_out, multiplexer_10_out, multiplexer_11_out,
       multiplexer_14_out, multiplexer_16_out, multiplexer_17_out, multiplexer_18_out, multiplexer_20_out,
       multiplexer_21_out, multiplexer_22_out, multiplexer_23_out, multiplexer_24_out, multiplexer_25_out,
       multiplexer_26_out, multiplexer_27_out, multiplexer_28_out, multiplexer_29_out, multiplexer_30_out,
       multiplexer_31_out, multiplexer_32_out, multiplexer_33_out, multiplexer_34_out, multiplexer_35_out,
       multiplexer_36_out, multiplexer_37_out, multiplexer_38_out, multiplexer_39_out, multiplexer_40_out,
       multiplexer_41_out, multiplexer_42_out, multiplexer_43_out, multiplexer_44_out, multiplexer_45_out,
       multiplexer_46_out, multiplexer_47_out, multiplexer_48_out, multiplexer_49_out, PC_4, PCin, R1, R2,
       ram_1_data, Result, WB_IR, WB_PC, \地图_1_行1 , \地图_1_行2 , \地图_1_行3 , \地图_1_行4 , \地图_1_行5 , \地图_1_行6 ,
       \地图_1_行7 , \地图_1_行8 , \地图_1_行9 , \地图_1_行10 , \地图_1_行11 , \地图_1_行12 , \地图_1_行13 , \地图_1_行14 ,
       \地图_1_行15 , \地图_1_行16 , \地图_1_行17 , \地图_1_行18 , \地图_1_行19 , \地图_1_行20 , \地图_1_行21 , \地图_1_行22 ,
       \地图_1_行23 , \地图_1_行24 , \地图_1_行25 , \地图_1_行26 , \地图_1_行27 , \地图_1_行28 , \地图_1_行29 , \地图_1_行30 ,
       \地图_1_行31 , \地图_1_行32 , \点阵_1__2_2 , \点阵_1__3_2 , \点阵_1__4_2 , \点阵_1__5_2 , \点阵_1__6_2 , \点阵_1__7_2 ,
       \点阵_1__8_2 , \点阵_1__9_2 , \点阵_1__10_2 , \点阵_1__11_2 , \点阵_1__12_2 , \点阵_1__13_2 , \点阵_1__14_2 ,
       \点阵_1__15_2 , \点阵_1__16_2 , \点阵_1__17_2 , \点阵_1__18_2 , \点阵_1__19_2 , \点阵_1__20_2 , \点阵_1__21_2 ,
       \点阵_1__22_2 , \点阵_1__23_2 , \点阵_1__24_2 , \点阵_1__25_2 , \点阵_1__26_2 , \点阵_1__27_2 , \点阵_1__28_2 ,
       \点阵_1__29_2 , \点阵_1__30_2 , \点阵_1__31_2 ;

  D_Flip_Flop #(.Pre_Clr_Positions("LEGACY"), .enable("true"), .NewFFLayout("false")) d_ff_1 (
    .clk(CLK), .D(EX_URET), .Q(d_ff_1_q));  // open: Qn, preset, en, reset
  Priority_Encoder #(.select(2)) priority_encoder_1 (
    .in0(1'b1), .in1(EX_call), .in2(EX_URET), .out(priority_encoder_1_out));  // open: in3, gs, en_out, en_in
  Multiplexer #(.select(2), .width(32), .enable("false")) multiplexer_1 (
    .in0(multiplexer_5_out), .in1(IR_PC), .in2(MEPC), .out(PCin), .sel(priority_encoder_1_out));  // open: in3
  or or_1 (or_1_out, jal, jalr, Branch);
  Multiplexer #(.width(32), .enable("false")) multiplexer_2 (
    .in0(ID_PC), .in1(IF_PC), .out(multiplexer_2_out), .sel(d_ff_1_q));
  D_Flip_Flop #(.Pre_Clr_Positions("LEGACY"), .enable("true"), .NewFFLayout("false")) d_ff_2 (
    .clk(IR1), .D(1'b1), .Q(d_ff_2_q), .reset(INTR1));  // open: Qn, preset, en
  or or_2 (W1, INTR1, d_ff_2_q);
  D_Flip_Flop #(.Pre_Clr_Positions("LEGACY"), .enable("true"), .NewFFLayout("false")) d_ff_3 (
    .clk(IR2), .D(1'b1), .Q(d_ff_3_q), .reset(INTR2));  // open: Qn, preset, en
  or or_3 (W2, INTR2, d_ff_3_q);
  D_Flip_Flop #(.Pre_Clr_Positions("LEGACY"), .enable("true"), .NewFFLayout("false")) d_ff_4 (
    .clk(IR3), .D(1'b1), .Q(d_ff_4_q), .reset(INTR3));  // open: Qn, preset, en
  or or_4 (W3, INTR3, d_ff_4_q);
  Multiplexer #(.width(32), .enable("false")) multiplexer_3 (
    .in0(multiplexer_2_out), .in1(multiplexer_5_out), .out(multiplexer_3_out), .sel(or_1_out));
  Priority_Encoder #(.select(2)) priority_encoder_2 (
    .in0(EX_call), .in1(INTR2), .in2(INTR3), .out(priority_encoder_2_out));  // open: in3, gs, en_out, en_in
  or or_5 (IRHAVE, INTR1, INTR2, INTR3);
  or or_6 (or_6_out, ~IRHAVE, EX_URET);  // OR_Gate
  or or_7 (or_7_out, d_ff_2_q, INTR1);
  or or_8 (or_8_out, d_ff_3_q, INTR2);
  Register #(.width(32), .Select("low")) register_1 (
    .D(multiplexer_3_out), .en(EX_call), .Q(MEPC), .clk(CLK));  // open: clr
  Multiplexer #(.select(2), .width(32), .enable("false")) multiplexer_4 (
    .in0(32'h31cc), .in1(32'h3150), .in2(32'h31f4), .out(IR_PC), .sel(priority_encoder_2_out));  // open: in3
  D_Flip_Flop #(.Pre_Clr_Positions("LEGACY"), .enable("true")) d_ff_5 (
    .clk(CLK), .D(or_6_out), .Q(IE));  // open: Qn, preset, en, reset
  and and_1 (and_1_out, or_7_out, ~CLR1);  // AND_Gate
  and and_2 (and_2_out, or_8_out, ~CLR2);  // AND_Gate
  or or_9 (or_9_out, d_ff_4_q, INTR3);
  and and_3 (and_3_out, or_9_out, ~CLR3);  // AND_Gate
  D_Flip_Flop #(.Pre_Clr_Positions("LEGACY"), .enable("true"), .NewFFLayout("false")) u_IR1 (
    .clk(CLK), .D(and_1_out), .Q(INTR1));  // open: Qn, preset, en, reset
  D_Flip_Flop #(.Pre_Clr_Positions("LEGACY"), .enable("true"), .NewFFLayout("false")) IR1_2 (
    .clk(CLK), .D(and_2_out), .Q(INTR2));  // open: Qn, preset, en, reset
  D_Flip_Flop #(.Pre_Clr_Positions("LEGACY"), .enable("true"), .NewFFLayout("false")) IR1_3 (
    .clk(CLK), .D(and_3_out), .Q(INTR3));  // open: Qn, preset, en, reset
  not not_1 (not_1_out, halt);
  not not_2 (not_2_out, Load_Use);
  and and_4 (INTR, IRHAVE, IE);
  and and_5 (and_5_out, not_1_out, not_2_out);
  Register #(.width(2), .Select("low")) register_2 (
    .D(priority_encoder_2_out), .en(INTR), .Q(register_2_q), .clk(CLK));  // open: clr
  Multiplexer #(.width(32), .enable("false")) multiplexer_5 (
    .in0(multiplexer_6_out), .in1(adder_1_out), .out(multiplexer_5_out), .sel(Branch));
  Demultiplexer #(.select(2), .enable("false")) demultiplexer_1 (
    .out0(CLR1), .out1(CLR2), .out2(CLR3), .in(EX_URET), .sel(register_2_q));  // open: out3
  or or_10 (or_10_out, GO, and_5_out);
  Multiplexer #(.width(32), .enable("false")) multiplexer_6 (
    .in0(multiplexer_7_out), .in1(and_7_out), .out(multiplexer_6_out), .sel(jalr));
  Adder #(.width(32)) adder_1 (.a(imm_B), .b(EX_PC), .out(adder_1_out));  // open: cin, cout
  and and_6 (and_6_out, or_10_out, not_2_out);
  Multiplexer #(.width(32), .enable("false")) multiplexer_7 (
    .in0(PC_4), .in1(adder_2_out), .out(multiplexer_7_out), .sel(jal));
  assign and_7_out = Result & 32'hfffffffe;  // AND_Gate and_7, 32 bits wide
  Adder #(.width(32)) adder_2 (.a(imm_J), .b(EX_PC), .out(adder_2_out));  // open: cin, cout
  Register #(.width(32), .Select("low")) PC (.D(PCin), .en(and_6_out), .Q(IF_PC), .clk(CLK), .clr(RST));
  not not_3 (not_3_out, halt);
  Counter #(.width(16), .max('hffff)) counter_1 (
    .count(not_3_out), .Q(\总周期数 ), .clk(CLK), .clr(RST));  // open: load, D, carry, preset, down
  Adder #(.width(32)) adder_3 (.a(IF_PC), .b(32'h4), .out(PC_4));  // open: cin, cout
  or or_11 (or_11_out, EX_URET, jal, jalr, Branch, EX_call);
  ROM #(.addrWidth(10), .dataWidth(32), .Select("high")) rom_1 (.addr(IF_PC[11:2]), .data(IF_IR));
  not not_4 (not_4_out, Load_Use);
  or or_12 (or_12_out, RST, or_11_out);
  IF_ID if_id_1 (
    .PCin(IF_PC), .IRin(IF_IR), .PCout(ID_PC),
    .IRout({ID_IR[31], ID_Funct[4], ID_IR[29:26], ID_Funct[3], ID_IR[24:15], ID_Funct[2:0], ID_IR[11:0]}),
    .RST(or_12_out), .EN_H(and_8_out), .CLK(CLK));  // open: Predictin, Predictout
  and and_8 (and_8_out, en, not_4_out);
  // Probe on Result
  // RiscV_Probe riscv_probe_1: pin names not known; wires that end beside it: {ID_IR[31], ID_Funct[4], ID_IR[29:26], ID_Funct[3], ID_IR[24:15], ID_Funct[2:0], ID_IR[11:0]}, ID_IR[19:15], ID_IR[11:7]
  \重定向组合逻辑  \u_重定向组合逻辑_1  (
    .ID_R1_num(ID_R1_num), .EX_W_num(EX_W_num), .EX_RegWrite(EX_RegWrite_num), .EX_OP(EX_IR[6:2]),
    .ID_R2_num(ID_R2_num), .MEM_W_num(MEM_W_num), .MEM_RegWrite(MEM_RegWrite_num), .ID_OP(ID_IR[6:2]),
    .ID_Funct(ID_Funct), .\数据相关 (\数据相关 ), .R1Forward(R1Forward), .Load_Use(Load_Use), .R2Forward(R2Forward));
  \单周期硬布线控制器  \u_单周期硬布线控制器_1  (
    .Funct(ID_Funct), .OP(ID_IR[6:2]), .ALU_OP(\单周期硬布线控制器_1_alu_op ), .MemToReg(\单周期硬布线控制器_1_memtoreg ),
    .MemWrite(\单周期硬布线控制器_1_memwrite ), .ALU_SRC(\单周期硬布线控制器_1_alu_src ), .RegWrite(\单周期硬布线控制器_1_regwrite ),
    .ecall(ecall), .S_type(\单周期硬布线控制器_1_s_type ), .Jalr(\单周期硬布线控制器_1_jalr ), .Beq(\单周期硬布线控制器_1_beq ),
    .JAL(\单周期硬布线控制器_1_jal ), .Bne(\单周期硬布线控制器_1_bne ), .in_3(ID_IR[21]), .uret(uret), .sltiu(sltiu),
    .lhu(lhu), .bgeu(bgeu), .CSRRCI(call));  // open: CSRRSI
  Multiplexer #(.width(5), .enable("false")) multiplexer_8 (
    .in0(ID_IR[19:15]), .in1(5'b10001), .out(ID_R1_num), .sel(ecall));
  Multiplexer #(.width(5), .enable("false")) multiplexer_9 (
    .in0(ID_IR[24:20]), .in1(5'b01010), .out(ID_R2_num), .sel(ecall));
  Shifter #(.width(12)) shifter_1 (
    .in({ID_IR[31], ID_IR[7], ID_Funct[4], ID_IR[29:26], ID_Funct[3], ID_IR[11:8]}), .\dist (4'b0001),
    .out(shifter_1_out));
  Shifter #(.width(20)) shifter_2 (
    .in({ID_IR[31], ID_IR[19:15], ID_Funct[2:0], ID_IR[20], ID_Funct[4], ID_IR[29:26], ID_Funct[3], ID_IR[24:21]}),
    .\dist (5'b00001), .out(shifter_2_out));
  not not_5 (not_5_out, CLK);
  Regifile regifile_1 (
    .Din(MEMWB), .Clk(not_5_out), .R1(R1), .R2(R2), .WE(RegWrite), .W_num(W_num), .R1_num(ID_R1_num),
    .R2_num(ID_R2_num));
  assign bit_extender_1_out = {{20{ID_IR[31]}}, {ID_IR[31], ID_Funct[4], ID_IR[29:26], ID_Funct[3], ID_IR[11:7]}};  // Bit_Extender bit_extender_1
  assign bit_extender_2_out = {{20{shifter_1_out[11]}}, shifter_1_out};  // Bit_Extender bit_extender_2
  assign bit_extender_3_out = {{12{shifter_2_out[19]}}, shifter_2_out};  // Bit_Extender bit_extender_3
  assign bit_extender_4_out = {{20{ID_IR[31]}}, {ID_IR[31], ID_Funct[4], ID_IR[29:26], ID_Funct[3], ID_IR[24:20]}};  // Bit_Extender bit_extender_4
  assign bit_extender_5_out = {{20{1'b0}}, {ID_IR[31], ID_Funct[4], ID_IR[29:26], ID_Funct[3], ID_IR[24:20]}};  // Bit_Extender bit_extender_5
  Multiplexer #(.width(32), .enable("false")) multiplexer_10 (
    .in0(bit_extender_4_out), .in1(bit_extender_5_out), .out(multiplexer_10_out), .sel(sltiu));
  or or_13 (or_13_out, or_12_out, Load_Use);
  ID_EX id_ex_1 (
    .PCin(ID_PC), .Beqin(\单周期硬布线控制器_1_beq ), .Bnein(\单周期硬布线控制器_1_bne ),
    .IRin({ID_IR[31], ID_Funct[4], ID_IR[29:26], ID_Funct[3], ID_IR[24:15], ID_Funct[2:0], ID_IR[11:0]}),
    .MemToRegin(\单周期硬布线控制器_1_memtoreg ), .Imm_I_in(multiplexer_10_out), .MemWritein(\单周期硬布线控制器_1_memwrite ),
    .AluSrcBin(\单周期硬布线控制器_1_alu_src ), .Imm_S_in(bit_extender_1_out), .RegWritein(\单周期硬布线控制器_1_regwrite ),
    .S_typein(\单周期硬布线控制器_1_s_type ), .Imm_B_in(bit_extender_2_out), .Jalin(\单周期硬布线控制器_1_jal ),
    .Jalrin(\单周期硬布线控制器_1_jalr ), .Imm_J_in(bit_extender_3_out), .AluOpin(\单周期硬布线控制器_1_alu_op ),
    .Haltin(ecall), .W_in(ID_IR[11:7]), .R1in(R1), .R2in(R2), .PCout(EX_PC), .Beqout(beq), .Bneout(bne),
    .IRout(EX_IR), .MemToRegout(id_ex_1_memtoregout), .Imm_I_out(id_ex_1_imm_i_out),
    .MemWriteout(id_ex_1_memwriteout), .AluSrcBout(id_ex_1_alusrcbout), .Imm_S_out(id_ex_1_imm_s_out),
    .RegWriteout(EX_RegWrite_num), .S_Typeout(id_ex_1_s_typeout), .Imm_B_out(imm_B), .Jalout(jal),
    .Jalrout(jalr), .Imm_J_out(imm_J), .AluOpout(id_ex_1_aluopout), .Haltout(EX_ecall), .W_out(EX_W_num),
    .R1out(id_ex_1_r1out), .R2out(id_ex_1_r2out), .RST(or_13_out), .EN_H(en), .CLK(CLK), .sltiuin(sltiu),
    .sltiuout(id_ex_1_sltiuout), .lhuin(lhu), .lhuout(id_ex_1_lhuout), .bgeuin(bgeu),
    .bgeuout(id_ex_1_bgeuout), .R1Forwardin(R1Forward), .R1Forwardout(id_ex_1_r1forwardout),
    .R2Forwardin(R2Forward), .R2Forwardout(id_ex_1_r2forwardout), .uretin(uret), .uretout(EX_URET),
    .callin(call), .callout(EX_call));  // open: Predictin, Predictou9t
  Multiplexer #(.width(32), .enable("false")) multiplexer_11 (
    .in0(id_ex_1_imm_i_out), .in1(id_ex_1_imm_s_out), .out(multiplexer_11_out), .sel(id_ex_1_s_typeout));
  not not_6 (not_6_out, equal);
  and and_9 (and_9_out, beq, equal);
  and and_10 (and_10_out, not_6_out, bne);
  and and_11 (and_11_out, gae, id_ex_1_bgeuout);
  Multiplexer #(.select(2), .width(32), .enable("false")) multiplexer_12 (
    .in0(id_ex_1_r2out), .in1(MEMWB), .in2(ALUResult), .out(EX_R2), .sel(id_ex_1_r2forwardout));  // open: in3
  or or_14 (Branch, and_9_out, and_10_out, and_11_out);
  Counter #(.width(16), .max('hffff)) counter_2 (
    .count(Branch), .Q(\分支成功数 ), .clk(CLK), .clr(RST));  // open: load, D, carry, preset, down
  Multiplexer #(.select(2), .width(32), .enable("false")) multiplexer_13 (
    .in0(id_ex_1_r1out), .in1(MEMWB), .in2(ALUResult), .out(EX_R1), .sel(id_ex_1_r1forwardout));  // open: in3
  Multiplexer #(.width(32), .enable("false")) multiplexer_14 (
    .in0(EX_R2), .in1(multiplexer_11_out), .out(multiplexer_14_out), .sel(id_ex_1_alusrcbout));
  ALU alu_1 (
    .X(EX_R1), .Y(multiplexer_14_out), .AluOP(id_ex_1_aluopout), .Equal(equal), .Result(Result), .out_4(gae),
    .out_6(less));  // open: Result_2
  Comparator #(.width(32)) comparator_1 (.a(EX_R1), .b(32'h22), .eq(comparator_1_eq));  // open: gt, lt
  and and_12 (and_12_out, EX_ecall, comparator_1_eq);
  not not_7 (not_7_out, comparator_1_eq);
  and and_13 (and_13_out, not_7_out, EX_ecall);
  not not_8 (not_8_out, GO);
  Register #(.width(32), .Select("low")) register_3 (.D(EX_R2), .en(and_12_out), .Q(LedData), .clk(CLK), .clr(RST));
  or or_15 (or_15_out, jal, jalr);
  // AND_Gate and_14 has open pins: in0=and_13_out, in1=not_8_out, out=open
  EX_MEM ex_mem_1 (
    .MemToRegin(id_ex_1_memtoregout), .PCin(EX_PC), .MemWritein(id_ex_1_memwriteout), .IRin(EX_IR),
    .JAMPin(or_15_out), .RegWritein(EX_RegWrite_num), .Resultin(Result), .Haltin(1'b0), .MDatain(EX_R2),
    .W_in(EX_W_num), .MemToRegout(ex_mem_1_memtoregout), .PCout(MEM_PC), .MemWriteout(MemWrite),
    .IRout(MEM_IR), .JAMPout(ex_mem_1_jampout), .RegWriteout(MEM_RegWrite_num), .Resultout(ALUResult),
    .Haltout(ex_mem_1_haltout), .Mdataout(MDin), .W_out(MEM_W_num), .RST(RST), .EN_H(en), .CLK(CLK),
    .lessin(less), .lessout(ex_mem_1_lessout), .sltiuin(id_ex_1_sltiuout), .sltiuout(ex_mem_1_sltiuout),
    .lhuin(id_ex_1_lhuout), .lhuout(ex_mem_1_lhuout));
  RAM #(.addrWidth(10), .dataWidth(32), .bus("separate"), .Select("high"), .simpleMode("false")) ram_1 (
    .addr(ALUResult[11:2]), .din(MDin), .data(ram_1_data), .str(MemWrite), .clk(CLK),
    .ld(ex_mem_1_memtoregout), .clr(RST));  // open: sel
  MEM_WB mem_wb_1 (
    .PCin(MEM_PC), .MemToRegin(ex_mem_1_memtoregout), .IRin(MEM_IR), .JAMPin(ex_mem_1_jampout),
    .RegWritein(MEM_RegWrite_num), .Resultin(ALUResult), .Haltin(ex_mem_1_haltout), .RMDatain(ram_1_data),
    .W_in(MEM_W_num), .PCout(WB_PC), .MemToRegout(mem_wb_1_memtoregout), .IRout(WB_IR),
    .JAMPout(mem_wb_1_jampout), .RegWriteout(RegWrite), .Resultout(mem_wb_1_resultout), .Haltout(halt),
    .RMdataout(mem_wb_1_rmdataout), .W_out(W_num), .RST(RST), .EN_H(en), .CLK(CLK),
    .lessin(ex_mem_1_lessout), .lessout(mem_wb_1_lessout), .sltiuin(ex_mem_1_sltiuout),
    .sltiuout(mem_wb_1_sltiuout), .lhuin(ex_mem_1_lhuout), .lhuout(mem_wb_1_lhuout), .highin(ALUResult[1]),
    .highout(mem_wb_1_highout));
  Adder #(.width(32)) adder_4 (.a(32'h4), .b(WB_PC), .out(adder_4_out));  // open: cin, cout
  Multiplexer #(.width(16), .enable("false")) multiplexer_15 (
    .in0(mem_wb_1_rmdataout[15:0]), .in1(mem_wb_1_rmdataout[31:16]), .out(multiplexer_15_out),
    .sel(mem_wb_1_highout));
  assign bit_extender_6_out = {{16{1'b0}}, multiplexer_15_out};  // Bit_Extender bit_extender_6
  and and_15 (and_15_out, halt, ~GO);  // AND_Gate
  not not_9 (not_9_out, and_15_out);
  not not_10 (not_10_out, halt);
  or or_16 (en, not_10_out, GO);
  Multiplexer #(.width(32), .enable("false")) multiplexer_16 (
    .in0(mem_wb_1_rmdataout), .in1(bit_extender_6_out), .out(multiplexer_16_out), .sel(mem_wb_1_lhuout));
  Multiplexer #(.width(32), .enable("false")) multiplexer_17 (
    .in0(mem_wb_1_resultout), .in1(multiplexer_16_out), .out(multiplexer_17_out), .sel(mem_wb_1_memtoregout));
  Multiplexer #(.width(32), .enable("false")) multiplexer_18 (
    .in0(multiplexer_17_out), .in1(adder_4_out), .out(multiplexer_18_out), .sel(mem_wb_1_jampout));
  assign bit_extender_7_out = {{31{1'b0}}, mem_wb_1_lessout};  // Bit_Extender bit_extender_7
  Multiplexer #(.width(32), .enable("false")) multiplexer_19 (
    .in0(multiplexer_18_out), .in1(bit_extender_7_out), .out(MEMWB), .sel(mem_wb_1_sltiuout));
  Comparator #(.width(32)) comparator_2 (.a(EX_R1), .b(32'h2), .eq(comparator_2_eq));  // open: gt, lt
  Comparator #(.width(32)) comparator_3 (.a(EX_R1), .b(32'h1), .eq(comparator_3_eq));  // open: gt, lt
  Comparator #(.width(32)) comparator_4 (.a(EX_R1), .b({32{1'b0}}), .eq(comparator_4_eq));  // open: gt, lt
  and and_16 (and_16_out, MemWrite, comparator_5_lt);
  Comparator #(.width(10), .mode("unsigned")) comparator_5 (
    .a(ALUResult[11:2]), .b(10'h20), .lt(comparator_5_lt));  // open: gt, eq
  or or_17 (or_17_out, comparator_2_eq, comparator_3_eq, comparator_4_eq);
  \地图  \u_地图_1  (
    .\写使能 (and_16_out), .Addr(ALUResult[11:2]), .CLK(CLK), .Data(MDin), .\行1 (\地图_1_行1 ), .\行9 (\地图_1_行9 ),
    .\行17 (\地图_1_行17 ), .\行25 (\地图_1_行25 ), .\行2 (\地图_1_行2 ), .\行10 (\地图_1_行10 ), .\行18 (\地图_1_行18 ),
    .\行26 (\地图_1_行26 ), .\行3 (\地图_1_行3 ), .\行11 (\地图_1_行11 ), .\行19 (\地图_1_行19 ), .\行27 (\地图_1_行27 ),
    .\行4 (\地图_1_行4 ), .\行12 (\地图_1_行12 ), .\行20 (\地图_1_行20 ), .\行28 (\地图_1_行28 ), .\行5 (\地图_1_行5 ),
    .\行13 (\地图_1_行13 ), .\行21 (\地图_1_行21 ), .\行29 (\地图_1_行29 ), .\行6 (\地图_1_行6 ), .\行14 (\地图_1_行14 ),
    .\行22 (\地图_1_行22 ), .\行30 (\地图_1_行30 ), .\行7 (\地图_1_行7 ), .\行15 (\地图_1_行15 ), .\行23 (\地图_1_行23 ),
    .\行31 (\地图_1_行31 ), .\行8 (\地图_1_行8 ), .\行16 (\地图_1_行16 ), .\行24 (\地图_1_行24 ), .\行32 (\地图_1_行32 ),
    .RST(RST));
  and and_17 (and_17_out, or_17_out, EX_ecall);
  \点阵  \u_点阵_1  (
    .\写使能 (and_17_out), ._1(\地图_1_行1 ), ._2(\地图_1_行2 ), ._3(\地图_1_行3 ), ._4(\地图_1_行4 ), ._5(\地图_1_行5 ),
    ._6(\地图_1_行6 ), ._7(\地图_1_行7 ), ._8(\地图_1_行8 ), ._9(\地图_1_行9 ), ._10(\地图_1_行10 ), ._11(\地图_1_行11 ),
    ._12(\地图_1_行12 ), ._13(\地图_1_行13 ), ._14(\地图_1_行14 ), ._15(\地图_1_行15 ), ._16(\地图_1_行16 ),
    ._17(\地图_1_行17 ), ._18(\地图_1_行18 ), ._19(\地图_1_行19 ), ._20(\地图_1_行20 ), ._21(\地图_1_行21 ),
    ._22(\地图_1_行22 ), ._23(\地图_1_行23 ), ._24(\地图_1_行24 ), ._25(\地图_1_行25 ), ._26(\地图_1_行26 ),
    ._27(\地图_1_行27 ), ._28(\地图_1_行28 ), ._29(\地图_1_行29 ), ._30(\地图_1_行30 ), ._31(\地图_1_行31 ),
    ._32(\地图_1_行32 ), .CLK(CLK), ._1_2(\行1 ), ._2_2(\点阵_1__2_2 ), ._3_2(\点阵_1__3_2 ), ._4_2(\点阵_1__4_2 ),
    ._5_2(\点阵_1__5_2 ), ._6_2(\点阵_1__6_2 ), ._7_2(\点阵_1__7_2 ), ._8_2(\点阵_1__8_2 ), ._9_2(\点阵_1__9_2 ),
    ._10_2(\点阵_1__10_2 ), ._11_2(\点阵_1__11_2 ), ._12_2(\点阵_1__12_2 ), ._13_2(\点阵_1__13_2 ),
    ._14_2(\点阵_1__14_2 ), ._15_2(\点阵_1__15_2 ), ._16_2(\点阵_1__16_2 ), ._17_2(\点阵_1__17_2 ),
    ._18_2(\点阵_1__18_2 ), ._19_2(\点阵_1__19_2 ), ._20_2(\点阵_1__20_2 ), ._21_2(\点阵_1__21_2 ),
    ._22_2(\点阵_1__22_2 ), ._23_2(\点阵_1__23_2 ), ._24_2(\点阵_1__24_2 ), ._25_2(\点阵_1__25_2 ),
    ._26_2(\点阵_1__26_2 ), ._27_2(\点阵_1__27_2 ), ._28_2(\点阵_1__28_2 ), ._29_2(\点阵_1__29_2 ),
    ._30_2(\点阵_1__30_2 ), ._31_2(\点阵_1__31_2 ), ._32_2(\行32 ), .RST(RST));
  Multiplexer #(.select(2), .width(32), .enable("false")) multiplexer_20 (
    .in0({32{1'b0}}), .in1({32{1'b0}}), .in2(32'h60), .out(multiplexer_20_out), .sel(register_4_q));  // open: in3
  Multiplexer #(.select(2), .width(32), .enable("false")) multiplexer_21 (
    .in0(32'h7e0), .in1(32'h1e0), .in2(32'h60), .out(multiplexer_21_out), .sel(register_4_q));  // open: in3
  Multiplexer #(.select(2), .width(32), .enable("false")) multiplexer_22 (
    .in0(32'h1e0), .in1(32'h3e0), .in2(32'h1e0), .out(multiplexer_22_out), .sel(register_4_q));  // open: in3
  Multiplexer #(.select(2), .width(32), .enable("false")) multiplexer_23 (
    .in0(32'h7e0), .in1(32'h1e0), .in2(32'h3e0), .out(multiplexer_23_out), .sel(register_4_q));  // open: in3
  Multiplexer #(.select(2), .width(32), .enable("false")) multiplexer_24 (
    .in0(32'h7e0), .in1(32'h1fe0), .in2(32'h7e0), .out(multiplexer_24_out), .sel(register_4_q));  // open: in3
  Multiplexer #(.select(2), .width(32), .enable("false")) multiplexer_25 (
    .in0(32'hfe2), .in1(32'h7e0), .in2(32'h1fe0), .out(multiplexer_25_out), .sel(register_4_q));  // open: in3
  Multiplexer #(.select(2), .width(32), .enable("false")) multiplexer_26 (
    .in0(32'h7e2), .in1(32'hfe2), .in2(32'h7e0), .out(multiplexer_26_out), .sel(register_4_q));  // open: in3
  Multiplexer #(.select(2), .width(32), .enable("false")) multiplexer_27 (
    .in0(32'h7e2), .in1(32'h7e2), .in2(32'hfe2), .out(multiplexer_27_out), .sel(register_4_q));  // open: in3
  Multiplexer #(.select(2), .width(32), .enable("false")) multiplexer_28 (
    .in0(32'h3ffe), .in1(32'h7e2), .in2(32'h7e2), .out(multiplexer_28_out), .sel(register_4_q));  // open: in3
  Multiplexer #(.select(2), .width(32), .enable("false")) multiplexer_29 (
    .in0(32'h1fffe), .in1(32'h3ffe), .in2(32'h7e2), .out(multiplexer_29_out), .sel(register_4_q));  // open: in3
  Multiplexer #(.select(2), .width(32), .enable("false")) multiplexer_30 (
    .in0(32'h3ffe), .in1(32'h1fffe), .in2(32'h3ffe), .out(multiplexer_30_out), .sel(register_4_q));  // open: in3
  Multiplexer #(.select(2), .width(32), .enable("false")) multiplexer_31 (
    .in0(32'h7e2), .in1(32'h3ffe), .in2(32'h1fffe), .out(multiplexer_31_out), .sel(register_4_q));  // open: in3
  Multiplexer #(.select(2), .width(32), .enable("false")) multiplexer_32 (
    .in0(32'h7e2), .in1(32'h7e2), .in2(32'h3ffe), .out(multiplexer_32_out), .sel(register_4_q));  // open: in3
  Multiplexer #(.select(2), .width(32), .enable("false")) multiplexer_33 (
    .in0(32'hfe2), .in1(32'h7e2), .in2(32'h7e2), .out(multiplexer_33_out), .sel(register_4_q));  // open: in3
  Multiplexer #(.select(2), .width(32), .enable("false")) multiplexer_34 (
    .in0(32'h7e0), .in1(32'hfe2), .in2(32'h7e2), .out(multiplexer_34_out), .sel(register_4_q));  // open: in3
  Multiplexer #(.select(2), .width(32), .enable("false")) multiplexer_35 (
    .in0(32'h7e0), .in1(32'h7e0), .in2(32'hfe2), .out(multiplexer_35_out), .sel(register_4_q));  // open: in3
  Multiplexer #(.select(2), .width(32), .enable("false")) multiplexer_36 (
    .in0(32'h1fe0), .in1(32'h7e0), .in2(32'h7e0), .out(multiplexer_36_out), .sel(register_4_q));  // open: in3
  Multiplexer #(.select(2), .width(32), .enable("false")) multiplexer_37 (
    .in0(32'h7e0), .in1(32'h1fe0), .in2(32'h7e0), .out(multiplexer_37_out), .sel(register_4_q));  // open: in3
  Multiplexer #(.select(2), .width(32), .enable("false")) multiplexer_38 (
    .in0(32'h1e0), .in1(32'h7e0), .in2(32'h1fe0), .out(multiplexer_38_out), .sel(register_4_q));  // open: in3
  Multiplexer #(.select(2), .width(32), .enable("false")) multiplexer_39 (
    .in0(32'h3e0), .in1(32'h1e0), .in2(32'h7e0), .out(multiplexer_39_out), .sel(register_4_q));  // open: in3
  Multiplexer #(.select(2), .width(32), .enable("false")) multiplexer_40 (
    .in0(32'h1e0), .in1(32'h3e0), .in2(32'h1e0), .out(multiplexer_40_out), .sel(register_4_q));  // open: in3
  Multiplexer #(.select(2), .width(32), .enable("false")) multiplexer_41 (
    .in0(32'h7e0), .in1(32'h1e0), .in2(32'h3e0), .out(multiplexer_41_out), .sel(register_4_q));  // open: in3
  Multiplexer #(.select(2), .width(32), .enable("false")) multiplexer_42 (
    .in0(32'h1e0), .in1(32'h7e0), .in2(32'h1e0), .out(multiplexer_42_out), .sel(register_4_q));  // open: in3
  Multiplexer #(.select(2), .width(32), .enable("false")) multiplexer_43 (
    .in0(32'h60), .in1(32'h1e0), .in2(32'h1e0), .out(multiplexer_43_out), .sel(register_4_q));  // open: in3
  Multiplexer #(.select(2), .width(32), .enable("false")) multiplexer_44 (
    .in0({32{1'b0}}), .in1(32'h60), .in2(32'h1e0), .out(multiplexer_44_out), .sel(register_4_q));  // open: in3
  Multiplexer #(.select(2), .width(32), .enable("false")) multiplexer_45 (
    .in0(32'h1e0), .in1(32'h60), .in2({32{1'b0}}), .out(multiplexer_45_out), .sel(register_4_q));  // open: in3
  Multiplexer #(.select(2), .width(32), .enable("false")) multiplexer_46 (
    .in0(32'h1e0), .in1(32'h7e0), .in2(32'h1e0), .out(multiplexer_46_out), .sel(register_4_q));  // open: in3
  Multiplexer #(.select(2), .width(32), .enable("false")) multiplexer_47 (
    .in0(32'h3e0), .in1(32'h1e0), .in2(32'h7e0), .out(multiplexer_47_out), .sel(register_4_q));  // open: in3
  Multiplexer #(.select(2), .width(32), .enable("false")) multiplexer_48 (
    .in0(32'h1fe0), .in1(32'h7e0), .in2(32'h1e0), .out(multiplexer_48_out), .sel(register_4_q));  // open: in3
  Register #(.width(2), .trigger("falling"), .Select("low")) register_4 (
    .D(register_5_q), .Q(register_4_q), .clk(EX_ecall));  // open: en, clr
  Register #(.width(2), .trigger("falling"), .Select("low")) register_5 (
    .D(EX_R1[1:0]), .Q(register_5_q), .clk(EX_ecall));  // open: en, clr
  Multiplexer #(.select(2), .width(32), .enable("false")) multiplexer_49 (
    .in0(32'h60), .in1({32{1'b0}}), .in2({32{1'b0}}), .out(multiplexer_49_out), .sel(register_4_q));  // open: in3
  assign \行2  = \点阵_1__2_2  | multiplexer_49_out;  // OR_Gate or_18, 32 bits wide
  assign \行7  = \点阵_1__7_2  | multiplexer_22_out;  // OR_Gate or_19, 32 bits wide
  assign \行8  = \点阵_1__8_2  | multiplexer_23_out;  // OR_Gate or_20, 32 bits wide
  assign \行9  = \点阵_1__9_2  | multiplexer_48_out;  // OR_Gate or_21, 32 bits wide
  assign \行10  = \点阵_1__10_2  | multiplexer_24_out;  // OR_Gate or_22, 32 bits wide
  assign \行11  = \点阵_1__11_2  | multiplexer_25_out;  // OR_Gate or_23, 32 bits wide
  assign \行12  = \点阵_1__12_2  | multiplexer_26_out;  // OR_Gate or_24, 32 bits wide
  assign \行13  = \点阵_1__13_2  | multiplexer_27_out;  // OR_Gate or_25, 32 bits wide
  assign \行14  = \点阵_1__14_2  | multiplexer_28_out;  // OR_Gate or_26, 32 bits wide
  assign \行15  = \点阵_1__15_2  | multiplexer_29_out;  // OR_Gate or_27, 32 bits wide
  assign \行16  = \点阵_1__16_2  | multiplexer_30_out;  // OR_Gate or_28, 32 bits wide
  assign \行17  = \点阵_1__17_2  | multiplexer_31_out;  // OR_Gate or_29, 32 bits wide
  assign \行18  = \点阵_1__18_2  | multiplexer_32_out;  // OR_Gate or_30, 32 bits wide
  assign \行19  = \点阵_1__19_2  | multiplexer_33_out;  // OR_Gate or_31, 32 bits wide
  assign \行20  = \点阵_1__20_2  | multiplexer_34_out;  // OR_Gate or_32, 32 bits wide
  assign \行21  = \点阵_1__21_2  | multiplexer_35_out;  // OR_Gate or_33, 32 bits wide
  assign \行22  = \点阵_1__22_2  | multiplexer_36_out;  // OR_Gate or_34, 32 bits wide
  assign \行23  = \点阵_1__23_2  | multiplexer_37_out;  // OR_Gate or_35, 32 bits wide
  assign \行24  = \点阵_1__24_2  | multiplexer_38_out;  // OR_Gate or_36, 32 bits wide
  assign \行25  = \点阵_1__25_2  | multiplexer_39_out;  // OR_Gate or_37, 32 bits wide
  assign \行26  = \点阵_1__26_2  | multiplexer_40_out;  // OR_Gate or_38, 32 bits wide
  assign \行27  = \点阵_1__27_2  | multiplexer_41_out;  // OR_Gate or_39, 32 bits wide
  assign \行28  = \点阵_1__28_2  | multiplexer_42_out;  // OR_Gate or_40, 32 bits wide
  assign \行29  = \点阵_1__29_2  | multiplexer_43_out;  // OR_Gate or_41, 32 bits wide
  assign \行30  = \点阵_1__30_2  | multiplexer_44_out;  // OR_Gate or_42, 32 bits wide
  assign \行31  = \点阵_1__31_2  | multiplexer_20_out;  // OR_Gate or_43, 32 bits wide
  assign \行3  = \点阵_1__3_2  | multiplexer_45_out;  // OR_Gate or_44, 32 bits wide
  assign \行4  = \点阵_1__4_2  | multiplexer_21_out;  // OR_Gate or_45, 32 bits wide
  assign \行5  = \点阵_1__5_2  | multiplexer_46_out;  // OR_Gate or_46, 32 bits wide
  assign \行6  = \点阵_1__6_2  | multiplexer_47_out;  // OR_Gate or_47, 32 bits wide

  // Other names for the same wires on the sheet: IR[31:0] = {ID_IR[31], ID_Funct[4], ID_IR[29:26], ID_Funct[3], ID_IR[24:15], ID_Funct[2:0], ID_IR[11:0]};
  //   RD_num[4:0] = ID_IR[11:7]; ID_IR (some bits) = ID_Funct; high = ALUResult[1]; EM_ADDR[9:0] = ALUResult[11:2];
  //   控制信号[1:0] = EX_R1[1:0]; ID_OP[4:0] = ID_IR[6:2]; RDin[31:0] = MEMWB

  // Notes on the sheet:
  //   时空图监测，可删除
  //   0号为刷新地址
  //   中断响应阶段
  //   保存断点
  //   中断使能位(用于开关中断)
  //   判断中断使能
  //   Reset 
  //   Reset 
  //   Reset 
  //   中断响应
  //   清除中断
  //   contents of rom_1 (hex, n*v repeats v):
  //   b13 293 ffc00313 393 413 493 913 993 300513 a00613 693 168693 18b2403 2cb2483 20040413 100c13 bc1c13
  //   18484b3 8b2c23 68b2223 29b2623 49b2623 593 158593 7073 feb51ce3 10b2903 24b2983 40090913 100c13
  //   cc1c13 18989b3 12b2823 72b2623 33b2223 53b2c23 593 158593 7073 feb51ce3 f8d616e3 693 168693 18b2403
  //   2cb2483 30040413 300c13 ac1c13 18484b3 8b2c23 68b2223 29b2623 49b2623 593 158593 7073 feb51ce3
  //   10b2903 24b2983 60090913 300c13 bc1c13 18989b3 12b2823 72b2623 33b2223 53b2c23 593 158593 7073
  //   feb51ce3 f8d616e3 3cb2a03 300c13 10c1c13 18a0a33 34b2c23 34b2e23 54b2023 18b2403 2cb2483 30040413
  //   300c13 ac1c13 18484b3 8b2c23 68b2223 29b2623 49b2623 593 158593 7073 feb51ce3 3cb2a03 300c13 10c1c13
  //   18a0a33 34b2c23 34b2e23 54b2023 10b2903 24b2983 60090913 300c13 bc1c13 18989b3 12b2823 72b2623
  //   33b2223 53b2c23 593 158593 7073 feb51ce3 f59ff06f 8000c93 d93 dad03 1d1d13 1ada023 4d8d93 ff9d98e3
  //   27b1a63 e13 5e1c63 400b13 100293 200893 73 240006f ffc00b13 293 893 73 100006f b13 100893 73 200073
  //   指令存储器
  //   指令探针
  //   指令字
  //   JAL
  //   JALR
  //   URET
  //   Beq
  //   Bne
  //   MemToReg
  //   MemWrite
  //   AluOP
  //   AluSrcB
  //   RegWrite
  //   数据存储器
endmodule

module IF_ID (
  input  Predictin,
  input  [31:0] PCin,
  input  [31:0] IRin,
  input  RST,
  input  EN_H,
  input  CLK,
  output Predictout,
  output [31:0] PCout,
  output [31:0] IRout
);

  wire multiplexer_1_out;
  wire [31:0] multiplexer_2_out, multiplexer_3_out;

  Multiplexer #(.enable("false")) multiplexer_1 (.in0(Predictin), .in1(1'b0), .out(multiplexer_1_out), .sel(RST));
  Multiplexer #(.width(32), .enable("false")) multiplexer_2 (
    .in0(PCin), .in1({32{1'b0}}), .out(multiplexer_2_out), .sel(RST));
  Multiplexer #(.width(32), .enable("false")) multiplexer_3 (
    .in0(IRin), .in1({32{1'b0}}), .out(multiplexer_3_out), .sel(RST));
  Register #(.width(1), .Select("low")) register_1 (
    .D(multiplexer_1_out), .en(EN_H), .Q(Predictout), .clk(CLK));  // open: clr
  Register #(.width(32), .Select("low")) register_2 (
    .D(multiplexer_2_out), .en(EN_H), .Q(PCout), .clk(CLK));  // open: clr
  Register #(.width(32), .Select("low")) register_3 (
    .D(multiplexer_3_out), .en(EN_H), .Q(IRout), .clk(CLK));  // open: clr
endmodule

module ID_EX (
  input  callin,
  input  Predictin,
  input  uretin,
  input  [1:0] R2Forwardin,
  input  bgeuin,
  input  [1:0] R1Forwardin,
  input  lhuin,
  input  [31:0] PCin,
  input  Beqin,
  input  Bnein,
  input  [31:0] IRin,
  input  MemToRegin,
  input  [31:0] Imm_I_in,
  input  MemWritein,
  input  AluSrcBin,
  input  [31:0] Imm_S_in,
  input  RegWritein,
  input  S_typein,
  input  [31:0] Imm_B_in,
  input  Jalin,
  input  Jalrin,
  input  [31:0] Imm_J_in,
  input  [3:0] AluOpin,
  input  Haltin,
  input  [4:0] W_in,
  input  [31:0] R1in,
  input  sltiuin,
  input  [31:0] R2in,
  input  RST,
  input  EN_H,
  input  CLK,
  output callout,
  output Predictou9t,
  output uretout,
  output [1:0] R2Forwardout,
  output bgeuout,
  output [1:0] R1Forwardout,
  output lhuout,
  output [31:0] PCout,
  output Beqout,
  output Bneout,
  output [31:0] IRout,
  output MemToRegout,
  output [31:0] Imm_I_out,
  output MemWriteout,
  output AluSrcBout,
  output [31:0] Imm_S_out,
  output RegWriteout,
  output S_Typeout,
  output [31:0] Imm_B_out,
  output Jalout,
  output Jalrout,
  output [31:0] Imm_J_out,
  output [3:0] AluOpout,
  output Haltout,
  output [4:0] W_out,
  output [31:0] R1out,
  output sltiuout,
  output [31:0] R2out
);

  wire multiplexer_1_out, multiplexer_13_out, multiplexer_14_out, multiplexer_15_out, multiplexer_16_out,
       multiplexer_17_out, multiplexer_18_out, multiplexer_19_out, multiplexer_20_out, multiplexer_21_out,
       multiplexer_22_out, multiplexer_23_out, multiplexer_24_out, multiplexer_25_out, multiplexer_26_out,
       multiplexer_28_out;
  wire [1:0] multiplexer_2_out, multiplexer_3_out;
  wire [3:0] multiplexer_10_out;
  wire [4:0] multiplexer_27_out;
  wire [31:0] multiplexer_4_out, multiplexer_5_out, multiplexer_6_out, multiplexer_7_out, multiplexer_8_out,
       multiplexer_9_out, multiplexer_11_out, multiplexer_12_out;

  Multiplexer #(.enable("false")) multiplexer_1 (.in0(callin), .in1(1'b0), .out(multiplexer_1_out), .sel(RST));
  Multiplexer #(.width(2), .enable("false")) multiplexer_2 (
    .in0(R2Forwardin), .in1(2'b00), .out(multiplexer_2_out), .sel(RST));
  Multiplexer #(.width(2), .enable("false")) multiplexer_3 (
    .in0(R1Forwardin), .in1(2'b00), .out(multiplexer_3_out), .sel(RST));
  Multiplexer #(.width(32), .enable("false")) multiplexer_4 (
    .in0(PCin), .in1({32{1'b0}}), .out(multiplexer_4_out), .sel(RST));
  Multiplexer #(.width(32), .enable("false")) multiplexer_5 (
    .in0(IRin), .in1({32{1'b0}}), .out(multiplexer_5_out), .sel(RST));
  Multiplexer #(.width(32), .enable("false")) multiplexer_6 (
    .in0(Imm_I_in), .in1({32{1'b0}}), .out(multiplexer_6_out), .sel(RST));
  Multiplexer #(.width(32), .enable("false")) multiplexer_7 (
    .in0(Imm_S_in), .in1({32{1'b0}}), .out(multiplexer_7_out), .sel(RST));
  Multiplexer #(.width(32), .enable("false")) multiplexer_8 (
    .in0(Imm_B_in), .in1({32{1'b0}}), .out(multiplexer_8_out), .sel(RST));
  Multiplexer #(.width(32), .enable("false")) multiplexer_9 (
    .in0(Imm_J_in), .in1({32{1'b0}}), .out(multiplexer_9_out), .sel(RST));
  Multiplexer #(.width(4), .enable("false")) multiplexer_10 (
    .in0(AluOpin), .in1(4'b0000), .out(multiplexer_10_out), .sel(RST));
  Multiplexer #(.width(32), .enable("false")) multiplexer_11 (
    .in0(R1in), .in1({32{1'b0}}), .out(multiplexer_11_out), .sel(RST));
  Multiplexer #(.width(32), .enable("false")) multiplexer_12 (
    .in0(R2in), .in1({32{1'b0}}), .out(multiplexer_12_out), .sel(RST));
  Register #(.width(1), .Select("low")) register_1 (
    .D(multiplexer_1_out), .en(EN_H), .Q(callout), .clk(CLK));  // open: clr
  Register #(.width(2), .Select("low")) register_2 (
    .D(multiplexer_2_out), .en(EN_H), .Q(R2Forwardout), .clk(CLK));  // open: clr
  Register #(.width(2), .Select("low")) register_3 (
    .D(multiplexer_3_out), .en(EN_H), .Q(R1Forwardout), .clk(CLK));  // open: clr
  Register #(.width(32), .Select("low")) register_4 (
    .D(multiplexer_4_out), .en(EN_H), .Q(PCout), .clk(CLK));  // open: clr
  Register #(.width(32), .Select("low")) register_5 (
    .D(multiplexer_5_out), .en(EN_H), .Q(IRout), .clk(CLK));  // open: clr
  Register #(.width(32), .Select("low")) register_6 (
    .D(multiplexer_6_out), .en(EN_H), .Q(Imm_I_out), .clk(CLK));  // open: clr
  Register #(.width(32), .Select("low")) register_7 (
    .D(multiplexer_7_out), .en(EN_H), .Q(Imm_S_out), .clk(CLK));  // open: clr
  Register #(.width(32), .Select("low")) register_8 (
    .D(multiplexer_8_out), .en(EN_H), .Q(Imm_B_out), .clk(CLK));  // open: clr
  Register #(.width(32), .Select("low")) register_9 (
    .D(multiplexer_9_out), .en(EN_H), .Q(Imm_J_out), .clk(CLK));  // open: clr
  Register #(.width(4), .Select("low")) register_10 (
    .D(multiplexer_10_out), .en(EN_H), .Q(AluOpout), .clk(CLK));  // open: clr
  Register #(.width(32), .Select("low")) register_11 (
    .D(multiplexer_11_out), .en(EN_H), .Q(R1out), .clk(CLK));  // open: clr
  Register #(.width(32), .Select("low")) register_12 (
    .D(multiplexer_12_out), .en(EN_H), .Q(R2out), .clk(CLK));  // open: clr
  Multiplexer #(.enable("false")) multiplexer_13 (.in0(Predictin), .in1(1'b0), .out(multiplexer_13_out), .sel(RST));
  Multiplexer #(.enable("false")) multiplexer_14 (.in0(uretin), .in1(1'b0), .out(multiplexer_14_out), .sel(RST));
  Multiplexer #(.enable("false")) multiplexer_15 (.in0(bgeuin), .in1(1'b0), .out(multiplexer_15_out), .sel(RST));
  Multiplexer #(.enable("false")) multiplexer_16 (.in0(lhuin), .in1(1'b0), .out(multiplexer_16_out), .sel(RST));
  Multiplexer #(.enable("false")) multiplexer_17 (.in0(Beqin), .in1(1'b0), .out(multiplexer_17_out), .sel(RST));
  Multiplexer #(.enable("false")) multiplexer_18 (.in0(Bnein), .in1(1'b0), .out(multiplexer_18_out), .sel(RST));
  Multiplexer #(.enable("false")) multiplexer_19 (.in0(MemToRegin), .in1(1'b0), .out(multiplexer_19_out), .sel(RST));
  Multiplexer #(.enable("false")) multiplexer_20 (.in0(MemWritein), .in1(1'b0), .out(multiplexer_20_out), .sel(RST));
  Multiplexer #(.enable("false")) multiplexer_21 (.in0(AluSrcBin), .in1(1'b0), .out(multiplexer_21_out), .sel(RST));
  Multiplexer #(.enable("false")) multiplexer_22 (.in0(RegWritein), .in1(1'b0), .out(multiplexer_22_out), .sel(RST));
  Multiplexer #(.enable("false")) multiplexer_23 (.in0(S_typein), .in1(1'b0), .out(multiplexer_23_out), .sel(RST));
  Multiplexer #(.enable("false")) multiplexer_24 (.in0(Jalin), .in1(1'b0), .out(multiplexer_24_out), .sel(RST));
  Multiplexer #(.enable("false")) multiplexer_25 (.in0(Jalrin), .in1(1'b0), .out(multiplexer_25_out), .sel(RST));
  Multiplexer #(.enable("false")) multiplexer_26 (.in0(Haltin), .in1(1'b0), .out(multiplexer_26_out), .sel(RST));
  Multiplexer #(.width(5), .enable("false")) multiplexer_27 (
    .in0(W_in), .in1({5{1'b0}}), .out(multiplexer_27_out), .sel(RST));
  Multiplexer #(.enable("false")) multiplexer_28 (.in0(sltiuin), .in1(1'b0), .out(multiplexer_28_out), .sel(RST));
  Register #(.width(1), .Select("low")) register_13 (
    .D(multiplexer_13_out), .en(EN_H), .Q(Predictou9t), .clk(CLK));  // open: clr
  Register #(.width(1), .Select("low")) register_14 (
    .D(multiplexer_14_out), .en(EN_H), .Q(uretout), .clk(CLK));  // open: clr
  Register #(.width(1), .Select("low")) register_15 (
    .D(multiplexer_15_out), .en(EN_H), .Q(bgeuout), .clk(CLK));  // open: clr
  Register #(.width(1), .Select("low")) register_16 (
    .D(multiplexer_16_out), .en(EN_H), .Q(lhuout), .clk(CLK));  // open: clr
  Register #(.width(1), .Select("low")) register_17 (
    .D(multiplexer_17_out), .en(EN_H), .Q(Beqout), .clk(CLK));  // open: clr
  Register #(.width(1), .Select("low")) register_18 (
    .D(multiplexer_18_out), .en(EN_H), .Q(Bneout), .clk(CLK));  // open: clr
  Register #(.width(1), .Select("low")) register_19 (
    .D(multiplexer_19_out), .en(EN_H), .Q(MemToRegout), .clk(CLK));  // open: clr
  Register #(.width(1), .Select("low")) register_20 (
    .D(multiplexer_20_out), .en(EN_H), .Q(MemWriteout), .clk(CLK));  // open: clr
  Register #(.width(1), .Select("low")) register_21 (
    .D(multiplexer_21_out), .en(EN_H), .Q(AluSrcBout), .clk(CLK));  // open: clr
  Register #(.width(1), .Select("low")) register_22 (
    .D(multiplexer_22_out), .en(EN_H), .Q(RegWriteout), .clk(CLK));  // open: clr
  Register #(.width(1), .Select("low")) register_23 (
    .D(multiplexer_23_out), .en(EN_H), .Q(S_Typeout), .clk(CLK));  // open: clr
  Register #(.width(1), .Select("low")) register_24 (
    .D(multiplexer_24_out), .en(EN_H), .Q(Jalout), .clk(CLK));  // open: clr
  Register #(.width(1), .Select("low")) register_25 (
    .D(multiplexer_25_out), .en(EN_H), .Q(Jalrout), .clk(CLK));  // open: clr
  Register #(.width(1), .Select("low")) register_26 (
    .D(multiplexer_26_out), .en(EN_H), .Q(Haltout), .clk(CLK));  // open: clr
  Register #(.width(5), .Select("low")) register_27 (
    .D(multiplexer_27_out), .en(EN_H), .Q(W_out), .clk(CLK));  // open: clr
  Register #(.width(1), .Select("low")) register_28 (
    .D(multiplexer_28_out), .en(EN_H), .Q(sltiuout), .clk(CLK));  // open: clr
endmodule

module EX_MEM (
  input  lhuin,
  input  MemToRegin,
  input  [31:0] PCin,
  input  MemWritein,
  input  [31:0] IRin,
  input  JAMPin,
  input  RegWritein,
  input  [31:0] Resultin,
  input  Haltin,
  input  [31:0] MDatain,
  input  [4:0] W_in,
  input  lessin,
  input  sltiuin,
  input  RST,
  input  EN_H,
  input  CLK,
  output lhuout,
  output MemToRegout,
  output [31:0] PCout,
  output MemWriteout,
  output [31:0] IRout,
  output JAMPout,
  output RegWriteout,
  output [31:0] Resultout,
  output Haltout,
  output [31:0] Mdataout,
  output [4:0] W_out,
  output lessout,
  output sltiuout
);

  wire multiplexer_5_out, multiplexer_6_out, multiplexer_7_out, multiplexer_8_out, multiplexer_9_out,
       multiplexer_10_out, multiplexer_12_out, multiplexer_13_out;
  wire [4:0] multiplexer_11_out;
  wire [31:0] multiplexer_1_out, multiplexer_2_out, multiplexer_3_out, multiplexer_4_out;

  Multiplexer #(.width(32), .enable("false")) multiplexer_1 (
    .in0(PCin), .in1({32{1'b0}}), .out(multiplexer_1_out), .sel(RST));
  Multiplexer #(.width(32), .enable("false")) multiplexer_2 (
    .in0(IRin), .in1({32{1'b0}}), .out(multiplexer_2_out), .sel(RST));
  Multiplexer #(.width(32), .enable("false")) multiplexer_3 (
    .in0(Resultin), .in1({32{1'b0}}), .out(multiplexer_3_out), .sel(RST));
  Multiplexer #(.width(32), .enable("false")) multiplexer_4 (
    .in0(MDatain), .in1({32{1'b0}}), .out(multiplexer_4_out), .sel(RST));
  Register #(.width(32), .Select("low")) register_1 (
    .D(multiplexer_1_out), .en(EN_H), .Q(PCout), .clk(CLK));  // open: clr
  Register #(.width(32), .Select("low")) register_2 (
    .D(multiplexer_2_out), .en(EN_H), .Q(IRout), .clk(CLK));  // open: clr
  Register #(.width(32), .Select("low")) register_3 (
    .D(multiplexer_3_out), .en(EN_H), .Q(Resultout), .clk(CLK));  // open: clr
  Register #(.width(32), .Select("low")) register_4 (
    .D(multiplexer_4_out), .en(EN_H), .Q(Mdataout), .clk(CLK));  // open: clr
  Multiplexer #(.enable("false")) multiplexer_5 (.in0(lhuin), .in1(1'b0), .out(multiplexer_5_out), .sel(RST));
  Multiplexer #(.enable("false")) multiplexer_6 (.in0(MemToRegin), .in1(1'b0), .out(multiplexer_6_out), .sel(RST));
  Multiplexer #(.enable("false")) multiplexer_7 (.in0(MemWritein), .in1(1'b0), .out(multiplexer_7_out), .sel(RST));
  Multiplexer #(.enable("false")) multiplexer_8 (.in0(JAMPin), .in1(1'b0), .out(multiplexer_8_out), .sel(RST));
  Multiplexer #(.enable("false")) multiplexer_9 (.in0(RegWritein), .in1(1'b0), .out(multiplexer_9_out), .sel(RST));
  Multiplexer #(.enable("false")) multiplexer_10 (.in0(Haltin), .in1(1'b0), .out(multiplexer_10_out), .sel(RST));
  Multiplexer #(.width(5), .enable("false")) multiplexer_11 (
    .in0(W_in), .in1({5{1'b0}}), .out(multiplexer_11_out), .sel(RST));
  Multiplexer #(.enable("false")) multiplexer_12 (.in0(lessin), .in1(1'b0), .out(multiplexer_12_out), .sel(RST));
  Multiplexer #(.enable("false")) multiplexer_13 (.in0(sltiuin), .in1(1'b0), .out(multiplexer_13_out), .sel(RST));
  Register #(.width(1), .Select("low")) register_5 (
    .D(multiplexer_5_out), .en(EN_H), .Q(lhuout), .clk(CLK));  // open: clr
  Register #(.width(1), .Select("low")) register_6 (
    .D(multiplexer_6_out), .en(EN_H), .Q(MemToRegout), .clk(CLK));  // open: clr
  Register #(.width(1), .Select("low")) register_7 (
    .D(multiplexer_7_out), .en(EN_H), .Q(MemWriteout), .clk(CLK));  // open: clr
  Register #(.width(1), .Select("low")) register_8 (
    .D(multiplexer_8_out), .en(EN_H), .Q(JAMPout), .clk(CLK));  // open: clr
  Register #(.width(1), .Select("low")) register_9 (
    .D(multiplexer_9_out), .en(EN_H), .Q(RegWriteout), .clk(CLK));  // open: clr
  Register #(.width(1), .Select("low")) register_10 (
    .D(multiplexer_10_out), .en(EN_H), .Q(Haltout), .clk(CLK));  // open: clr
  Register #(.width(5), .Select("low")) register_11 (
    .D(multiplexer_11_out), .en(EN_H), .Q(W_out), .clk(CLK));  // open: clr
  Register #(.width(1), .Select("low")) register_12 (
    .D(multiplexer_12_out), .en(EN_H), .Q(lessout), .clk(CLK));  // open: clr
  Register #(.width(1), .Select("low")) register_13 (
    .D(multiplexer_13_out), .en(EN_H), .Q(sltiuout), .clk(CLK));  // open: clr
endmodule

module MEM_WB (
  input  lhuin,
  input  highin,
  input  [31:0] PCin,
  input  MemToRegin,
  input  [31:0] IRin,
  input  JAMPin,
  input  RegWritein,
  input  [31:0] Resultin,
  input  Haltin,
  input  [31:0] RMDatain,
  input  [4:0] W_in,
  input  lessin,
  input  sltiuin,
  input  RST,
  input  EN_H,
  input  CLK,
  output lhuout,
  output highout,
  output [31:0] PCout,
  output MemToRegout,
  output [31:0] IRout,
  output JAMPout,
  output RegWriteout,
  output [31:0] Resultout,
  output Haltout,
  output [31:0] RMdataout,
  output [4:0] W_out,
  output lessout,
  output sltiuout
);

  wire multiplexer_5_out, multiplexer_6_out, multiplexer_7_out, multiplexer_8_out, multiplexer_9_out,
       multiplexer_10_out, multiplexer_12_out, multiplexer_13_out;
  wire [4:0] multiplexer_11_out;
  wire [31:0] multiplexer_1_out, multiplexer_2_out, multiplexer_3_out, multiplexer_4_out;

  Multiplexer #(.width(32), .enable("false")) multiplexer_1 (
    .in0(PCin), .in1({32{1'b0}}), .out(multiplexer_1_out), .sel(RST));
  Multiplexer #(.width(32), .enable("false")) multiplexer_2 (
    .in0(IRin), .in1({32{1'b0}}), .out(multiplexer_2_out), .sel(RST));
  Multiplexer #(.width(32), .enable("false")) multiplexer_3 (
    .in0(Resultin), .in1({32{1'b0}}), .out(multiplexer_3_out), .sel(RST));
  Multiplexer #(.width(32), .enable("false")) multiplexer_4 (
    .in0(RMDatain), .in1({32{1'b0}}), .out(multiplexer_4_out), .sel(RST));
  Register #(.width(32), .Select("low")) register_1 (
    .D(multiplexer_1_out), .en(EN_H), .Q(PCout), .clk(CLK));  // open: clr
  Register #(.width(32), .Select("low")) register_2 (
    .D(multiplexer_2_out), .en(EN_H), .Q(IRout), .clk(CLK));  // open: clr
  Register #(.width(32), .Select("low")) register_3 (
    .D(multiplexer_3_out), .en(EN_H), .Q(Resultout), .clk(CLK));  // open: clr
  Register #(.width(32), .Select("low")) register_4 (
    .D(multiplexer_4_out), .en(EN_H), .Q(RMdataout), .clk(CLK));  // open: clr
  Multiplexer #(.enable("false")) multiplexer_5 (.in0(lhuin), .in1(1'b0), .out(multiplexer_5_out), .sel(RST));
  Multiplexer #(.enable("false")) multiplexer_6 (.in0(highin), .in1(1'b0), .out(multiplexer_6_out), .sel(RST));
  Multiplexer #(.enable("false")) multiplexer_7 (.in0(MemToRegin), .in1(1'b0), .out(multiplexer_7_out), .sel(RST));
  Multiplexer #(.enable("false")) multiplexer_8 (.in0(JAMPin), .in1(1'b0), .out(multiplexer_8_out), .sel(RST));
  Multiplexer #(.enable("false")) multiplexer_9 (.in0(RegWritein), .in1(1'b0), .out(multiplexer_9_out), .sel(RST));
  Multiplexer #(.enable("false")) multiplexer_10 (.in0(Haltin), .in1(1'b0), .out(multiplexer_10_out), .sel(RST));
  Multiplexer #(.width(5), .enable("false")) multiplexer_11 (
    .in0(W_in), .in1({5{1'b0}}), .out(multiplexer_11_out), .sel(RST));
  Multiplexer #(.enable("false")) multiplexer_12 (.in0(lessin), .in1(1'b0), .out(multiplexer_12_out), .sel(RST));
  Multiplexer #(.enable("false")) multiplexer_13 (.in0(sltiuin), .in1(1'b0), .out(multiplexer_13_out), .sel(RST));
  Register #(.width(1), .Select("low")) register_5 (
    .D(multiplexer_5_out), .en(EN_H), .Q(lhuout), .clk(CLK));  // open: clr
  Register #(.width(1), .Select("low")) register_6 (
    .D(multiplexer_6_out), .en(EN_H), .Q(highout), .clk(CLK));  // open: clr
  Register #(.width(1), .Select("low")) register_7 (
    .D(multiplexer_7_out), .en(EN_H), .Q(MemToRegout), .clk(CLK));  // open: clr
  Register #(.width(1), .Select("low")) register_8 (
    .D(multiplexer_8_out), .en(EN_H), .Q(JAMPout), .clk(CLK));  // open: clr
  Register #(.width(1), .Select("low")) register_9 (
    .D(multiplexer_9_out), .en(EN_H), .Q(RegWriteout), .clk(CLK));  // open: clr
  Register #(.width(1), .Select("low")) register_10 (
    .D(multiplexer_10_out), .en(EN_H), .Q(Haltout), .clk(CLK));  // open: clr
  Register #(.width(5), .Select("low")) register_11 (
    .D(multiplexer_11_out), .en(EN_H), .Q(W_out), .clk(CLK));  // open: clr
  Register #(.width(1), .Select("low")) register_12 (
    .D(multiplexer_12_out), .en(EN_H), .Q(lessout), .clk(CLK));  // open: clr
  Register #(.width(1), .Select("low")) register_13 (
    .D(multiplexer_13_out), .en(EN_H), .Q(sltiuout), .clk(CLK));  // open: clr
endmodule

module \地图  (
  input  \写使能 ,
  input  [9:0] Addr,
  input  CLK,
  input  RST,
  input  [31:0] Data,
  output [31:0] \行1 ,
  output [31:0] \行9 ,
  output [31:0] \行17 ,
  output [31:0] \行25 ,
  output [31:0] \行2 ,
  output [31:0] \行10 ,
  output [31:0] \行18 ,
  output [31:0] \行26 ,
  output [31:0] \行3 ,
  output [31:0] \行11 ,
  output [31:0] \行19 ,
  output [31:0] \行27 ,
  output [31:0] \行4 ,
  output [31:0] \行12 ,
  output [31:0] \行20 ,
  output [31:0] \行28 ,
  output [31:0] \行5 ,
  output [31:0] \行13 ,
  output [31:0] \行21 ,
  output [31:0] \行29 ,
  output [31:0] \行6 ,
  output [31:0] \行14 ,
  output [31:0] \行22 ,
  output [31:0] \行30 ,
  output [31:0] \行7 ,
  output [31:0] \行15 ,
  output [31:0] \行23 ,
  output [31:0] \行31 ,
  output [31:0] \行8 ,
  output [31:0] \行16 ,
  output [31:0] \行24 ,
  output [31:0] \行32 
);

  wire and_1_out, and_2_out, and_3_out, and_4_out, and_5_out, and_6_out, and_7_out, and_8_out, and_9_out,
       and_10_out, and_11_out, and_12_out, and_13_out, and_14_out, and_15_out, and_16_out, and_17_out,
       and_18_out, and_19_out, and_20_out, and_21_out, and_22_out, and_23_out, and_24_out, and_25_out,
       and_26_out, and_27_out, and_28_out, and_29_out, and_30_out, and_31_out, and_32_out, \行1_t , \行2_t ,
       \行3_t , \行4_t , \行5_t , \行6_t , \行7_t , \行8_t , \行9_t , \行10_t , \行11_t , \行12_t , \行13_t , \行14_t ,
       \行15_t , \行16_t , \行17_t , \行18_t , \行19_t , \行20_t , \行21_t , \行22_t , \行23_t , \行24_t , \行25_t ,
       \行26_t , \行27_t , \行28_t , \行29_t , \行30_t , \行31_t , \行32_t ;

  and and_1 (and_1_out, \写使能 , \行1_t );
  and and_2 (and_2_out, \写使能 , \行2_t );
  and and_3 (and_3_out, \写使能 , \行3_t );
  and and_4 (and_4_out, \写使能 , \行4_t );
  and and_5 (and_5_out, \写使能 , \行5_t );
  and and_6 (and_6_out, \写使能 , \行6_t );
  and and_7 (and_7_out, \写使能 , \行7_t );
  and and_8 (and_8_out, \写使能 , \行8_t );
  Register #(.width(32), .Select("low")) register_1 (.D(Data), .en(and_1_out), .Q(\行1 ), .clk(CLK), .clr(RST));
  Register #(.width(32), .Select("low")) register_2 (.D(Data), .en(and_2_out), .Q(\行2 ), .clk(CLK), .clr(RST));
  Register #(.width(32), .Select("low")) register_3 (.D(Data), .en(and_3_out), .Q(\行3 ), .clk(CLK), .clr(RST));
  Register #(.width(32), .Select("low")) register_4 (.D(Data), .en(and_4_out), .Q(\行4 ), .clk(CLK), .clr(RST));
  Register #(.width(32), .Select("low")) register_5 (.D(Data), .en(and_5_out), .Q(\行5 ), .clk(CLK), .clr(RST));
  Register #(.width(32), .Select("low")) register_6 (.D(Data), .en(and_6_out), .Q(\行6 ), .clk(CLK), .clr(RST));
  Register #(.width(32), .Select("low")) register_7 (.D(Data), .en(and_7_out), .Q(\行7 ), .clk(CLK), .clr(RST));
  Register #(.width(32), .Select("low")) register_8 (.D(Data), .en(and_8_out), .Q(\行8 ), .clk(CLK), .clr(RST));
  and and_9 (and_9_out, \写使能 , \行9_t );
  and and_10 (and_10_out, \写使能 , \行10_t );
  and and_11 (and_11_out, \写使能 , \行11_t );
  and and_12 (and_12_out, \写使能 , \行12_t );
  and and_13 (and_13_out, \写使能 , \行13_t );
  and and_14 (and_14_out, \写使能 , \行14_t );
  and and_15 (and_15_out, \写使能 , \行15_t );
  and and_16 (and_16_out, \写使能 , \行16_t );
  Register #(.width(32), .Select("low")) register_9 (.D(Data), .en(and_9_out), .Q(\行9 ), .clk(CLK), .clr(RST));
  Register #(.width(32), .Select("low")) register_10 (.D(Data), .en(and_10_out), .Q(\行10 ), .clk(CLK), .clr(RST));
  Register #(.width(32), .Select("low")) register_11 (.D(Data), .en(and_11_out), .Q(\行11 ), .clk(CLK), .clr(RST));
  Register #(.width(32), .Select("low")) register_12 (.D(Data), .en(and_12_out), .Q(\行12 ), .clk(CLK), .clr(RST));
  Register #(.width(32), .Select("low")) register_13 (.D(Data), .en(and_13_out), .Q(\行13 ), .clk(CLK), .clr(RST));
  Register #(.width(32), .Select("low")) register_14 (.D(Data), .en(and_14_out), .Q(\行14 ), .clk(CLK), .clr(RST));
  Register #(.width(32), .Select("low")) register_15 (.D(Data), .en(and_15_out), .Q(\行15 ), .clk(CLK), .clr(RST));
  Register #(.width(32), .Select("low")) register_16 (.D(Data), .en(and_16_out), .Q(\行16 ), .clk(CLK), .clr(RST));
  and and_17 (and_17_out, \写使能 , \行17_t );
  and and_18 (and_18_out, \写使能 , \行18_t );
  and and_19 (and_19_out, \写使能 , \行19_t );
  and and_20 (and_20_out, \写使能 , \行20_t );
  and and_21 (and_21_out, \写使能 , \行21_t );
  and and_22 (and_22_out, \写使能 , \行22_t );
  and and_23 (and_23_out, \写使能 , \行23_t );
  and and_24 (and_24_out, \写使能 , \行24_t );
  Register #(.width(32), .Select("low")) register_17 (.D(Data), .en(and_17_out), .Q(\行17 ), .clk(CLK), .clr(RST));
  Register #(.width(32), .Select("low")) register_18 (.D(Data), .en(and_18_out), .Q(\行18 ), .clk(CLK), .clr(RST));
  Register #(.width(32), .Select("low")) register_19 (.D(Data), .en(and_19_out), .Q(\行19 ), .clk(CLK), .clr(RST));
  Register #(.width(32), .Select("low")) register_20 (.D(Data), .en(and_20_out), .Q(\行20 ), .clk(CLK), .clr(RST));
  Register #(.width(32), .Select("low")) register_21 (.D(Data), .en(and_21_out), .Q(\行21 ), .clk(CLK), .clr(RST));
  Register #(.width(32), .Select("low")) register_22 (.D(Data), .en(and_22_out), .Q(\行22 ), .clk(CLK), .clr(RST));
  Register #(.width(32), .Select("low")) register_23 (.D(Data), .en(and_23_out), .Q(\行23 ), .clk(CLK), .clr(RST));
  Register #(.width(32), .Select("low")) register_24 (.D(Data), .en(and_24_out), .Q(\行24 ), .clk(CLK), .clr(RST));
  and and_25 (and_25_out, \写使能 , \行25_t );
  and and_26 (and_26_out, \写使能 , \行26_t );
  and and_27 (and_27_out, \写使能 , \行27_t );
  and and_28 (and_28_out, \写使能 , \行28_t );
  and and_29 (and_29_out, \写使能 , \行29_t );
  and and_30 (and_30_out, \写使能 , \行30_t );
  and and_31 (and_31_out, \写使能 , \行31_t );
  and and_32 (and_32_out, \写使能 , \行32_t );
  Register #(.width(32), .Select("low")) register_25 (.D(Data), .en(and_25_out), .Q(\行25 ), .clk(CLK), .clr(RST));
  Register #(.width(32), .Select("low")) register_26 (.D(Data), .en(and_26_out), .Q(\行26 ), .clk(CLK), .clr(RST));
  Register #(.width(32), .Select("low")) register_27 (.D(Data), .en(and_27_out), .Q(\行27 ), .clk(CLK), .clr(RST));
  Register #(.width(32), .Select("low")) register_28 (.D(Data), .en(and_28_out), .Q(\行28 ), .clk(CLK), .clr(RST));
  Register #(.width(32), .Select("low")) register_29 (.D(Data), .en(and_29_out), .Q(\行29 ), .clk(CLK), .clr(RST));
  Register #(.width(32), .Select("low")) register_30 (.D(Data), .en(and_30_out), .Q(\行30 ), .clk(CLK), .clr(RST));
  Register #(.width(32), .Select("low")) register_31 (.D(Data), .en(and_31_out), .Q(\行31 ), .clk(CLK), .clr(RST));
  Register #(.width(32), .Select("low")) register_32 (.D(Data), .en(and_32_out), .Q(\行32 ), .clk(CLK), .clr(RST));
  Demultiplexer #(.select(5), .enable("false")) demultiplexer_1 (
    .out0(\行1_t ), .out1(\行2_t ), .out2(\行3_t ), .out3(\行4_t ), .out4(\行5_t ), .out5(\行6_t ), .out6(\行7_t ),
    .out7(\行8_t ), .out8(\行9_t ), .out9(\行10_t ), .out10(\行11_t ), .out11(\行12_t ), .out12(\行13_t ),
    .out13(\行14_t ), .out14(\行15_t ), .out15(\行16_t ), .out16(\行17_t ), .out17(\行18_t ), .out18(\行19_t ),
    .out19(\行20_t ), .out20(\行21_t ), .out21(\行22_t ), .out22(\行23_t ), .out23(\行24_t ), .out24(\行25_t ),
    .out25(\行26_t ), .out26(\行27_t ), .out27(\行28_t ), .out28(\行29_t ), .out29(\行30_t ), .out30(\行31_t ),
    .out31(\行32_t ), .in(1'b1), .sel(Addr[4:0]));
endmodule
module \点阵  (
  input  \写使能 ,
  input  [31:0] _1,
  input  [31:0] _2,
  input  [31:0] _3,
  input  [31:0] _4,
  input  [31:0] _5,
  input  [31:0] _6,
  input  [31:0] _7,
  input  [31:0] _8,
  input  [31:0] _9,
  input  [31:0] _10,
  input  [31:0] _11,
  input  [31:0] _12,
  input  [31:0] _13,
  input  [31:0] _14,
  input  [31:0] _15,
  input  [31:0] _16,
  input  [31:0] _17,
  input  [31:0] _18,
  input  [31:0] _19,
  input  [31:0] _20,
  input  [31:0] _21,
  input  [31:0] _22,
  input  [31:0] _23,
  input  [31:0] _24,
  input  [31:0] _25,
  input  [31:0] _26,
  input  [31:0] _27,
  input  [31:0] _28,
  input  [31:0] _29,
  input  [31:0] _30,
  input  [31:0] _31,
  input  [31:0] _32,
  input  CLK,
  input  RST,
  output [31:0] _1_2,
  output [31:0] _2_2,
  output [31:0] _3_2,
  output [31:0] _4_2,
  output [31:0] _5_2,
  output [31:0] _6_2,
  output [31:0] _7_2,
  output [31:0] _8_2,
  output [31:0] _9_2,
  output [31:0] _10_2,
  output [31:0] _11_2,
  output [31:0] _12_2,
  output [31:0] _13_2,
  output [31:0] _14_2,
  output [31:0] _15_2,
  output [31:0] _16_2,
  output [31:0] _17_2,
  output [31:0] _18_2,
  output [31:0] _19_2,
  output [31:0] _20_2,
  output [31:0] _21_2,
  output [31:0] _22_2,
  output [31:0] _23_2,
  output [31:0] _24_2,
  output [31:0] _25_2,
  output [31:0] _26_2,
  output [31:0] _27_2,
  output [31:0] _28_2,
  output [31:0] _29_2,
  output [31:0] _30_2,
  output [31:0] _31_2,
  output [31:0] _32_2
);

  Register #(.width(32), .Select("low")) register_1 (.D(_1), .en(\写使能 ), .Q(_1_2), .clk(CLK), .clr(RST));
  Register #(.width(32), .Select("low")) register_2 (.D(_5), .en(\写使能 ), .Q(_5_2), .clk(CLK), .clr(RST));
  Register #(.width(32), .Select("low")) register_3 (.D(_9), .en(\写使能 ), .Q(_9_2), .clk(CLK), .clr(RST));
  Register #(.width(32), .Select("low")) register_4 (.D(_13), .en(\写使能 ), .Q(_13_2), .clk(CLK), .clr(RST));
  Register #(.width(32), .Select("low")) register_5 (.D(_17), .en(\写使能 ), .Q(_17_2), .clk(CLK), .clr(RST));
  Register #(.width(32), .Select("low")) register_6 (.D(_21), .en(\写使能 ), .Q(_21_2), .clk(CLK), .clr(RST));
  Register #(.width(32), .Select("low")) register_7 (.D(_25), .en(\写使能 ), .Q(_25_2), .clk(CLK), .clr(RST));
  Register #(.width(32), .Select("low")) register_8 (.D(_29), .en(\写使能 ), .Q(_29_2), .clk(CLK), .clr(RST));
  Register #(.width(32), .Select("low")) register_9 (.D(_2), .en(\写使能 ), .Q(_2_2), .clk(CLK), .clr(RST));
  Register #(.width(32), .Select("low")) register_10 (.D(_6), .en(\写使能 ), .Q(_6_2), .clk(CLK), .clr(RST));
  Register #(.width(32), .Select("low")) register_11 (.D(_10), .en(\写使能 ), .Q(_10_2), .clk(CLK), .clr(RST));
  Register #(.width(32), .Select("low")) register_12 (.D(_14), .en(\写使能 ), .Q(_14_2), .clk(CLK), .clr(RST));
  Register #(.width(32), .Select("low")) register_13 (.D(_18), .en(\写使能 ), .Q(_18_2), .clk(CLK), .clr(RST));
  Register #(.width(32), .Select("low")) register_14 (.D(_22), .en(\写使能 ), .Q(_22_2), .clk(CLK), .clr(RST));
  Register #(.width(32), .Select("low")) register_15 (.D(_26), .en(\写使能 ), .Q(_26_2), .clk(CLK), .clr(RST));
  Register #(.width(32), .Select("low")) register_16 (.D(_30), .en(\写使能 ), .Q(_30_2), .clk(CLK), .clr(RST));
  Register #(.width(32), .Select("low")) register_17 (.D(_3), .en(\写使能 ), .Q(_3_2), .clk(CLK), .clr(RST));
  Register #(.width(32), .Select("low")) register_18 (.D(_7), .en(\写使能 ), .Q(_7_2), .clk(CLK), .clr(RST));
  Register #(.width(32), .Select("low")) register_19 (.D(_11), .en(\写使能 ), .Q(_11_2), .clk(CLK), .clr(RST));
  Register #(.width(32), .Select("low")) register_20 (.D(_15), .en(\写使能 ), .Q(_15_2), .clk(CLK), .clr(RST));
  Register #(.width(32), .Select("low")) register_21 (.D(_19), .en(\写使能 ), .Q(_19_2), .clk(CLK), .clr(RST));
  Register #(.width(32), .Select("low")) register_22 (.D(_23), .en(\写使能 ), .Q(_23_2), .clk(CLK), .clr(RST));
  Register #(.width(32), .Select("low")) register_23 (.D(_27), .en(\写使能 ), .Q(_27_2), .clk(CLK), .clr(RST));
  Register #(.width(32), .Select("low")) register_24 (.D(_31), .en(\写使能 ), .Q(_31_2), .clk(CLK), .clr(RST));
  Register #(.width(32), .Select("low")) register_25 (.D(_4), .en(\写使能 ), .Q(_4_2), .clk(CLK), .clr(RST));
  Register #(.width(32), .Select("low")) register_26 (.D(_8), .en(\写使能 ), .Q(_8_2), .clk(CLK), .clr(RST));
  Register #(.width(32), .Select("low")) register_27 (.D(_12), .en(\写使能 ), .Q(_12_2), .clk(CLK), .clr(RST));
  Register #(.width(32), .Select("low")) register_28 (.D(_16), .en(\写使能 ), .Q(_16_2), .clk(CLK), .clr(RST));
  Register #(.width(32), .Select("low")) register_29 (.D(_20), .en(\写使能 ), .Q(_20_2), .clk(CLK), .clr(RST));
  Register #(.width(32), .Select("low")) register_30 (.D(_24), .en(\写使能 ), .Q(_24_2), .clk(CLK), .clr(RST));
  Register #(.width(32), .Select("low")) register_31 (.D(_28), .en(\写使能 ), .Q(_28_2), .clk(CLK), .clr(RST));
  Register #(.width(32), .Select("low")) register_32 (.D(_32), .en(\写使能 ), .Q(_32_2), .clk(CLK), .clr(RST));
endmodule

module test (
);

  wire button_1_out, button_2_out, button_3_out, CLK, clock_1_out, comparator_1_eq, comparator_1_lt,
       d_ff_1_q, nand_1_out;
  wire [12:0] CNT_num;
  wire [31:0] \玩家飞机_1_行1 , \玩家飞机_1_行2 , \玩家飞机_1_行3 , \玩家飞机_1_行4 , \玩家飞机_1_行5 , \玩家飞机_1_行6 , \玩家飞机_1_行7 ,
       \玩家飞机_1_行8 , \玩家飞机_1_行9 , \玩家飞机_1_行10 , \玩家飞机_1_行11 , \玩家飞机_1_行12 , \玩家飞机_1_行13 , \玩家飞机_1_行14 ,
       \玩家飞机_1_行15 , \玩家飞机_1_行16 , \玩家飞机_1_行17 , \玩家飞机_1_行18 , \玩家飞机_1_行19 , \玩家飞机_1_行20 , \玩家飞机_1_行21 ,
       \玩家飞机_1_行22 , \玩家飞机_1_行23 , \玩家飞机_1_行24 , \玩家飞机_1_行25 , \玩家飞机_1_行26 , \玩家飞机_1_行27 , \玩家飞机_1_行28 ,
       \玩家飞机_1_行29 , \玩家飞机_1_行30 , \玩家飞机_1_行31 , \玩家飞机_1_行32 ;

  Button button_1 (.out(button_1_out));
  Button button_2 (.out(button_2_out));
  Button button_3 (.out(button_3_out));
  \玩家飞机  \u_玩家飞机_1  (
    .IR1(button_1_out), .CLK(CLK), .IR2(button_2_out), .IR3(button_3_out), .\行1 (\玩家飞机_1_行1 ),
    .\行2 (\玩家飞机_1_行2 ), .\行3 (\玩家飞机_1_行3 ), .\行4 (\玩家飞机_1_行4 ), .\行5 (\玩家飞机_1_行5 ), .\行6 (\玩家飞机_1_行6 ),
    .\行7 (\玩家飞机_1_行7 ), .\行8 (\玩家飞机_1_行8 ), .\行9 (\玩家飞机_1_行9 ), .\行10 (\玩家飞机_1_行10 ), .\行11 (\玩家飞机_1_行11 ),
    .\行12 (\玩家飞机_1_行12 ), .\行13 (\玩家飞机_1_行13 ), .\行14 (\玩家飞机_1_行14 ), .\行15 (\玩家飞机_1_行15 ),
    .\行16 (\玩家飞机_1_行16 ), .\行17 (\玩家飞机_1_行17 ), .\行18 (\玩家飞机_1_行18 ), .\行19 (\玩家飞机_1_行19 ),
    .\行20 (\玩家飞机_1_行20 ), .\行21 (\玩家飞机_1_行21 ), .\行22 (\玩家飞机_1_行22 ), .\行23 (\玩家飞机_1_行23 ),
    .\行24 (\玩家飞机_1_行24 ), .\行25 (\玩家飞机_1_行25 ), .\行26 (\玩家飞机_1_行26 ), .\行27 (\玩家飞机_1_行27 ),
    .\行28 (\玩家飞机_1_行28 ), .\行29 (\玩家飞机_1_行29 ), .\行30 (\玩家飞机_1_行30 ), .\行31 (\玩家飞机_1_行31 ),
    .\行32 (\玩家飞机_1_行32 ));  // open: 警报铃声
  DotMatrix #(.inputtype("row"), .matrixcols(32), .matrixrows(32)) dotmatrix_1 (
    .row0(\玩家飞机_1_行1 ), .row1(\玩家飞机_1_行2 ), .row2(\玩家飞机_1_行3 ), .row3(\玩家飞机_1_行4 ), .row4(\玩家飞机_1_行5 ),
    .row5(\玩家飞机_1_行6 ), .row6(\玩家飞机_1_行7 ), .row7(\玩家飞机_1_行8 ), .row8(\玩家飞机_1_行9 ), .row9(\玩家飞机_1_行10 ),
    .row10(\玩家飞机_1_行11 ), .row11(\玩家飞机_1_行12 ), .row12(\玩家飞机_1_行13 ), .row13(\玩家飞机_1_行14 ),
    .row14(\玩家飞机_1_行15 ), .row15(\玩家飞机_1_行16 ), .row16(\玩家飞机_1_行17 ), .row17(\玩家飞机_1_行18 ),
    .row18(\玩家飞机_1_行19 ), .row19(\玩家飞机_1_行20 ), .row20(\玩家飞机_1_行21 ), .row21(\玩家飞机_1_行22 ),
    .row22(\玩家飞机_1_行23 ), .row23(\玩家飞机_1_行24 ), .row24(\玩家飞机_1_行25 ), .row25(\玩家飞机_1_行26 ),
    .row26(\玩家飞机_1_行27 ), .row27(\玩家飞机_1_行28 ), .row28(\玩家飞机_1_行29 ), .row29(\玩家飞机_1_行30 ),
    .row30(\玩家飞机_1_行31 ), .row31(\玩家飞机_1_行32 ));
  D_Flip_Flop #(.trigger("high"), .Pre_Clr_Positions("LEGACY"), .enable("true"), .NewFFLayout("false")) d_ff_1 (.Q(d_ff_1_q));  // open: clk, D, Qn, preset, en, reset
  // Probe on 13'h8f7
  Comparator #(.width(13)) comparator_1 (
    .a(CNT_num), .b(13'h8f7), .eq(comparator_1_eq), .lt(comparator_1_lt));  // open: gt
  Clock clock_1 (.out(clock_1_out));
  nand nand_1 (nand_1_out, d_ff_1_q, comparator_1_eq);
  Counter #(.width(13), .max('h1fff), .ongoal("stay"), .behavior("old")) counter_1 (
    .count(comparator_1_lt), .Q(CNT_num), .clk(clock_1_out));  // open: load, D, carry, clr, preset
  assign CLK = nand_1_out ? clock_1_out : 1'bz;  // Controlled_Buffer controlled_buffer_1
  Pull_Resistor #(.pull(1)) pull_resistor_1 (.node(CLK));

  // Notes on the sheet:
  //   控制位
  //   暂停节拍，不能为0
  //   戳工具置1进入计数暂停模式，ctrl+k时钟自动运行到对应节拍暂停
  //   ctrl+k关闭时钟连续运行，将控制位置零，进入单步调试模式调试
  //   可计数暂停的时钟源
endmodule

module \点阵显示  (
  input  \开始 ,
  input  CLK,
  input  RST,
  input  \上 ,
  input  \下 ,
  input  \end ,
  output [31:0] line1,
  output [31:0] line2,
  output [31:0] line3,
  output [31:0] line4,
  output [31:0] line5,
  output [31:0] line6,
  output [31:0] line7,
  output [31:0] line8,
  output [31:0] line9,
  output [31:0] line10,
  output [31:0] line11,
  output [31:0] line12,
  output [31:0] line13,
  output [31:0] line14,
  output WHIT,
  output [31:0] line15,
  output [31:0] line16,
  output [31:0] line17,
  output [31:0] line18,
  output [31:0] line19,
  output [31:0] line20,
  output [31:0] line21,
  output [31:0] line22,
  output [31:0] line23,
  output [31:0] line24,
  output [31:0] line25,
  output [31:0] line26,
  output [31:0] line27,
  output [31:0] line28,
  output [31:0] line29,
  output [31:0] line30,
  output [31:0] line31,
  output [31:0] line32,
  output BHIT
);

  wire comparator_1_gt, comparator_2_gt, comparator_3_gt, comparator_4_gt, comparator_5_gt, comparator_6_gt,
       comparator_7_gt, comparator_8_gt, comparator_9_gt, comparator_10_gt, comparator_11_gt,
       comparator_12_gt, comparator_13_gt, comparator_14_gt, comparator_15_gt, comparator_16_gt,
       comparator_17_gt, comparator_18_gt, comparator_19_gt, comparator_20_gt, comparator_21_gt,
       comparator_22_gt, comparator_23_gt, comparator_24_gt, comparator_25_gt, comparator_26_gt,
       comparator_27_gt, comparator_28_gt, comparator_29_gt, comparator_30_gt, comparator_31_gt,
       comparator_32_gt, comparator_33_gt, comparator_34_gt, comparator_35_gt, comparator_36_gt,
       comparator_37_gt, comparator_38_gt, comparator_39_gt, comparator_40_gt, comparator_41_gt,
       comparator_42_gt, comparator_43_gt, comparator_44_gt, comparator_45_gt, comparator_46_gt,
       comparator_47_gt, comparator_48_gt, comparator_49_gt, comparator_50_gt, comparator_51_gt,
       comparator_52_gt, comparator_53_gt, comparator_54_gt, comparator_55_gt, comparator_56_gt,
       comparator_57_gt, comparator_58_gt, comparator_59_gt, comparator_60_gt, comparator_61_gt,
       comparator_62_gt, comparator_63_gt, comparator_64_gt;
  wire [31:0] and_1_out, and_2_out, and_3_out, and_4_out, and_5_out, and_6_out, and_7_out, and_8_out,
       and_9_out, and_10_out, and_11_out, and_12_out, and_13_out, and_14_out, and_15_out, and_16_out,
       and_17_out, and_18_out, and_19_out, and_20_out, and_21_out, and_22_out, and_23_out, and_24_out,
       and_25_out, and_26_out, and_27_out, and_28_out, and_29_out, and_30_out, and_31_out, and_32_out,
       and_33_out, and_34_out, and_35_out, and_36_out, and_37_out, and_38_out, and_39_out, and_40_out,
       and_41_out, and_42_out, and_43_out, and_44_out, and_45_out, and_46_out, and_47_out, and_48_out,
       and_49_out, and_50_out, and_51_out, and_52_out, and_53_out, and_54_out, and_55_out, and_56_out,
       and_57_out, and_58_out, and_59_out, and_60_out, and_61_out, and_62_out, and_63_out, and_64_out,
       and_65_out, and_66_out, and_67_out, and_68_out, and_69_out, and_70_out, and_71_out, and_72_out,
       and_73_out, and_74_out, and_75_out, and_76_out, and_77_out, and_78_out, and_79_out, and_80_out,
       and_81_out, and_82_out, and_83_out, and_84_out, and_85_out, and_86_out, and_87_out, and_88_out,
       and_89_out, and_90_out, and_91_out, and_92_out, and_93_out, and_94_out, and_95_out, and_96_out,
       and_97_out, and_98_out, and_99_out, and_100_out, and_101_out, and_102_out, and_103_out, and_104_out,
       and_105_out, and_106_out, and_107_out, and_108_out, and_109_out, and_110_out, and_111_out,
       and_112_out, and_113_out, and_114_out, and_115_out, and_116_out, and_117_out, and_118_out,
       and_119_out, and_120_out, and_121_out, and_122_out, and_123_out, and_124_out, and_125_out,
       and_126_out, and_127_out, and_128_out, b1, b2, b3, b4, b5, b6, b7, b8, b9, b10, b11, b12, b13, b14,
       b15, b16, b17, b18, b19, b20, b21, b22, b23, b24, b25, b26, b27, b28, b29, b30, b31, b32, or_3_out,
       or_4_out, or_5_out, or_6_out, or_7_out, or_8_out, or_9_out, or_10_out, or_11_out, or_12_out,
       or_13_out, or_14_out, or_15_out, or_16_out, or_17_out, or_18_out, or_19_out, or_20_out, or_21_out,
       or_22_out, or_23_out, or_24_out, or_25_out, or_26_out, or_27_out, or_28_out, or_29_out, or_30_out,
       or_31_out, or_32_out, or_33_out, or_34_out, w1, w2, w3, w4, w5, w6, w7, w8, w9, w10, w11, w12, w13,
       w14, w15, w16, w17, w18, w19, w20, w21, w22, w23, w24, w25, w26, w27, w28, w29, w30, w31, w32;

  assign and_1_out = 32'hc0000000 & w1;  // AND_Gate and_1, 32 bits wide
  assign and_2_out = 32'hc0000000 & w3;  // AND_Gate and_2, 32 bits wide
  assign and_3_out = 32'hc0000000 & w4;  // AND_Gate and_3, 32 bits wide
  assign and_4_out = 32'hc0000000 & w5;  // AND_Gate and_4, 32 bits wide
  assign and_5_out = 32'hc0000000 & w6;  // AND_Gate and_5, 32 bits wide
  assign and_6_out = 32'hc0000000 & w7;  // AND_Gate and_6, 32 bits wide
  assign and_7_out = 32'hc0000000 & w8;  // AND_Gate and_7, 32 bits wide
  assign and_8_out = 32'hc0000000 & w9;  // AND_Gate and_8, 32 bits wide
  \流水线中断  \u_流水线中断_1  (
    .GO(\开始 ), .RST(RST), .CLK(CLK), .\行1 (b1), .\行2 (b2), .\行3 (b3), .\行4 (b4), .\行5 (b5), .\行6 (b6),
    .\行7 (b7), .\行8 (b8), .\行9 (b9), .\行10 (b10), .\行11 (b11), .\行12 (b12), .\行13 (b13), .\行14 (b14),
    .\行15 (b15), .\行16 (b16), .\行17 (b17), .\行18 (b18), .\行19 (b19), .\行20 (b20), .\行21 (b21), .\行22 (b22),
    .\行23 (b23), .\行24 (b24), .\行25 (b25), .\行26 (b26), .\行27 (b27), .\行28 (b28), .\行29 (b29), .\行30 (b30),
    .\行31 (b31), .\行32 (b32));
  assign and_9_out = 32'hc0000000 & w2;  // AND_Gate and_9, 32 bits wide
  assign and_10_out = 32'hc0000000 & w10;  // AND_Gate and_10, 32 bits wide
  assign and_11_out = 32'hc0000000 & w11;  // AND_Gate and_11, 32 bits wide
  assign and_12_out = 32'hc0000000 & w12;  // AND_Gate and_12, 32 bits wide
  assign and_13_out = 32'hc0000000 & w13;  // AND_Gate and_13, 32 bits wide
  assign and_14_out = 32'hc0000000 & w14;  // AND_Gate and_14, 32 bits wide
  assign and_15_out = 32'hc0000000 & w15;  // AND_Gate and_15, 32 bits wide
  assign and_16_out = 32'hc0000000 & w16;  // AND_Gate and_16, 32 bits wide
  assign and_17_out = 32'hc0000000 & w17;  // AND_Gate and_17, 32 bits wide
  assign and_18_out = 32'hc0000000 & w18;  // AND_Gate and_18, 32 bits wide
  assign and_19_out = 32'hc0000000 & w19;  // AND_Gate and_19, 32 bits wide
  assign and_20_out = 32'hc0000000 & w20;  // AND_Gate and_20, 32 bits wide
  assign and_21_out = 32'hc0000000 & w21;  // AND_Gate and_21, 32 bits wide
  assign and_22_out = 32'hc0000000 & w22;  // AND_Gate and_22, 32 bits wide
  assign and_23_out = 32'hc0000000 & w23;  // AND_Gate and_23, 32 bits wide
  assign and_24_out = 32'hc0000000 & w24;  // AND_Gate and_24, 32 bits wide
  assign and_25_out = 32'hc0000000 & w25;  // AND_Gate and_25, 32 bits wide
  assign and_26_out = 32'hc0000000 & w26;  // AND_Gate and_26, 32 bits wide
  assign and_27_out = 32'hc0000000 & w27;  // AND_Gate and_27, 32 bits wide
  assign and_28_out = 32'hc0000000 & w28;  // AND_Gate and_28, 32 bits wide
  assign and_29_out = 32'hc0000000 & w29;  // AND_Gate and_29, 32 bits wide
  assign and_30_out = 32'hc0000000 & w30;  // AND_Gate and_30, 32 bits wide
  assign and_31_out = 32'hc0000000 & w31;  // AND_Gate and_31, 32 bits wide
  assign and_32_out = 32'hc0000000 & w32;  // AND_Gate and_32, 32 bits wide
  assign and_33_out = 32'h100 & b1;  // AND_Gate and_33, 32 bits wide
  assign and_34_out = 32'h100 & b2;  // AND_Gate and_34, 32 bits wide
  assign and_35_out = 32'h100 & b3;  // AND_Gate and_35, 32 bits wide
  assign and_36_out = 32'h100 & b4;  // AND_Gate and_36, 32 bits wide
  assign and_37_out = 32'h100 & b5;  // AND_Gate and_37, 32 bits wide
  assign and_38_out = 32'h100 & b6;  // AND_Gate and_38, 32 bits wide
  assign and_39_out = 32'h100 & b7;  // AND_Gate and_39, 32 bits wide
  assign and_40_out = 32'h100 & b8;  // AND_Gate and_40, 32 bits wide
  assign and_41_out = 32'h100 & b9;  // AND_Gate and_41, 32 bits wide
  assign and_42_out = 32'h100 & b10;  // AND_Gate and_42, 32 bits wide
  assign and_43_out = 32'h100 & b13;  // AND_Gate and_43, 32 bits wide
  assign and_44_out = 32'h100 & b14;  // AND_Gate and_44, 32 bits wide
  assign and_45_out = b1 & and_1_out;  // AND_Gate and_45, 32 bits wide
  assign and_46_out = b2 & and_9_out;  // AND_Gate and_46, 32 bits wide
  assign and_47_out = b3 & and_2_out;  // AND_Gate and_47, 32 bits wide
  assign and_48_out = b4 & and_3_out;  // AND_Gate and_48, 32 bits wide
  assign and_49_out = b5 & and_4_out;  // AND_Gate and_49, 32 bits wide
  assign and_50_out = b6 & and_5_out;  // AND_Gate and_50, 32 bits wide
  assign and_51_out = b7 & and_6_out;  // AND_Gate and_51, 32 bits wide
  assign and_52_out = b8 & and_7_out;  // AND_Gate and_52, 32 bits wide
  assign and_53_out = b9 & and_8_out;  // AND_Gate and_53, 32 bits wide
  assign and_54_out = b10 & and_10_out;  // AND_Gate and_54, 32 bits wide
  assign and_55_out = b11 & and_11_out;  // AND_Gate and_55, 32 bits wide
  assign and_56_out = b12 & and_12_out;  // AND_Gate and_56, 32 bits wide
  assign and_57_out = b13 & and_13_out;  // AND_Gate and_57, 32 bits wide
  assign and_58_out = b14 & and_14_out;  // AND_Gate and_58, 32 bits wide
  assign and_59_out = b15 & and_15_out;  // AND_Gate and_59, 32 bits wide
  assign and_60_out = b16 & and_16_out;  // AND_Gate and_60, 32 bits wide
  assign and_61_out = b17 & and_17_out;  // AND_Gate and_61, 32 bits wide
  assign and_62_out = b18 & and_18_out;  // AND_Gate and_62, 32 bits wide
  assign and_63_out = b22 & and_22_out;  // AND_Gate and_63, 32 bits wide
  assign and_64_out = b24 & and_24_out;  // AND_Gate and_64, 32 bits wide
  assign and_65_out = 32'h100 & b11;  // AND_Gate and_65, 32 bits wide
  assign and_66_out = 32'h100 & b12;  // AND_Gate and_66, 32 bits wide
  assign and_67_out = 32'h100 & b15;  // AND_Gate and_67, 32 bits wide
  assign and_68_out = 32'h100 & b16;  // AND_Gate and_68, 32 bits wide
  assign and_69_out = 32'h100 & b17;  // AND_Gate and_69, 32 bits wide
  assign and_70_out = 32'h100 & b18;  // AND_Gate and_70, 32 bits wide
  assign and_71_out = 32'h100 & b19;  // AND_Gate and_71, 32 bits wide
  assign and_72_out = 32'h100 & b20;  // AND_Gate and_72, 32 bits wide
  assign and_73_out = 32'h100 & b21;  // AND_Gate and_73, 32 bits wide
  assign and_74_out = 32'h100 & b22;  // AND_Gate and_74, 32 bits wide
  assign and_75_out = 32'h100 & b23;  // AND_Gate and_75, 32 bits wide
  assign and_76_out = 32'h100 & b24;  // AND_Gate and_76, 32 bits wide
  assign and_77_out = 32'h100 & b25;  // AND_Gate and_77, 32 bits wide
  assign and_78_out = 32'h100 & b26;  // AND_Gate and_78, 32 bits wide
  assign and_79_out = 32'h100 & b27;  // AND_Gate and_79, 32 bits wide
  assign and_80_out = 32'h100 & b28;  // AND_Gate and_80, 32 bits wide
  assign and_81_out = 32'h100 & b29;  // AND_Gate and_81, 32 bits wide
  assign and_82_out = 32'h100 & b30;  // AND_Gate and_82, 32 bits wide
  assign and_83_out = 32'h100 & b31;  // AND_Gate and_83, 32 bits wide
  assign and_84_out = 32'h100 & b32;  // AND_Gate and_84, 32 bits wide
  \玩家飞机  \u_玩家飞机_1  (
    .IR1(\下 ), .CLK(CLK), .IR2(\上 ), .IR3(\开始 ), .\行1 (w1), .\行2 (w2), .\行3 (w3), .\行4 (w4), .\行5 (w5),
    .\行6 (w6), .\行7 (w7), .\行8 (w8), .\行9 (w9), .\行10 (w10), .\行11 (w11), .\行12 (w12), .\行13 (w13),
    .\行14 (w14), .\行15 (w15), .\行16 (w16), .\行17 (w17), .\行18 (w18), .\行19 (w19), .\行20 (w20), .\行21 (w21),
    .\行22 (w22), .\行23 (w23), .\行24 (w24), .\行25 (w25), .\行26 (w26), .\行27 (w27), .\行28 (w28), .\行29 (w29),
    .\行30 (w30), .\行31 (w31), .\行32 (w32));  // open: 警报铃声
  assign and_85_out = b19 & and_19_out;  // AND_Gate and_85, 32 bits wide
  assign and_86_out = b20 & and_20_out;  // AND_Gate and_86, 32 bits wide
  assign and_87_out = b21 & and_21_out;  // AND_Gate and_87, 32 bits wide
  assign and_88_out = b23 & and_23_out;  // AND_Gate and_88, 32 bits wide
  assign and_89_out = b25 & and_25_out;  // AND_Gate and_89, 32 bits wide
  assign and_90_out = b26 & and_26_out;  // AND_Gate and_90, 32 bits wide
  assign and_91_out = b27 & and_27_out;  // AND_Gate and_91, 32 bits wide
  assign and_92_out = b28 & and_28_out;  // AND_Gate and_92, 32 bits wide
  assign and_93_out = b29 & and_29_out;  // AND_Gate and_93, 32 bits wide
  assign and_94_out = b30 & and_30_out;  // AND_Gate and_94, 32 bits wide
  assign and_95_out = b31 & and_31_out;  // AND_Gate and_95, 32 bits wide
  assign and_96_out = b32 & and_32_out;  // AND_Gate and_96, 32 bits wide
  assign and_97_out = w1 & and_33_out;  // AND_Gate and_97, 32 bits wide
  assign and_98_out = w2 & and_34_out;  // AND_Gate and_98, 32 bits wide
  assign and_99_out = w3 & and_35_out;  // AND_Gate and_99, 32 bits wide
  assign and_100_out = w4 & and_36_out;  // AND_Gate and_100, 32 bits wide
  assign and_101_out = w5 & and_37_out;  // AND_Gate and_101, 32 bits wide
  assign and_102_out = w6 & and_38_out;  // AND_Gate and_102, 32 bits wide
  assign and_103_out = w7 & and_39_out;  // AND_Gate and_103, 32 bits wide
  assign and_104_out = w8 & and_40_out;  // AND_Gate and_104, 32 bits wide
  assign and_105_out = w9 & and_41_out;  // AND_Gate and_105, 32 bits wide
  assign and_106_out = w10 & and_42_out;  // AND_Gate and_106, 32 bits wide
  assign and_107_out = w11 & and_65_out;  // AND_Gate and_107, 32 bits wide
  assign and_108_out = w12 & and_66_out;  // AND_Gate and_108, 32 bits wide
  assign and_109_out = w13 & and_43_out;  // AND_Gate and_109, 32 bits wide
  assign and_110_out = w14 & and_44_out;  // AND_Gate and_110, 32 bits wide
  assign and_111_out = w15 & and_67_out;  // AND_Gate and_111, 32 bits wide
  assign and_112_out = w16 & and_68_out;  // AND_Gate and_112, 32 bits wide
  assign and_113_out = w17 & and_69_out;  // AND_Gate and_113, 32 bits wide
  assign and_114_out = w18 & and_70_out;  // AND_Gate and_114, 32 bits wide
  assign and_115_out = w19 & and_71_out;  // AND_Gate and_115, 32 bits wide
  assign and_116_out = w20 & and_72_out;  // AND_Gate and_116, 32 bits wide
  assign and_117_out = w21 & and_73_out;  // AND_Gate and_117, 32 bits wide
  assign and_118_out = w22 & and_74_out;  // AND_Gate and_118, 32 bits wide
  assign and_119_out = w23 & and_75_out;  // AND_Gate and_119, 32 bits wide
  assign and_120_out = w24 & and_76_out;  // AND_Gate and_120, 32 bits wide
  assign and_121_out = w25 & and_77_out;  // AND_Gate and_121, 32 bits wide
  assign and_122_out = w26 & and_78_out;  // AND_Gate and_122, 32 bits wide
  assign and_123_out = w28 & and_80_out;  // AND_Gate and_123, 32 bits wide
  assign and_124_out = w30 & and_82_out;  // AND_Gate and_124, 32 bits wide
  assign and_125_out = w31 & and_83_out;  // AND_Gate and_125, 32 bits wide
  assign and_126_out = w32 & and_84_out;  // AND_Gate and_126, 32 bits wide
  Comparator #(.width(32), .mode("unsigned")) comparator_1 (
    .a(and_45_out), .b({32{1'b0}}), .gt(comparator_1_gt));  // open: eq, lt
  Comparator #(.width(32), .mode("unsigned")) comparator_2 (
    .a(and_46_out), .b({32{1'b0}}), .gt(comparator_2_gt));  // open: eq, lt
  Comparator #(.width(32), .mode("unsigned")) comparator_3 (
    .a(and_47_out), .b({32{1'b0}}), .gt(comparator_3_gt));  // open: eq, lt
  Comparator #(.width(32), .mode("unsigned")) comparator_4 (
    .a(and_48_out), .b({32{1'b0}}), .gt(comparator_4_gt));  // open: eq, lt
  Comparator #(.width(32), .mode("unsigned")) comparator_5 (
    .a(and_49_out), .b({32{1'b0}}), .gt(comparator_5_gt));  // open: eq, lt
  Comparator #(.width(32), .mode("unsigned")) comparator_6 (
    .a(and_50_out), .b({32{1'b0}}), .gt(comparator_6_gt));  // open: eq, lt
  Comparator #(.width(32), .mode("unsigned")) comparator_7 (
    .a(and_51_out), .b({32{1'b0}}), .gt(comparator_7_gt));  // open: eq, lt
  Comparator #(.width(32), .mode("unsigned")) comparator_8 (
    .a(and_52_out), .b({32{1'b0}}), .gt(comparator_8_gt));  // open: eq, lt
  Comparator #(.width(32), .mode("unsigned")) comparator_9 (
    .a(and_53_out), .b({32{1'b0}}), .gt(comparator_9_gt));  // open: eq, lt
  Comparator #(.width(32), .mode("unsigned")) comparator_10 (
    .a(and_54_out), .b({32{1'b0}}), .gt(comparator_10_gt));  // open: eq, lt
  Comparator #(.width(32), .mode("unsigned")) comparator_11 (
    .a(and_55_out), .b({32{1'b0}}), .gt(comparator_11_gt));  // open: eq, lt
  Comparator #(.width(32), .mode("unsigned")) comparator_12 (
    .a(and_56_out), .b({32{1'b0}}), .gt(comparator_12_gt));  // open: eq, lt
  Comparator #(.width(32), .mode("unsigned")) comparator_13 (
    .a(and_57_out), .b({32{1'b0}}), .gt(comparator_13_gt));  // open: eq, lt
  Comparator #(.width(32), .mode("unsigned")) comparator_14 (
    .a(and_58_out), .b({32{1'b0}}), .gt(comparator_14_gt));  // open: eq, lt
  Comparator #(.width(32), .mode("unsigned")) comparator_15 (
    .a(and_59_out), .b({32{1'b0}}), .gt(comparator_15_gt));  // open: eq, lt
  Comparator #(.width(32), .mode("unsigned")) comparator_16 (
    .a(and_60_out), .b({32{1'b0}}), .gt(comparator_16_gt));  // open: eq, lt
  Comparator #(.width(32), .mode("unsigned")) comparator_17 (
    .a(and_61_out), .b({32{1'b0}}), .gt(comparator_17_gt));  // open: eq, lt
  Comparator #(.width(32), .mode("unsigned")) comparator_18 (
    .a(and_62_out), .b({32{1'b0}}), .gt(comparator_18_gt));  // open: eq, lt
  Comparator #(.width(32), .mode("unsigned")) comparator_19 (
    .a(and_85_out), .b({32{1'b0}}), .gt(comparator_19_gt));  // open: eq, lt
  Comparator #(.width(32), .mode("unsigned")) comparator_20 (
    .a(and_86_out), .b({32{1'b0}}), .gt(comparator_20_gt));  // open: eq, lt
  Comparator #(.width(32), .mode("unsigned")) comparator_21 (
    .a(and_87_out), .b({32{1'b0}}), .gt(comparator_21_gt));  // open: eq, lt
  Comparator #(.width(32), .mode("unsigned")) comparator_22 (
    .a(and_63_out), .b({32{1'b0}}), .gt(comparator_22_gt));  // open: eq, lt
  Comparator #(.width(32), .mode("unsigned")) comparator_23 (
    .a(and_88_out), .b({32{1'b0}}), .gt(comparator_23_gt));  // open: eq, lt
  Comparator #(.width(32), .mode("unsigned")) comparator_24 (
    .a(and_64_out), .b({32{1'b0}}), .gt(comparator_24_gt));  // open: eq, lt
  Comparator #(.width(32), .mode("unsigned")) comparator_25 (
    .a(and_89_out), .b({32{1'b0}}), .gt(comparator_25_gt));  // open: eq, lt
  Comparator #(.width(32), .mode("unsigned")) comparator_26 (
    .a(and_90_out), .b({32{1'b0}}), .gt(comparator_26_gt));  // open: eq, lt
  Comparator #(.width(32), .mode("unsigned")) comparator_27 (
    .a(and_91_out), .b({32{1'b0}}), .gt(comparator_27_gt));  // open: eq, lt
  Comparator #(.width(32), .mode("unsigned")) comparator_28 (
    .a(and_92_out), .b({32{1'b0}}), .gt(comparator_28_gt));  // open: eq, lt
  Comparator #(.width(32), .mode("unsigned")) comparator_29 (
    .a(and_93_out), .b({32{1'b0}}), .gt(comparator_29_gt));  // open: eq, lt
  Comparator #(.width(32), .mode("unsigned")) comparator_30 (
    .a(and_94_out), .b({32{1'b0}}), .gt(comparator_30_gt));  // open: eq, lt
  Comparator #(.width(32), .mode("unsigned")) comparator_31 (
    .a(and_95_out), .b({32{1'b0}}), .gt(comparator_31_gt));  // open: eq, lt
  Comparator #(.width(32), .mode("unsigned")) comparator_32 (
    .a(and_96_out), .b({32{1'b0}}), .gt(comparator_32_gt));  // open: eq, lt
  Comparator #(.width(32), .mode("unsigned")) comparator_33 (
    .a(and_99_out), .b({32{1'b0}}), .gt(comparator_33_gt));  // open: eq, lt
  Comparator #(.width(32), .mode("unsigned")) comparator_34 (
    .a(and_100_out), .b({32{1'b0}}), .gt(comparator_34_gt));  // open: eq, lt
  Comparator #(.width(32), .mode("unsigned")) comparator_35 (
    .a(and_101_out), .b({32{1'b0}}), .gt(comparator_35_gt));  // open: eq, lt
  Comparator #(.width(32), .mode("unsigned")) comparator_36 (
    .a(and_102_out), .b({32{1'b0}}), .gt(comparator_36_gt));  // open: eq, lt
  Comparator #(.width(32), .mode("unsigned")) comparator_37 (
    .a(and_103_out), .b({32{1'b0}}), .gt(comparator_37_gt));  // open: eq, lt
  Comparator #(.width(32), .mode("unsigned")) comparator_38 (
    .a(and_104_out), .b({32{1'b0}}), .gt(comparator_38_gt));  // open: eq, lt
  Comparator #(.width(32), .mode("unsigned")) comparator_39 (
    .a(and_105_out), .b({32{1'b0}}), .gt(comparator_39_gt));  // open: eq, lt
  assign and_127_out = w27 & and_79_out;  // AND_Gate and_127, 32 bits wide
  assign and_128_out = w29 & and_81_out;  // AND_Gate and_128, 32 bits wide
  Comparator #(.width(32), .mode("unsigned")) comparator_40 (
    .a(and_97_out), .b({32{1'b0}}), .gt(comparator_40_gt));  // open: eq, lt
  Comparator #(.width(32), .mode("unsigned")) comparator_41 (
    .a(and_98_out), .b({32{1'b0}}), .gt(comparator_41_gt));  // open: eq, lt
  Comparator #(.width(32), .mode("unsigned")) comparator_42 (
    .a(and_106_out), .b({32{1'b0}}), .gt(comparator_42_gt));  // open: eq, lt
  Comparator #(.width(32), .mode("unsigned")) comparator_43 (
    .a(and_107_out), .b({32{1'b0}}), .gt(comparator_43_gt));  // open: eq, lt
  Comparator #(.width(32), .mode("unsigned")) comparator_44 (
    .a(and_108_out), .b({32{1'b0}}), .gt(comparator_44_gt));  // open: eq, lt
  Comparator #(.width(32), .mode("unsigned")) comparator_45 (
    .a(and_109_out), .b({32{1'b0}}), .gt(comparator_45_gt));  // open: eq, lt
  Comparator #(.width(32), .mode("unsigned")) comparator_46 (
    .a(and_110_out), .b({32{1'b0}}), .gt(comparator_46_gt));  // open: eq, lt
  Comparator #(.width(32), .mode("unsigned")) comparator_47 (
    .a(and_111_out), .b({32{1'b0}}), .gt(comparator_47_gt));  // open: eq, lt
  Comparator #(.width(32), .mode("unsigned")) comparator_48 (
    .a(and_112_out), .b({32{1'b0}}), .gt(comparator_48_gt));  // open: eq, lt
  Comparator #(.width(32), .mode("unsigned")) comparator_49 (
    .a(and_113_out), .b({32{1'b0}}), .gt(comparator_49_gt));  // open: eq, lt
  Comparator #(.width(32), .mode("unsigned")) comparator_50 (
    .a(and_114_out), .b({32{1'b0}}), .gt(comparator_50_gt));  // open: eq, lt
  Comparator #(.width(32), .mode("unsigned")) comparator_51 (
    .a(and_115_out), .b({32{1'b0}}), .gt(comparator_51_gt));  // open: eq, lt
  Comparator #(.width(32), .mode("unsigned")) comparator_52 (
    .a(and_116_out), .b({32{1'b0}}), .gt(comparator_52_gt));  // open: eq, lt
  Comparator #(.width(32), .mode("unsigned")) comparator_53 (
    .a(and_117_out), .b({32{1'b0}}), .gt(comparator_53_gt));  // open: eq, lt
  Comparator #(.width(32), .mode("unsigned")) comparator_54 (
    .a(and_118_out), .b({32{1'b0}}), .gt(comparator_54_gt));  // open: eq, lt
  Comparator #(.width(32), .mode("unsigned")) comparator_55 (
    .a(and_119_out), .b({32{1'b0}}), .gt(comparator_55_gt));  // open: eq, lt
  Comparator #(.width(32), .mode("unsigned")) comparator_56 (
    .a(and_120_out), .b({32{1'b0}}), .gt(comparator_56_gt));  // open: eq, lt
  Comparator #(.width(32), .mode("unsigned")) comparator_57 (
    .a(and_121_out), .b({32{1'b0}}), .gt(comparator_57_gt));  // open: eq, lt
  Comparator #(.width(32), .mode("unsigned")) comparator_58 (
    .a(and_122_out), .b({32{1'b0}}), .gt(comparator_58_gt));  // open: eq, lt
  Comparator #(.width(32), .mode("unsigned")) comparator_59 (
    .a(and_127_out), .b({32{1'b0}}), .gt(comparator_59_gt));  // open: eq, lt
  Comparator #(.width(32), .mode("unsigned")) comparator_60 (
    .a(and_123_out), .b({32{1'b0}}), .gt(comparator_60_gt));  // open: eq, lt
  Comparator #(.width(32), .mode("unsigned")) comparator_61 (
    .a(and_128_out), .b({32{1'b0}}), .gt(comparator_61_gt));  // open: eq, lt
  Comparator #(.width(32), .mode("unsigned")) comparator_62 (
    .a(and_124_out), .b({32{1'b0}}), .gt(comparator_62_gt));  // open: eq, lt
  Comparator #(.width(32), .mode("unsigned")) comparator_63 (
    .a(and_125_out), .b({32{1'b0}}), .gt(comparator_63_gt));  // open: eq, lt
  Comparator #(.width(32), .mode("unsigned")) comparator_64 (
    .a(and_126_out), .b({32{1'b0}}), .gt(comparator_64_gt));  // open: eq, lt
  or or_1 (WHIT, comparator_1_gt, comparator_2_gt, comparator_3_gt, comparator_4_gt, comparator_5_gt, comparator_6_gt, comparator_7_gt, comparator_8_gt, comparator_9_gt, comparator_10_gt, comparator_11_gt, comparator_12_gt, comparator_13_gt, comparator_14_gt, comparator_15_gt, comparator_16_gt, comparator_17_gt, comparator_18_gt, comparator_19_gt, comparator_20_gt, comparator_21_gt, comparator_22_gt, comparator_23_gt, comparator_24_gt, comparator_25_gt, comparator_26_gt, comparator_27_gt, comparator_28_gt, comparator_29_gt, comparator_30_gt, comparator_31_gt, comparator_32_gt);
  or or_2 (BHIT, comparator_40_gt, comparator_41_gt, comparator_33_gt, comparator_34_gt, comparator_35_gt, comparator_36_gt, comparator_37_gt, comparator_38_gt, comparator_39_gt, comparator_42_gt, comparator_43_gt, comparator_44_gt, comparator_45_gt, comparator_46_gt, comparator_47_gt, comparator_48_gt, comparator_49_gt, comparator_50_gt, comparator_51_gt, comparator_52_gt, comparator_53_gt, comparator_54_gt, comparator_55_gt, comparator_56_gt, comparator_57_gt, comparator_58_gt, comparator_59_gt, comparator_60_gt, comparator_61_gt, comparator_62_gt, comparator_63_gt, comparator_64_gt);
  assign or_3_out = b1 | w1;  // OR_Gate or_3, 32 bits wide
  assign or_4_out = b2 | w2;  // OR_Gate or_4, 32 bits wide
  assign or_5_out = b3 | w3;  // OR_Gate or_5, 32 bits wide
  assign or_6_out = b6 | w6;  // OR_Gate or_6, 32 bits wide
  assign or_7_out = b7 | w7;  // OR_Gate or_7, 32 bits wide
  assign or_8_out = b8 | w8;  // OR_Gate or_8, 32 bits wide
  assign or_9_out = b9 | w9;  // OR_Gate or_9, 32 bits wide
  assign or_10_out = b10 | w10;  // OR_Gate or_10, 32 bits wide
  assign or_11_out = b11 | w11;  // OR_Gate or_11, 32 bits wide
  assign or_12_out = b12 | w12;  // OR_Gate or_12, 32 bits wide
  assign or_13_out = b13 | w13;  // OR_Gate or_13, 32 bits wide
  assign or_14_out = b14 | w14;  // OR_Gate or_14, 32 bits wide
  assign or_15_out = b15 | w15;  // OR_Gate or_15, 32 bits wide
  assign or_16_out = b16 | w16;  // OR_Gate or_16, 32 bits wide
  assign or_17_out = b17 | w17;  // OR_Gate or_17, 32 bits wide
  assign or_18_out = b18 | w18;  // OR_Gate or_18, 32 bits wide
  assign or_19_out = b19 | w19;  // OR_Gate or_19, 32 bits wide
  assign or_20_out = b20 | w20;  // OR_Gate or_20, 32 bits wide
  assign or_21_out = b21 | w21;  // OR_Gate or_21, 32 bits wide
  assign or_22_out = b22 | w22;  // OR_Gate or_22, 32 bits wide
  assign or_23_out = b23 | w23;  // OR_Gate or_23, 32 bits wide
  Multiplexer #(.width(32), .enable("false")) multiplexer_1 (
    .in0(or_3_out), .in1({32{1'b0}}), .out(line1), .sel(\end ));
  Multiplexer #(.width(32), .enable("false")) multiplexer_2 (
    .in0(or_4_out), .in1({32{1'b0}}), .out(line2), .sel(\end ));
  Multiplexer #(.width(32), .enable("false")) multiplexer_3 (
    .in0(or_5_out), .in1({32{1'b0}}), .out(line3), .sel(\end ));
  assign or_24_out = b4 | w4;  // OR_Gate or_24, 32 bits wide
  assign or_25_out = b5 | w5;  // OR_Gate or_25, 32 bits wide
  assign or_26_out = b24 | w24;  // OR_Gate or_26, 32 bits wide
  assign or_27_out = b25 | w25;  // OR_Gate or_27, 32 bits wide
  assign or_28_out = b26 | w26;  // OR_Gate or_28, 32 bits wide
  assign or_29_out = b27 | w27;  // OR_Gate or_29, 32 bits wide
  assign or_30_out = b29 | w29;  // OR_Gate or_30, 32 bits wide
  assign or_31_out = b30 | w30;  // OR_Gate or_31, 32 bits wide
  assign or_32_out = b31 | w31;  // OR_Gate or_32, 32 bits wide
  assign or_33_out = b32 | w32;  // OR_Gate or_33, 32 bits wide
  Multiplexer #(.width(32), .enable("false")) multiplexer_4 (
    .in0(or_24_out), .in1({32{1'b0}}), .out(line4), .sel(\end ));
  Multiplexer #(.width(32), .enable("false")) multiplexer_5 (
    .in0(or_25_out), .in1({32{1'b0}}), .out(line5), .sel(\end ));
  Multiplexer #(.width(32), .enable("false")) multiplexer_6 (
    .in0(or_6_out), .in1({32{1'b0}}), .out(line6), .sel(\end ));
  Multiplexer #(.width(32), .enable("false")) multiplexer_7 (
    .in0(or_7_out), .in1({32{1'b0}}), .out(line7), .sel(\end ));
  Multiplexer #(.width(32), .enable("false")) multiplexer_8 (
    .in0(or_8_out), .in1({32{1'b0}}), .out(line8), .sel(\end ));
  Multiplexer #(.width(32), .enable("false")) multiplexer_9 (
    .in0(or_9_out), .in1(32'h3fc81300), .out(line9), .sel(\end ));
  Multiplexer #(.width(32), .enable("false")) multiplexer_10 (
    .in0(or_10_out), .in1(32'h200c1280), .out(line10), .sel(\end ));
  Multiplexer #(.width(32), .enable("false")) multiplexer_11 (
    .in0(or_11_out), .in1(32'h200a1240), .out(line11), .sel(\end ));
  Multiplexer #(.width(32), .enable("false")) multiplexer_12 (
    .in0(or_12_out), .in1(32'h200a1220), .out(line12), .sel(\end ));
  Multiplexer #(.width(32), .enable("false")) multiplexer_13 (
    .in0(or_13_out), .in1(32'h200a1210), .out(line13), .sel(\end ));
  Multiplexer #(.width(32), .enable("false")) multiplexer_14 (
    .in0(or_14_out), .in1(32'h20091208), .out(line14), .sel(\end ));
  Multiplexer #(.width(32), .enable("false")) multiplexer_15 (
    .in0(or_15_out), .in1(32'h20091204), .out(line15), .sel(\end ));
  Multiplexer #(.width(32), .enable("false")) multiplexer_16 (
    .in0(or_16_out), .in1(32'h3fc91204), .out(line16), .sel(\end ));
  Multiplexer #(.width(32), .enable("false")) multiplexer_17 (
    .in0(or_17_out), .in1(32'h20089204), .out(line17), .sel(\end ));
  Multiplexer #(.width(32), .enable("false")) multiplexer_18 (
    .in0(or_18_out), .in1(32'h20089204), .out(line18), .sel(\end ));
  Multiplexer #(.width(32), .enable("false")) multiplexer_19 (
    .in0(or_19_out), .in1(32'h20089208), .out(line19), .sel(\end ));
  Multiplexer #(.width(32), .enable("false")) multiplexer_20 (
    .in0(or_20_out), .in1(32'h20085210), .out(line20), .sel(\end ));
  Multiplexer #(.width(32), .enable("false")) multiplexer_21 (
    .in0(or_27_out), .in1({32{1'b0}}), .out(line25), .sel(\end ));
  assign or_34_out = b28 | w28;  // OR_Gate or_34, 32 bits wide
  Multiplexer #(.width(32), .enable("false")) multiplexer_22 (
    .in0(or_21_out), .in1(32'h20085220), .out(line21), .sel(\end ));
  Multiplexer #(.width(32), .enable("false")) multiplexer_23 (
    .in0(or_22_out), .in1(32'h20085240), .out(line22), .sel(\end ));
  Multiplexer #(.width(32), .enable("false")) multiplexer_24 (
    .in0(or_23_out), .in1(32'h20083280), .out(line23), .sel(\end ));
  Multiplexer #(.width(32), .enable("false")) multiplexer_25 (
    .in0(or_26_out), .in1(32'h3fc81300), .out(line24), .sel(\end ));
  Multiplexer #(.width(32), .enable("false")) multiplexer_26 (
    .in0(or_28_out), .in1({32{1'b0}}), .out(line26), .sel(\end ));
  Multiplexer #(.width(32), .enable("false")) multiplexer_27 (
    .in0(or_29_out), .in1({32{1'b0}}), .out(line27), .sel(\end ));
  Multiplexer #(.width(32), .enable("false")) multiplexer_28 (
    .in0(or_34_out), .in1({32{1'b0}}), .out(line28), .sel(\end ));
  Multiplexer #(.width(32), .enable("false")) multiplexer_29 (
    .in0(or_30_out), .in1({32{1'b0}}), .out(line29), .sel(\end ));
  Multiplexer #(.width(32), .enable("false")) multiplexer_30 (
    .in0(or_31_out), .in1({32{1'b0}}), .out(line30), .sel(\end ));
  Multiplexer #(.width(32), .enable("false")) multiplexer_31 (
    .in0(or_32_out), .in1({32{1'b0}}), .out(line31), .sel(\end ));
  Multiplexer #(.width(32), .enable("false")) multiplexer_32 (
    .in0(or_33_out), .in1({32{1'b0}}), .out(line32), .sel(\end ));
endmodule

module \玩家飞机  (
  input  IR1,
  input  CLK,
  input  IR2,
  input  IR3,
  output [31:0] \行1 ,
  output [31:0] \行2 ,
  output [31:0] \行3 ,
  output [31:0] \行4 ,
  output [31:0] \行5 ,
  output [31:0] \行6 ,
  output [31:0] \行7 ,
  output [31:0] \行8 ,
  output [31:0] \行9 ,
  output [31:0] \行10 ,
  output [31:0] \行11 ,
  output [31:0] \行12 ,
  output [31:0] \行13 ,
  output [31:0] \行14 ,
  output [31:0] \行15 ,
  output [31:0] \行16 ,
  output [31:0] \行17 ,
  output [31:0] \行18 ,
  output [31:0] \行19 ,
  output [31:0] \行20 ,
  output [31:0] \行21 ,
  output [31:0] \行22 ,
  output [31:0] \行23 ,
  output [31:0] \行24 ,
  output [31:0] \行25 ,
  output [31:0] \行26 ,
  output [31:0] \行27 ,
  output [31:0] \行28 ,
  output [31:0] \行29 ,
  output [31:0] \行30 ,
  output [31:0] \行31 ,
  output [31:0] \行32 ,
  output \警报铃声 
);

  wire AluSrcB, and_1_out, and_2_out, and_3_out, and_6_out, and_7_out, and_9_out, and_10_out, and_11_out,
       and_12_out, and_13_out, and_14_out, beq, bgeu, bne, Branch, clock_1_out, CLR1, CLR2, CLR3,
       comparator_1_eq, comparator_2_eq, comparator_2_lt, comparator_3_lt, comparator_4_eq, comparator_5_eq,
       controlled_buffer_1_out, d_ff_1_q, d_ff_2_q, d_ff_3_q, d_ff_5_q, ecall, equal, gae, Go, halt, high,
       IE, INTR, INTR1, INTR2, INTR3, IRHAVE, jal, jalr, JAMP, less, lhu, MemToReg, MemWrite, nand_1_out,
       not_1_out, not_2_out, not_3_out, not_4_out, not_5_out, or_4_out, or_5_out, or_6_out, or_7_out,
       or_9_out, or_10_out, register_4_q, register_5_q, register_6_q, register_7_q, register_8_q,
       register_9_q, register_10_q, register_11_q, register_12_q, register_13_q, register_14_q,
       register_15_q, register_16_q, register_17_q, register_18_q, register_19_q, RegWrite, riscv_probe_1_p4,
       RST, S_type, sltiu, uret, W1, W2, W3;
  wire [1:0] priority_encoder_1_out, priority_encoder_2_out, register_1_q;
  wire [3:0] AluOP;
  wire [4:0] imm12_S, multiplexer_7_out, multiplexer_8_out;
  wire [9:0] EM_ADDR;
  wire [11:0] imm12_B, imm12_I;
  wire [12:0] CNT_num;
  wire [15:0] multiplexer_14_out, \分支成功数 , \总周期数 ;
  wire [19:0] imm20_J, IR;
  wire [31:0] adder_1_out, adder_3_out, and_5_out, Bin, bit_extender_1_out, bit_extender_2_out,
       bit_extender_3_out, bit_extender_4_out, bit_extender_5_out, bit_extender_6_out, bit_extender_7_out,
       IR_PC, LedData, MDin, MDout, MEPC, multiplexer_2_out, multiplexer_4_out, multiplexer_5_out,
       multiplexer_6_out, multiplexer_9_out, multiplexer_11_out, multiplexer_12_out, PC, PC_4, PCin, R1,
       ram_1_data, RDin, Result, \地图_1_行1 , \地图_1_行2 , \地图_1_行3 , \地图_1_行4 , \地图_1_行5 , \地图_1_行6 , \地图_1_行7 ,
       \地图_1_行8 , \地图_1_行9 , \地图_1_行10 , \地图_1_行11 , \地图_1_行12 , \地图_1_行13 , \地图_1_行14 , \地图_1_行15 ,
       \地图_1_行16 , \地图_1_行17 , \地图_1_行18 , \地图_1_行19 , \地图_1_行20 , \地图_1_行21 , \地图_1_行22 , \地图_1_行23 ,
       \地图_1_行24 , \地图_1_行25 , \地图_1_行26 , \地图_1_行27 , \地图_1_行28 , \地图_1_行29 , \地图_1_行30 , \地图_1_行31 ,
       \地图_1_行32 ;

  Button \u_继续运行  (.out(Go));
  LED led_1 (.in(W1));
  LED led_2 (.in(W2));
  LED led_3 (.in(W3));
  Hex_Digit_Display hex_digit_display_1 (.value(LedData[31:28]));  // open: dp
  D_Flip_Flop #(.Pre_Clr_Positions("LEGACY"), .enable("true"), .NewFFLayout("false")) d_ff_1 (
    .clk(IR1), .D(1'b1), .Q(d_ff_1_q), .reset(INTR1));  // open: Qn, preset, en
  or or_1 (W1, INTR1, d_ff_1_q);
  D_Flip_Flop #(.Pre_Clr_Positions("LEGACY"), .enable("true"), .NewFFLayout("false")) d_ff_2 (
    .clk(IR2), .D(1'b1), .Q(d_ff_2_q), .reset(INTR2));  // open: Qn, preset, en
  or or_2 (W2, INTR2, d_ff_2_q);
  D_Flip_Flop #(.Pre_Clr_Positions("LEGACY"), .enable("true"), .NewFFLayout("false")) d_ff_3 (
    .clk(IR3), .D(1'b1), .Q(d_ff_3_q), .reset(INTR3));  // open: Qn, preset, en
  or or_3 (W3, INTR3, d_ff_3_q);
  Multiplexer #(.select(2), .width(32), .enable("false")) multiplexer_1 (
    .in0(32'h3010), .in1(32'h3038), .in2(32'h3004), .out(IR_PC), .sel(priority_encoder_1_out));  // open: in3
  Priority_Encoder #(.select(2)) priority_encoder_1 (
    .in0(INTR1), .in1(INTR2), .in2(INTR3), .out(priority_encoder_1_out));  // open: in3, gs, en_out, en_in
  Hex_Digit_Display hex_digit_display_2 (.value(LedData[23:20]));  // open: dp
  Hex_Digit_Display hex_digit_display_3 (.value(LedData[27:24]));  // open: dp
  or or_4 (or_4_out, d_ff_1_q, INTR1);
  or or_5 (or_5_out, d_ff_2_q, INTR2);
  Hex_Digit_Display hex_digit_display_4 (.value(LedData[15:12]));  // open: dp
  Hex_Digit_Display hex_digit_display_5 (.value(LedData[19:16]));  // open: dp
  and and_1 (and_1_out, or_4_out, ~CLR1);  // AND_Gate
  and and_2 (and_2_out, or_5_out, ~CLR2);  // AND_Gate
  or or_6 (or_6_out, d_ff_3_q, INTR3);
  and and_3 (and_3_out, or_6_out, ~CLR3);  // AND_Gate
  Register #(.width(2), .Select("low")) register_1 (
    .D(priority_encoder_1_out), .en(INTR), .Q(register_1_q), .clk(CLK));  // open: clr
  Hex_Digit_Display hex_digit_display_6 (.value(LedData[11:8]));  // open: dp
  Hex_Digit_Display hex_digit_display_7 (.value(LedData[7:4]));  // open: dp
  // Probe on \总周期数 
  D_Flip_Flop #(.Pre_Clr_Positions("LEGACY"), .enable("true"), .NewFFLayout("false")) u_IR1 (
    .clk(CLK), .D(and_1_out), .Q(INTR1));  // open: Qn, preset, en, reset
  D_Flip_Flop #(.Pre_Clr_Positions("LEGACY"), .enable("true"), .NewFFLayout("false")) IR1_2 (
    .clk(CLK), .D(and_2_out), .Q(INTR2));  // open: Qn, preset, en, reset
  D_Flip_Flop #(.Pre_Clr_Positions("LEGACY"), .enable("true"), .NewFFLayout("false")) IR1_3 (
    .clk(CLK), .D(and_3_out), .Q(INTR3));  // open: Qn, preset, en, reset
  Demultiplexer #(.select(2), .enable("false")) demultiplexer_1 (
    .out0(CLR1), .out1(CLR2), .out2(CLR3), .in(uret), .sel(register_1_q));  // open: out3
  Hex_Digit_Display hex_digit_display_8 (.value(LedData[3:0]));  // open: dp
  or or_7 (or_7_out, ~IRHAVE, uret);  // OR_Gate
  Button button_1 (.out(RST));
  or or_8 (IRHAVE, INTR1, INTR2, INTR3);
  D_Flip_Flop #(.Pre_Clr_Positions("LEGACY"), .enable("true")) d_ff_4 (
    .clk(CLK), .D(or_7_out), .Q(IE));  // open: Qn, preset, en, reset
  Multiplexer #(.select(2), .width(32), .enable("false")) multiplexer_2 (
    .in0(PCin), .in1(IR_PC), .in2(MEPC), .out(multiplexer_2_out), .sel(priority_encoder_2_out));  // open: in3
  and and_4 (INTR, IRHAVE, IE);
  Priority_Encoder #(.select(2)) priority_encoder_2 (
    .in0(1'b1), .in1(INTR), .in2(uret), .out(priority_encoder_2_out));  // open: in3, gs, en_out, en_in
  Register #(.width(32), .Select("low")) register_2 (.D(PCin), .en(INTR), .Q(MEPC), .clk(CLK));  // open: clr
  or or_9 (or_9_out, Go, not_1_out);
  not not_1 (not_1_out, halt);
  Register #(.width(32), .Select("low")) u_PC (.D(multiplexer_2_out), .en(or_9_out), .Q(PC), .clk(CLK), .clr(RST));
  not not_2 (not_2_out, halt);
  or or_10 (or_10_out, not_2_out, Go);
  Multiplexer #(.width(32), .enable("false")) multiplexer_3 (
    .in0(multiplexer_4_out), .in1(adder_1_out), .out(PCin), .sel(Branch));
  assign bit_extender_1_out = {{20{imm12_B[11]}}, imm12_B};  // Bit_Extender bit_extender_1
  Adder #(.width(32)) adder_1 (.a(bit_extender_1_out), .b(PC), .out(adder_1_out));  // open: cin, cout
  Counter #(.width(16), .max('hffff)) counter_1 (
    .count(or_10_out), .Q(\总周期数 ), .clk(CLK), .clr(RST));  // open: load, D, carry, preset, down
  or or_11 (JAMP, jal, jalr);
  Multiplexer #(.width(32), .enable("false")) multiplexer_4 (
    .in0(multiplexer_5_out), .in1(and_5_out), .out(multiplexer_4_out), .sel(jalr));
  assign and_5_out = {Result[31:12], EM_ADDR, high, Result[0]} & 32'hfffffffe;  // AND_Gate and_5, 32 bits wide
  assign bit_extender_2_out = {{12{imm20_J[19]}}, imm20_J};  // Bit_Extender bit_extender_2
  // RiscV_Probe riscv_probe_1: pin names not known; wires that end beside it: {imm12_I, IR[19:12], imm12_S, IR[6:0]}, IR[19:15], imm12_S, riscv_probe_1_p4
  Adder #(.width(32)) adder_2 (.a(PC), .b(32'h4), .out(PC_4));  // open: cin, cout
  Multiplexer #(.width(32), .enable("false")) multiplexer_5 (
    .in0(PC_4), .in1(adder_3_out), .out(multiplexer_5_out), .sel(jal));
  Adder #(.width(32)) adder_3 (.a(bit_extender_2_out), .b(PC), .out(adder_3_out));  // open: cin, cout
  ROM #(.addrWidth(10), .dataWidth(32), .Select("high")) rom_1 (
    .addr(PC[11:2]), .data({imm12_I, IR[19:12], imm12_S, IR[6:0]}));
  Multiplexer #(.width(32), .enable("false")) multiplexer_6 (
    .in0({Result[31:12], EM_ADDR, high, Result[0]}), .in1(MDout), .out(multiplexer_6_out), .sel(MemToReg));
  \单周期硬布线控制器  \u_单周期硬布线控制器_1  (
    .Funct({imm12_I[10], imm12_I[5], IR[14:12]}), .OP(IR[6:2]), .ALU_OP(AluOP), .MemToReg(MemToReg),
    .MemWrite(MemWrite), .ALU_SRC(AluSrcB), .RegWrite(RegWrite), .ecall(ecall), .S_type(S_type), .Jalr(jalr),
    .Beq(beq), .JAL(jal), .Bne(bne), .in_3(imm12_I[1]), .uret(uret), .sltiu(sltiu), .lhu(lhu), .bgeu(bgeu));  // open: CSRRSI, CSRRCI
  Multiplexer #(.width(5), .enable("false")) multiplexer_7 (
    .in0(IR[19:15]), .in1(5'b10001), .out(multiplexer_7_out), .sel(ecall));
  Multiplexer #(.width(5), .enable("false")) multiplexer_8 (
    .in0(imm12_I[4:0]), .in1(5'b01010), .out(multiplexer_8_out), .sel(ecall));
  Shifter #(.width(12)) shifter_1 (
    .in({imm12_I[11], imm12_S[0], imm12_I[10:5], imm12_S[4:1]}), .\dist (4'b0001), .out(imm12_B));
  Shifter #(.width(20)) shifter_2 (
    .in({imm12_I[11], IR[19:12], imm12_I[0], imm12_I[10:1]}), .\dist (5'b00001), .out(imm20_J));
  Multiplexer #(.width(32), .enable("false")) multiplexer_9 (
    .in0(multiplexer_6_out), .in1(PC_4), .out(multiplexer_9_out), .sel(JAMP));
  assign bit_extender_3_out = {{31{1'b0}}, less};  // Bit_Extender bit_extender_3
  D_Flip_Flop #(.trigger("high"), .Pre_Clr_Positions("LEGACY"), .enable("true"), .NewFFLayout("false")) d_ff_5 (.Q(d_ff_5_q));  // open: clk, D, Qn, preset, en, reset
  // Probe on 13'hc
  Multiplexer #(.width(32), .enable("false")) multiplexer_10 (
    .in0(multiplexer_9_out), .in1(bit_extender_3_out), .out(RDin), .sel(sltiu));
  Comparator #(.width(32)) comparator_1 (.a(R1), .b(32'h22), .eq(comparator_1_eq));  // open: gt, lt
  not not_3 (not_3_out, comparator_1_eq);
  and and_6 (and_6_out, ecall, comparator_1_eq);
  Comparator #(.width(13)) comparator_2 (
    .a(CNT_num), .b(13'hc), .eq(comparator_2_eq), .lt(comparator_2_lt));  // open: gt
  Clock clock_1 (.out(clock_1_out));
  Regifile regifile_1 (
    .Din(RDin), .Clk(CLK), .R1(R1), .R2(MDin), .WE(RegWrite), .W_num(imm12_S), .R1_num(multiplexer_7_out),
    .R2_num(multiplexer_8_out));
  and and_7 (and_7_out, not_3_out, ecall);
  Counter #(.width(13), .max('h1fff), .ongoal("stay"), .behavior("old")) counter_2 (
    .count(comparator_2_lt), .Q(CNT_num), .clk(clock_1_out));  // open: load, D, carry, clr, preset
  Multiplexer #(.width(32), .enable("false")) multiplexer_11 (
    .in0(MDin), .in1(Bin), .out(multiplexer_11_out), .sel(AluSrcB));
  and and_8 (halt, and_7_out, not_4_out);
  not not_4 (not_4_out, Go);
  Register #(.width(32), .Select("low")) register_3 (.D(MDin), .en(and_6_out), .Q(LedData), .clk(CLK), .clr(RST));
  nand nand_1 (nand_1_out, d_ff_5_q, comparator_2_eq);
  ALU alu_1 (
    .X(R1), .Y(multiplexer_11_out), .AluOP(AluOP), .Equal(equal),
    .Result({Result[31:12], EM_ADDR, high, Result[0]}), .out_4(gae), .out_6(less));  // open: Result_2
  assign bit_extender_4_out = {{20{imm12_I[11]}}, imm12_I};  // Bit_Extender bit_extender_4
  assign bit_extender_5_out = {{20{1'b0}}, imm12_I};  // Bit_Extender bit_extender_5
  assign controlled_buffer_1_out = nand_1_out ? clock_1_out : 1'bz;  // Controlled_Buffer controlled_buffer_1
  Pull_Resistor #(.pull(1)) pull_resistor_1 (.node(controlled_buffer_1_out));
  assign bit_extender_6_out = {{20{imm12_I[11]}}, {imm12_I[11:5], imm12_S}};  // Bit_Extender bit_extender_6
  not not_5 (not_5_out, equal);
  Multiplexer #(.width(32), .enable("false")) multiplexer_12 (
    .in0(bit_extender_4_out), .in1(bit_extender_5_out), .out(multiplexer_12_out), .sel(sltiu));
  and and_9 (and_9_out, beq, equal);
  and and_10 (and_10_out, not_5_out, bne);
  Multiplexer #(.width(32), .enable("false")) multiplexer_13 (
    .in0(multiplexer_12_out), .in1(bit_extender_6_out), .out(Bin), .sel(S_type));
  or or_12 (Branch, and_9_out, and_10_out, and_11_out);
  and and_11 (and_11_out, gae, bgeu);
  Counter #(.width(16), .max('hffff)) counter_3 (
    .count(Branch), .Q(\分支成功数 ), .clk(CLK), .clr(RST));  // open: load, D, carry, preset, down
  RAM #(.addrWidth(10), .dataWidth(32), .bus("separate"), .Select("high"), .simpleMode("false")) ram_1 (
    .addr(EM_ADDR), .din(MDin), .data(ram_1_data), .str(MemWrite), .clk(CLK), .ld(MemToReg), .clr(RST));  // open: sel
  Multiplexer #(.width(16), .enable("false")) multiplexer_14 (
    .in0(ram_1_data[15:0]), .in1(ram_1_data[31:16]), .out(multiplexer_14_out), .sel(high));
  assign bit_extender_7_out = {{16{1'b0}}, multiplexer_14_out};  // Bit_Extender bit_extender_7
  Multiplexer #(.width(32), .enable("false")) multiplexer_15 (
    .in0(ram_1_data), .in1(bit_extender_7_out), .out(MDout), .sel(lhu));
  and and_12 (and_12_out, MemWrite, comparator_3_lt);
  Comparator #(.width(10), .mode("unsigned")) comparator_3 (
    .a(EM_ADDR), .b(10'h20), .lt(comparator_3_lt));  // open: gt, eq
  Comparator #(.width(32)) comparator_4 (.a(R1), .b(32'h22), .eq(comparator_4_eq));  // open: gt, lt
  Comparator #(.width(32)) comparator_5 (.a(R1), .b(32'h64), .eq(comparator_5_eq));  // open: gt, lt
  and and_13 (and_13_out, comparator_4_eq, ecall);
  \地图  \u_地图_1  (
    .\写使能 (and_12_out), .Addr(EM_ADDR), .CLK(CLK), .Data(MDin), .\行1 (\地图_1_行1 ), .\行9 (\地图_1_行9 ),
    .\行17 (\地图_1_行17 ), .\行25 (\地图_1_行25 ), .\行2 (\地图_1_行2 ), .\行10 (\地图_1_行10 ), .\行18 (\地图_1_行18 ),
    .\行26 (\地图_1_行26 ), .\行3 (\地图_1_行3 ), .\行11 (\地图_1_行11 ), .\行19 (\地图_1_行19 ), .\行27 (\地图_1_行27 ),
    .\行4 (\地图_1_行4 ), .\行12 (\地图_1_行12 ), .\行20 (\地图_1_行20 ), .\行28 (\地图_1_行28 ), .\行5 (\地图_1_行5 ),
    .\行13 (\地图_1_行13 ), .\行21 (\地图_1_行21 ), .\行29 (\地图_1_行29 ), .\行6 (\地图_1_行6 ), .\行14 (\地图_1_行14 ),
    .\行22 (\地图_1_行22 ), .\行30 (\地图_1_行30 ), .\行7 (\地图_1_行7 ), .\行15 (\地图_1_行15 ), .\行23 (\地图_1_行23 ),
    .\行31 (\地图_1_行31 ), .\行8 (\地图_1_行8 ), .\行16 (\地图_1_行16 ), .\行24 (\地图_1_行24 ), .\行32 (\地图_1_行32 ),
    .RST(RST));
  and and_14 (and_14_out, comparator_5_eq, ecall);
  \点阵  \u_点阵_1  (
    .\写使能 (and_13_out), ._1(\地图_1_行1 ), ._2(\地图_1_行2 ), ._3(\地图_1_行3 ), ._4(\地图_1_行4 ), ._5(\地图_1_行5 ),
    ._6(\地图_1_行6 ), ._7(\地图_1_行7 ), ._8(\地图_1_行8 ), ._9(\地图_1_行9 ), ._10(\地图_1_行10 ), ._11(\地图_1_行11 ),
    ._12(\地图_1_行12 ), ._13(\地图_1_行13 ), ._14(\地图_1_行14 ), ._15(\地图_1_行15 ), ._16(\地图_1_行16 ),
    ._17(\地图_1_行17 ), ._18(\地图_1_行18 ), ._19(\地图_1_行19 ), ._20(\地图_1_行20 ), ._21(\地图_1_行21 ),
    ._22(\地图_1_行22 ), ._23(\地图_1_行23 ), ._24(\地图_1_行24 ), ._25(\地图_1_行25 ), ._26(\地图_1_行26 ),
    ._27(\地图_1_行27 ), ._28(\地图_1_行28 ), ._29(\地图_1_行29 ), ._30(\地图_1_行30 ), ._31(\地图_1_行31 ),
    ._32(\地图_1_行32 ), .CLK(CLK), ._1_2(\行1 ), ._2_2(\行2 ), ._3_2(\行3 ), ._4_2(\行4 ), ._5_2(\行5 ),
    ._6_2(\行6 ), ._7_2(\行7 ), ._8_2(\行8 ), ._9_2(\行9 ), ._10_2(\行10 ), ._11_2(\行11 ), ._12_2(\行12 ),
    ._13_2(\行13 ), ._14_2(\行14 ), ._15_2(\行15 ), ._16_2(\行16 ), ._17_2(\行17 ), ._18_2(\行18 ), ._19_2(\行19 ),
    ._20_2(\行20 ), ._21_2(\行21 ), ._22_2(\行22 ), ._23_2(\行23 ), ._24_2(\行24 ), ._25_2(\行25 ), ._26_2(\行26 ),
    ._27_2(\行27 ), ._28_2(\行28 ), ._29_2(\行29 ), ._30_2(\行30 ), ._31_2(\行31 ), ._32_2(\行32 ), .RST(RST));
  Register #(.width(1), .Select("low")) register_4 (
    .D(register_5_q), .Q(register_4_q), .clk(CLK), .clr(RST));  // open: en
  Register #(.width(1), .Select("low")) register_5 (
    .D(and_14_out), .Q(register_5_q), .clk(CLK), .clr(RST));  // open: en
  Register #(.width(1), .Select("low")) register_6 (
    .D(register_4_q), .Q(register_6_q), .clk(CLK), .clr(RST));  // open: en
  Register #(.width(1), .Select("low")) register_7 (
    .D(register_6_q), .Q(register_7_q), .clk(CLK), .clr(RST));  // open: en
  Register #(.width(1), .Select("low")) register_8 (
    .D(register_7_q), .Q(register_8_q), .clk(CLK), .clr(RST));  // open: en
  Register #(.width(1), .Select("low")) register_9 (
    .D(register_8_q), .Q(register_9_q), .clk(CLK), .clr(RST));  // open: en
  Register #(.width(1), .Select("low")) register_10 (
    .D(register_9_q), .Q(register_10_q), .clk(CLK), .clr(RST));  // open: en
  Register #(.width(1), .Select("low")) register_11 (
    .D(register_10_q), .Q(register_11_q), .clk(CLK), .clr(RST));  // open: en
  Register #(.width(1), .Select("low")) register_12 (
    .D(register_13_q), .Q(register_12_q), .clk(CLK), .clr(RST));  // open: en
  Register #(.width(1), .Select("low")) register_13 (
    .D(register_11_q), .Q(register_13_q), .clk(CLK), .clr(RST));  // open: en
  Register #(.width(1), .Select("low")) register_14 (
    .D(register_12_q), .Q(register_14_q), .clk(CLK), .clr(RST));  // open: en
  Register #(.width(1), .Select("low")) register_15 (
    .D(register_14_q), .Q(register_15_q), .clk(CLK), .clr(RST));  // open: en
  Register #(.width(1), .Select("low")) register_16 (
    .D(register_15_q), .Q(register_16_q), .clk(CLK), .clr(RST));  // open: en
  Register #(.width(1), .Select("low")) register_17 (
    .D(register_16_q), .Q(register_17_q), .clk(CLK), .clr(RST));  // open: en
  Register #(.width(1), .Select("low")) register_18 (
    .D(register_17_q), .Q(register_18_q), .clk(CLK), .clr(RST));  // open: en
  Register #(.width(1), .Select("low")) register_19 (
    .D(register_18_q), .Q(register_19_q), .clk(CLK), .clr(RST));  // open: en
  or or_13 (\警报铃声 , register_5_q, register_4_q, register_6_q, register_7_q, register_8_q, register_9_q, register_10_q, register_11_q, register_13_q, register_12_q, register_14_q, register_15_q, register_16_q, register_17_q, register_18_q, register_19_q);

  // Other names for the same wires on the sheet: IR (some bits) = {imm12_I, imm12_S}; imm12_S[11:5] = imm12_I[11:5];
  //   IRA = IR1; IRB = IR2; IRC = IR3; R2[31:0] = MDin; Result[11:1] = {EM_ADDR, high}

  // Notes on the sheet:
  //   中断源
  //   中断等待指示
  //   总复位信号应将除ROM以外所有存储组件全部清零
  //   识别中断类型找地址
  //   数码管输出
  //   数码管输出应该用寄存器锁存，否则显示数据只能一闪而过
  //   Reset 
  //   Reset 
  //   Reset 
  //   中断响应阶段
  //   中断使能位(用于开关中断)
  //   判断中断使能
  //   保存断点
  //   中断响应
  //   指令探针
  //   指令存储器
  //   指令字
  //   contents of rom_1 (hex, n*v repeats v):
  //   680006f 31463 100313 200073 2030263 7000f13 5e48663 4a023 e2023 ea023 448493 4e0e13 4e8e93 200073
  //   2030463 c00f13 3e48263 4a023 e2023 ea023 400513 40a484b3 40ae0e33 40ae8eb3 200073 200073 4000493
  //   3c00e13 4400e93 100413 1f41593 1e41413 ff00f93 8f9f93 fffef93 8f9f93 fffef93 8f9f93 fffef93 1f02023
  //   1f02223 7f02c23 7f02e23 84a023 be2023 bea023 2200893 73 1800b13 a93 40913 48993 999c63 8963b3 74a023
  //   be2023 bea023 440006f 1c99c63 b963b3 7e2023 84a023 bea023 2c0006f 1d99c63 b963b3 7ea023 be2023
  //   84a023 140006f 129a023 84a023 be2023 bea023 2200893 73 195913 1a8a93 f96a9ce3 f85ff06f
  //   JAL
  //   JALR
  //   URET
  //   Beq
  //   Bne
  //   MemToReg
  //   MemWrite
  //   AluOP
  //   AluSrcB
  //   RegWrite
  //   控制位
  //   暂停节拍，不能为0
  //   戳工具置1进入计数暂停模式，ctrl+k时钟自动运行到对应节拍暂停
  //   ctrl+k关闭时钟连续运行，将控制位置零，进入单步调试模式调试
  //   可计数暂停的时钟源
  //   数据存储器
endmodule

module \玩家交互  (
);

  wire bgm_1_enable, \bgm_1_音量 , CLK, comparator_1_lt, comparator_2_lt, d_ff_1_q, or_1_out, RST, \上 , \下 ,
       \开始 , \得分 , \点阵显示_1_whit , \结束 ;
  wire [6:0] keyboard_1_data;
  wire [7:0] counter_1_q, counter_2_q;
  wire [13:0] bgm_1_out_5;
  wire [31:0] \点阵显示_1_line1 , \点阵显示_1_line2 , \点阵显示_1_line3 , \点阵显示_1_line4 , \点阵显示_1_line5 , \点阵显示_1_line6 ,
       \点阵显示_1_line7 , \点阵显示_1_line8 , \点阵显示_1_line9 , \点阵显示_1_line10 , \点阵显示_1_line11 , \点阵显示_1_line12 ,
       \点阵显示_1_line13 , \点阵显示_1_line14 , \点阵显示_1_line15 , \点阵显示_1_line16 , \点阵显示_1_line17 , \点阵显示_1_line18 ,
       \点阵显示_1_line19 , \点阵显示_1_line20 , \点阵显示_1_line21 , \点阵显示_1_line22 , \点阵显示_1_line23 , \点阵显示_1_line24 ,
       \点阵显示_1_line25 , \点阵显示_1_line26 , \点阵显示_1_line27 , \点阵显示_1_line28 , \点阵显示_1_line29 , \点阵显示_1_line30 ,
       \点阵显示_1_line31 , \点阵显示_1_line32 ;

  Counter counter_1 (.Q(counter_1_q), .clk(\点阵显示_1_whit ));  // open: load, D, count, carry, clr, preset, down
  Comparator comparator_1 (.a(8'h3), .b(counter_1_q), .lt(comparator_1_lt));  // open: gt, eq
  Button button_1 (.out(\开始 ));
  Button button_2 (.out(RST));
  Clock clock_1 (.out(CLK));
  \点阵显示  \u_点阵显示_1  (
    .\开始 (\开始 ), .CLK(CLK), .RST(RST), .\上 (\上 ), .\下 (\下 ), .line1(\点阵显示_1_line1 ), .line2(\点阵显示_1_line2 ),
    .line3(\点阵显示_1_line3 ), .line4(\点阵显示_1_line4 ), .line5(\点阵显示_1_line5 ), .line6(\点阵显示_1_line6 ),
    .line7(\点阵显示_1_line7 ), .line8(\点阵显示_1_line8 ), .line9(\点阵显示_1_line9 ), .line10(\点阵显示_1_line10 ),
    .line11(\点阵显示_1_line11 ), .line12(\点阵显示_1_line12 ), .line13(\点阵显示_1_line13 ), .line14(\点阵显示_1_line14 ),
    .WHIT(\点阵显示_1_whit ), .line15(\点阵显示_1_line15 ), .line16(\点阵显示_1_line16 ), .line17(\点阵显示_1_line17 ),
    .line18(\点阵显示_1_line18 ), .line19(\点阵显示_1_line19 ), .line20(\点阵显示_1_line20 ), .line21(\点阵显示_1_line21 ),
    .line22(\点阵显示_1_line22 ), .line23(\点阵显示_1_line23 ), .line24(\点阵显示_1_line24 ), .line25(\点阵显示_1_line25 ),
    .line26(\点阵显示_1_line26 ), .line27(\点阵显示_1_line27 ), .line28(\点阵显示_1_line28 ), .line29(\点阵显示_1_line29 ),
    .line30(\点阵显示_1_line30 ), .line31(\点阵显示_1_line31 ), .line32(\点阵显示_1_line32 ), .BHIT(\得分 ), .\end (\结束 ));
  DotMatrix #(.inputtype("row"), .matrixcols(32), .matrixrows(32)) dotmatrix_1 (
    .row0(\点阵显示_1_line1 ), .row1(\点阵显示_1_line2 ), .row2(\点阵显示_1_line3 ), .row3(\点阵显示_1_line4 ),
    .row4(\点阵显示_1_line5 ), .row5(\点阵显示_1_line6 ), .row6(\点阵显示_1_line7 ), .row7(\点阵显示_1_line8 ),
    .row8(\点阵显示_1_line9 ), .row9(\点阵显示_1_line10 ), .row10(\点阵显示_1_line11 ), .row11(\点阵显示_1_line12 ),
    .row12(\点阵显示_1_line13 ), .row13(\点阵显示_1_line14 ), .row14(\点阵显示_1_line15 ), .row15(\点阵显示_1_line16 ),
    .row16(\点阵显示_1_line17 ), .row17(\点阵显示_1_line18 ), .row18(\点阵显示_1_line19 ), .row19(\点阵显示_1_line20 ),
    .row20(\点阵显示_1_line21 ), .row21(\点阵显示_1_line22 ), .row22(\点阵显示_1_line23 ), .row23(\点阵显示_1_line24 ),
    .row24(\点阵显示_1_line25 ), .row25(\点阵显示_1_line26 ), .row26(\点阵显示_1_line27 ), .row27(\点阵显示_1_line28 ),
    .row28(\点阵显示_1_line29 ), .row29(\点阵显示_1_line30 ), .row30(\点阵显示_1_line31 ), .row31(\点阵显示_1_line32 ));
  Keyboard keyboard_1 (.clk(CLK), .clr(RST), .data(keyboard_1_data));  // open: re, avail
  \键盘输入  \u_键盘输入_1  (.UP_W(\上 ), .Down_S(\下 ), .\键盘输入 (keyboard_1_data), .CLK(CLK), .RST(RST));
  Counter #(.behavior("old")) counter_2 (
    .count(1'b1), .Q(counter_2_q), .clk(\得分 ), .clr(RST));  // open: load, D, carry, preset
  Comparator comparator_2 (.a(8'h64), .b(counter_2_q), .lt(comparator_2_lt));  // open: gt, eq
  D_Flip_Flop #(.Pre_Clr_Positions("LEGACY"), .enable("true"), .NewFFLayout("false")) d_ff_1 (
    .clk(\开始 ), .D(1'b1), .Q(d_ff_1_q), .reset(or_1_out));  // open: Qn, preset, en
  or or_1 (or_1_out, \结束 , RST);
  or or_2 (\结束 , comparator_1_lt, comparator_2_lt);
  bgm bgm_1 (
    .\频率延缓倍数 (16'h21), .CLK(CLK), .play(d_ff_1_q), .RST(RST), .out_5(bgm_1_out_5), .Enable(bgm_1_enable),
    .\音量 (\bgm_1_音量 ));
  // Buzzer #(.vol_width(1)) buzzer_1: pin names not known; wires that end beside it: bgm_1_out_5, bgm_1_enable, \bgm_1_音量 
endmodule

module \键盘输入  (
  input  [6:0] \键盘输入 ,
  input  CLK,
  input  RST,
  output UP_W,
  output Down_S
);

  wire comparator_1_eq, comparator_2_eq;

  Comparator #(.width(7)) comparator_1 (.a(\键盘输入 ), .b(7'b1110111), .eq(comparator_1_eq));  // open: gt, lt
  Comparator #(.width(7)) comparator_2 (.a(\键盘输入 ), .b(7'b1110011), .eq(comparator_2_eq));  // open: gt, lt
  Register #(.width(1), .Select("low")) register_1 (.D(comparator_1_eq), .Q(UP_W), .clk(CLK), .clr(RST));  // open: en
  Register #(.width(1), .Select("low")) register_2 (.D(comparator_2_eq), .Q(Down_S), .clk(CLK), .clr(RST));  // open: en
endmodule

module \频率转换  (
  input  [15:0] \延缓倍数 ,
  input  \原CLK ,
  input  RST,
  output \后CLK 
);

  wire comparator_1_eq, comparator_2_eq, comparator_2_gt, or_1_out;
  wire [15:0] counter_1_q, shifter_1_out;

  Shifter #(.width(16), .shift("lr")) shifter_1 (.in(\延缓倍数 ), .\dist (4'b0001), .out(shifter_1_out));
  Counter #(.width(16), .max('hffff)) counter_1 (
    .load(comparator_1_eq), .D({16{1'b0}}), .Q(counter_1_q), .clk(\原CLK ), .clr(RST));  // open: count, carry, preset, down
  Comparator #(.width(16), .mode("unsigned")) comparator_1 (
    .a(\延缓倍数 ), .b(counter_1_q), .eq(comparator_1_eq));  // open: gt, lt
  Comparator #(.width(16), .mode("unsigned")) comparator_2 (
    .a(shifter_1_out), .b(counter_1_q), .gt(comparator_2_gt), .eq(comparator_2_eq));  // open: lt
  or or_1 (or_1_out, comparator_2_gt, comparator_2_eq);
  Multiplexer #(.enable("false")) multiplexer_1 (.in0(1'b1), .in1(1'b0), .out(\后CLK ), .sel(or_1_out));
endmodule

module bgm (
  input  [15:0] \频率延缓倍数 ,
  input  CLK,
  input  play,
  input  RST,
  output [13:0] out_5,
  output Enable,
  output \音量 
);

  wire Now_CLK;
  wire [31:0] adder_1_out, PC_q;
  wire [31:14] \主_data ;

  Register #(.width(32), .Select("low")) PC (.D(adder_1_out), .en(play), .Q(PC_q), .clk(Now_CLK), .clr(RST));
  \频率转换  \u_频率转换_1  (.\延缓倍数 (\频率延缓倍数 ), .\原CLK (CLK), .RST(RST), .\后CLK (Now_CLK));
  Adder #(.width(32)) adder_1 (.a(PC_q), .b(32'h4), .out(adder_1_out), .cout(RST));  // open: cin
  ROM #(.addrWidth(10), .dataWidth(32), .Select("high")) \u_主  (.addr(PC_q[11:2]), .data({\主_data , out_5}));

  assign Enable = play;
  assign \音量  = play;

  // Notes on the sheet:
  //   contents of 主 (hex, n*v repeats v):
  //   526 620 620 6ec 620 526 416 416 497 526 526 497 416 497 526 620 620 6ec 620 526 416 416 497 526 526
  //   497 497 416 57c 57c 526 57c 6ec 0 620 620 526 497 526 620 620 6ec 620 526 416 416 497 526 526 497
  //   497 416 526 620 620 6ec 620 526 416 416 497 526 526 497 416 497 526 620 620 6ec 620 526 416 416 497
  //   526 526 497 497 416 57c 57c 526 57c 6ec 0 620 620 526 497 526 620 620 6ec 620 526 416 416 497 526
  //   526 497 497 416 526 620 620 6ec 620 526 416 416 497 526 526 497 416 497 526 620 620 6ec 620 526 416
  //   416 497 526 526 497 497 416 57c 57c 526 57c 6ec 0 620 620 526 497 526 620 620 6ec 620 526 416 416
  //   497 526 526 497 497 416 526 620 620 6ec 620 526 416 416 497 526 526 497 416 497 526 620 620 6ec 620
  //   526 416 416 497 526 526 497 497 416 57c 57c 526 57c 6ec 0 620 620 526 497 526 620 620 6ec 620 526
  //   416 416 497 526 526 497 497 416 526 620 620 6ec 620 526 416 416 497 526 526 497 416 497 526 620 620
  //   6ec 620 526 416 416 497 526 526 497 497 416 57c 57c 526 57c 6ec 0 620 620 526 497 526 620 620 6ec
  //   620 526 416 416 497 526 526 497 497 416 526 620 620 6ec 620 526 416 416 497 526 526 497 416 497 526
  //   620 620 6ec 620 526 416 416 497 526 526 497 497 416 57c 57c 526 57c 6ec 0 620 620 526 497 526 620
  //   620 6ec 620 526 416 416 497 526 526 497 497 416 526 620 620 6ec 620 526 416 416 497 526 526 497 416
  //   497 526 620 620 6ec 620 526 416 416 497 526 526 497 497 416 57c 57c 526 57c 6ec 0 620 620 526 497
  //   526 620 620 6ec 620 526 416 416 497 526 526 497 497 416 526 620 620 6ec 620 526 416 416 497 526 526
  //   497 416 497 526 620 620 6ec 620 526 416 416 497 526 526 497 497 416 57c 57c 526 57c 6ec 0 620 620
  //   526 497 526 620 620 6ec 620 526 416 416 497 526 526 497 497 416 526 620 620 6ec 620 526 416 416 497
  //   526 526 497 416 497 526 620 620 6ec 620 526 416 416 497 526 526 497 497 416 57c 57c 526 57c 6ec 0
  //   620 620 526 497 526 620 620 6ec 620 526 416 416 497 526 526 497 497 416 526 620 620 6ec 620 526 416
  //   416 497 526 526 497 416 497 526 620 620 6ec 620 526 416 416 497 526 526 497 497 416 57c 57c 526 57c
  //   6ec 0 620 620 526 497 526 620 620 6ec 620 526 416 416 497 526 526 497 497 416
endmodule
